// Logisim project Circuit.circ as structural Verilog
module half_adder (
  input  A,
  input  B,
  output sum,
  output carry_out
);

  xor xor_1 (sum, A, B);
  and and_1 (carry_out, A, B);
endmodule

module full_adder (
  input  A,
  input  B,
  input  Cin,
  output Sum_out,
  output carry_out
);

  wire half_adder_1_carry_out, half_adder_1_sum, half_adder_2_carry_out;

  half_adder half_adder_1 (.A(A), .B(B), .sum(half_adder_1_sum), .carry_out(half_adder_1_carry_out));
  half_adder half_adder_2 (.A(half_adder_1_sum), .B(Cin), .sum(Sum_out), .carry_out(half_adder_2_carry_out));
  or or_1 (carry_out, half_adder_2_carry_out, half_adder_1_carry_out);
endmodule

module two_bit_adder (
  input  cin,
  input  [1:0] A,
  input  [1:0] B,
  output [1:0] sum_out,
  output carry_out
);

  wire full_adder_1_carry_out;

  full_adder full_adder_1 (.A(A[0]), .B(B[0]), .Cin(cin), .Sum_out(sum_out[0]), .carry_out(full_adder_1_carry_out));
  full_adder full_adder_2 (
    .A(A[1]), .B(B[1]), .Cin(full_adder_1_carry_out), .Sum_out(sum_out[1]), .carry_out(carry_out));
endmodule

module four_bit_adder (
  input  cin,
  input  [3:0] A,
  input  [3:0] B,
  output [3:0] sum_out,
  output cout
);

  wire two_bit_adder_1_carry_out;

  two_bit_adder two_bit_adder_1 (
    .cin(cin), .A(A[1:0]), .B(B[1:0]), .sum_out(sum_out[1:0]), .carry_out(two_bit_adder_1_carry_out));
  two_bit_adder two_bit_adder_2 (
    .cin(two_bit_adder_1_carry_out), .A(A[3:2]), .B(B[3:2]), .sum_out(sum_out[3:2]), .carry_out(cout));
endmodule

module eight_bit_adder (
  input  cin,
  input  [7:0] A,
  input  [7:0] B,
  output [7:0] sum_out,
  output cout
);

  wire four_bit_adder_1_cout;

  four_bit_adder four_bit_adder_1 (
    .cin(cin), .A(A[3:0]), .B(B[3:0]), .sum_out(sum_out[3:0]), .cout(four_bit_adder_1_cout));
  four_bit_adder four_bit_adder_2 (
    .cin(four_bit_adder_1_cout), .A(A[7:4]), .B(B[7:4]), .sum_out(sum_out[7:4]), .cout(cout));
endmodule

module sixteen_bit_adder (
  input  cin,
  input  [15:0] A,
  input  [15:0] B,
  output [15:0] sum_out,
  output cout
);

  wire eight_bit_adder_1_cout;

  eight_bit_adder eight_bit_adder_1 (
    .cin(cin), .A(A[7:0]), .B(B[7:0]), .sum_out(sum_out[7:0]), .cout(eight_bit_adder_1_cout));
  eight_bit_adder eight_bit_adder_2 (
    .cin(eight_bit_adder_1_cout), .A(A[15:8]), .B(B[15:8]), .sum_out(sum_out[15:8]), .cout(cout));
endmodule

module thirtyTwo_bit_Adder (
  input  cin,
  input  [31:0] A,
  input  [31:0] B,
  output [31:0] sum_out,
  output cout
);

  wire sixteen_bit_adder_1_cout;

  sixteen_bit_adder sixteen_bit_adder_1 (
    .cin(cin), .A(A[15:0]), .B(B[15:0]), .sum_out(sum_out[15:0]), .cout(sixteen_bit_adder_1_cout));
  sixteen_bit_adder sixteen_bit_adder_2 (
    .cin(sixteen_bit_adder_1_cout), .A(A[31:16]), .B(B[31:16]), .sum_out(sum_out[31:16]), .cout(cout));
endmodule

module sixtyFour_bit_Adder (
  input  cin,
  input  [63:0] A,
  input  [63:0] B,
  output [63:0] sum_out,
  output cout
);

  wire thirtytwo_bit_adder_1_cout;

  thirtyTwo_bit_Adder thirtytwo_bit_adder_1 (
    .cin(cin), .A(A[31:0]), .B(B[31:0]), .sum_out(sum_out[31:0]), .cout(thirtytwo_bit_adder_1_cout));
  thirtyTwo_bit_Adder thirtytwo_bit_adder_2 (
    .cin(thirtytwo_bit_adder_1_cout), .A(A[63:32]), .B(B[63:32]), .sum_out(sum_out[63:32]), .cout(cout));
endmodule

module matrixAdder2x2Core (
  input  [63:0] A11,
  input  [63:0] A12,
  input  [63:0] A21,
  input  [63:0] A22,
  input  [63:0] B11,
  input  [63:0] B12,
  input  [63:0] B21,
  input  [63:0] B22,
  output [63:0] R11,
  output [63:0] R12,
  output [63:0] R21,
  output [63:0] R22
);

  sixtyFour_bit_Adder Node_1 (.A(A11), .B(B11), .sum_out(R11));  // open: cin, cout
  sixtyFour_bit_Adder Node_3 (.A(A21), .B(B21), .sum_out(R21));  // open: cin, cout
  sixtyFour_bit_Adder Node_2 (.A(A12), .B(B12), .sum_out(R12));  // open: cin, cout
  sixtyFour_bit_Adder Node_4 (.A(A22), .B(B22), .sum_out(R22));  // open: cin, cout
endmodule

module testBench (
  input  [63:0] in_1,
  input  [63:0] in_2,
  input  [63:0] in_3,
  input  [63:0] in_4,
  input  [63:0] in_5,
  input  [63:0] in_6,
  input  [63:0] in_7,
  input  [63:0] in_8,
  output [63:0] out_9,
  output [63:0] out_10,
  output [63:0] out_11,
  output [63:0] out_12
);

  matrixAdder2x2Core matrixadder2x2core_1 (
    .A11(in_1), .A12(in_2), .A21(in_3), .A22(in_4), .B11(in_5), .B12(in_7), .B21(in_8), .B22(in_6),
    .R11(out_9), .R12(out_10), .R21(out_11), .R22(out_12));
endmodule

module Assembly (
  input  OUTPUT_ENABLE,
  input  write_ENNBLE,
  input  WRITE_ENABLE
);

  wire clock_1_out, Delay_Counter_carry;
  wire [3:0] counter_1_q;
  wire [63:0] mat_mult_node_1_r11, mat_mult_node_1_r12, mat_mult_node_1_r21, mat_mult_node_1_r22, R_11_dout,
       RAM_A11_dout, RAM_A12_dout, RAM_A21_dout, RAM_A22_dout, RAM_B11_dout, RAM_B12_dout, RAM_B21_dout,
       RAM_B22_dout, undriven;

  Clock clock_1 (.out(clock_1_out));
  RAM #(.addrWidth(4), .dataWidth(64), .\type ("nonvolatile")) RAM_A11 (
    .addr(counter_1_q), .we(write_ENNBLE), .oe(1'b1), .clk(clock_1_out), .dout(RAM_A11_dout));  // open: din
  // Probe on RAM_A21_dout
  // Probe on RAM_B21_dout
  Counter #(.max('h2), .width(4)) Delay_Counter (
    .count(clock_1_out), .clk(clock_1_out), .carry(Delay_Counter_carry));  // open: clr, load, up, D, Q
  // Probe on RAM_A11_dout
  RAM #(.addrWidth(4), .dataWidth(64), .\type ("nonvolatile")) RAM_A12 (
    .addr(counter_1_q), .we(write_ENNBLE), .clk(clock_1_out), .dout(RAM_A12_dout));  // open: oe, din
  Counter #(.max('h7), .width(4)) counter_1 (
    .count(Delay_Counter_carry), .clk(clock_1_out), .Q(counter_1_q));  // open: clr, load, up, D, carry
  mat_mult_node mat_mult_node_1 (
    .A11(RAM_A11_dout), .A12(RAM_A12_dout), .A21(RAM_A21_dout), .A22(RAM_A22_dout), .B11(RAM_B11_dout),
    .B12(RAM_B12_dout), .B21(RAM_B21_dout), .B22(RAM_B22_dout), .R11(mat_mult_node_1_r11),
    .R12(mat_mult_node_1_r12), .R21(mat_mult_node_1_r21), .R22(mat_mult_node_1_r22));
  RAM #(.addrWidth(4), .dataWidth(64), .\type ("nonvolatile")) RAM_A21 (
    .addr(counter_1_q), .we(write_ENNBLE), .oe(1'b1), .clk(clock_1_out), .dout(RAM_A21_dout));  // open: din
  // Probe on mat_mult_node_1_r11
  // Probe on mat_mult_node_1_r12
  RAM #(.addrWidth(4), .dataWidth(64), .\type ("nonvolatile")) RAM_A22 (
    .addr(counter_1_q), .we(write_ENNBLE), .oe(1'b1), .clk(clock_1_out), .dout(RAM_A22_dout));  // open: din
  RAM #(.addrWidth(4), .dataWidth(64)) R_11 (
    .addr(counter_1_q), .we(1'b1), .clk(clock_1_out), .din(mat_mult_node_1_r11), .dout(R_11_dout));  // open: oe
  // Probe on mat_mult_node_1_r21
  RAM #(.addrWidth(4), .dataWidth(64), .\type ("nonvolatile")) RAM_B11 (
    .addr(counter_1_q), .we(write_ENNBLE), .oe(1'b1), .clk(clock_1_out), .din(undriven), .dout(RAM_B11_dout));
  // Probe on mat_mult_node_1_r22
  RAM #(.addrWidth(4), .dataWidth(64), .\type ("nonvolatile")) RAM_B12 (
    .addr(counter_1_q), .we(write_ENNBLE), .oe(1'b1), .clk(clock_1_out), .dout(RAM_B12_dout));  // open: din
  RAM #(.addrWidth(4), .dataWidth(64)) R_12 (
    .addr(counter_1_q), .we(1'b1), .clk(clock_1_out), .din(mat_mult_node_1_r12));  // open: oe, dout
  RAM #(.addrWidth(4), .dataWidth(64), .\type ("nonvolatile")) RAM_B21 (
    .addr(counter_1_q), .we(write_ENNBLE), .oe(1'b1), .clk(clock_1_out), .dout(RAM_B21_dout));  // open: din
  // Probe on mat_mult_node_1_r22
  RAM #(.addrWidth(4), .dataWidth(64)) R_21 (
    .addr(counter_1_q), .we(1'b1), .clk(clock_1_out), .din(mat_mult_node_1_r22));  // open: oe, dout
  RAM #(.addrWidth(4), .dataWidth(64), .\type ("nonvolatile")) RAM_B22 (
    .addr(counter_1_q), .we(write_ENNBLE), .oe(1'b1), .clk(clock_1_out), .dout(RAM_B22_dout));  // open: din
  RAM #(.addrWidth(4), .dataWidth(64)) R_22 (
    .addr(counter_1_q), .we(1'b1), .clk(clock_1_out), .din(mat_mult_node_1_r21));  // open: oe, dout

  // Notes on the sheet:
  //   Matrix_A
  //   Matrix_B
endmodule

module counterdemo (
  input  in_1,
  input  in_2,
  input  in_3,
  input  in_4,
  input  [3:0] in_5,
  output [3:0] out_6
);

  Counter #(.max('h3), .ongoal("load"), .width(4)) counter_1 (
    .load(in_1), .up(in_2), .count(in_3), .clk(in_4), .D(in_5), .Q(out_6));  // open: clr, carry
endmodule

module assembly2 (
  input  OUTPUT_ENABLE,
  input  WE,
  input  OE,
  input  WRITE_ENABLE
);

  wire clock_1_out, Delay_Counter_carry;
  wire [4:0] counter_1_q;
  wire [63:0] matrixadder2x2core_1_r11, matrixadder2x2core_1_r12, matrixadder2x2core_1_r21,
       matrixadder2x2core_1_r22, R_11_dout, R_12_dout, R_21_dout, R_22_dout, RAM_A11_dout, RAM_A12_dout,
       RAM_A21_dout, RAM_A22_dout, RAM_B11_dout, RAM_B12_dout, RAM_B21_dout, RAM_B22_dout;

  Clock clock_1 (.out(clock_1_out));
  RAM #(.addrWidth(5), .dataWidth(64), .\type ("nonvolatile")) RAM_A11 (
    .addr(counter_1_q), .we(WE), .oe(1'b1), .clk(clock_1_out), .din(R_11_dout), .dout(RAM_A11_dout));
  // Probe on RAM_B12_dout
  Counter #(.max('h2), .width(4)) Delay_Counter (
    .count(clock_1_out), .clk(clock_1_out), .carry(Delay_Counter_carry));  // open: clr, load, up, D, Q
  // Probe on RAM_A12_dout
  // Probe on RAM_A11_dout
  RAM #(.addrWidth(5), .dataWidth(64), .\type ("nonvolatile")) RAM_A12 (
    .addr(counter_1_q), .oe(1'b1), .clk(clock_1_out), .din(R_21_dout), .dout(RAM_A12_dout));  // open: we
  Counter #(.max('h7), .width(5)) counter_1 (
    .count(Delay_Counter_carry), .clk(clock_1_out), .Q(counter_1_q));  // open: clr, load, up, D, carry
  matrixAdder2x2Core matrixadder2x2core_1 (
    .A11(RAM_A11_dout), .A12(RAM_A12_dout), .A21(RAM_A21_dout), .A22(RAM_A22_dout), .B11(RAM_B11_dout),
    .B12(RAM_B12_dout), .B21(RAM_B21_dout), .B22(RAM_B22_dout), .R11(matrixadder2x2core_1_r11),
    .R12(matrixadder2x2core_1_r12), .R21(matrixadder2x2core_1_r21), .R22(matrixadder2x2core_1_r22));
  RAM #(.addrWidth(5), .dataWidth(64), .\type ("nonvolatile")) RAM_A21 (
    .addr(counter_1_q), .we(WE), .oe(1'b1), .clk(clock_1_out), .dout(RAM_A21_dout));  // open: din
  // Probe on matrixadder2x2core_1_r11
  // Probe on matrixadder2x2core_1_r12
  RAM #(.addrWidth(5), .dataWidth(64), .\type ("nonvolatile")) RAM_A22 (
    .addr(counter_1_q), .we(WE), .oe(1'b1), .clk(clock_1_out), .dout(RAM_A22_dout));  // open: din
  RAM #(.addrWidth(5), .dataWidth(64)) R_11 (
    .addr(counter_1_q), .we(1'b1), .oe(OE), .clk(clock_1_out), .din(matrixadder2x2core_1_r11),
    .dout(R_11_dout));
  // Probe on matrixadder2x2core_1_r21
  RAM #(.addrWidth(5), .dataWidth(64), .\type ("nonvolatile")) RAM_B11 (
    .addr(counter_1_q), .we(WE), .oe(1'b1), .clk(clock_1_out), .din(R_12_dout), .dout(RAM_B11_dout));
  // Probe on matrixadder2x2core_1_r12
  RAM #(.addrWidth(5), .dataWidth(64), .\type ("nonvolatile")) RAM_B12 (
    .addr(counter_1_q), .we(WE), .oe(1'b1), .clk(clock_1_out), .din(R_22_dout), .dout(RAM_B12_dout));
  RAM #(.addrWidth(5), .dataWidth(64)) R_12 (
    .addr(counter_1_q), .we(1'b1), .oe(OE), .clk(clock_1_out), .din(matrixadder2x2core_1_r12),
    .dout(R_12_dout));
  RAM #(.addrWidth(5), .dataWidth(64), .\type ("nonvolatile")) RAM_B21 (
    .addr(counter_1_q), .we(WE), .oe(1'b1), .clk(clock_1_out), .dout(RAM_B21_dout));  // open: din
  RAM #(.addrWidth(5), .dataWidth(64)) R_21 (
    .addr(counter_1_q), .we(1'b1), .oe(OE), .clk(clock_1_out), .din(matrixadder2x2core_1_r22),
    .dout(R_21_dout));
  RAM #(.addrWidth(5), .dataWidth(64), .\type ("nonvolatile")) RAM_B22 (
    .addr(counter_1_q), .we(WE), .oe(1'b1), .clk(clock_1_out), .dout(RAM_B22_dout));  // open: din
  RAM #(.addrWidth(5), .dataWidth(64)) R_22 (
    .addr(counter_1_q), .we(1'b1), .oe(OE), .clk(clock_1_out), .din(matrixadder2x2core_1_r21),
    .dout(R_22_dout));

  // Notes on the sheet:
  //   Matrix_A
  //   Matrix_B
endmodule

module test_assembly (
  input  OUTPUT_ENABLE,
  input  WE,
  input  OE,
  input  WRITE_ENABLE
);

  wire clock_1_out, Delay_Counter_carry;
  wire [4:0] counter_1_q, counter_2_q;
  wire [63:0] matrixadder2x2core_1_r11, matrixadder2x2core_1_r12, matrixadder2x2core_1_r21,
       matrixadder2x2core_1_r22, R_11_dout, R_12_dout, R_21_dout, R_22_dout, RAM_A11_dout, RAM_A12_dout,
       RAM_A21_dout, RAM_A22_dout, RAM_B11_dout, RAM_B12_dout, RAM_B21_dout, RAM_B22_dout;

  Clock clock_1 (.out(clock_1_out));
  RAM #(.addrWidth(5), .dataWidth(64), .\type ("nonvolatile")) RAM_A11 (
    .addr(counter_2_q), .we(WE), .oe(1'b1), .clk(clock_1_out), .din(R_11_dout), .dout(RAM_A11_dout));
  // Probe on RAM_B12_dout
  Counter #(.max('h2), .width(4)) Delay_Counter (
    .count(clock_1_out), .clk(clock_1_out), .carry(Delay_Counter_carry));  // open: clr, load, up, D, Q
  // Probe on RAM_A12_dout
  // Probe on RAM_A11_dout
  Counter #(.max('h7), .width(5)) counter_1 (
    .clk(clock_1_out), .Q(counter_1_q));  // open: clr, load, up, count, D, carry
  RAM #(.addrWidth(5), .dataWidth(64), .\type ("nonvolatile")) RAM_A12 (
    .addr(counter_2_q), .oe(1'b1), .clk(clock_1_out), .din(R_21_dout), .dout(RAM_A12_dout));  // open: we
  Counter #(.max('h18), .width(5)) counter_2 (
    .count(Delay_Counter_carry), .clk(clock_1_out), .Q(counter_2_q));  // open: clr, load, up, D, carry
  matrixAdder2x2Core matrixadder2x2core_1 (
    .A11(RAM_A11_dout), .A12(RAM_A12_dout), .A21(RAM_A21_dout), .A22(RAM_A22_dout), .B11(RAM_B11_dout),
    .B12(RAM_B12_dout), .B21(RAM_B21_dout), .B22(RAM_B22_dout), .R11(matrixadder2x2core_1_r11),
    .R12(matrixadder2x2core_1_r12), .R21(matrixadder2x2core_1_r21), .R22(matrixadder2x2core_1_r22));
  RAM #(.addrWidth(5), .dataWidth(64), .\type ("nonvolatile")) RAM_A21 (
    .addr(counter_2_q), .we(WE), .oe(1'b1), .clk(clock_1_out), .dout(RAM_A21_dout));  // open: din
  // Probe on matrixadder2x2core_1_r11
  // Probe on matrixadder2x2core_1_r12
  RAM #(.addrWidth(5), .dataWidth(64), .\type ("nonvolatile")) RAM_A22 (
    .addr(counter_2_q), .we(WE), .oe(1'b1), .clk(clock_1_out), .dout(RAM_A22_dout));  // open: din
  RAM #(.addrWidth(5), .dataWidth(64)) R_11 (
    .addr(counter_1_q), .we(1'b1), .oe(OE), .clk(clock_1_out), .din(matrixadder2x2core_1_r11),
    .dout(R_11_dout));
  // Probe on matrixadder2x2core_1_r21
  RAM #(.addrWidth(5), .dataWidth(64), .\type ("nonvolatile")) RAM_B11 (
    .addr(counter_2_q), .we(WE), .oe(1'b1), .clk(clock_1_out), .din(R_12_dout), .dout(RAM_B11_dout));
  // Probe on matrixadder2x2core_1_r12
  RAM #(.addrWidth(5), .dataWidth(64), .\type ("nonvolatile")) RAM_B12 (
    .addr(counter_2_q), .we(WE), .oe(1'b1), .clk(clock_1_out), .din(R_22_dout), .dout(RAM_B12_dout));
  RAM #(.addrWidth(5), .dataWidth(64)) R_12 (
    .addr(counter_1_q), .we(1'b1), .oe(OE), .clk(clock_1_out), .din(matrixadder2x2core_1_r12),
    .dout(R_12_dout));
  RAM #(.addrWidth(5), .dataWidth(64), .\type ("nonvolatile")) RAM_B21 (
    .addr(counter_2_q), .we(WE), .oe(1'b1), .clk(clock_1_out), .dout(RAM_B21_dout));  // open: din
  RAM #(.addrWidth(5), .dataWidth(64)) R_21 (
    .addr(counter_1_q), .we(1'b1), .oe(OE), .clk(clock_1_out), .din(matrixadder2x2core_1_r22),
    .dout(R_21_dout));
  RAM #(.addrWidth(5), .dataWidth(64), .\type ("nonvolatile")) RAM_B22 (
    .addr(counter_2_q), .we(WE), .oe(1'b1), .clk(clock_1_out), .dout(RAM_B22_dout));  // open: din
  RAM #(.addrWidth(5), .dataWidth(64)) R_22 (
    .addr(counter_1_q), .we(1'b1), .oe(OE), .clk(clock_1_out), .din(matrixadder2x2core_1_r21),
    .dout(R_22_dout));

  // Notes on the sheet:
  //   Matrix_A
  //   Matrix_B
endmodule

module multiplier_Core (
  input  [63:0] A11,
  input  [63:0] B11,
  input  [63:0] A12,
  input  [63:0] B12,
  input  [63:0] A21,
  input  [63:0] B21,
  input  [63:0] A22,
  input  [63:0] B22,
  output [63:0] R11,
  output [63:0] xtra64bits,
  output [63:0] R12,
  output [63:0] xtra64bits2,
  output [63:0] R21,
  output [63:0] xtra64bits3,
  output [63:0] R22,
  output [63:0] xtra64bits4
);

  // Probe on A11
  // Probe on A12
  // Probe on A21
  // Probe on A22
  // Probe on B11
  // Probe on B12
  // Probe on B21
  // Probe on B22
  Multiplier #(.width(64)) multiplier_1 (.a(A11), .b(B11), .out(R11), .cout(xtra64bits));  // open: cin
  Multiplier #(.width(64)) multiplier_2 (.a(A12), .b(B12), .out(R12), .cout(xtra64bits2));  // open: cin
  Multiplier #(.width(64)) multiplier_3 (.a(A21), .b(B21), .out(R21), .cout(xtra64bits3));  // open: cin
  Multiplier #(.width(64)) multiplier_4 (.a(A22), .b(B22), .out(R22), .cout(xtra64bits4));  // open: cin
  // Probe on R11
  // Probe on R12
  // Probe on R21
  // Probe on R22
endmodule

module mat_mult_node (
  input  [63:0] A11,
  input  [63:0] A12,
  input  [63:0] A21,
  input  [63:0] A22,
  input  [63:0] B11,
  input  [63:0] B12,
  input  [63:0] B21,
  input  [63:0] B22,
  output [63:0] R11,
  output [63:0] R12,
  output [63:0] R21,
  output [63:0] R22
);

  wire [63:0] multiplier_1_out, multiplier_2_out, multiplier_3_out, multiplier_4_out, multiplier_5_out,
       multiplier_6_out, multiplier_7_out, multiplier_8_out;

  // Probe on A12
  // Probe on B11
  // Probe on B21
  // Probe on A11
  // Probe on A21
  // Probe on B11
  Multiplier #(.width(64)) multiplier_1 (.a(A11), .b(B11), .out(multiplier_1_out));  // open: cin, cout
  Multiplier #(.width(64)) multiplier_2 (.a(A12), .b(B21), .out(multiplier_2_out));  // open: cin, cout
  Multiplier #(.width(64)) multiplier_3 (.a(A11), .b(B12), .out(multiplier_3_out));  // open: cin, cout
  Multiplier #(.width(64)) multiplier_4 (.a(A12), .b(B22), .out(multiplier_4_out));  // open: cin, cout
  Multiplier #(.width(64)) multiplier_5 (.a(A21), .b(B11), .out(multiplier_5_out));  // open: cin, cout
  Multiplier #(.width(64)) multiplier_6 (.a(A22), .b(B21), .out(multiplier_6_out));  // open: cin, cout
  Multiplier #(.width(64)) multiplier_7 (.a(A21), .b(B12), .out(multiplier_7_out));  // open: cin, cout
  Multiplier #(.width(64)) multiplier_8 (.a(A22), .b(B22), .out(multiplier_8_out));  // open: cin, cout
  // Probe on multiplier_1_out
  // Probe on multiplier_3_out
  // Probe on multiplier_7_out
  // Probe on multiplier_2_out
  // Probe on multiplier_4_out
  // Probe on multiplier_5_out
  // Probe on multiplier_6_out
  // Probe on multiplier_8_out
  sixtyFour_bit_Adder sixtyfour_bit_adder_1 (
    .A(multiplier_1_out), .B(multiplier_2_out), .sum_out(R11));  // open: cin, cout
  sixtyFour_bit_Adder sixtyfour_bit_adder_2 (
    .A(multiplier_3_out), .B(multiplier_4_out), .sum_out(R12));  // open: cin, cout
  sixtyFour_bit_Adder sixtyfour_bit_adder_3 (
    .A(multiplier_5_out), .B(multiplier_6_out), .sum_out(R21));  // open: cin, cout
  sixtyFour_bit_Adder sixtyfour_bit_adder_4 (
    .A(multiplier_7_out), .B(multiplier_8_out), .sum_out(R22));  // open: cin, cout
  // Probe on R11
  // Probe on R12
  // Probe on R21
  // Probe on R22
endmodule

module Assembly_With_MatMult (
  input  OUTPUT_ENABLE,
  input  write_ENNBLE,
  input  WRITE_ENABLE
);

  wire clock_1_out, Delay_Counter_carry;
  wire [3:0] counter_1_q;
  wire [63:0] mat_mult_node_1_r11, mat_mult_node_1_r12, mat_mult_node_1_r21, mat_mult_node_1_r22, R_11_dout,
       RAM_A11_dout, RAM_A12_dout, RAM_A21_dout, RAM_A22_dout, RAM_B11_dout, RAM_B12_dout, RAM_B21_dout,
       RAM_B22_dout, undriven;

  Clock clock_1 (.out(clock_1_out));
  RAM #(.addrWidth(4), .dataWidth(64), .\type ("nonvolatile")) RAM_A11 (
    .addr(counter_1_q), .we(write_ENNBLE), .oe(1'b1), .clk(clock_1_out), .dout(RAM_A11_dout));  // open: din
  // Probe on RAM_A21_dout
  // Probe on RAM_B21_dout
  Counter #(.max('h2), .width(4)) Delay_Counter (
    .count(clock_1_out), .clk(clock_1_out), .carry(Delay_Counter_carry));  // open: clr, load, up, D, Q
  // Probe on RAM_A11_dout
  RAM #(.addrWidth(4), .dataWidth(64), .\type ("nonvolatile")) RAM_A12 (
    .addr(counter_1_q), .we(write_ENNBLE), .clk(clock_1_out), .dout(RAM_A12_dout));  // open: oe, din
  Counter #(.max('h7), .width(4)) counter_1 (
    .count(Delay_Counter_carry), .clk(clock_1_out), .Q(counter_1_q));  // open: clr, load, up, D, carry
  mat_mult_node mat_mult_node_1 (
    .A11(RAM_A11_dout), .A12(RAM_A12_dout), .A21(RAM_A21_dout), .A22(RAM_A22_dout), .B11(RAM_B11_dout),
    .B12(RAM_B12_dout), .B21(RAM_B21_dout), .B22(RAM_B22_dout), .R11(mat_mult_node_1_r11),
    .R12(mat_mult_node_1_r12), .R21(mat_mult_node_1_r21), .R22(mat_mult_node_1_r22));
  RAM #(.addrWidth(4), .dataWidth(64), .\type ("nonvolatile")) RAM_A21 (
    .addr(counter_1_q), .we(write_ENNBLE), .oe(1'b1), .clk(clock_1_out), .dout(RAM_A21_dout));  // open: din
  // Probe on mat_mult_node_1_r11
  // Probe on mat_mult_node_1_r12
  RAM #(.addrWidth(4), .dataWidth(64), .\type ("nonvolatile")) RAM_A22 (
    .addr(counter_1_q), .we(write_ENNBLE), .oe(1'b1), .clk(clock_1_out), .dout(RAM_A22_dout));  // open: din
  RAM #(.addrWidth(4), .dataWidth(64)) R_11 (
    .addr(counter_1_q), .we(1'b1), .clk(clock_1_out), .din(mat_mult_node_1_r11), .dout(R_11_dout));  // open: oe
  // Probe on mat_mult_node_1_r21
  RAM #(.addrWidth(4), .dataWidth(64), .\type ("nonvolatile")) RAM_B11 (
    .addr(counter_1_q), .we(write_ENNBLE), .oe(1'b1), .clk(clock_1_out), .din(undriven), .dout(RAM_B11_dout));
  // Probe on mat_mult_node_1_r22
  RAM #(.addrWidth(4), .dataWidth(64), .\type ("nonvolatile")) RAM_B12 (
    .addr(counter_1_q), .we(write_ENNBLE), .oe(1'b1), .clk(clock_1_out), .dout(RAM_B12_dout));  // open: din
  RAM #(.addrWidth(4), .dataWidth(64)) R_12 (
    .addr(counter_1_q), .we(1'b1), .clk(clock_1_out), .din(mat_mult_node_1_r12));  // open: oe, dout
  RAM #(.addrWidth(4), .dataWidth(64), .\type ("nonvolatile")) RAM_B21 (
    .addr(counter_1_q), .we(write_ENNBLE), .oe(1'b1), .clk(clock_1_out), .dout(RAM_B21_dout));  // open: din
  // Probe on mat_mult_node_1_r22
  RAM #(.addrWidth(4), .dataWidth(64)) R_21 (
    .addr(counter_1_q), .we(1'b1), .clk(clock_1_out), .din(mat_mult_node_1_r22));  // open: oe, dout
  RAM #(.addrWidth(4), .dataWidth(64), .\type ("nonvolatile")) RAM_B22 (
    .addr(counter_1_q), .we(write_ENNBLE), .oe(1'b1), .clk(clock_1_out), .dout(RAM_B22_dout));  // open: din
  RAM #(.addrWidth(4), .dataWidth(64)) R_22 (
    .addr(counter_1_q), .we(1'b1), .clk(clock_1_out), .din(mat_mult_node_1_r21));  // open: oe, dout

  // Notes on the sheet:
  //   Matrix_A
  //   Matrix_B
endmodule

module debugger_or_sumshi (
  input  [1:0] in_1,
  output ioe,
  output owe,
  output ooe,
  output iwe
);

  wire not_1_out;

  not not_1 (not_1_out, in_1[1]);
  and and_1 (ioe, ~in_1[0], ~in_1[1]);  // AND_Gate
  and and_2 (owe, in_1[0], not_1_out);
  and and_3 (ooe, ~in_1[0], in_1[1]);  // AND_Gate
  and and_4 (iwe, in_1[0], in_1[1]);
endmodule

module mat_mult_4x4 (
  input  [63:0] A11_11,
  input  [63:0] A11_12,
  input  [63:0] A11_21,
  input  [63:0] A11_22,
  input  [63:0] A12_11,
  input  [63:0] A12_12,
  input  [63:0] A12_21,
  input  [63:0] A12_22,
  input  [63:0] B11_11,
  input  [63:0] B11_12,
  input  [63:0] B11_21,
  input  [63:0] B11_22,
  input  [63:0] B21_11,
  input  [63:0] B21_12,
  input  [63:0] B21_21,
  input  [63:0] B21_22,
  output [63:0] R11,
  output [63:0] R12,
  output [63:0] R21,
  output [63:0] R22
);

  wire [63:0] mat_mult_node_1_r11, mat_mult_node_1_r12, mat_mult_node_1_r21, mat_mult_node_1_r22,
       mat_mult_node_2_r11, mat_mult_node_2_r12, mat_mult_node_2_r21, mat_mult_node_2_r22;

  // Probe on B11_12
  // Probe on B11_11
  // Probe on B21_11
  // Probe on B21_12
  // Probe on B21_21
  // Probe on B11_21
  // Probe on B21_22
  // Probe on A11_11
  // Probe on B11_22
  // Probe on A11_12
  // Probe on A12_11
  // Probe on A11_21
  // Probe on A12_12
  // Probe on A11_22
  // Probe on A12_21
  // Probe on A12_22
  // Probe on mat_mult_node_1_r22
  // Probe on mat_mult_node_1_r21
  // Probe on mat_mult_node_1_r12
  // Probe on mat_mult_node_1_r11
  mat_mult_node mat_mult_node_1 (
    .A11(A12_11), .A12(A12_12), .A21(A12_21), .A22(A12_22), .B11(B21_11), .B12(B21_12), .B21(B21_21),
    .B22(B21_22), .R11(mat_mult_node_1_r11), .R12(mat_mult_node_1_r12), .R21(mat_mult_node_1_r21),
    .R22(mat_mult_node_1_r22));
  // Probe on mat_mult_node_2_r11
  mat_mult_node mat_mult_node_2 (
    .A11(A11_11), .A12(A11_12), .A21(A11_21), .A22(A11_22), .B11(B11_11), .B12(B11_12), .B21(B11_21),
    .B22(B11_22), .R11(mat_mult_node_2_r11), .R12(mat_mult_node_2_r12), .R21(mat_mult_node_2_r21),
    .R22(mat_mult_node_2_r22));
  // Probe on mat_mult_node_2_r12
  // Probe on mat_mult_node_2_r22
  // Probe on mat_mult_node_2_r21
  // Probe on R21
  // Probe on R12
  // Probe on R11
  matrixAdder2x2Core matrixadder2x2core_1 (
    .A11(mat_mult_node_2_r11), .A12(mat_mult_node_2_r12), .A21(mat_mult_node_2_r21),
    .A22(mat_mult_node_2_r22), .B11(mat_mult_node_1_r11), .B12(mat_mult_node_1_r12),
    .B21(mat_mult_node_1_r21), .B22(mat_mult_node_1_r22), .R11(R11), .R12(R12), .R21(R21), .R22(R22));
  // Probe on R22

  // Notes on the sheet:
  //   A11
  //   A12
  //   B11
  //   B21
endmodule

module Assembly_4x4_mat_mult (
);

  wire clock_1_out, counter_1_carry, counter_2_carry, counter_3_carry;
  wire [3:0] counter_3_q, counter_4_q, counter_5_q;
  wire [63:0] A11_11_dout, A11_12_dout, A11_21_dout, A11_22_dout, A12_11_dout, A12_12_dout, A12_21_dout,
       A12_22_dout, B11_11_dout, B11_12_dout, B11_21_dout, B11_22_dout, B12_11_dout, B12_12_dout,
       B12_21_dout, B12_22_dout, mat_mult_4x4_1_r11, mat_mult_4x4_1_r12, mat_mult_4x4_1_r21,
       mat_mult_4x4_1_r22;

  RAM #(.addrWidth(4), .dataWidth(64), .\type ("nonvolatile")) B11_11 (
    .addr(counter_3_q), .oe(1'b1), .clk(clock_1_out), .dout(B11_11_dout));  // open: we, din
  RAM #(.addrWidth(4), .dataWidth(64), .\type ("nonvolatile")) B11_12 (
    .addr(counter_3_q), .oe(1'b1), .clk(clock_1_out), .dout(B11_12_dout));  // open: we, din
  // Probe on B11_11_dout
  // Probe on B11_12_dout
  RAM #(.addrWidth(4), .dataWidth(64), .\type ("nonvolatile")) B11_21 (
    .addr(counter_3_q), .oe(1'b1), .clk(clock_1_out), .dout(B11_21_dout));  // open: we, din
  RAM #(.addrWidth(4), .dataWidth(64), .\type ("nonvolatile")) B11_22 (
    .addr(counter_3_q), .oe(1'b1), .clk(clock_1_out), .dout(B11_22_dout));  // open: we, din
  // Probe on B11_21_dout
  // Probe on B11_22_dout
  RAM #(.addrWidth(4), .dataWidth(64), .\type ("nonvolatile")) B12_11 (
    .addr(counter_3_q), .oe(1'b1), .clk(clock_1_out), .dout(B12_11_dout));  // open: we, din
  RAM #(.addrWidth(4), .dataWidth(64), .\type ("nonvolatile")) B12_12 (
    .addr(counter_3_q), .oe(1'b1), .clk(clock_1_out), .dout(B12_12_dout));  // open: we, din
  // Probe on B12_11_dout
  // Probe on B12_12_dout
  RAM #(.addrWidth(4), .dataWidth(64), .\type ("nonvolatile")) B12_21 (
    .addr(counter_3_q), .oe(1'b1), .clk(clock_1_out), .dout(B12_21_dout));  // open: we, din
  RAM #(.addrWidth(4), .dataWidth(64), .\type ("nonvolatile")) B12_22 (
    .addr(counter_3_q), .oe(1'b1), .clk(clock_1_out), .dout(B12_22_dout));  // open: we, din
  Counter #(.max('h1), .width(2)) counter_1 (
    .count(clock_1_out), .clk(clock_1_out), .carry(counter_1_carry));  // open: clr, load, up, D, Q
  // Probe on B12_22_dout
  Counter #(.max('h1), .width(1)) counter_2 (
    .clk(clock_1_out), .carry(counter_2_carry));  // open: clr, load, up, count, D, Q
  // Probe on B12_21_dout
  Counter #(.max('h1), .width(4)) counter_3 (
    .count(counter_1_carry), .clk(clock_1_out), .carry(counter_3_carry), .Q(counter_3_q));  // open: clr, load, up, D
  Counter #(.max('h1), .ongoal("stay"), .width(4)) counter_4 (
    .count(counter_3_carry), .clk(clock_1_out), .Q(counter_4_q));  // open: clr, load, up, D, carry
  // Probe on B11_11_dout
  Counter #(.max('h3), .width(4)) counter_5 (
    .count(counter_2_carry), .clk(clock_1_out), .Q(counter_5_q));  // open: clr, load, up, D, carry
  Clock clock_1 (.out(clock_1_out));
  // Probe on mat_mult_4x4_1_r22
  // Probe on mat_mult_4x4_1_r21
  // Probe on mat_mult_4x4_1_r12
  // Probe on mat_mult_4x4_1_r11
  mat_mult_4x4 mat_mult_4x4_1 (
    .A11_11(A11_11_dout), .A11_12(A11_12_dout), .A11_21(A11_21_dout), .A11_22(A11_22_dout),
    .A12_11(A12_11_dout), .A12_12(A12_12_dout), .A12_21(A12_21_dout), .A12_22(A12_22_dout),
    .B11_11(B11_11_dout), .B11_12(B11_12_dout), .B11_21(B11_21_dout), .B11_22(B11_22_dout),
    .B21_11(B12_11_dout), .B21_12(B12_12_dout), .B21_21(B12_21_dout), .B21_22(B12_22_dout),
    .R11(mat_mult_4x4_1_r11), .R12(mat_mult_4x4_1_r12), .R21(mat_mult_4x4_1_r21), .R22(mat_mult_4x4_1_r22));
  // Probe on A11_11_dout
  RAM #(.addrWidth(4), .dataWidth(64), .\type ("nonvolatile")) A11_11 (
    .addr(counter_4_q), .oe(1'b1), .clk(clock_1_out), .dout(A11_11_dout));  // open: we, din
  RAM #(.addrWidth(4), .dataWidth(64), .\type ("nonvolatile")) A11_12 (
    .addr(counter_4_q), .oe(1'b1), .clk(clock_1_out), .dout(A11_12_dout));  // open: we, din
  RAM #(.addrWidth(4), .dataWidth(64)) ram_1 (
    .addr(counter_5_q), .we(1'b1), .clk(clock_1_out), .din(mat_mult_4x4_1_r11));  // open: oe, dout
  // Probe on A11_11_dout
  // Probe on A11_12_dout
  RAM #(.addrWidth(4), .dataWidth(64), .\type ("nonvolatile")) A11_21 (
    .addr(counter_4_q), .oe(1'b1), .clk(clock_1_out), .dout(A11_21_dout));  // open: we, din
  RAM #(.addrWidth(4), .dataWidth(64), .\type ("nonvolatile")) A11_22 (
    .addr(counter_4_q), .oe(1'b1), .clk(clock_1_out), .dout(A11_22_dout));  // open: we, din
  RAM #(.addrWidth(4), .dataWidth(64)) ram_2 (
    .addr(counter_5_q), .we(1'b1), .clk(clock_1_out), .din(mat_mult_4x4_1_r12));  // open: oe, dout
  // Probe on A11_21_dout
  // Probe on A11_22_dout
  RAM #(.addrWidth(4), .dataWidth(64), .\type ("nonvolatile")) A12_11 (
    .addr(counter_4_q), .oe(1'b1), .clk(clock_1_out), .dout(A12_11_dout));  // open: we, din
  RAM #(.addrWidth(4), .dataWidth(64), .\type ("nonvolatile")) A12_12 (
    .addr(counter_4_q), .oe(1'b1), .clk(clock_1_out), .dout(A12_12_dout));  // open: we, din
  RAM #(.addrWidth(4), .dataWidth(64)) ram_3 (
    .addr(counter_5_q), .we(1'b1), .clk(clock_1_out), .din(mat_mult_4x4_1_r21));  // open: oe, dout
  // Probe on A12_11_dout
  // Probe on A12_12_dout
  RAM #(.addrWidth(4), .dataWidth(64), .\type ("nonvolatile")) A12_21 (
    .addr(counter_4_q), .oe(1'b1), .clk(clock_1_out), .dout(A12_21_dout));  // open: we, din
  RAM #(.addrWidth(4), .dataWidth(64), .\type ("nonvolatile")) A12_22 (
    .addr(counter_4_q), .oe(1'b1), .clk(clock_1_out), .dout(A12_22_dout));  // open: we, din
  RAM #(.addrWidth(4), .dataWidth(64)) ram_4 (
    .addr(counter_5_q), .we(1'b1), .clk(clock_1_out), .din(mat_mult_4x4_1_r22));  // open: oe, dout
  // Probe on A12_21_dout
  // Probe on A12_22_dout
endmodule

module mat_mult_8x8 (
  input  [63:0] A12_22_22,
  input  [63:0] A12_22_21,
  input  [63:0] A12_22_12,
  input  [63:0] A12_22_11,
  input  [63:0] A12_21_22,
  input  [63:0] A12_21_21,
  input  [63:0] A12_21_12,
  input  [63:0] A12_21_11,
  input  [63:0] B12_22_22,
  input  [63:0] B12_22_21,
  input  [63:0] B12_22_12,
  input  [63:0] B12_22_11,
  input  [63:0] B12_21_22,
  input  [63:0] B12_21_21,
  input  [63:0] B12_21_12,
  input  [63:0] in_16,
  input  [63:0] B12_12_22,
  input  [63:0] B12_12_21,
  input  [63:0] B12_12_12,
  input  [63:0] B12_12_11,
  input  [63:0] B12_11_22,
  input  [63:0] B12_11_21,
  input  [63:0] B12_11_12,
  input  [63:0] B12_11_11,
  input  [63:0] A12_12_22,
  input  [63:0] A12_12_21,
  input  [63:0] A12_12_12,
  input  [63:0] A12_12_11,
  input  [63:0] in_29,
  input  [63:0] A12_11_22,
  input  [63:0] A12_11_12,
  input  [63:0] A12_11_11,
  input  [63:0] A11_22_22,
  input  [63:0] A11_22_21,
  input  [63:0] A11_22_12,
  input  [63:0] A11_22_11,
  input  [63:0] A11_21_22,
  input  [63:0] A11_21_21,
  input  [63:0] A11_21_12,
  input  [63:0] A11_21_11,
  input  [63:0] B11_22_22,
  input  [63:0] B11_22_21,
  input  [63:0] B11_22_12,
  input  [63:0] B11_22_11,
  input  [63:0] B11_21_22,
  input  [63:0] B11_21_21,
  input  [63:0] B11_21_12,
  input  [63:0] B12_21_11,
  input  [63:0] B11_12_22,
  input  [63:0] B11_12_21,
  input  [63:0] B11_12_12,
  input  [63:0] B11_12_11,
  input  [63:0] B11_11_22,
  input  [63:0] B11_11_21,
  input  [63:0] B11_11_12,
  input  [63:0] B11_11_11,
  input  [63:0] A11_12_22,
  input  [63:0] A11_12_21,
  input  [63:0] A11_12_12,
  input  [63:0] A11_12_11,
  input  [63:0] A11_11_22,
  input  [63:0] A11_11_21,
  input  [63:0] A11_11_12,
  input  [63:0] A11_11_11,
  output [63:0] out_65,
  output [63:0] out_66,
  output [63:0] out_67,
  output [63:0] out_68,
  output [63:0] out_69,
  output [63:0] out_70,
  output [63:0] out_71,
  output [63:0] out_72
);

  wire [63:0] mat_mult_4x4_1_r11, mat_mult_4x4_1_r12, mat_mult_4x4_1_r21, mat_mult_4x4_1_r22,
       mat_mult_4x4_2_r11, mat_mult_4x4_2_r12, mat_mult_4x4_2_r21, mat_mult_4x4_2_r22, mat_mult_4x4_3_r11,
       mat_mult_4x4_3_r12, mat_mult_4x4_3_r21, mat_mult_4x4_3_r22, mat_mult_4x4_4_r11, mat_mult_4x4_4_r12,
       mat_mult_4x4_4_r21, mat_mult_4x4_4_r22;

  mat_mult_4x4 mat_mult_4x4_1 (
    .A11_11(A12_21_11), .A11_12(A12_21_12), .A11_21(A12_21_21), .A11_22(A12_21_22), .A12_11(A12_22_11),
    .A12_12(A12_22_12), .A12_21(A12_22_21), .A12_22(A12_22_22), .B11_11(in_16), .B11_12(B12_21_12),
    .B11_21(B12_21_21), .B11_22(B12_21_22), .B21_11(B12_22_11), .B21_12(B12_22_12), .B21_21(B12_22_21),
    .B21_22(B12_22_22), .R11(mat_mult_4x4_1_r11), .R12(mat_mult_4x4_1_r12), .R21(mat_mult_4x4_1_r21),
    .R22(mat_mult_4x4_1_r22));
  mat_mult_4x4 mat_mult_4x4_2 (
    .A11_11(A12_11_11), .A11_12(A12_11_12), .A11_21(A12_11_22), .A11_22(in_29), .A12_11(A12_12_11),
    .A12_12(A12_12_12), .A12_21(A12_12_21), .A12_22(A12_12_22), .B11_11(B12_11_11), .B11_12(B12_11_12),
    .B11_21(B12_11_21), .B11_22(B12_11_22), .B21_11(B12_12_11), .B21_12(B12_12_12), .B21_21(B12_12_21),
    .B21_22(B12_12_22), .R11(mat_mult_4x4_2_r11), .R12(mat_mult_4x4_2_r12), .R21(mat_mult_4x4_2_r21),
    .R22(mat_mult_4x4_2_r22));
  matrixAdder4x4 matrixadder4x4_1 (
    .A11_11(mat_mult_4x4_4_r11), .A11_12(mat_mult_4x4_4_r12), .A11_21(mat_mult_4x4_4_r21),
    .A11_22(mat_mult_4x4_4_r22), .A12_11(mat_mult_4x4_2_r11), .A12_12(mat_mult_4x4_2_r12),
    .A12_21(mat_mult_4x4_2_r21), .A12_22(mat_mult_4x4_2_r22), .B11_11(mat_mult_4x4_3_r11),
    .B11_12(mat_mult_4x4_3_r12), .B11_21(mat_mult_4x4_3_r21), .B11_22(mat_mult_4x4_3_r22),
    .B12_11(mat_mult_4x4_1_r11), .B12_12(mat_mult_4x4_1_r12), .B12_21(mat_mult_4x4_1_r21),
    .B12_22(mat_mult_4x4_1_r22), .R11_11(out_68), .R11_12(out_67), .R11_21(out_66), .R11_22(out_65),
    .R12_11(out_72), .R12_12(out_71), .R12_21(out_70), .R12_22(out_69));  // open: A21_11, A21_12, A21_21, A21_22, A22_11, A22_12, A22_21, A22_22, B21_11, B21_12, B21_21, B21_22, B22_11, B22_12, B22_21, B22_22, R21_11, R21_12, R21_21, R21_22, R22_11, R22_12, R22_21, R22_22
  // Probe on out_68
  // Probe on out_67
  // Probe on out_66
  // Probe on out_65
  mat_mult_4x4 mat_mult_4x4_3 (
    .A11_11(A11_21_11), .A11_12(A11_21_12), .A11_21(A11_21_21), .A11_22(A11_21_22), .A12_11(A11_22_11),
    .A12_12(A11_22_12), .A12_21(A11_22_21), .A12_22(A11_22_22), .B11_11(B12_21_11), .B11_12(B11_21_12),
    .B11_21(B11_21_21), .B11_22(B11_21_22), .B21_11(B11_22_11), .B21_12(B11_22_12), .B21_21(B11_22_21),
    .B21_22(B11_22_22), .R11(mat_mult_4x4_3_r11), .R12(mat_mult_4x4_3_r12), .R21(mat_mult_4x4_3_r21),
    .R22(mat_mult_4x4_3_r22));
  // Probe on out_72
  // Probe on out_69
  // Probe on out_70
  // Probe on out_71
  // Probe on mat_mult_4x4_3_r11
  // Probe on mat_mult_4x4_3_r12
  // Probe on mat_mult_4x4_3_r21
  // Probe on mat_mult_4x4_3_r22
  mat_mult_4x4 mat_mult_4x4_4 (
    .A11_11(A11_11_11), .A11_12(A11_11_12), .A11_21(A11_11_21), .A11_22(A11_11_22), .A12_11(A11_12_11),
    .A12_12(A11_12_12), .A12_21(A11_12_21), .A12_22(A11_12_22), .B11_11(B11_11_11), .B11_12(B11_11_12),
    .B11_21(B11_11_21), .B11_22(B11_11_22), .B21_11(B11_12_11), .B21_12(B11_12_12), .B21_21(B11_12_21),
    .B21_22(B11_12_22), .R11(mat_mult_4x4_4_r11), .R12(mat_mult_4x4_4_r12), .R21(mat_mult_4x4_4_r21),
    .R22(mat_mult_4x4_4_r22));
  // Probe on mat_mult_4x4_4_r11
  // Probe on mat_mult_4x4_4_r12
  // Probe on mat_mult_4x4_4_r21
  // Probe on mat_mult_4x4_4_r22
endmodule

module matrixAdder4x4 (
  input  [63:0] A11_11,
  input  [63:0] A11_12,
  input  [63:0] A11_21,
  input  [63:0] A11_22,
  input  [63:0] A12_11,
  input  [63:0] A12_12,
  input  [63:0] A12_21,
  input  [63:0] A12_22,
  input  [63:0] A21_11,
  input  [63:0] A21_12,
  input  [63:0] A21_21,
  input  [63:0] A21_22,
  input  [63:0] A22_11,
  input  [63:0] A22_12,
  input  [63:0] A22_21,
  input  [63:0] A22_22,
  input  [63:0] B11_11,
  input  [63:0] B11_12,
  input  [63:0] B11_21,
  input  [63:0] B11_22,
  input  [63:0] B12_11,
  input  [63:0] B12_12,
  input  [63:0] B12_21,
  input  [63:0] B12_22,
  input  [63:0] B21_11,
  input  [63:0] B21_12,
  input  [63:0] B21_21,
  input  [63:0] B21_22,
  input  [63:0] B22_11,
  input  [63:0] B22_12,
  input  [63:0] B22_21,
  input  [63:0] B22_22,
  output [63:0] R11_11,
  output [63:0] R11_12,
  output [63:0] R11_21,
  output [63:0] R11_22,
  output [63:0] R12_11,
  output [63:0] R12_12,
  output [63:0] R12_21,
  output [63:0] R12_22,
  output [63:0] R21_11,
  output [63:0] R21_12,
  output [63:0] R21_21,
  output [63:0] R21_22,
  output [63:0] R22_11,
  output [63:0] R22_12,
  output [63:0] R22_21,
  output [63:0] R22_22
);

  matrixAdder2x2Core matrixadder2x2core_1 (
    .A11(A11_11), .A12(A11_12), .A21(A11_21), .A22(A11_22), .B11(B11_11), .B12(B11_12), .B21(B11_21),
    .B22(B11_22), .R11(R11_11), .R12(R11_12), .R21(R11_21), .R22(R11_22));
  matrixAdder2x2Core matrixadder2x2core_2 (
    .A11(A12_11), .A12(A12_12), .A21(A12_21), .A22(A12_22), .B11(B12_11), .B12(B12_12), .B21(B12_21),
    .B22(B12_22), .R11(R12_11), .R12(R12_12), .R21(R12_21), .R22(R12_22));
  matrixAdder2x2Core matrixadder2x2core_3 (
    .A11(A21_11), .A12(A21_12), .A21(A21_21), .A22(A21_22), .B11(B21_11), .B12(B21_12), .B21(B21_21),
    .B22(B21_22), .R11(R21_11), .R12(R21_12), .R21(R21_21), .R22(R21_22));
  matrixAdder2x2Core matrixadder2x2core_4 (
    .A11(A22_11), .A12(A22_12), .A21(A22_21), .A22(A22_22), .B11(B22_11), .B12(B22_12), .B21(B22_21),
    .B22(B22_22), .R11(R22_11), .R12(R22_12), .R21(R22_21), .R22(R22_22));
endmodule
