// Logisim project FINAL_FINAL_FINAL_BOSS_VIVAV2.circ as structural Verilog
module my4bitadder (
  input  [3:0] A,
  input  carry_in,
  input  [3:0] B,
  output [3:0] sum_out,
  output carry_out
);

  wire my2bitadder_1_carry_out, my2bitadder_2_carry_out, my2bitadder_3_carry_out;

  my2bitadder my2bitadder_1 (
    .Inputa(A[0]), .InputB(B[0]), .carry_in(carry_in), .Sum(sum_out[0]), .carry_out(my2bitadder_1_carry_out));
  my2bitadder my2bitadder_2 (
    .Inputa(A[2]), .InputB(B[2]), .carry_in(my2bitadder_3_carry_out), .Sum(sum_out[2]),
    .carry_out(my2bitadder_2_carry_out));
  my2bitadder my2bitadder_3 (
    .Inputa(A[1]), .InputB(B[1]), .carry_in(my2bitadder_1_carry_out), .Sum(sum_out[1]),
    .carry_out(my2bitadder_3_carry_out));
  my2bitadder my2bitadder_4 (
    .Inputa(A[3]), .InputB(B[3]), .carry_in(my2bitadder_2_carry_out), .Sum(sum_out[3]), .carry_out(carry_out));
  LED led_1 (.in(carry_out));
endmodule

module my8bitadder (
  input  carry_in,
  input  [7:0] A,
  input  [7:0] B,
  output [7:0] sum_out,
  output carry_out
);

  wire my4bitadder_1_carry_out;

  // Probe on A
  // Probe on B
  my4bitadder my4bitadder_1 (
    .A(A[3:0]), .carry_in(carry_in), .B(B[3:0]), .sum_out(sum_out[3:0]), .carry_out(my4bitadder_1_carry_out));
  my4bitadder my4bitadder_2 (
    .A(A[7:4]), .carry_in(my4bitadder_1_carry_out), .B(B[7:4]), .sum_out(sum_out[7:4]), .carry_out(carry_out));
  // Probe on sum_out
  LED led_1 (.in(carry_out));
endmodule

module my2bitadder (
  input  Inputa,
  input  InputB,
  input  carry_in,
  output Sum,
  output carry_out
);

  wire and_1_out, and_2_out, xor_1_out;

  xor xor_1 (xor_1_out, Inputa, InputB);
  and and_1 (and_1_out, Inputa, InputB);
  xor xor_2 (Sum, xor_1_out, carry_in);
  and and_2 (and_2_out, xor_1_out, carry_in);
  LED led_1 (.in(Sum));
  LED led_2 (.in(carry_out));
  or or_1 (carry_out, and_1_out, and_2_out);
endmodule

module my2bitsubtractor (
  input  A,
  input  B,
  input  carry_in,
  input  s2,
  input  s1,
  input  [15:0] E0000,
  input  [15:0] E0001,
  input  [15:0] E0010,
  input  [15:0] E0011,
  input  [15:0] E0100,
  input  [15:0] E0101,
  input  [15:0] E0110,
  input  [15:0] E0111,
  input  [15:0] E1000,
  input  [15:0] E1001,
  input  [15:0] E1011,
  input  [15:0] E_1010,
  input  s3,
  input  s4,
  input  [15:0] E1100,
  input  [15:0] E1101,
  input  [15:0] E1110,
  input  [15:0] E1111,
  output out_24,
  output Carry_out,
  output [15:0] out_26
);

  wire and_1_out, and_2_out, not_1_out, not_2_out, xor_1_out;
  wire [15:0] sixteen_bit_mux_4by1_1_out_7, sixteen_bit_mux_4by1_2_out_7, sixteen_bit_mux_4by1_3_out_7,
       sixteen_bit_mux_4by1_4_out_7;

  not not_1 (not_1_out, A);
  xor xor_1 (xor_1_out, A, B);
  and and_1 (and_1_out, not_1_out, B);
  not not_2 (not_2_out, xor_1_out);
  and and_2 (and_2_out, not_2_out, carry_in);
  LED led_1 (.in(out_24));
  xor xor_2 (out_24, xor_1_out, carry_in);
  LED led_2 (.in(Carry_out));
  or or_1 (Carry_out, and_1_out, and_2_out);
  sixteen_bit_mux_4by1 sixteen_bit_mux_4by1_1 (
    .E11(E0000), .E10(E0001), .E01(E0010), .E00(E0011), .s1(s1), .s2(s2), .out_7(sixteen_bit_mux_4by1_1_out_7));
  sixteen_bit_mux_4by1 sixteen_bit_mux_4by1_2 (
    .E11(E0100), .E10(E0101), .E01(E0110), .E00(E0111), .s1(s1), .s2(s2), .out_7(sixteen_bit_mux_4by1_2_out_7));
  sixteen_bit_mux_4by1 sixteen_bit_mux_4by1_3 (
    .E11(E1000), .E10(E1001), .E01(E1011), .E00(E_1010), .s1(s1), .s2(s2),
    .out_7(sixteen_bit_mux_4by1_3_out_7));
  sixteen_bit_mux_4by1 sixteen_bit_mux_4by1_4 (
    .E11(E1100), .E10(E1101), .E01(E1110), .E00(E1111), .s1(s1), .s2(s2), .out_7(sixteen_bit_mux_4by1_4_out_7));
  sixteen_bit_mux_4by1 sixteen_bit_mux_4by1_5 (
    .E11(sixteen_bit_mux_4by1_1_out_7), .E10(sixteen_bit_mux_4by1_2_out_7),
    .E01(sixteen_bit_mux_4by1_3_out_7), .E00(sixteen_bit_mux_4by1_4_out_7), .s1(s3), .s2(s4), .out_7(out_26));
endmodule

module my16bit_adder (
  input  Carry_in,
  input  [15:0] A,
  input  [15:0] B,
  output [15:0] sum_out,
  output carry_out
);

  wire my8bitadder_1_carry_out;

  // Probe on A
  // Probe on B
  my8bitadder my8bitadder_1 (
    .carry_in(Carry_in), .A(A[7:0]), .B(B[7:0]), .sum_out(sum_out[7:0]), .carry_out(my8bitadder_1_carry_out));
  my8bitadder my8bitadder_2 (
    .carry_in(my8bitadder_1_carry_out), .A(A[15:8]), .B(B[15:8]), .sum_out(sum_out[15:8]),
    .carry_out(carry_out));
  LED led_1 (.in(carry_out));
  // Probe on sum_out
endmodule

module addsub_8 (
  input  [7:0] A,
  input  [7:0] B,
  input  Carry_in,
  input  [7:0] Sum,
  output [7:0] out_5,
  output Carry_out
);

  wire [7:0] xor_1_out;

  // Probe on A
  // Probe on B
  assign xor_1_out = B ^ Sum;  // XOR_Gate xor_1, 8 bits wide
  // Probe on out_5
  my8bitadder my8bitadder_1 (.carry_in(Carry_in), .A(A), .B(xor_1_out), .sum_out(out_5), .carry_out(Carry_out));
  LED led_1 (.in(Carry_out));
endmodule

module addsub_16 (
  input  [15:0] A,
  input  [15:0] B,
  input  carry_in,
  input  [15:0] sum,
  output [15:0] out_5,
  output carry_out
);

  wire [15:0] xor_1_out;

  // Probe on B
  // Probe on A
  assign xor_1_out = B ^ sum;  // XOR_Gate xor_1, 16 bits wide
  // Probe on out_5
  my16bit_adder my16bit_adder_1 (.Carry_in(carry_in), .A(A), .B(xor_1_out), .sum_out(out_5), .carry_out(carry_out));
  LED led_1 (.in(carry_out));
endmodule

module memory_cellDflip (
  input  clock,
  input  WE,
  input  carry_in,
  input  OE,
  input  Reset,
  input  s2,
  input  s1,
  input  [15:0] E0000,
  input  [15:0] E0001,
  input  [15:0] E0010,
  input  [15:0] E0011,
  input  [15:0] E0100,
  input  [15:0] E0101,
  input  [15:0] E0110,
  input  [15:0] E0111,
  input  [15:0] E1000,
  input  [15:0] E1001,
  input  [15:0] E1011,
  input  [15:0] E_1010,
  input  s3,
  input  s4,
  input  [15:0] E1100,
  input  [15:0] E1101,
  input  [15:0] E1110,
  input  [15:0] E1111,
  output carry_out,
  output [15:0] out_27
);

  wire and_1_out, and_2_out, d_ff_1_q, not_1_out, or_1_out;
  wire [15:0] sixteen_bit_mux_4by1_1_out_7, sixteen_bit_mux_4by1_2_out_7, sixteen_bit_mux_4by1_3_out_7,
       sixteen_bit_mux_4by1_4_out_7;

  not not_1 (not_1_out, WE);
  and and_1 (and_1_out, d_ff_1_q, not_1_out);
  and and_2 (and_2_out, WE, carry_in);
  or or_1 (or_1_out, and_1_out, and_2_out);
  D_Flip_Flop d_ff_1 (.D(clock), .clk(or_1_out), .Q(d_ff_1_q), .reset(Reset));  // open: Qn, preset
  assign carry_out = OE ? d_ff_1_q : 1'bz;  // Controlled_Buffer controlled_buffer_1
  sixteen_bit_mux_4by1 sixteen_bit_mux_4by1_1 (
    .E11(E0000), .E10(E0001), .E01(E0010), .E00(E0011), .s1(s1), .s2(s2), .out_7(sixteen_bit_mux_4by1_1_out_7));
  sixteen_bit_mux_4by1 sixteen_bit_mux_4by1_2 (
    .E11(E0100), .E10(E0101), .E01(E0110), .E00(E0111), .s1(s1), .s2(s2), .out_7(sixteen_bit_mux_4by1_2_out_7));
  sixteen_bit_mux_4by1 sixteen_bit_mux_4by1_3 (
    .E11(E1000), .E10(E1001), .E01(E1011), .E00(E_1010), .s1(s1), .s2(s2),
    .out_7(sixteen_bit_mux_4by1_3_out_7));
  sixteen_bit_mux_4by1 sixteen_bit_mux_4by1_4 (
    .E11(E1100), .E10(E1101), .E01(E1110), .E00(E1111), .s1(s1), .s2(s2), .out_7(sixteen_bit_mux_4by1_4_out_7));
  sixteen_bit_mux_4by1 sixteen_bit_mux_4by1_5 (
    .E11(sixteen_bit_mux_4by1_1_out_7), .E10(sixteen_bit_mux_4by1_2_out_7),
    .E01(sixteen_bit_mux_4by1_3_out_7), .E00(sixteen_bit_mux_4by1_4_out_7), .s1(s3), .s2(s4), .out_7(out_27));
endmodule

module MAR (
  input  Clock,
  input  WE,
  input  [3:0] carry_in,
  input  OE,
  input  s2,
  input  s1,
  input  in_7,
  input  in_8,
  input  [15:0] E0000,
  input  [15:0] in_10,
  input  [15:0] E0001,
  input  [15:0] in_12,
  input  [15:0] E0010,
  input  [15:0] in_14,
  input  [15:0] E0011,
  input  [15:0] in_16,
  input  [15:0] E0100,
  input  [15:0] in_18,
  input  [15:0] E0101,
  input  [15:0] in_20,
  input  [15:0] E0110,
  input  [15:0] in_22,
  input  [15:0] E0111,
  input  [15:0] in_24,
  input  [15:0] E1000,
  input  [15:0] in_26,
  input  [15:0] E1001,
  input  [15:0] in_28,
  input  [15:0] E1011,
  input  [15:0] in_30,
  input  [15:0] E_1010,
  input  s3,
  input  [15:0] in_33,
  input  in_34,
  input  s4,
  input  in_36,
  input  [15:0] E1100,
  input  [15:0] in_38,
  input  [15:0] E1101,
  input  [15:0] in_40,
  input  [15:0] E1110,
  input  [15:0] in_42,
  input  [15:0] E1111,
  input  [15:0] in_44,
  output [3:0] Data_out,
  output [3:0] Stored_data,
  output [15:0] out_47,
  output [15:0] out_48
);

  wire [15:0] sixteen_bit_mux_4by1_1_out_7, sixteen_bit_mux_4by1_2_out_7, sixteen_bit_mux_4by1_3_out_7,
       sixteen_bit_mux_4by1_4_out_7, sixteen_bit_mux_4by1_5_out_7, sixteen_bit_mux_4by1_6_out_7,
       sixteen_bit_mux_4by1_7_out_7, sixteen_bit_mux_4by1_8_out_7;

  memory_cell memory_cell_1 (
    .Clock(Clock), .WE(WE), .Data_in(carry_in[0]), .OE(OE), .Dout(Data_out[0]), .Stored_data(Stored_data[0]));  // open: Reset
  memory_cell memory_cell_2 (
    .Clock(Clock), .WE(WE), .Data_in(carry_in[1]), .OE(WE), .Dout(Data_out[1]), .Stored_data(Stored_data[1]));  // open: Reset
  memory_cell memory_cell_3 (
    .Clock(Clock), .WE(WE), .Data_in(carry_in[2]), .OE(OE), .Dout(Data_out[2]), .Stored_data(Stored_data[2]));  // open: Reset
  memory_cell memory_cell_4 (
    .Clock(Clock), .WE(WE), .Data_in(carry_in[3]), .OE(WE), .Dout(Data_out[3]), .Stored_data(Stored_data[3]));  // open: Reset
  sixteen_bit_mux_4by1 sixteen_bit_mux_4by1_1 (
    .E11(E0000), .E10(E0001), .E01(E0010), .E00(E0011), .s1(s1), .s2(s2), .out_7(sixteen_bit_mux_4by1_1_out_7));
  sixteen_bit_mux_4by1 sixteen_bit_mux_4by1_2 (
    .E11(in_10), .E10(in_12), .E01(in_14), .E00(in_16), .s1(in_8), .s2(in_7),
    .out_7(sixteen_bit_mux_4by1_2_out_7));
  sixteen_bit_mux_4by1 sixteen_bit_mux_4by1_3 (
    .E11(E0100), .E10(E0101), .E01(E0110), .E00(E0111), .s1(s1), .s2(s2), .out_7(sixteen_bit_mux_4by1_3_out_7));
  sixteen_bit_mux_4by1 sixteen_bit_mux_4by1_4 (
    .E11(in_18), .E10(in_20), .E01(in_22), .E00(in_24), .s1(in_8), .s2(in_7),
    .out_7(sixteen_bit_mux_4by1_4_out_7));
  sixteen_bit_mux_4by1 sixteen_bit_mux_4by1_5 (
    .E11(E1000), .E10(E1001), .E01(E1011), .E00(E_1010), .s1(s1), .s2(s2),
    .out_7(sixteen_bit_mux_4by1_5_out_7));
  sixteen_bit_mux_4by1 sixteen_bit_mux_4by1_6 (
    .E11(in_26), .E10(in_28), .E01(in_30), .E00(in_33), .s1(in_8), .s2(in_7),
    .out_7(sixteen_bit_mux_4by1_6_out_7));
  sixteen_bit_mux_4by1 sixteen_bit_mux_4by1_7 (
    .E11(E1100), .E10(E1101), .E01(E1110), .E00(E1111), .s1(s1), .s2(s2), .out_7(sixteen_bit_mux_4by1_7_out_7));
  sixteen_bit_mux_4by1 sixteen_bit_mux_4by1_8 (
    .E11(in_38), .E10(in_40), .E01(in_42), .E00(in_44), .s1(in_8), .s2(in_7),
    .out_7(sixteen_bit_mux_4by1_8_out_7));
  sixteen_bit_mux_4by1 sixteen_bit_mux_4by1_9 (
    .E11(sixteen_bit_mux_4by1_1_out_7), .E10(sixteen_bit_mux_4by1_3_out_7),
    .E01(sixteen_bit_mux_4by1_5_out_7), .E00(sixteen_bit_mux_4by1_7_out_7), .s1(s3), .s2(in_34),
    .out_7(out_47));
  sixteen_bit_mux_4by1 sixteen_bit_mux_4by1_10 (
    .E11(sixteen_bit_mux_4by1_2_out_7), .E10(sixteen_bit_mux_4by1_4_out_7),
    .E01(sixteen_bit_mux_4by1_6_out_7), .E00(sixteen_bit_mux_4by1_8_out_7), .s1(in_34), .s2(in_36),
    .out_7(out_48));

  assign s4 = in_34;
endmodule

module my8bit_ORgate (
  input  [7:0] in_1,
  input  [7:0] in_2,
  output [7:0] out_3
);

  assign out_3 = in_1 | in_2;  // OR_Gate or_1, 8 bits wide
endmodule

module my8bit_XORgate (
  input  [7:0] in_1,
  input  [7:0] in_2,
  output [7:0] out_3
);

  assign out_3 = in_1 ^ in_2;  // XOR_Gate xor_1, 8 bits wide
endmodule

module my8bit_ANDgate (
  input  [7:0] in_1,
  input  [7:0] in_2,
  output [7:0] out_3
);

  assign out_3 = in_1 & in_2;  // AND_Gate and_1, 8 bits wide
endmodule

module my8bit_NOTgate (
  input  [7:0] in_1,
  output [7:0] out_2
);

  assign out_2 = ~in_1;  // NOT_Gate not_1, 8 bits wide
endmodule

module eightbit_mux (
  input  Switch,
  input  [7:0] A,
  input  [7:0] B,
  output out_4
);

  wire [7:0] and_1_out, and_2_out, bit_extender_1_out, not_1_out, or_1_out;

  assign bit_extender_1_out = {{7{Switch}}, Switch};  // Bit_Extender bit_extender_1
  assign and_1_out = A & not_1_out;  // AND_Gate and_1, 8 bits wide
  assign not_1_out = ~bit_extender_1_out;  // NOT_Gate not_1, 8 bits wide
  assign and_2_out = B & bit_extender_1_out;  // AND_Gate and_2, 8 bits wide
  assign or_1_out = and_1_out | and_2_out;  // OR_Gate or_1, 8 bits wide
  Bit_Extender #(.out_width(1)) bit_extender_2 (.in(or_1_out), .out(out_4));
endmodule

module twobit_mult (
  input  Carry_in,
  input  [3:0] A,
  input  [3:0] B,
  output [3:0] Product
);

  wire and_2_out, and_3_out, and_4_out, my2bitadder_1_carry_out;

  and and_1 (Product[0], A[0], B[0]);
  and and_2 (and_2_out, A[1], B[1]);
  and and_3 (and_3_out, A[2], B[2]);
  and and_4 (and_4_out, A[3], B[3]);
  my2bitadder my2bitadder_1 (
    .Inputa(and_2_out), .InputB(and_3_out), .carry_in(Carry_in), .Sum(Product[1]),
    .carry_out(my2bitadder_1_carry_out));
  my2bitadder my2bitadder_2 (
    .Inputa(and_4_out), .carry_in(my2bitadder_1_carry_out), .Sum(Product[2]), .carry_out(Product[3]));  // open: InputB
endmodule

module eightbbit_multivv2 (
  input  [7:0] A,
  input  [7:0] B,
  output [15:0] sum_out,
  output carry_out
);

  wire [3:0] undriven, undriven_2, undriven_3, undriven_4;
  wire [7:0] fourbit_multiplier_1_out_6, fourbit_multiplier_2_out_6, fourbit_multiplier_3_out_6,
       fourbit_multiplier_4_out_6, undriven_5, undriven_6;
  wire [15:0] my16bit_adder_1_sum_out, my16bit_adder_2_sum_out;

  // Probe on B
  // Probe on A
  fourbit_multiplier fourbit_multiplier_1 (
    .A(A[3:0]), .B(B[3:0]), .out_6(fourbit_multiplier_1_out_6));  // open: in_2, in_3, in_4
  // Probe on fourbit_multiplier_2_out_6
  fourbit_multiplier fourbit_multiplier_2 (
    .A(A[3:0]), .B(B[7:4]), .out_6(fourbit_multiplier_2_out_6));  // open: in_2, in_3, in_4
  // Probe on fourbit_multiplier_3_out_6
  fourbit_multiplier fourbit_multiplier_3 (
    .A(A[7:4]), .B(B[3:0]), .out_6(fourbit_multiplier_3_out_6));  // open: in_2, in_3, in_4
  // Probe on fourbit_multiplier_4_out_6
  fourbit_multiplier fourbit_multiplier_4 (
    .A(A[7:4]), .B(B[7:4]), .out_6(fourbit_multiplier_4_out_6));  // open: in_2, in_3, in_4
  // Probe on fourbit_multiplier_1_out_6
  my16bit_adder my16bit_adder_1 (
    .A({undriven_6, fourbit_multiplier_1_out_6}), .B({undriven_2, fourbit_multiplier_2_out_6, undriven}),
    .sum_out(my16bit_adder_1_sum_out));  // open: Carry_in, carry_out
  // Probe on my16bit_adder_2_sum_out
  my16bit_adder my16bit_adder_2 (
    .A({undriven_4, fourbit_multiplier_3_out_6, undriven_3}), .B({fourbit_multiplier_4_out_6, undriven_5}),
    .sum_out(my16bit_adder_2_sum_out));  // open: Carry_in, carry_out
  // Probe on my16bit_adder_1_sum_out
  // Probe on sum_out
  my16bit_adder my16bit_adder_3 (
    .A(my16bit_adder_2_sum_out), .B(my16bit_adder_1_sum_out), .sum_out(sum_out), .carry_out(carry_out));  // open: Carry_in
endmodule

module fourbit_multiplier (
  input  [3:0] A,
  input  in_2,
  input  in_3,
  input  in_4,
  input  [3:0] B,
  output [7:0] out_6
);

  wire [2:0] and_2_out;
  wire [3:0] and_5_out, and_9_out, and_13_out, my4bitadder_2_sum_out;
  wire [3:1] my4bitadder_1_sum_out;
  wire [3:3] my4bitadder_1_carry_out;

  // Probe on A
  // Probe on B
  and and_1 (out_6[0], A[0], B[0]);
  and and_2 (and_2_out[0], A[0], B[1]);
  and and_3 (and_2_out[1], A[0], B[2]);
  and and_4 (and_2_out[2], A[0], B[3]);
  and and_5 (and_5_out[0], A[1], B[0]);
  and and_6 (and_5_out[1], A[1], B[1]);
  and and_7 (and_5_out[2], A[1], B[2]);
  and and_8 (and_5_out[3], A[1], B[3]);
  and and_9 (and_9_out[0], A[2], B[0]);
  and and_10 (and_9_out[1], A[2], B[1]);
  and and_11 (and_9_out[2], A[2], B[2]);
  and and_12 (and_9_out[3], A[2], B[3]);
  and and_13 (and_13_out[0], A[3], B[0]);
  and and_14 (and_13_out[1], A[3], B[1]);
  and and_15 (and_13_out[2], A[3], B[2]);
  and and_16 (and_13_out[3], A[3], B[3]);
  // Probe on {in_2, and_2_out}
  // Probe on and_5_out
  // Probe on {my4bitadder_1_sum_out, out_6[1]}
  my4bitadder my4bitadder_1 (
    .A({in_2, and_2_out}), .B(and_5_out), .sum_out({my4bitadder_1_sum_out, out_6[1]}),
    .carry_out(my4bitadder_1_carry_out[3]));  // open: carry_in
  // Probe on {my4bitadder_1_carry_out[3], my4bitadder_1_sum_out}
  // Probe on and_9_out
  // Probe on {my4bitadder_2_sum_out[2:0], out_6[2]}
  my4bitadder my4bitadder_2 (
    .A({my4bitadder_1_carry_out[3], my4bitadder_1_sum_out}), .carry_in(in_3), .B(and_9_out),
    .sum_out({my4bitadder_2_sum_out[2:0], out_6[2]}), .carry_out(my4bitadder_2_sum_out[3]));
  // Probe on and_13_out
  // Probe on my4bitadder_2_sum_out
  // Probe on out_6[6:3]
  my4bitadder my4bitadder_3 (
    .A(my4bitadder_2_sum_out), .carry_in(in_4), .B(and_13_out), .sum_out(out_6[6:3]), .carry_out(out_6[7]));
  // Probe on out_6
endmodule

module EightBit_ALU (
  input  [7:0] A,
  input  [7:0] B,
  input  OE,
  input  in_4,
  output [7:0] Data_out,
  output [7:0] Result
);

  wire eightbit_mux_1_out_4;
  wire [1:0] bit_extender_3_out, bit_extender_4_out, bit_extender_5_out, bit_extender_6_out,
       bit_extender_7_out, bit_extender_8_out, undriven, undriven_2;
  wire [3:0] bit_extender_1_out, bit_extender_2_out;
  wire [7:0] addsub_8_1_out_5, fourbit_multiplier_1_out_6, my8bit_andgate_1_out_3, my8bit_notgate_1_out_2,
       my8bit_orgate_1_out_3, my8bit_xorgate_1_out_3;

  // Probe on A
  // Probe on B
  Bit_Extender #(.out_width(4)) bit_extender_1 (.in(A), .out(bit_extender_1_out));
  Bit_Extender #(.out_width(4)) bit_extender_2 (.in(B), .out(bit_extender_2_out));
  fourbit_multiplier fourbit_multiplier_1 (
    .A(bit_extender_1_out), .B(bit_extender_2_out), .out_6(fourbit_multiplier_1_out_6));  // open: in_2, in_3, in_4
  my8bit_NOTgate my8bit_notgate_1 (.in_1(A), .out_2(my8bit_notgate_1_out_2));
  Bit_Extender #(.out_width(2)) bit_extender_3 (.in(my8bit_orgate_1_out_3), .out(bit_extender_3_out));
  my8bit_ORgate my8bit_orgate_1 (.in_1(A), .in_2(B), .out_3(my8bit_orgate_1_out_3));
  Bit_Extender #(.out_width(2)) bit_extender_4 (.in(my8bit_xorgate_1_out_3), .out(bit_extender_4_out));
  my8bit_XORgate my8bit_xorgate_1 (.in_1(A), .in_2(B), .out_3(my8bit_xorgate_1_out_3));
  Bit_Extender #(.out_width(2)) bit_extender_5 (.in(my8bit_andgate_1_out_3), .out(bit_extender_5_out));
  my8bit_ANDgate my8bit_andgate_1 (.in_1(A), .in_2(B), .out_3(my8bit_andgate_1_out_3));
  // Probe on addsub_8_1_out_5
  addsub_8 addsub_8_1 (.A(A), .B(B), .out_5(addsub_8_1_out_5));  // open: Carry_in, Sum, Carry_out
  // Probe on fourbit_multiplier_1_out_6
  Bit_Extender #(.out_width(2)) bit_extender_6 (.in(fourbit_multiplier_1_out_6), .out(bit_extender_6_out));
  Bit_Extender #(.out_width(2)) bit_extender_7 (.in(my8bit_notgate_1_out_2), .out(bit_extender_7_out));
  // Probe on {bit_extender_5_out, bit_extender_4_out, bit_extender_3_out, bit_extender_7_out}
  Bit_Extender #(.out_width(2)) bit_extender_8 (.in(addsub_8_1_out_5), .out(bit_extender_8_out));
  assign Result = {{7{eightbit_mux_1_out_4}}, eightbit_mux_1_out_4};  // Bit_Extender bit_extender_9
  eightbit_mux eightbit_mux_1 (
    .Switch(in_4), .A({bit_extender_8_out, bit_extender_6_out, undriven_2, undriven}),
    .B({bit_extender_5_out, bit_extender_4_out, bit_extender_3_out, bit_extender_7_out}),
    .out_4(eightbit_mux_1_out_4));
  // Probe on Result
  assign Data_out = OE ? Result : 8'bz;  // Controlled_Buffer controlled_buffer_1
  // Probe on Data_out
endmodule

module comp_1_bit (
  input  A,
  input  B,
  output A_eq_B,
  output A_grt_B,
  output A_less_B
);

  wire not_1_out, not_2_out, xor_1_out;

  not not_1 (not_1_out, B);
  not not_2 (not_2_out, A);
  xor xor_1 (xor_1_out, A, B);
  not not_3 (A_eq_B, xor_1_out);
  and and_1 (A_grt_B, A, not_1_out);
  and and_2 (A_less_B, not_2_out, B);

  // Notes on the sheet:
  //   a=b
  //   a>b
  //   a<b
endmodule

module comp_2_bit (
  input  [1:0] A,
  input  [1:0] B,
  output A_eq_B,
  output A_grt_B,
  output B_grt_A
);

  wire and_1_out, and_2_out, and_3_out, and_4_out, and_5_out, and_6_out, comp_1_bit_1_a_eq_b,
       comp_1_bit_1_a_grt_b, comp_1_bit_1_a_less_b, comp_1_bit_2_a_eq_b, comp_1_bit_2_a_grt_b,
       comp_1_bit_2_a_less_b, not_1_out, not_2_out, not_3_out, not_4_out;

  comp_1_bit comp_1_bit_1 (
    .A(A[0]), .B(B[0]), .A_eq_B(comp_1_bit_1_a_eq_b), .A_grt_B(comp_1_bit_1_a_grt_b),
    .A_less_B(comp_1_bit_1_a_less_b));
  comp_1_bit comp_1_bit_2 (
    .A(A[1]), .B(B[1]), .A_eq_B(comp_1_bit_2_a_eq_b), .A_grt_B(comp_1_bit_2_a_grt_b),
    .A_less_B(comp_1_bit_2_a_less_b));
  not not_1 (not_1_out, comp_1_bit_1_a_less_b);
  not not_2 (not_2_out, comp_1_bit_1_a_grt_b);
  not not_3 (not_3_out, comp_1_bit_2_a_less_b);
  not not_4 (not_4_out, comp_1_bit_2_a_grt_b);
  and and_1 (and_1_out, comp_1_bit_1_a_grt_b, not_1_out);
  and and_2 (and_2_out, not_2_out, comp_1_bit_1_a_less_b);
  and and_3 (and_3_out, comp_1_bit_2_a_grt_b, not_3_out);
  and and_4 (and_4_out, not_4_out, comp_1_bit_2_a_less_b);
  and and_5 (and_5_out, and_2_out, comp_1_bit_2_a_eq_b);
  and and_6 (and_6_out, and_1_out, comp_1_bit_2_a_eq_b);
  and and_7 (A_eq_B, comp_1_bit_1_a_eq_b, comp_1_bit_2_a_eq_b);
  or or_1 (A_grt_B, and_6_out, and_3_out);
  or or_2 (B_grt_A, and_5_out, and_4_out);
endmodule

module comp_4_bit (
  input  [3:0] A,
  input  [3:0] B,
  output A_eq_B,
  output A_grt_B,
  output B_grt_A
);

  wire and_1_out, and_2_out, and_3_out, and_4_out, and_5_out, and_6_out, comp_2_bit_1_a_eq_b,
       comp_2_bit_1_a_grt_b, comp_2_bit_1_b_grt_a, comp_2_bit_2_a_eq_b, comp_2_bit_2_a_grt_b,
       comp_2_bit_2_b_grt_a, not_1_out, not_2_out, not_3_out, not_4_out;

  comp_2_bit comp_2_bit_1 (
    .A(A[1:0]), .B(B[1:0]), .A_eq_B(comp_2_bit_1_a_eq_b), .A_grt_B(comp_2_bit_1_a_grt_b),
    .B_grt_A(comp_2_bit_1_b_grt_a));
  comp_2_bit comp_2_bit_2 (
    .A(A[3:2]), .B(B[3:2]), .A_eq_B(comp_2_bit_2_a_eq_b), .A_grt_B(comp_2_bit_2_a_grt_b),
    .B_grt_A(comp_2_bit_2_b_grt_a));
  not not_1 (not_1_out, comp_2_bit_1_b_grt_a);
  not not_2 (not_2_out, comp_2_bit_1_a_grt_b);
  not not_3 (not_3_out, comp_2_bit_2_b_grt_a);
  not not_4 (not_4_out, comp_2_bit_2_a_grt_b);
  and and_1 (and_1_out, comp_2_bit_1_a_grt_b, not_1_out);
  and and_2 (and_2_out, not_2_out, comp_2_bit_1_b_grt_a);
  and and_3 (and_3_out, comp_2_bit_2_a_grt_b, not_3_out);
  and and_4 (and_4_out, not_4_out, comp_2_bit_2_b_grt_a);
  and and_5 (and_5_out, and_2_out, comp_2_bit_2_a_eq_b);
  and and_6 (and_6_out, comp_2_bit_2_a_eq_b, and_1_out);
  and and_7 (A_eq_B, comp_2_bit_1_a_eq_b, comp_2_bit_2_a_eq_b);
  or or_1 (A_grt_B, and_6_out, and_3_out);
  or or_2 (B_grt_A, and_5_out, and_4_out);
endmodule

module comp_8 (
  input  [7:0] A,
  input  [7:0] B,
  output A_eq_B,
  output A_grt_B,
  output B_grt_A
);

  wire and_1_out, and_2_out, and_3_out, and_4_out, and_5_out, and_6_out, comp_4_bit_1_a_eq_b,
       comp_4_bit_1_a_grt_b, comp_4_bit_1_b_grt_a, comp_4_bit_2_a_eq_b, comp_4_bit_2_a_grt_b,
       comp_4_bit_2_b_grt_a, not_1_out, not_2_out, not_3_out, not_4_out;

  // Probe on A
  // Probe on B
  comp_4_bit comp_4_bit_1 (
    .A(A[3:0]), .B(B[3:0]), .A_eq_B(comp_4_bit_1_a_eq_b), .A_grt_B(comp_4_bit_1_a_grt_b),
    .B_grt_A(comp_4_bit_1_b_grt_a));
  comp_4_bit comp_4_bit_2 (
    .A(A[7:4]), .B(B[7:4]), .A_eq_B(comp_4_bit_2_a_eq_b), .A_grt_B(comp_4_bit_2_a_grt_b),
    .B_grt_A(comp_4_bit_2_b_grt_a));
  and and_1 (and_1_out, comp_4_bit_1_a_grt_b, not_1_out);
  not not_1 (not_1_out, comp_4_bit_1_b_grt_a);
  not not_2 (not_2_out, comp_4_bit_1_a_grt_b);
  and and_2 (and_2_out, not_2_out, comp_4_bit_1_b_grt_a);
  not not_3 (not_3_out, comp_4_bit_2_b_grt_a);
  not not_4 (not_4_out, comp_4_bit_2_a_grt_b);
  and and_3 (and_3_out, comp_4_bit_2_a_grt_b, not_3_out);
  and and_4 (and_4_out, not_4_out, comp_4_bit_2_b_grt_a);
  and and_5 (and_5_out, and_2_out, comp_4_bit_2_a_eq_b);
  and and_6 (and_6_out, comp_4_bit_2_a_eq_b, and_1_out);
  and and_7 (A_eq_B, comp_4_bit_1_a_eq_b, comp_4_bit_2_a_eq_b);
  or or_1 (A_grt_B, and_6_out, and_3_out);
  or or_2 (B_grt_A, and_5_out, and_4_out);
endmodule

module comp_16 (
  input  [15:0] in_1,
  input  [15:0] in_2,
  output [3:0] out_3
);

  wire and_1_out, and_2_out, and_3_out, and_4_out, and_5_out, and_6_out, comp_8_1_a_eq_b, comp_8_1_a_grt_b,
       comp_8_1_b_grt_a, comp_8_2_a_eq_b, comp_8_2_a_grt_b, comp_8_2_b_grt_a, not_1_out, not_2_out,
       not_3_out, not_4_out;

  // Probe on in_1
  // Probe on in_2
  comp_8 comp_8_1 (
    .A(in_1[7:0]), .B(in_2[7:0]), .A_eq_B(comp_8_1_a_eq_b), .A_grt_B(comp_8_1_a_grt_b),
    .B_grt_A(comp_8_1_b_grt_a));
  comp_8 comp_8_2 (
    .A(in_1[15:8]), .B(in_2[15:8]), .A_eq_B(comp_8_2_a_eq_b), .A_grt_B(comp_8_2_a_grt_b),
    .B_grt_A(comp_8_2_b_grt_a));
  and and_1 (and_1_out, comp_8_1_a_grt_b, not_1_out);
  not not_1 (not_1_out, comp_8_1_b_grt_a);
  not not_2 (not_2_out, comp_8_1_a_grt_b);
  and and_2 (and_2_out, not_2_out, comp_8_1_b_grt_a);
  not not_3 (not_3_out, comp_8_2_b_grt_a);
  not not_4 (not_4_out, comp_8_2_a_grt_b);
  and and_3 (and_3_out, comp_8_2_a_grt_b, not_3_out);
  and and_4 (and_4_out, not_4_out, comp_8_2_b_grt_a);
  and and_5 (and_5_out, and_2_out, comp_8_2_a_eq_b);
  and and_6 (and_6_out, comp_8_2_a_eq_b, and_1_out);
  and and_7 (out_3[1], comp_8_1_a_eq_b, comp_8_2_a_eq_b);
  or or_1 (out_3[2], and_6_out, and_3_out);
  or or_2 (out_3[0], and_5_out, and_4_out);
  // Probe on {1'b0, out_3[2:0]}

  assign out_3[3] = 1'b0;

  // Notes on the sheet:
  //   A_grt_B
  //   A_eq_B
  //   A_less_B
endmodule

module sixteen_bit_OR_GATE (
  input  [15:0] A,
  input  [15:0] B,
  output [15:0] out_3
);

  assign out_3 = A | B;  // OR_Gate or_1, 16 bits wide
endmodule

module Sixteen_bit_AND_GATE (
  input  [15:0] A,
  input  [15:0] B,
  output [15:0] out_3
);

  assign out_3 = A & B;  // AND_Gate and_1, 16 bits wide
endmodule

module Sixteen_bit_XOR_GATE (
  input  [15:0] A,
  input  [15:0] B,
  output [15:0] out_3
);

  assign out_3 = A ^ B;  // XOR_Gate xor_1, 16 bits wide
endmodule

module CPU_8_Bit (
  input  WE,
  input  Count_enable,
  input  OE,
  input  OE_2,
  input  OE_testing_data,
  input  OE_3,
  input  in_7,
  input  in_8,
  input  in_9,
  input  in_10,
  input  WE_2,
  input  OE_4,
  input  OE_5,
  input  WE_3,
  input  OE_6,
  input  WE_4,
  output [3:0] out_17,
  output [3:0] Counter_content,
  output [7:0] Testing_data,
  output [7:0] IR_result,
  output [7:0] MBR_content,
  output [7:0] Reg_A_result,
  output [7:0] ALU_content,
  output [7:0] out_24,
  output [7:0] REG_B_Result
);

  wire clk_out;
  wire [3:0] controlled_buffer_1_out, mar_1_p8;
  wire [7:0] eightbit_alu_1_data_out, regist_1_data_out;
  wire [31:0] bit_extender_1_out, bit_extender_2_out;

  Clock clk (.out(clk_out));
  Counter #(.max('hf), .width(4)) counter_1 (
    .count(Count_enable), .clk(clk_out), .D(controlled_buffer_1_out), .Q(Counter_content));  // open: clr, load, up, carry
  regist REG_A (
    .Clk(clk_out), .WE(in_9), .OE(in_10), .Data_in(eightbit_alu_1_data_out), .Stored_data(Reg_A_result));  // open: Data_out
  EightBit_ALU eightbit_alu_1 (
    .A(Reg_A_result), .B(REG_B_Result), .OE(OE_5), .Data_out(eightbit_alu_1_data_out), .Result(ALU_content));  // open: in_4
  assign bit_extender_1_out = {{24{REG_B_Result[7]}}, REG_B_Result};  // Bit_Extender bit_extender_1
  assign controlled_buffer_1_out = OE ? Counter_content : 4'bz;  // Controlled_Buffer controlled_buffer_1
  assign bit_extender_2_out = {{24{Reg_A_result[7]}}, Reg_A_result};  // Bit_Extender bit_extender_2
  regist regist_1 (
    .Clk(clk_out), .WE(in_7), .OE(in_8), .Data_in(eightbit_alu_1_data_out), .Data_out(regist_1_data_out),
    .Stored_data(IR_result));
  _7_Segment_Display u_7_segment_display_1 (
    .g(bit_extender_2_out[15]), .f(bit_extender_2_out[14]), .a(bit_extender_2_out[13]),
    .b(bit_extender_2_out[12]), .e(bit_extender_2_out[31]), .d(bit_extender_2_out[30]),
    .c(bit_extender_2_out[29]), .dp(bit_extender_2_out[28]));
  _7_Segment_Display u_7_segment_display_2 (
    .g(bit_extender_1_out[15]), .f(bit_extender_1_out[14]), .a(bit_extender_1_out[13]),
    .b(bit_extender_1_out[12]), .e(bit_extender_1_out[31]), .d(bit_extender_1_out[30]),
    .c(bit_extender_1_out[29]), .dp(bit_extender_1_out[28]));
  _7_Segment_Display u_7_segment_display_3 (
    .g(bit_extender_1_out[11]), .f(bit_extender_1_out[10]), .a(bit_extender_1_out[9]),
    .b(bit_extender_1_out[8]), .e(bit_extender_1_out[27]), .d(bit_extender_1_out[26]),
    .c(bit_extender_1_out[25]), .dp(bit_extender_1_out[24]));
  regist REG_B (
    .Clk(clk_out), .WE(WE_4), .Data_in(eightbit_alu_1_data_out), .Stored_data(REG_B_Result));  // open: OE, Data_out
  _7_Segment_Display u_7_segment_display_4 (
    .g(bit_extender_2_out[11]), .f(bit_extender_2_out[10]), .a(bit_extender_2_out[9]),
    .b(bit_extender_2_out[8]), .e(bit_extender_2_out[27]), .d(bit_extender_2_out[26]),
    .c(bit_extender_2_out[25]), .dp(bit_extender_2_out[24]));
  _7_Segment_Display u_7_segment_display_5 (
    .g(bit_extender_2_out[7]), .f(bit_extender_2_out[6]), .a(bit_extender_2_out[5]),
    .b(bit_extender_2_out[4]), .e(bit_extender_2_out[23]), .d(bit_extender_2_out[22]),
    .c(bit_extender_2_out[21]), .dp(bit_extender_2_out[20]));
  _7_Segment_Display u_7_segment_display_6 (
    .g(bit_extender_1_out[7]), .f(bit_extender_1_out[6]), .a(bit_extender_1_out[5]),
    .b(bit_extender_1_out[4]), .e(bit_extender_1_out[23]), .d(bit_extender_1_out[22]),
    .c(bit_extender_1_out[21]), .dp(bit_extender_1_out[20]));
  _7_Segment_Display u_7_segment_display_7 (
    .g(bit_extender_1_out[3]), .f(bit_extender_1_out[2]), .a(bit_extender_1_out[1]),
    .b(bit_extender_1_out[0]), .e(bit_extender_1_out[19]), .d(bit_extender_1_out[18]),
    .c(bit_extender_1_out[17]), .dp(bit_extender_1_out[16]));
  BitSelector #(.group(4)) bitselector_1 (.in(regist_1_data_out), .out(controlled_buffer_1_out), .sel(1'b0));
  _7_Segment_Display u_7_segment_display_8 (
    .g(bit_extender_2_out[3]), .f(bit_extender_2_out[2]), .a(bit_extender_2_out[1]),
    .b(bit_extender_2_out[0]), .e(bit_extender_2_out[19]), .d(bit_extender_2_out[18]),
    .c(bit_extender_2_out[17]), .dp(bit_extender_2_out[16]));
  LED D7 (.in(eightbit_alu_1_data_out[7]));
  assign eightbit_alu_1_data_out = OE_testing_data ? Testing_data : 8'bz;  // Controlled_Buffer controlled_buffer_2
  LED D6 (.in(eightbit_alu_1_data_out[6]));
  LED D5 (.in(eightbit_alu_1_data_out[5]));
  LED D4 (.in(eightbit_alu_1_data_out[4]));
  LED D3 (.in(eightbit_alu_1_data_out[3]));
  LED D2 (.in(eightbit_alu_1_data_out[2]));
  LED D1 (.in(eightbit_alu_1_data_out[1]));
  LED D0 (.in(eightbit_alu_1_data_out[0]));
  assign eightbit_alu_1_data_out = OE_3 ? MBR_content : 8'bz;  // Controlled_Buffer controlled_buffer_3
  regist Output_register (
    .Clk(clk_out), .WE(WE_3), .OE(OE_6), .Data_in(eightbit_alu_1_data_out),
    .Data_out(eightbit_alu_1_data_out), .Stored_data(out_24));
  // MAR mar_1: pin names not known; wires that end beside it: clk_out, WE, controlled_buffer_1_out, OE_2, MBR_content, eightbit_alu_1_data_out, eightbit_alu_1_data_out, mar_1_p8, out_17, out_17, out_17
  regist MBR (
    .Clk(clk_out), .WE(WE_2), .OE(OE_4), .Data_in(eightbit_alu_1_data_out),
    .Data_out(eightbit_alu_1_data_out), .Stored_data(MBR_content));
  LED led_1 (.in(eightbit_alu_1_data_out[7]));
  LED led_2 (.in(eightbit_alu_1_data_out[6]));
  LED led_3 (.in(eightbit_alu_1_data_out[5]));
  LED led_4 (.in(eightbit_alu_1_data_out[4]));
  LED led_5 (.in(eightbit_alu_1_data_out[3]));
  LED led_6 (.in(eightbit_alu_1_data_out[2]));
  LED led_7 (.in(eightbit_alu_1_data_out[1]));
  LED led_8 (.in(eightbit_alu_1_data_out[0]));

  // Notes on the sheet:
  //   Internal Data Bus
  //   External Data Bus
endmodule

module Dec (
  input  A_in,
  input  B_in,
  input  C_in,
  input  Enable,
  output D0,
  output D1,
  output D2,
  output D3,
  output D4,
  output D5,
  output D6,
  output D7
);

  wire buffer_1_out, not_1_out, not_2_out, not_3_out;

  not not_1 (not_1_out, C_in);
  not not_2 (not_2_out, B_in);
  not not_3 (not_3_out, A_in);
  buf buffer_1 (buffer_1_out, Enable);
  and and_1 (D0, not_3_out, not_2_out, not_1_out, buffer_1_out);
  and and_2 (D1, not_3_out, not_2_out, C_in, buffer_1_out);
  and and_3 (D2, not_3_out, B_in, not_1_out, buffer_1_out);
  and and_4 (D3, not_3_out, B_in, C_in, buffer_1_out);
  and and_5 (D4, A_in, not_2_out, not_1_out, buffer_1_out);
  and and_6 (D5, A_in, not_2_out, C_in, buffer_1_out);
  and and_7 (D6, A_in, B_in, not_1_out, buffer_1_out);
  and and_8 (D7, A_in, B_in, C_in, buffer_1_out);

  // Notes on the sheet:
  //   A' B' C'
  //   A' B' C
  //   A' B C'
  //   A' B C
  //   A B' C'
  //   A B' C
  //   A B C'
  //   A B C 
endmodule

module Dec_2X4 (
  input  A_0,
  input  A_1,
  input  Enable,
  output E_1,
  output E_2,
  output E_3,
  output E_4
);

  wire not_1_out, not_2_out;

  not not_1 (not_1_out, A_0);
  not not_2 (not_2_out, A_1);
  and and_1 (E_1, not_1_out, not_2_out, Enable);
  and and_2 (E_2, not_1_out, A_1, Enable);
  and and_3 (E_3, A_0, not_2_out, Enable);
  and and_4 (E_4, A_0, A_1, Enable);
endmodule

module Dec_5x32 (
  input  A0,
  input  A1,
  input  A2,
  input  A_0,
  input  A_1,
  input  Enable,
  output D0,
  output D1,
  output D2,
  output D3,
  output D4,
  output D5,
  output D6,
  output D7,
  output D8,
  output D9,
  output D10,
  output D11,
  output D12,
  output D13,
  output D14,
  output D15,
  output D16,
  output D17,
  output D18,
  output D19,
  output D20,
  output D21,
  output D22,
  output D23,
  output D24,
  output D25,
  output D26,
  output D27,
  output D28,
  output D29,
  output D30,
  output D31
);

  wire dec_2x4_1_e_1, dec_2x4_1_e_2, dec_2x4_1_e_3, dec_2x4_1_e_4;

  Dec_2X4 dec_2x4_1 (
    .A_0(A_0), .A_1(A_1), .Enable(Enable), .E_1(dec_2x4_1_e_1), .E_2(dec_2x4_1_e_2), .E_3(dec_2x4_1_e_3),
    .E_4(dec_2x4_1_e_4));
  Dec dec_1 (
    .A_in(A0), .B_in(A1), .C_in(A2), .Enable(dec_2x4_1_e_1), .D0(D0), .D1(D1), .D2(D2), .D3(D3), .D4(D4),
    .D5(D5), .D6(D6), .D7(D7));
  Dec dec_2 (
    .A_in(A0), .B_in(A1), .C_in(A2), .Enable(dec_2x4_1_e_2), .D0(D8), .D1(D9), .D2(D10), .D3(D11), .D4(D12),
    .D5(D13), .D6(D14), .D7(D15));
  Dec dec_3 (
    .A_in(A0), .B_in(A1), .C_in(A2), .Enable(dec_2x4_1_e_3), .D0(D16), .D1(D17), .D2(D18), .D3(D19),
    .D4(D20), .D5(D21), .D6(D22), .D7(D23));
  Dec dec_4 (
    .A_in(A0), .B_in(A1), .C_in(A2), .Enable(dec_2x4_1_e_4), .D0(D24), .D1(D25), .D2(D26), .D3(D27),
    .D4(D28), .D5(D29), .D6(D30), .D7(D31));
endmodule

module memory_cell (
  input  Clock,
  input  WE,
  input  Data_in,
  input  OE,
  input  Reset,
  output Dout,
  output Stored_data
);

  wire and_1_out, and_2_out, not_1_out, or_1_out;

  not not_1 (not_1_out, WE);
  and and_1 (and_1_out, Stored_data, not_1_out);
  and and_2 (and_2_out, WE, Data_in);
  or or_1 (or_1_out, and_1_out, and_2_out);
  D_Flip_Flop d_ff_1 (.D(or_1_out), .clk(Clock), .Q(Stored_data), .reset(Reset));  // open: Qn, preset
  assign Dout = OE ? Stored_data : 1'bz;  // Controlled_Buffer controlled_buffer_1
endmodule

module regist (
  input  Clk,
  input  WE,
  input  OE,
  input  [7:0] Data_in,
  output [7:0] Data_out,
  output [7:0] Stored_data
);

  memory_cell memory_cell_1 (
    .Clock(Clk), .WE(WE), .Data_in(Data_in[0]), .OE(OE), .Dout(Data_out[0]), .Stored_data(Stored_data[0]));  // open: Reset
  memory_cell memory_cell_2 (
    .Clock(Clk), .WE(WE), .Data_in(Data_in[2]), .OE(OE), .Dout(Data_out[1]), .Stored_data(Stored_data[1]));  // open: Reset
  memory_cell memory_cell_3 (
    .Clock(Clk), .WE(WE), .Data_in(Data_in[2]), .OE(OE), .Dout(Data_out[2]), .Stored_data(Stored_data[2]));  // open: Reset
  memory_cell memory_cell_4 (
    .Clock(Clk), .WE(WE), .Data_in(Data_in[3]), .OE(OE), .Dout(Data_out[3]), .Stored_data(Stored_data[3]));  // open: Reset
  memory_cell memory_cell_5 (
    .Clock(Clk), .WE(WE), .Data_in(Data_in[4]), .OE(OE), .Dout(Data_out[4]), .Stored_data(Stored_data[4]));  // open: Reset
  memory_cell memory_cell_6 (
    .Clock(Clk), .WE(WE), .Data_in(Data_in[5]), .OE(OE), .Dout(Data_out[5]), .Stored_data(Stored_data[5]));  // open: Reset
  memory_cell memory_cell_7 (
    .Clock(Clk), .WE(WE), .Data_in(Data_in[6]), .OE(OE), .Dout(Data_out[6]), .Stored_data(Stored_data[6]));  // open: Reset
  memory_cell memory_cell_8 (
    .Clock(Clk), .WE(WE), .Data_in(Data_in[7]), .OE(OE), .Dout(Data_out[7]), .Stored_data(Stored_data[7]));  // open: Reset

  assign Data_in[1] = Data_in[2];
endmodule

module sixteenbit_mux (
  input  Flag,
  input  [15:0] A,
  input  [15:0] B,
  output [15:0] out_4
);

  wire [15:0] and_1_out, and_2_out, bit_extender_1_out, not_1_out;

  assign bit_extender_1_out = {{15{Flag}}, Flag};  // Bit_Extender bit_extender_1
  assign not_1_out = ~bit_extender_1_out;  // NOT_Gate not_1, 16 bits wide
  assign and_1_out = A & not_1_out;  // AND_Gate and_1, 16 bits wide
  assign and_2_out = B & bit_extender_1_out;  // AND_Gate and_2, 16 bits wide
  assign out_4 = and_1_out | and_2_out;  // OR_Gate or_1, 16 bits wide
endmodule

module ALU_16_bit (
  input  [15:0] A,
  input  [15:0] B,
  input  [4:0] Opcode,
  input  mult,
  input  Sub_control,
  input  addsub,
  input  Carry_in,
  output [15:0] data_out,
  output overflow_addsub
);

  wire [3:0] comp_16_1_out_3;
  wire [7:0] bit_extender_2_out, bit_extender_3_out;
  wire [15:0] addsub_16_1_out_5, bit_extender_1_out, bit_extender_4_out, controlled_buffer_1_out,
       controlled_buffer_2_out, eightbbit_multivv2_1_sum_out, logical_not_16_bit_1_out_2,
       sixteen_bit_and_gate_1_out_3, sixteen_bit_xor_gate_1_out_3;

  // Probe on A
  // Probe on B
  assign bit_extender_1_out = {{15{Sub_control}}, Sub_control};  // Bit_Extender bit_extender_1
  Bit_Extender #(.in_width(16), .out_width(8)) bit_extender_2 (.in(A), .out(bit_extender_2_out));
  Bit_Extender #(.in_width(16), .out_width(8)) bit_extender_3 (.in(B), .out(bit_extender_3_out));
  logical_NOT_16_bit logical_not_16_bit_1 (.in_1(A), .out_2(logical_not_16_bit_1_out_2));
  Sixteen_bit_XOR_GATE sixteen_bit_xor_gate_1 (.A(A), .B(B), .out_3(sixteen_bit_xor_gate_1_out_3));
  sixteen_bit_OR_GATE sixteen_bit_or_gate_1 (.A(A), .B(B));  // open: out_3
  Sixteen_bit_AND_GATE sixteen_bit_and_gate_1 (.A(A), .B(B), .out_3(sixteen_bit_and_gate_1_out_3));
  eightbbit_multivv2 eightbbit_multivv2_1 (
    .A(bit_extender_2_out), .B(bit_extender_3_out), .sum_out(eightbbit_multivv2_1_sum_out));  // open: carry_out
  comp_16 comp_16_1 (.in_1(A), .in_2(B), .out_3(comp_16_1_out_3));
  addsub_16 addsub_16_1 (
    .A(A), .B(B), .carry_in(Carry_in), .sum(bit_extender_1_out), .out_5(addsub_16_1_out_5),
    .carry_out(overflow_addsub));
  assign bit_extender_4_out = {{12{comp_16_1_out_3[3]}}, comp_16_1_out_3};  // Bit_Extender bit_extender_4
  assign controlled_buffer_1_out = addsub ? addsub_16_1_out_5 : 16'bz;  // Controlled_Buffer controlled_buffer_1
  assign controlled_buffer_2_out = mult ? eightbbit_multivv2_1_sum_out : 16'bz;  // Controlled_Buffer controlled_buffer_2
  Sixteen_bit_MUX_16by1 sixteen_bit_mux_16by1_1 (
    .Op_code(Opcode), .E_0001(controlled_buffer_1_out), .E_0011(controlled_buffer_2_out),
    .E_1010(bit_extender_4_out), .E_1011(sixteen_bit_and_gate_1_out_3),
    .E_1100(sixteen_bit_xor_gate_1_out_3), .E_1101(logical_not_16_bit_1_out_2), .out_18(data_out));  // open: E_0000, E_0010, E_0100, E_0101, E_0110, E_0111, E_1000, E_1001, E_1110, E_1111
  // Probe on data_out

  // Notes on the sheet:
  //   ADD=00001
  //   SUBTRACT= 00001
  //   MULTIPLIER=00011
  //   STORE=00100
  //   0100. With Flag = 1 • Store Over Flow
  //   0100. With Flag = 1 • Store Over Flow
  //   1011 • And 
  //   1100 • XOR
  //   1101 • NOT (A)
  //   1110 • NOP 
  //   1110. With Flag = 1 • HALT 
endmodule

module Sixteen_bit_MUX_16by1 (
  input  [4:0] Op_code,
  input  [15:0] E_0000,
  input  [15:0] E_0001,
  input  [15:0] E_0010,
  input  [15:0] E_0011,
  input  [15:0] E_0100,
  input  [15:0] E_0101,
  input  [15:0] E_0110,
  input  [15:0] E_0111,
  input  [15:0] E_1000,
  input  [15:0] E_1001,
  input  [15:0] E_1010,
  input  [15:0] E_1011,
  input  [15:0] E_1100,
  input  [15:0] E_1101,
  input  [15:0] E_1110,
  input  [15:0] E_1111,
  output [15:0] out_18
);

  wire [15:0] and_1_out, and_2_out, and_3_out, and_4_out, and_5_out, and_6_out, and_7_out, and_8_out,
       and_9_out, and_10_out, and_11_out, and_12_out, and_13_out, and_14_out, and_15_out, and_16_out,
       bit_extender_1_out, bit_extender_2_out, bit_extender_3_out, bit_extender_4_out, bit_extender_5_out,
       not_1_out, not_2_out, not_3_out, not_4_out;

  assign bit_extender_1_out = {{15{Op_code[4]}}, Op_code[4]};  // Bit_Extender bit_extender_1
  assign bit_extender_2_out = {{15{Op_code[3]}}, Op_code[3]};  // Bit_Extender bit_extender_2
  assign not_1_out = ~bit_extender_2_out;  // NOT_Gate not_1, 16 bits wide
  assign bit_extender_3_out = {{15{Op_code[2]}}, Op_code[2]};  // Bit_Extender bit_extender_3
  assign not_2_out = ~bit_extender_3_out;  // NOT_Gate not_2, 16 bits wide
  assign bit_extender_4_out = {{15{Op_code[1]}}, Op_code[1]};  // Bit_Extender bit_extender_4
  assign not_3_out = ~bit_extender_4_out;  // NOT_Gate not_3, 16 bits wide
  assign bit_extender_5_out = {{15{Op_code[0]}}, Op_code[0]};  // Bit_Extender bit_extender_5
  assign not_4_out = ~bit_extender_5_out;  // NOT_Gate not_4, 16 bits wide
  assign and_1_out = E_0000 & not_4_out & not_3_out & not_2_out & not_1_out;  // AND_Gate and_1, 16 bits wide
  assign and_2_out = E_0001 & bit_extender_5_out & not_3_out & not_2_out & not_1_out;  // AND_Gate and_2, 16 bits wide
  assign and_3_out = E_0010 & not_4_out & bit_extender_4_out & not_2_out & not_1_out;  // AND_Gate and_3, 16 bits wide
  assign and_4_out = E_0011 & bit_extender_5_out & bit_extender_4_out & not_2_out & not_1_out;  // AND_Gate and_4, 16 bits wide
  assign and_5_out = E_0100 & not_4_out & not_3_out & bit_extender_3_out & not_1_out;  // AND_Gate and_5, 16 bits wide
  assign and_6_out = E_0101 & bit_extender_5_out & not_3_out & bit_extender_3_out & not_1_out;  // AND_Gate and_6, 16 bits wide
  assign and_7_out = E_0110 & not_4_out & bit_extender_4_out & bit_extender_3_out & not_1_out;  // AND_Gate and_7, 16 bits wide
  assign and_8_out = E_0111 & bit_extender_5_out & bit_extender_4_out & bit_extender_3_out & not_1_out;  // AND_Gate and_8, 16 bits wide
  assign and_9_out = E_1000 & not_4_out & not_3_out & not_2_out & bit_extender_2_out;  // AND_Gate and_9, 16 bits wide
  assign and_10_out = E_1001 & bit_extender_5_out & not_3_out & not_2_out & bit_extender_2_out;  // AND_Gate and_10, 16 bits wide
  assign and_11_out = E_1010 & not_4_out & bit_extender_4_out & not_2_out & bit_extender_2_out;  // AND_Gate and_11, 16 bits wide
  assign and_12_out = E_1011 & bit_extender_5_out & bit_extender_4_out & not_2_out & bit_extender_2_out;  // AND_Gate and_12, 16 bits wide
  assign and_13_out = E_1100 & not_4_out & not_3_out & bit_extender_3_out & bit_extender_2_out;  // AND_Gate and_13, 16 bits wide
  assign and_14_out = E_1101 & bit_extender_5_out & not_3_out & bit_extender_3_out & bit_extender_2_out;  // AND_Gate and_14, 16 bits wide
  assign and_15_out = E_1110 & not_4_out & bit_extender_4_out & bit_extender_3_out & bit_extender_2_out;  // AND_Gate and_15, 16 bits wide
  assign and_16_out = E_1111 & bit_extender_5_out & bit_extender_4_out & bit_extender_3_out & bit_extender_2_out;  // AND_Gate and_16, 16 bits wide
  assign out_18 = and_1_out | and_2_out | and_3_out | and_4_out | and_5_out | and_6_out | and_7_out | and_8_out | and_9_out | and_10_out | and_11_out | and_12_out | and_13_out | and_14_out | and_15_out | and_16_out;  // OR_Gate or_1, 16 bits wide
  // Probe on out_18
endmodule

module sixteen_bit_MUX_2by1 (
  input  [15:0] A,
  input  [15:0] B,
  input  S1,
  output [15:0] out_4
);

  wire [15:0] and_1_out, and_2_out, bit_extender_1_out, not_1_out;

  assign bit_extender_1_out = {{15{S1}}, S1};  // Bit_Extender bit_extender_1
  assign not_1_out = ~bit_extender_1_out;  // NOT_Gate not_1, 16 bits wide
  assign and_1_out = A & not_1_out;  // AND_Gate and_1, 16 bits wide
  assign and_2_out = B & not_1_out;  // AND_Gate and_2, 16 bits wide
  assign out_4 = and_1_out | and_2_out;  // OR_Gate or_1, 16 bits wide
endmodule

module sixteen_bit_mux_4by1 (
  input  [15:0] E11,
  input  [15:0] E10,
  input  [15:0] E01,
  input  [15:0] E00,
  input  s1,
  input  s2,
  output [15:0] out_7
);

  wire [15:0] and_1_out, and_2_out, and_3_out, and_4_out, bit_extender_1_out, bit_extender_2_out, not_1_out,
       not_2_out;

  assign bit_extender_1_out = {{15{s1}}, s1};  // Bit_Extender bit_extender_1
  assign bit_extender_2_out = {{15{s2}}, s2};  // Bit_Extender bit_extender_2
  assign not_1_out = ~bit_extender_1_out;  // NOT_Gate not_1, 16 bits wide
  assign not_2_out = ~bit_extender_2_out;  // NOT_Gate not_2, 16 bits wide
  assign and_1_out = E11 & bit_extender_1_out & bit_extender_2_out;  // AND_Gate and_1, 16 bits wide
  assign and_2_out = E10 & bit_extender_2_out & not_1_out;  // AND_Gate and_2, 16 bits wide
  assign and_3_out = E01 & not_2_out & bit_extender_1_out;  // AND_Gate and_3, 16 bits wide
  assign and_4_out = E00 & not_2_out & not_1_out;  // AND_Gate and_4, 16 bits wide
  assign out_7 = and_1_out | and_2_out | and_3_out | and_4_out;  // OR_Gate or_1, 16 bits wide
endmodule

module sixteen_bit_8by1 (
  input  s3,
  input  s2,
  input  s1,
  input  [15:0] E000,
  input  [15:0] E001,
  input  [15:0] E011,
  input  [15:0] E010,
  input  [15:0] E100,
  input  [15:0] E101,
  input  [15:0] E110,
  input  [15:0] E111,
  output [15:0] out_12
);

  wire [15:0] and_1_out, and_2_out, and_3_out, and_4_out, and_5_out, and_6_out, and_7_out, and_8_out,
       bit_extender_1_out, bit_extender_2_out, bit_extender_3_out, not_1_out, not_2_out, not_3_out;

  assign bit_extender_1_out = {{15{s3}}, s3};  // Bit_Extender bit_extender_1
  assign not_1_out = ~bit_extender_1_out;  // NOT_Gate not_1, 16 bits wide
  assign bit_extender_2_out = {{15{s2}}, s2};  // Bit_Extender bit_extender_2
  assign not_2_out = ~bit_extender_2_out;  // NOT_Gate not_2, 16 bits wide
  assign bit_extender_3_out = {{15{s1}}, s1};  // Bit_Extender bit_extender_3
  assign not_3_out = ~bit_extender_3_out;  // NOT_Gate not_3, 16 bits wide
  assign and_1_out = E000 & not_3_out & not_2_out & not_1_out;  // AND_Gate and_1, 16 bits wide
  assign and_2_out = E001 & bit_extender_3_out & not_2_out & not_1_out;  // AND_Gate and_2, 16 bits wide
  assign and_3_out = E011 & bit_extender_3_out & bit_extender_2_out & not_1_out;  // AND_Gate and_3, 16 bits wide
  assign and_4_out = E010 & not_3_out & bit_extender_2_out & not_1_out;  // AND_Gate and_4, 16 bits wide
  assign and_5_out = E100 & not_3_out & not_2_out & bit_extender_1_out;  // AND_Gate and_5, 16 bits wide
  assign and_6_out = E101 & bit_extender_3_out & not_2_out & bit_extender_1_out;  // AND_Gate and_6, 16 bits wide
  assign and_7_out = E110 & not_3_out & bit_extender_2_out & bit_extender_1_out;  // AND_Gate and_7, 16 bits wide
  assign and_8_out = E111 & bit_extender_3_out & bit_extender_2_out & bit_extender_1_out;  // AND_Gate and_8, 16 bits wide
  // Probe on out_12
  assign out_12 = and_1_out | and_2_out | and_3_out | and_4_out | and_5_out | and_6_out | and_7_out | and_8_out;  // OR_Gate or_1, 16 bits wide
endmodule

module Viva_test (
  input  in_1,
  input  in_2,
  input  in_3,
  input  in_4,
  input  in_5,
  input  in_6,
  input  in_7,
  input  in_8,
  input  in_9,
  input  in_10,
  input  in_11,
  input  in_12,
  input  in_13,
  input  in_14,
  input  in_15,
  input  in_16,
  input  in_17,
  input  in_18,
  input  in_19,
  input  in_20,
  input  in_21,
  input  in_22,
  input  in_23,
  input  in_24,
  input  in_25,
  input  in_26,
  input  in_27,
  input  in_28,
  input  in_29,
  input  in_30,
  input  in_31,
  input  Mult_OE,
  input  in_33,
  input  in_34,
  input  in_35,
  input  in_36,
  input  SC_clock_reset,
  input  in_38,
  output A_eq_B,
  output A_grt_B,
  output A_less_B
);

  wire alu_16_bit_1_p6, alu_16_bit_1_p9, alu_16_bit_1_p13, CLK_out, controlled_buffer_2_out,
       overflow_addsub_q, undriven, undriven_2;
  wire [3:0] counter_2_q;
  wire [4:0] controlled_buffer_1_out, controlled_buffer_5_out, controlled_buffer_11_out, counter_1_q,
       instruction_splitter_1_address_a, instruction_splitter_1_address_b, MAR_A_q, MAR_B_q, MAR_Z_q;
  wire [4:4] register_1_q;
  wire [7:4] register_1_q_2;
  wire [15:0] alu_16_bit_1_p1, alu_16_bit_1_p2, alu_16_bit_1_p8, ALU_out_register_q, bit_extender_1_out,
       controlled_buffer_3_out, controlled_buffer_4_out, controlled_buffer_17_out, Instruction_REG_dout,
       MBR_A_q, MBR_B_q, MBR_Z_q, ram_1_dout, ram_3_dout, Reg_1_q, Reg_2_q, Reg_3_q, Reg_5_q, Reg_6_q,
       Reg_7_q, Reg_8_q, sixteenbit_mux_1_out_4;
  wire [36:0] rom_1_data;

  // Probe on {register_1_q[4], register_1_q_2}
  // Probe on controlled_buffer_3_out
  Register #(.width(1)) overflow_addsub (
    .D(alu_16_bit_1_p13), .en(rom_1_data[3]), .clk(CLK_out), .Q(overflow_addsub_q));  // open: clr
  Controlled_Buffer #(.width(5)) controlled_buffer_1 (.in({5{1'b0}}), .out(controlled_buffer_1_out));  // open: en
  Register #(.width(5)) register_1 (
    .D(controlled_buffer_1_out), .en(rom_1_data[7]), .clk(CLK_out), .Q({register_1_q[4], register_1_q_2}));  // open: clr
  Register #(.width(16)) ALU_out_register (
    .D(controlled_buffer_3_out), .en(rom_1_data[6]), .clk(CLK_out), .Q(ALU_out_register_q));  // open: clr
  // Probe on alu_16_bit_1_p1
  // ALU_16_bit alu_16_bit_1: pin names not known; wires that end beside it: alu_16_bit_1_p1, alu_16_bit_1_p2, {register_1_q[4], register_1_q_2}, rom_1_data[5], {register_1_q[4], register_1_q_2}, alu_16_bit_1_p6, rom_1_data[4], alu_16_bit_1_p8, alu_16_bit_1_p9, A_eq_B, A_grt_B, A_less_B, alu_16_bit_1_p13
  assign bit_extender_1_out = {{15{overflow_addsub_q}}, overflow_addsub_q};  // Bit_Extender bit_extender_1
  assign controlled_buffer_2_out = rom_1_data[1] ? CLK_out : 1'bz;  // Controlled_Buffer controlled_buffer_2
  // Probe on {register_1_q[4], register_1_q_2}
  // Probe on alu_16_bit_1_p8
  // Probe on alu_16_bit_1_p2
  Counter #(.max('h1f), .width(5)) counter_1 (
    .clk(controlled_buffer_2_out), .Q(counter_1_q));  // open: clr, load, up, count, D, carry
  assign controlled_buffer_3_out = rom_1_data[8] ? alu_16_bit_1_p8 : 16'bz;  // Controlled_Buffer controlled_buffer_3
  // Probe on controlled_buffer_17_out
  // Probe on MBR_A_q
  sixteenbit_mux sixteenbit_mux_1 (
    .Flag(alu_16_bit_1_p6), .A(ALU_out_register_q), .B(bit_extender_1_out), .out_4(sixteenbit_mux_1_out_4));
  Register #(.width(16)) Reg_1 (.D(MBR_A_q), .en(rom_1_data[11]), .clk(CLK_out), .Q(Reg_1_q));  // open: clr
  Register #(.width(16)) Reg_3 (.D(MBR_A_q), .en(rom_1_data[12]), .clk(CLK_out), .Q(Reg_3_q));  // open: clr
  // Probe on MBR_B_q
  Register #(.width(16)) Reg_5 (.D(MBR_B_q), .en(rom_1_data[13]), .clk(CLK_out), .Q(Reg_5_q));  // open: clr
  Register #(.width(16)) Reg_7 (.D(MBR_B_q), .en(rom_1_data[14]), .clk(CLK_out), .Q(Reg_7_q));  // open: clr
  Clock CLK (.out(CLK_out));
  // Probe on counter_1_q
  Register #(.width(5)) MAR_Z (.D(counter_1_q), .en(rom_1_data[21]), .clk(CLK_out), .Q(MAR_Z_q));  // open: clr
  instruction_splitter instruction_splitter_1 (
    .Instruction(controlled_buffer_17_out), .WE(rom_1_data[25]), .Clk(CLK_out),
    .Address_A(instruction_splitter_1_address_a), .Address_B(instruction_splitter_1_address_b),
    .Opcode(controlled_buffer_1_out), .Flag(alu_16_bit_1_p6));
  Register #(.width(16)) Reg_2 (.D(MBR_A_q), .en(rom_1_data[16]), .clk(CLK_out), .Q(Reg_2_q));  // open: clr
  Controlled_Buffer #(.width(16)) controlled_buffer_4 (.in(Reg_3_q), .out(controlled_buffer_4_out));  // open: en
  Register #(.width(16)) Reg_4 (
    .D(MBR_A_q), .en(rom_1_data[17]), .clk(CLK_out), .Q(controlled_buffer_4_out));  // open: clr
  Register #(.width(16)) Reg_6 (.D(MBR_B_q), .en(rom_1_data[15]), .clk(CLK_out), .Q(Reg_6_q));  // open: clr
  Register #(.width(16)) Reg_8 (.D(MBR_B_q), .en(rom_1_data[18]), .clk(CLK_out), .Q(Reg_8_q));  // open: clr
  assign controlled_buffer_5_out = undriven ? instruction_splitter_1_address_b : 5'bz;  // Controlled_Buffer controlled_buffer_5
  // Probe on instruction_splitter_1_address_a
  // Probe on controlled_buffer_1_out
  Controlled_Buffer #(.width(16)) controlled_buffer_6 (.in(Reg_1_q), .out(controlled_buffer_4_out));  // open: en
  Controlled_Buffer #(.width(16)) controlled_buffer_7 (.in(Reg_5_q), .out(Reg_8_q));  // open: en
  Controlled_Buffer #(.width(16)) controlled_buffer_8 (.in(Reg_6_q), .out(Reg_8_q));  // open: en
  Controlled_Buffer #(.width(16)) controlled_buffer_9 (.in(Reg_7_q), .out(Reg_8_q));  // open: en
  // Probe on MAR_Z_q
  Register #(.width(5)) MAR_A (
    .D(controlled_buffer_5_out), .en(rom_1_data[20]), .clk(CLK_out), .Q(MAR_A_q));  // open: clr
  Controlled_Buffer #(.width(5)) controlled_buffer_10 (
    .in(instruction_splitter_1_address_a), .out(controlled_buffer_5_out));  // open: en
  assign controlled_buffer_11_out = undriven_2 ? instruction_splitter_1_address_b : 5'bz;  // Controlled_Buffer controlled_buffer_11
  Controlled_Buffer #(.width(16)) controlled_buffer_12 (.in(Reg_2_q), .out(controlled_buffer_4_out));  // open: en
  assign alu_16_bit_1_p1 = rom_1_data[10] ? controlled_buffer_4_out : 16'bz;  // Controlled_Buffer controlled_buffer_13
  Controlled_Buffer #(.width(5)) controlled_buffer_14 (
    .in(instruction_splitter_1_address_a), .out(controlled_buffer_11_out));  // open: en
  // Probe on controlled_buffer_11_out
  assign alu_16_bit_1_p2 = rom_1_data[9] ? Reg_8_q : 16'bz;  // Controlled_Buffer controlled_buffer_15
  Register #(.width(16)) MBR_Z (
    .D(Instruction_REG_dout), .en(rom_1_data[26]), .clk(CLK_out), .Q(MBR_Z_q));  // open: clr
  // Probe on ram_1_dout
  Register #(.width(16)) MBR_A (.D(ram_1_dout), .en(rom_1_data[27]), .clk(CLK_out), .Q(MBR_A_q));  // open: clr
  // Probe on ram_3_dout
  Register #(.width(16)) MBR_B (.D(ram_3_dout), .en(rom_1_data[28]), .clk(CLK_out), .Q(MBR_B_q));  // open: clr
  Register #(.width(5)) MAR_B (
    .D(controlled_buffer_11_out), .en(rom_1_data[19]), .clk(CLK_out), .Q(MAR_B_q));  // open: clr
  // Probe on Instruction_REG_dout
  assign alu_16_bit_1_p1 = rom_1_data[23] ? MBR_A_q : 16'bz;  // Controlled_Buffer controlled_buffer_16
  assign controlled_buffer_17_out = rom_1_data[22] ? MBR_Z_q : 16'bz;  // Controlled_Buffer controlled_buffer_17
  assign alu_16_bit_1_p2 = rom_1_data[24] ? MBR_B_q : 16'bz;  // Controlled_Buffer controlled_buffer_18
  RAM #(.addrWidth(5), .dataWidth(16)) Instruction_REG (
    .addr(MAR_Z_q), .we(rom_1_data[31]), .oe(rom_1_data[32]), .clk(CLK_out), .din(controlled_buffer_17_out),
    .dout(Instruction_REG_dout));
  RAM #(.addrWidth(5), .dataWidth(16)) ram_1 (
    .addr(MAR_A_q), .we(rom_1_data[36]), .oe(rom_1_data[35]), .clk(CLK_out), .din(alu_16_bit_1_p1),
    .dout(ram_1_dout));
  // Probe on Instruction_REG_dout
  Controlled_Buffer #(.width(16)) controlled_buffer_19 (
    .in(controlled_buffer_17_out), .out(sixteenbit_mux_1_out_4));  // open: en
  RAM #(.addrWidth(5), .dataWidth(16)) ram_2 (
    .addr(MAR_Z_q), .we(rom_1_data[29]), .oe(rom_1_data[30]), .clk(CLK_out), .din(sixteenbit_mux_1_out_4),
    .dout(Instruction_REG_dout));
  RAM #(.addrWidth(5), .dataWidth(16)) ram_3 (
    .addr(MAR_B_q), .we(rom_1_data[33]), .oe(rom_1_data[34]), .clk(CLK_out), .din(alu_16_bit_1_p2),
    .dout(ram_3_dout));
  ROM #(.dataWidth(37)) rom_1 (.addr({register_1_q_2, counter_2_q}), .data(rom_1_data));
  Counter #(.max('hf), .width(4)) counter_2 (
    .clr(rom_1_data[0]), .clk(CLK_out), .Q(counter_2_q));  // open: load, up, count, D, carry

  // Notes on the sheet:
  //   ADD=00001
  //   SUBTRACT= 00001
  //   MULTIPLIER=00011
  //   STORE=00100
  //   0100. With Flag = 1 • Store Over Flow
  //   0100. With Flag = 1 • Store Over Flow
  //   1011 • And 
  //   1100 • XOR
  //   1101 • NOT (A)
  //   1110 • NOP 
  //   1110. With Flag = 1 • HALT 
  //   REG_bank A
  //   REG-bank B
  //   NOTE!!!!!
  //   THIS IS FOR TESTING REG SWAP AND MEM SWAP(PLUS LOGICAL OPERATIONS)
  //   Instruction RAM
  //   RAM A
  //   System RAM
  //   RAM B
  //   RAM_A_WE
  //   RAM_A_OE
  //   RAM_B_OE
  //   RAM_B_WE
  //   SYSTEM_RAM_WE
  //   MBR_B_WE
  //   MBR_A_WE
  //   MBR_Z_WE
  //   INST_SPLITTER_WE
  //   MBR_B_CB
  //   MBR_A_CB
  //   MBR_Z_CB
  //   MAR_A_WE
  //   MAR_B_WE
  //   Reg_8_WE
  //    Reg_4_WE
  //   Reg_2_WE
  //   Reg_6_WE
  //   Reg_7_WE
  //   Reg_5_WE
  //   Reg_3_WE
  //   Reg_1_WE
  //   Reg_Bank_A_CB
  //   Reg_Bank_B_CB
  //   ALU_data_out
  //   Opcode_reg_WE
  //   ALU_out_reg_WE
  //   Addsub_OE
  //   Carry_in_sub 
  //   PC_counter_clock_CB
  //   INST_RAM_OE
  //   INST_RAM_WE
  //   SYSTEM_RAM_OE
  //   MAR_Z_WE
  //   Overflow_addsub_Reg_WE
  //   Address_B_to_A
  //   NOTE!!!!!
  //   THIS IS FOR TESTING REG SWAP AND MEM SWAP
  //   contents of rom_1 (hex, n*v repeats v):
  //   100200000 104000000 2400000 180080 1 11*0 100200000 104000000 2400000 180080 c00000000 c18000000
  //   187f800 75a 1 23*0 100200000 104000000 2400000 180080 c00000000 c18000000 187f800 762 1 7*0
  //   100200000 104000000 2400000 180080 20000002 1
endmodule

module instruction_splitter (
  input  [15:0] Instruction,
  input  WE,
  input  Clk,
  output [4:0] Address_A,
  output [4:0] Address_B,
  output [4:0] Opcode,
  output Flag
);

  Register #(.width(16)) register_1 (
    .D(Instruction), .en(WE), .clk(Clk), .Q({Flag, Opcode, Address_B, Address_A}));  // open: clr
endmodule

module logical_NOT_16_bit (
  input  [15:0] in_1,
  output [15:0] out_2
);

  assign out_2 = ~in_1;  // NOT_Gate not_1, 16 bits wide
endmodule

module logical_NOT_B_16_bit (
  input  [15:0] in_1,
  output [15:0] out_2
);

  assign out_2 = ~in_1;  // NOT_Gate not_1, 16 bits wide
endmodule

// Dont_move_the_bloody_matmult
module MAT_MULT_16_bit (
  input  [4:0] Opcode,
  input  [7:0] A11,
  input  [7:0] A12,
  input  [7:0] A21,
  input  [7:0] A22,
  input  [7:0] B11,
  input  [7:0] B12,
  input  [7:0] B21,
  input  [7:0] B22,
  output [15:0] C_1_1,
  output out_11,
  output [15:0] C_1_2,
  output out_13,
  output [15:0] C_2_1,
  output out_15,
  output [15:0] C_2_2,
  output out_17
);

  wire and_1_out, my16bit_adder_1_carry_out, my16bit_adder_2_carry_out, my16bit_adder_3_carry_out,
       my16bit_adder_4_carry_out, not_1_out, not_2_out, not_3_out;
  wire [15:0] eightbbit_multivv2_1_sum_out, eightbbit_multivv2_2_sum_out, eightbbit_multivv2_3_sum_out,
       eightbbit_multivv2_4_sum_out, eightbbit_multivv2_5_sum_out, eightbbit_multivv2_6_sum_out,
       eightbbit_multivv2_7_sum_out, eightbbit_multivv2_8_sum_out, my16bit_adder_1_sum_out,
       my16bit_adder_2_sum_out, my16bit_adder_3_sum_out, my16bit_adder_4_sum_out;

  eightbbit_multivv2 eightbbit_multivv2_1 (
    .A(A11), .B(B11), .sum_out(eightbbit_multivv2_1_sum_out));  // open: carry_out
  eightbbit_multivv2 eightbbit_multivv2_2 (
    .A(A12), .B(B21), .sum_out(eightbbit_multivv2_2_sum_out));  // open: carry_out
  eightbbit_multivv2 eightbbit_multivv2_3 (
    .A(A11), .B(B12), .sum_out(eightbbit_multivv2_3_sum_out));  // open: carry_out
  eightbbit_multivv2 eightbbit_multivv2_4 (
    .A(A12), .B(B22), .sum_out(eightbbit_multivv2_4_sum_out));  // open: carry_out
  eightbbit_multivv2 eightbbit_multivv2_5 (
    .A(A21), .B(B11), .sum_out(eightbbit_multivv2_5_sum_out));  // open: carry_out
  eightbbit_multivv2 eightbbit_multivv2_6 (
    .A(A22), .B(B21), .sum_out(eightbbit_multivv2_6_sum_out));  // open: carry_out
  eightbbit_multivv2 eightbbit_multivv2_7 (
    .A(A21), .B(B12), .sum_out(eightbbit_multivv2_7_sum_out));  // open: carry_out
  eightbbit_multivv2 eightbbit_multivv2_8 (
    .A(A22), .B(B22), .sum_out(eightbbit_multivv2_8_sum_out));  // open: carry_out
  not not_1 (not_1_out, Opcode[1]);
  not not_2 (not_2_out, Opcode[2]);
  not not_3 (not_3_out, Opcode[4]);
  and and_1 (and_1_out, Opcode[0], not_1_out, not_2_out, Opcode[3], not_3_out);
  my16bit_adder my16bit_adder_1 (
    .A(eightbbit_multivv2_1_sum_out), .B(eightbbit_multivv2_2_sum_out), .sum_out(my16bit_adder_1_sum_out),
    .carry_out(my16bit_adder_1_carry_out));  // open: Carry_in
  my16bit_adder my16bit_adder_2 (
    .A(eightbbit_multivv2_3_sum_out), .B(eightbbit_multivv2_4_sum_out), .sum_out(my16bit_adder_2_sum_out),
    .carry_out(my16bit_adder_2_carry_out));  // open: Carry_in
  my16bit_adder my16bit_adder_3 (
    .A(eightbbit_multivv2_5_sum_out), .B(eightbbit_multivv2_6_sum_out), .sum_out(my16bit_adder_3_sum_out),
    .carry_out(my16bit_adder_3_carry_out));  // open: Carry_in
  my16bit_adder my16bit_adder_4 (
    .A(eightbbit_multivv2_7_sum_out), .B(eightbbit_multivv2_8_sum_out), .sum_out(my16bit_adder_4_sum_out),
    .carry_out(my16bit_adder_4_carry_out));  // open: Carry_in
  assign C_1_1 = and_1_out ? my16bit_adder_1_sum_out : 16'bz;  // Controlled_Buffer controlled_buffer_1
  assign out_11 = and_1_out ? my16bit_adder_1_carry_out : 1'bz;  // Controlled_Buffer controlled_buffer_2
  assign C_1_2 = and_1_out ? my16bit_adder_2_sum_out : 16'bz;  // Controlled_Buffer controlled_buffer_3
  assign out_13 = and_1_out ? my16bit_adder_2_carry_out : 1'bz;  // Controlled_Buffer controlled_buffer_4
  assign C_2_1 = and_1_out ? my16bit_adder_3_sum_out : 16'bz;  // Controlled_Buffer controlled_buffer_5
  assign C_2_2 = and_1_out ? my16bit_adder_4_sum_out : 16'bz;  // Controlled_Buffer controlled_buffer_6
  assign out_15 = and_1_out ? my16bit_adder_3_carry_out : 1'bz;  // Controlled_Buffer controlled_buffer_7
  assign out_17 = and_1_out ? my16bit_adder_4_carry_out : 1'bz;  // Controlled_Buffer controlled_buffer_8
endmodule

module comparator_v2 (
  input  [4:0] A,
  input  [4:0] OPCODE,
  output A_EQ_B
);

  wire not_1_out, not_2_out, not_3_out, not_4_out, not_5_out, xor_1_out, xor_2_out, xor_3_out, xor_4_out,
       xor_5_out;

  xor xor_1 (xor_1_out, A[0], OPCODE[0]);
  xor xor_2 (xor_2_out, A[1], OPCODE[1]);
  xor xor_3 (xor_3_out, A[2], OPCODE[2]);
  xor xor_4 (xor_4_out, A[3], OPCODE[3]);
  xor xor_5 (xor_5_out, A[4], OPCODE[4]);
  not not_1 (not_1_out, xor_1_out);
  not not_2 (not_2_out, xor_2_out);
  not not_3 (not_3_out, xor_3_out);
  not not_4 (not_4_out, xor_4_out);
  not not_5 (not_5_out, xor_5_out);
  and and_1 (A_EQ_B, not_1_out, not_2_out, not_3_out, not_4_out, not_5_out);
endmodule

module Bus_terminus (
  input  [1:0] selector,
  input  ENABLE,
  output System_RAM,
  output RAM_A,
  output RAM_B,
  output INST_RAM
);

  wire not_1_out, not_2_out;

  not not_1 (not_1_out, selector[1]);
  not not_2 (not_2_out, selector[0]);
  and and_1 (System_RAM, not_2_out, not_1_out, ENABLE);
  and and_2 (RAM_A, not_1_out, selector[0], ENABLE);
  and and_3 (RAM_B, selector[1], not_2_out, ENABLE);
  and and_4 (INST_RAM, selector[0], selector[1], ENABLE);

  // Notes on the sheet:
  //   00
  //   01
  //   10
  //   11
endmodule

module REG_swap_test (
  input  in_1,
  input  in_2,
  input  in_3,
  input  in_4,
  input  in_5,
  input  in_6,
  input  in_7,
  input  in_8,
  input  in_9,
  input  in_10,
  input  in_11,
  input  in_12,
  input  in_13,
  input  in_14,
  input  in_15,
  input  MAR_Z_WE,
  input  MAR_A_WE,
  input  MAR_B_WE,
  input  in_19,
  input  in_20,
  input  in_21,
  input  in_22,
  input  in_23,
  input  in_24,
  input  in_25,
  input  in_26,
  input  in_27,
  input  in_28,
  input  in_29,
  input  in_30,
  input  in_31,
  input  in_32,
  input  in_33,
  input  in_34,
  input  in_35,
  input  in_36,
  input  in_37,
  input  in_38,
  input  in_39,
  input  in_40,
  input  in_41
);

  wire alu_16_bit_1_p6, alu_16_bit_1_p9, clock_1_out, controlled_buffer_19_out, controlled_buffer_34_out,
       controlled_buffer_48_out, controlled_buffer_49_out, controlled_buffer_55_out,
       mat_mult_16_bit_1_out_11, mat_mult_16_bit_1_out_13, mat_mult_16_bit_1_out_15,
       mat_mult_16_bit_1_out_17, nand_1_out, not_1_out, not_2_out, not_3_out, not_4_out, Overflow_q,
       reg_swap_a_1_p6, reg_swap_a_1_p8, reg_swap_a_1_p9, reg_swap_a_1_p10, reg_swap_b_1_r5, reg_swap_b_1_r6,
       reg_swap_b_1_r7, reg_swap_b_1_r8, register_1_q, register_2_q, undriven;
  wire [3:0] counter_2_q, counter_3_q;
  wire [4:0] alu_16_bit_1_p3, controlled_buffer_44_out, controlled_buffer_45_out, controlled_buffer_46_out,
       controlled_buffer_47_out, controlled_buffer_50_out, controlled_buffer_53_out, counter_1_q,
       COUNTER_RAMA_q, COUNTER_RAMB_q, instruction_splitter_1_address_a, instruction_splitter_1_address_b,
       instruction_splitter_1_opcode, MAR_A_q, MAR_B_q, MAR_Z_q, SYSTEM_RAM_q;
  wire [7:0] alu_16_bit_1_p1, alu_16_bit_1_p1_2, alu_16_bit_1_p2, alu_16_bit_1_p2_2,
       controlled_buffer_13_out, controlled_buffer_13_out_2, controlled_buffer_18_out,
       controlled_buffer_18_out_2, controlled_buffer_22_out, controlled_buffer_22_out_2;
  wire [15:0] alu_16_bit_1_p8, ALU_DATA_OUT_q, bit_extender_1_out, bit_extender_2_out, buffer_3_out, C1_1_q,
       C1_2_q, C2_1_q, C2_2_q, controlled_buffer_1_out, controlled_buffer_2_out, controlled_buffer_4_out,
       controlled_buffer_6_out, controlled_buffer_16_out, controlled_buffer_17_out, controlled_buffer_20_out,
       controlled_buffer_30_out, controlled_buffer_31_out, controlled_buffer_32_out,
       controlled_buffer_40_out, controlled_buffer_41_out, controlled_buffer_56_out,
       controlled_buffer_57_out, controlled_buffer_59_out, mat_mult_16_bit_1_c_1_1, mat_mult_16_bit_1_c_1_2,
       mat_mult_16_bit_1_c_2_1, mat_mult_16_bit_1_c_2_2, MBR_A_q, MBR_B_q, MBR_Z_q, ram_1_dout, ram_2_dout,
       ram_3_dout, ram_4_dout, REG_1_q, REG_2_q, REG_3_q, REG_4_q, REG_5_q, REG_6_q, REG_7_q, REG_8_q,
       reg_swap_a_1_p7, reg_swap_b_1_out_b, sixteenbit_mux_1_out_4, sixteenbit_mux_2_out_4;
  wire [19:0] rom_2_data;
  wire [63:0] rom_1_data;

  // ALU_16_bit alu_16_bit_1: pin names not known; wires that end beside it: {alu_16_bit_1_p1_2, alu_16_bit_1_p1}, {alu_16_bit_1_p2_2, alu_16_bit_1_p2}, alu_16_bit_1_p3, rom_1_data[32], alu_16_bit_1_p3, alu_16_bit_1_p6, rom_1_data[31], alu_16_bit_1_p8, alu_16_bit_1_p9
  Register #(.width(16)) ALU_DATA_OUT (
    .D(alu_16_bit_1_p8), .en(rom_1_data[33]), .clk(clock_1_out), .Q(ALU_DATA_OUT_q));  // open: clr
  Register #(.width(1)) Overflow (
    .D(alu_16_bit_1_p9), .en(rom_1_data[30]), .clk(clock_1_out), .Q(Overflow_q));  // open: clr
  assign bit_extender_1_out = {{15{Overflow_q}}, Overflow_q};  // Bit_Extender bit_extender_1
  sixteenbit_mux sixteenbit_mux_1 (
    .Flag(alu_16_bit_1_p6), .A(ALU_DATA_OUT_q), .B(bit_extender_1_out), .out_4(sixteenbit_mux_1_out_4));
  Register #(.width(5)) OPCODE_REG (
    .D(instruction_splitter_1_opcode), .en(rom_1_data[34]), .clk(clock_1_out), .Q(alu_16_bit_1_p3));  // open: clr
  assign controlled_buffer_1_out = rom_1_data[5] ? sixteenbit_mux_1_out_4 : 16'bz;  // Controlled_Buffer controlled_buffer_1
  assign controlled_buffer_2_out = reg_swap_a_1_p6 ? controlled_buffer_30_out : 16'bz;  // Controlled_Buffer controlled_buffer_2
  assign controlled_buffer_2_out = reg_swap_a_1_p8 ? controlled_buffer_30_out : 16'bz;  // Controlled_Buffer controlled_buffer_3
  assign controlled_buffer_4_out = reg_swap_a_1_p9 ? controlled_buffer_30_out : 16'bz;  // Controlled_Buffer controlled_buffer_4
  assign controlled_buffer_4_out = reg_swap_a_1_p10 ? controlled_buffer_30_out : 16'bz;  // Controlled_Buffer controlled_buffer_5
  assign controlled_buffer_6_out = reg_swap_b_1_r5 ? controlled_buffer_31_out : 16'bz;  // Controlled_Buffer controlled_buffer_6
  assign controlled_buffer_6_out = reg_swap_b_1_r6 ? controlled_buffer_31_out : 16'bz;  // Controlled_Buffer controlled_buffer_7
  assign controlled_buffer_6_out = reg_swap_b_1_r7 ? controlled_buffer_31_out : 16'bz;  // Controlled_Buffer controlled_buffer_8
  assign controlled_buffer_6_out = reg_swap_b_1_r8 ? controlled_buffer_31_out : 16'bz;  // Controlled_Buffer controlled_buffer_9
  assign controlled_buffer_2_out = controlled_buffer_41_out;  // Buffer buffer_1, 16 bits wide
  assign controlled_buffer_2_out = not_1_out ? controlled_buffer_16_out : 16'bz;  // Controlled_Buffer controlled_buffer_10
  not not_1 (not_1_out, reg_swap_a_1_p6);
  not not_2 (not_2_out, reg_swap_a_1_p8);
  Register #(.trigger("falling"), .width(16)) REG_3 (
    .D(controlled_buffer_4_out), .en(rom_1_data[39]), .clk(clock_1_out), .Q(REG_3_q));  // open: clr
  assign controlled_buffer_4_out = controlled_buffer_2_out;  // Buffer buffer_2, 16 bits wide
  not not_3 (not_3_out, reg_swap_a_1_p9);
  not not_4 (not_4_out, reg_swap_a_1_p10);
  Controlled_Buffer #(.width(16)) controlled_buffer_11 (
    .in(controlled_buffer_17_out), .out(controlled_buffer_6_out));  // open: en
  Register #(.trigger("falling"), .width(16)) REG_5 (
    .D(controlled_buffer_6_out), .en(rom_1_data[40]), .clk(clock_1_out), .Q(REG_5_q));  // open: clr
  Register #(.trigger("falling"), .width(16)) REG_7 (
    .D(controlled_buffer_6_out), .en(rom_1_data[41]), .clk(clock_1_out), .Q(REG_7_q));  // open: clr
  // Probe on controlled_buffer_40_out
  Register #(.trigger("falling"), .width(16)) REG_1 (
    .D(controlled_buffer_2_out), .en(rom_1_data[38]), .clk(clock_1_out), .Q(REG_1_q));  // open: clr
  assign controlled_buffer_2_out = not_2_out ? controlled_buffer_20_out : 16'bz;  // Controlled_Buffer controlled_buffer_12
  assign {controlled_buffer_13_out_2, controlled_buffer_13_out} = rom_1_data[20] ? REG_3_q : 16'bz;  // Controlled_Buffer controlled_buffer_13
  assign controlled_buffer_4_out = not_3_out ? {controlled_buffer_13_out_2, controlled_buffer_13_out} : 16'bz;  // Controlled_Buffer controlled_buffer_14
  assign controlled_buffer_4_out = not_4_out ? {alu_16_bit_1_p1_2, alu_16_bit_1_p1} : 16'bz;  // Controlled_Buffer controlled_buffer_15
  assign controlled_buffer_16_out = in_1 ? REG_1_q : 16'bz;  // Controlled_Buffer controlled_buffer_16
  Register #(.trigger("falling"), .width(16)) REG_2 (
    .D(controlled_buffer_2_out), .en(rom_1_data[43]), .clk(clock_1_out), .Q(REG_2_q));  // open: clr
  Register #(.trigger("falling"), .width(16)) REG_4 (
    .D(controlled_buffer_4_out), .en(rom_1_data[44]), .clk(clock_1_out), .Q(REG_4_q));  // open: clr
  assign controlled_buffer_17_out = rom_1_data[18] ? REG_5_q : 16'bz;  // Controlled_Buffer controlled_buffer_17
  Register #(.trigger("falling"), .width(16)) REG_6 (
    .D(controlled_buffer_6_out), .en(rom_1_data[42]), .clk(clock_1_out), .Q(REG_6_q));  // open: clr
  assign {controlled_buffer_18_out_2, controlled_buffer_18_out} = rom_1_data[16] ? REG_7_q : 16'bz;  // Controlled_Buffer controlled_buffer_18
  Register #(.trigger("falling"), .width(16)) REG_8 (
    .D(controlled_buffer_6_out), .en(rom_1_data[45]), .clk(clock_1_out), .Q(REG_8_q));  // open: clr
  assign controlled_buffer_19_out = rom_1_data[28] ? clock_1_out : 1'bz;  // Controlled_Buffer controlled_buffer_19
  instruction_splitter instruction_splitter_1 (
    .Instruction(controlled_buffer_40_out), .WE(rom_1_data[52]), .Clk(clock_1_out),
    .Address_A(instruction_splitter_1_address_a), .Address_B(instruction_splitter_1_address_b),
    .Opcode(instruction_splitter_1_opcode), .Flag(alu_16_bit_1_p6));
  assign controlled_buffer_20_out = rom_1_data[21] ? REG_2_q : 16'bz;  // Controlled_Buffer controlled_buffer_20
  assign {alu_16_bit_1_p1_2, alu_16_bit_1_p1} = rom_1_data[19] ? REG_4_q : 16'bz;  // Controlled_Buffer controlled_buffer_21
  assign {controlled_buffer_22_out_2, controlled_buffer_22_out} = rom_1_data[17] ? REG_6_q : 16'bz;  // Controlled_Buffer controlled_buffer_22
  assign {alu_16_bit_1_p2_2, alu_16_bit_1_p2} = rom_1_data[15] ? REG_8_q : 16'bz;  // Controlled_Buffer controlled_buffer_23
  Counter #(.max('h1f), .width(5)) counter_1 (
    .clk(controlled_buffer_19_out), .Q(counter_1_q));  // open: clr, load, up, count, D, carry
  Controlled_Buffer #(.width(16)) controlled_buffer_24 (
    .in(controlled_buffer_16_out), .out({alu_16_bit_1_p1_2, alu_16_bit_1_p1}));  // open: en
  Controlled_Buffer #(.width(16)) controlled_buffer_25 (
    .in(controlled_buffer_20_out), .out({alu_16_bit_1_p1_2, alu_16_bit_1_p1}));  // open: en
  Controlled_Buffer #(.width(16)) controlled_buffer_26 (
    .in({controlled_buffer_13_out_2, controlled_buffer_13_out}), .out({alu_16_bit_1_p1_2, alu_16_bit_1_p1}));  // open: en
  Controlled_Buffer #(.width(16)) controlled_buffer_27 (
    .in(controlled_buffer_17_out), .out({alu_16_bit_1_p2_2, alu_16_bit_1_p2}));  // open: en
  Controlled_Buffer #(.width(16)) controlled_buffer_28 (
    .in({controlled_buffer_18_out_2, controlled_buffer_18_out}), .out({alu_16_bit_1_p2_2, alu_16_bit_1_p2}));  // open: en
  Controlled_Buffer #(.width(16)) controlled_buffer_29 (
    .in({controlled_buffer_22_out_2, controlled_buffer_22_out}), .out({alu_16_bit_1_p2_2, alu_16_bit_1_p2}));  // open: en
  Register #(.width(16)) TERMINAL_A (
    .D({alu_16_bit_1_p1_2, alu_16_bit_1_p1}), .en(rom_1_data[8]), .clk(clock_1_out));  // open: Q, clr
  Register #(.width(16)) TERMINAL_B (
    .D({alu_16_bit_1_p2_2, alu_16_bit_1_p2}), .en(rom_1_data[7]), .clk(clock_1_out));  // open: Q, clr
  Register #(.width(5)) MAR_Z (.D(counter_1_q), .en(rom_1_data[48]), .clk(clock_1_out), .Q(MAR_Z_q));  // open: clr
  MAT_MULT_16_bit mat_mult_16_bit_1 (
    .Opcode(alu_16_bit_1_p3), .A11(controlled_buffer_16_out[7:0]), .A12(controlled_buffer_20_out[7:0]),
    .A21(controlled_buffer_13_out), .A22(alu_16_bit_1_p1), .B11(controlled_buffer_17_out[7:0]),
    .B12(controlled_buffer_22_out), .B21(controlled_buffer_18_out), .B22(alu_16_bit_1_p2),
    .C_1_1(mat_mult_16_bit_1_c_1_1), .out_11(mat_mult_16_bit_1_out_11), .C_1_2(mat_mult_16_bit_1_c_1_2),
    .out_13(mat_mult_16_bit_1_out_13), .C_2_1(mat_mult_16_bit_1_c_2_1), .out_15(mat_mult_16_bit_1_out_15),
    .C_2_2(mat_mult_16_bit_1_c_2_2), .out_17(mat_mult_16_bit_1_out_17));
  // Reg_swap_A reg_swap_a_1: pin names not known; wires that end beside it: instruction_splitter_1_address_a, controlled_buffer_16_out, controlled_buffer_20_out, {controlled_buffer_13_out_2, controlled_buffer_13_out}, {alu_16_bit_1_p1_2, alu_16_bit_1_p1}, reg_swap_a_1_p6, reg_swap_a_1_p7, reg_swap_a_1_p8, reg_swap_a_1_p9, reg_swap_a_1_p10
  Reg_swap_B reg_swap_b_1 (
    .Add_B(instruction_splitter_1_address_b), .Reg5(controlled_buffer_17_out),
    .Reg6({controlled_buffer_22_out_2, controlled_buffer_22_out}),
    .Reg7({controlled_buffer_18_out_2, controlled_buffer_18_out}),
    .Reg8({alu_16_bit_1_p2_2, alu_16_bit_1_p2}), .R5(reg_swap_b_1_r5), .OUT_B(reg_swap_b_1_out_b),
    .R6(reg_swap_b_1_r6), .R7(reg_swap_b_1_r7), .R8(reg_swap_b_1_r8));
  Controlled_Buffer #(.width(16)) controlled_buffer_30 (
    .in(reg_swap_b_1_out_b), .out(controlled_buffer_30_out));  // open: en
  Controlled_Buffer #(.width(16)) controlled_buffer_31 (
    .in(reg_swap_a_1_p7), .out(controlled_buffer_31_out));  // open: en
  Register #(.width(16)) C1_1 (
    .D(mat_mult_16_bit_1_c_1_1), .en(rom_2_data[11]), .clk(clock_1_out), .Q(C1_1_q));  // open: clr
  Register #(.width(16)) C2_1 (
    .D(mat_mult_16_bit_1_c_2_1), .en(rom_2_data[9]), .clk(clock_1_out), .Q(C2_1_q));  // open: clr
  Register #(.width(1)) register_1 (
    .D(mat_mult_16_bit_1_out_11), .en(rom_2_data[7]), .clk(clock_1_out), .Q(register_1_q), .clr(rom_2_data[6]));
  Register #(.width(1)) register_2 (
    .D(mat_mult_16_bit_1_out_15), .en(rom_2_data[5]), .clk(clock_1_out), .Q(register_2_q));  // open: clr
  Register #(.width(5)) MAR_A (
    .D(instruction_splitter_1_address_a), .en(rom_1_data[47]), .clk(clock_1_out), .Q(MAR_A_q));  // open: clr
  assign controlled_buffer_32_out = rom_2_data[19] ? C1_1_q : 16'bz;  // Controlled_Buffer controlled_buffer_32
  assign controlled_buffer_32_out = rom_2_data[17] ? C2_1_q : 16'bz;  // Controlled_Buffer controlled_buffer_33
  assign controlled_buffer_34_out = rom_2_data[15] ? register_1_q : 1'bz;  // Controlled_Buffer controlled_buffer_34
  assign controlled_buffer_34_out = rom_2_data[13] ? register_2_q : 1'bz;  // Controlled_Buffer controlled_buffer_35
  Register #(.width(16)) C1_2 (
    .D(mat_mult_16_bit_1_c_1_2), .en(rom_2_data[10]), .clk(clock_1_out), .Q(C1_2_q));  // open: clr
  Register #(.width(16)) C2_2 (
    .D(mat_mult_16_bit_1_c_2_2), .en(rom_2_data[8]), .clk(clock_1_out), .Q(C2_2_q));  // open: clr
  Register #(.width(1)) register_3 (
    .D(mat_mult_16_bit_1_out_13), .en(rom_2_data[6]), .clk(clock_1_out));  // open: Q, clr
  Register #(.width(1)) register_4 (
    .D(mat_mult_16_bit_1_out_17), .en(rom_2_data[4]), .clk(clock_1_out));  // open: Q, clr
  assign controlled_buffer_32_out = rom_2_data[18] ? C1_2_q : 16'bz;  // Controlled_Buffer controlled_buffer_36
  assign controlled_buffer_32_out = rom_2_data[16] ? C2_2_q : 16'bz;  // Controlled_Buffer controlled_buffer_37
  Controlled_Buffer controlled_buffer_38 (.out(controlled_buffer_34_out), .en(rom_2_data[14]));  // open: in
  assign bit_extender_2_out = {{15{controlled_buffer_34_out}}, controlled_buffer_34_out};  // Bit_Extender bit_extender_2
  Controlled_Buffer controlled_buffer_39 (.out(controlled_buffer_34_out), .en(rom_2_data[12]));  // open: in
  Clock clock_1 (.out(clock_1_out));
  Register #(.width(5)) MAR_B (
    .D(instruction_splitter_1_address_b), .en(rom_1_data[46]), .clk(clock_1_out), .Q(MAR_B_q));  // open: clr
  Register #(.width(16)) MBR_Z (
    .D(controlled_buffer_1_out), .en(rom_1_data[53]), .clk(clock_1_out), .Q(MBR_Z_q));  // open: clr
  Register #(.width(16)) MBR_A (
    .D(controlled_buffer_56_out), .en(rom_1_data[54]), .clk(clock_1_out), .Q(MBR_A_q));  // open: clr
  Register #(.width(16)) MBR_B (
    .D(controlled_buffer_57_out), .en(rom_1_data[55]), .clk(clock_1_out), .Q(MBR_B_q));  // open: clr
  // Probe on sixteenbit_mux_2_out_4
  sixteenbit_mux sixteenbit_mux_2 (
    .Flag(alu_16_bit_1_p6), .A(controlled_buffer_32_out), .B(bit_extender_2_out),
    .out_4(sixteenbit_mux_2_out_4));
  assign controlled_buffer_40_out = rom_1_data[49] ? MBR_Z_q : 16'bz;  // Controlled_Buffer controlled_buffer_40
  assign controlled_buffer_41_out = rom_1_data[50] ? MBR_A_q : 16'bz;  // Controlled_Buffer controlled_buffer_41
  assign controlled_buffer_6_out = rom_1_data[51] ? MBR_B_q : 16'bz;  // Controlled_Buffer controlled_buffer_42
  assign buffer_3_out = controlled_buffer_40_out;  // Buffer buffer_3, 16 bits wide
  // Probe on buffer_3_out
  assign buffer_3_out = rom_1_data[4] ? sixteenbit_mux_2_out_4 : 16'bz;  // Controlled_Buffer controlled_buffer_43
  assign controlled_buffer_44_out = rom_1_data[12] ? MAR_A_q : 5'bz;  // Controlled_Buffer controlled_buffer_44
  // Probe on controlled_buffer_46_out
  assign controlled_buffer_45_out = rom_1_data[37] ? MAR_A_q : 5'bz;  // Controlled_Buffer controlled_buffer_45
  // Probe on controlled_buffer_44_out
  assign controlled_buffer_46_out = rom_1_data[13] ? MAR_B_q : 5'bz;  // Controlled_Buffer controlled_buffer_46
  assign controlled_buffer_47_out = rom_1_data[36] ? MAR_B_q : 5'bz;  // Controlled_Buffer controlled_buffer_47
  Counter #(.max('h1f), .width(5)) COUNTER_RAMA (
    .load(rom_1_data[25]), .clk(controlled_buffer_48_out), .D(controlled_buffer_44_out), .Q(COUNTER_RAMA_q));  // open: clr, up, count, carry
  assign controlled_buffer_48_out = rom_1_data[29] ? clock_1_out : 1'bz;  // Controlled_Buffer controlled_buffer_48
  Counter #(.max('h1f), .width(5)) COUNTER_RAMB (
    .load(rom_1_data[26]), .clk(controlled_buffer_49_out), .D(controlled_buffer_46_out), .Q(COUNTER_RAMB_q));  // open: clr, up, count, carry
  assign controlled_buffer_49_out = rom_1_data[35] ? clock_1_out : 1'bz;  // Controlled_Buffer controlled_buffer_49
  // Probe on controlled_buffer_1_out
  assign controlled_buffer_50_out = rom_1_data[11] ? MAR_Z_q : 5'bz;  // Controlled_Buffer controlled_buffer_50
  assign controlled_buffer_45_out = rom_1_data[27] ? COUNTER_RAMA_q : 5'bz;  // Controlled_Buffer controlled_buffer_51
  assign controlled_buffer_47_out = rom_1_data[10] ? COUNTER_RAMB_q : 5'bz;  // Controlled_Buffer controlled_buffer_52
  RAM #(.addrWidth(5), .dataWidth(16), .enables("line"), .\type ("nonvolatile")) ram_1 (
    .addr(MAR_Z_q), .we(rom_1_data[58]), .clk(clock_1_out), .din(controlled_buffer_40_out), .dout(ram_1_dout));
  RAM #(.addrWidth(5), .dataWidth(16), .enables("line"), .\type ("nonvolatile")) ram_2 (
    .addr(controlled_buffer_45_out), .we(rom_1_data[63]), .clk(clock_1_out), .din(controlled_buffer_41_out),
    .dout(ram_2_dout));
  RAM #(.addrWidth(5), .dataWidth(16), .enables("line"), .\type ("nonvolatile")) ram_3 (
    .addr(controlled_buffer_47_out), .we(rom_1_data[60]), .clk(clock_1_out), .din(controlled_buffer_6_out),
    .dout(ram_3_dout));
  assign controlled_buffer_53_out = rom_1_data[14] ? MAR_Z_q : 5'bz;  // Controlled_Buffer controlled_buffer_53
  assign controlled_buffer_1_out = rom_1_data[59] ? ram_1_dout : 16'bz;  // Controlled_Buffer controlled_buffer_54
  // Probe on controlled_buffer_57_out
  Counter #(.max('h1f), .width(5)) SYSTEM_RAM (
    .load(rom_1_data[24]), .clk(controlled_buffer_55_out), .D(controlled_buffer_53_out), .Q(SYSTEM_RAM_q));  // open: clr, up, count, carry
  assign controlled_buffer_55_out = rom_1_data[23] ? clock_1_out : 1'bz;  // Controlled_Buffer controlled_buffer_55
  assign controlled_buffer_56_out = rom_1_data[62] ? ram_2_dout : 16'bz;  // Controlled_Buffer controlled_buffer_56
  assign controlled_buffer_57_out = rom_1_data[61] ? ram_3_dout : 16'bz;  // Controlled_Buffer controlled_buffer_57
  // Probe on buffer_3_out
  assign controlled_buffer_50_out = rom_1_data[9] ? SYSTEM_RAM_q : 5'bz;  // Controlled_Buffer controlled_buffer_58
  // Probe on controlled_buffer_59_out
  assign controlled_buffer_59_out = rom_1_data[6] ? buffer_3_out : 16'bz;  // Controlled_Buffer controlled_buffer_59
  RAM #(.addrWidth(5), .dataWidth(16), .enables("line")) ram_4 (
    .addr(controlled_buffer_50_out), .we(rom_1_data[56]), .clk(clock_1_out), .din(controlled_buffer_59_out),
    .dout(ram_4_dout));
  ROM #(.dataWidth(64)) rom_1 (.addr({alu_16_bit_1_p3[3:0], counter_2_q}), .data(rom_1_data));
  assign controlled_buffer_1_out = rom_1_data[57] ? ram_4_dout : 16'bz;  // Controlled_Buffer controlled_buffer_60
  nand nand_1 (nand_1_out, undriven, rom_1_data[1]);
  assign clock_1_out = rom_1_data[2] ? nand_1_out : 1'bz;  // Controlled_Buffer controlled_buffer_61
  Counter #(.max('hf), .width(4)) counter_2 (
    .clr(rom_1_data[0]), .clk(clock_1_out), .Q(counter_2_q));  // open: load, up, count, D, carry
  ROM #(.dataWidth(20)) rom_2 (.addr({alu_16_bit_1_p3[3:0], counter_3_q}), .data(rom_2_data));
  Counter #(.max('hf), .width(4)) counter_3 (
    .clr(rom_2_data[0]), .clk(clock_1_out), .Q(counter_3_q));  // open: load, up, count, D, carry

  // Notes on the sheet:
  //   INSTRUCTION RAM
  //   RAM A
  //   RAMB
  //   MBR_B_CB
  //   MBR_A_CB
  //   MBR_Z_CB
  //   Reg_8_WE
  //    Reg_4_WE
  //   Reg_3_WE
  //   Mult_OE
  //   Addsub_OE
  //   REG_1_OE
  //   REG_2_OE
  //   REG_3_OE
  //   REG_4_OE
  //   REG_5_OE
  //   REG_6_OE
  //   REG_7_OE
  //   REG_8_OE
  //   SYS_counter_address_CB
  //   RAMB_COUNTER_address_CB
  //   RAMA_COUNTER_address_CB
  //   MARZ_SYS_RAM
  //   Address_out_SYS_RAM
  //   TERMINAL_A_WE
  //   RAM_A_WE
  //   RAM_A_OE
  //   RAM_B_OE
  //   RAM_B_WE
  //   INST_RAM_OE
  //   INST_RAM_WE
  //   SYSTEM_RAM_OE
  //   SYSTEM_RAM_WE
  //   MBR_B_WE
  //   MBR_A_WE
  //   MBR_Z_WE
  //   INST_SPLITTER_WE
  //   Reg_2_WE
  //   Reg_6_WE
  //   Reg_7_WE
  //   Reg_5_WE
  //   Reg_1_WE
  //   MAR_A-RAM_A_CB
  //   MAR_B_RAM_B_CB
  //   RAM_B_CLOCK_BLOCK-load
  //   Opcode_reg_WE
  //   ALU_out_reg_WE
  //   Overflow_addsub_Reg_WE
  //   RAM_A_CLOCK_BLOCK-load
  //   PC_counter_clock_CB
  //   Address_out_RAM_A_BL
  //   RAM_B_COUNTER_LOAD
  //   RAM_A_COUNTER_LOAD
  //   SYS_RAM_LOAD
  //   SYS_RAM_CLOCK_BLOCK_STORE
  //   Address_OUT_RAMB_CB
  //   TERMINAL_B_WE
  //   Store_sys_CB
  //   BS_CB
  //   HALT_NAND
  //   STORE_CB
  //   SC_clock_reset
  //   SYSTEM RAM
  //   contents of rom_1 (hex, n*v repeats v):
  //   801000000000000 820000000000000 12000000000000 c00400000000 1 11*0 801000000000000 820000000000000
  //   12000000000000 c00400000000 60c0003000000000 c3fc000000000 2d07f8000 1 24*0 801000000000000
  //   820000000000000 12000000000000 c00400000000 60c0003000000000 c3fc000000000 3107f8000 1 8*0
  //   801000000000000 820000000000000 12000000000000 c00400000000 20000000000860 102000010000860 1 41*0
  //   801000000000000 820000000000000 12000000000000 c00400000000 826003000 60c0000008000400
  //   60cc014828000400 60cc000828000400 60cc0c0828000400 60cc028828000400 c300830000000 1 4*0
  //   801000000000000 820000000000000 12000000000000 c00400000000 1804000 100000000800250 100000000800250
  //   100000000800250 100000010800250 1 6*0 801000000000000 820000000000000 12000000000000 c00400000000
  //   107f8000 1 26*0 801000000000000 820000000000000 12000000000000 c00400000000 60c0003000000000
  //   c3fc000000000 2107f8000 1 8*0 801000000000000 820000000000000 12000000000000 c00400000000
  //   60c0003000000000 c3fc000000000 2107f8000 1 8*0 801000000000000 820000000000000 12000000000000
  //   c00400000000 60c0003000000000 c3fc000000000 2107f8000 1
  //   MATMULT_C1_1_CB
  //   MATMULT_C1_2_CB
  //   MATLMULT_C2_1CB
  //   MATMULT_C2_2_CB
  //   MATMULT_OVERLOW_1
  //   MATMULT_OVERFLOW_2
  //   MATMULT_OVERFLOW_3
  //   MATMULT_OVERFLOW_4
  //   MATMULT_C1_1WE
  //   MATMULT_C1_2WE
  //   MATMULT_C2_1WE
  //   MATMULT_C2_2WE
  //   OVERFLOW_1_WE
  //   OVERFLOW_2_WE
  //   OVERFLOW_3_WE
  //   OVERFLOW_4_WE
  //   SC_reset_2
  //   contents of rom_2 (hex, n*v repeats v):
  //   4*0 1 18*0 1 46*0 1 52*0 1 9*0 88000 44000 22000 11000 1 10*0 ff0 1 33*0 1 15*0 1 15*0 1
endmodule

module Reg_swap_A (
  input  [4:0] Add_A,
  input  [15:0] Reg1,
  input  [15:0] Reg2,
  input  [15:0] Reg3,
  input  [15:0] Reg4,
  output R1,
  output [15:0] OUT_A,
  output R2,
  output R3,
  output R4
);

  wire not_1_out, not_2_out, not_3_out, not_4_out, not_5_out;
  wire [15:0] and_1_out, and_2_out, and_3_out, and_4_out, bit_extender_1_out, bit_extender_2_out,
       bit_extender_3_out, bit_extender_4_out;

  not not_1 (not_1_out, Add_A[4]);
  not not_2 (not_2_out, Add_A[3]);
  not not_3 (not_3_out, Add_A[2]);
  not not_4 (not_4_out, Add_A[1]);
  not not_5 (not_5_out, Add_A[0]);
  and REG_1 (R1, Add_A[0], not_4_out, not_3_out, not_2_out, not_1_out);
  and REG_2 (R2, not_5_out, Add_A[1], not_3_out, not_2_out, not_1_out);
  and REG_3 (R3, Add_A[0], Add_A[1], not_3_out, not_2_out, not_1_out);
  and REG_4 (R4, not_5_out, not_4_out, not_3_out, Add_A[3], not_1_out);
  assign bit_extender_1_out = {{15{R1}}, R1};  // Bit_Extender bit_extender_1
  assign bit_extender_2_out = {{15{R2}}, R2};  // Bit_Extender bit_extender_2
  assign bit_extender_3_out = {{15{R3}}, R3};  // Bit_Extender bit_extender_3
  assign bit_extender_4_out = {{15{R4}}, R4};  // Bit_Extender bit_extender_4
  assign and_1_out = Reg1 & bit_extender_1_out;  // AND_Gate and_1, 16 bits wide
  assign and_2_out = Reg2 & bit_extender_2_out;  // AND_Gate and_2, 16 bits wide
  assign and_3_out = Reg3 & bit_extender_3_out;  // AND_Gate and_3, 16 bits wide
  assign and_4_out = Reg4 & bit_extender_4_out;  // AND_Gate and_4, 16 bits wide
  assign OUT_A = and_1_out | and_2_out | and_3_out | and_4_out;  // OR_Gate or_1, 16 bits wide
endmodule

module Reg_swap_B (
  input  [4:0] Add_B,
  input  [15:0] Reg5,
  input  [15:0] Reg6,
  input  [15:0] Reg7,
  input  [15:0] Reg8,
  output R5,
  output [15:0] OUT_B,
  output R6,
  output R7,
  output R8
);

  wire not_1_out, not_2_out, not_3_out, not_4_out, not_5_out;
  wire [15:0] and_1_out, and_2_out, and_3_out, and_4_out, bit_extender_1_out, bit_extender_2_out,
       bit_extender_3_out, bit_extender_4_out;

  not not_1 (not_1_out, Add_B[4]);
  not not_2 (not_2_out, Add_B[3]);
  not not_3 (not_3_out, Add_B[2]);
  not not_4 (not_4_out, Add_B[1]);
  not not_5 (not_5_out, Add_B[0]);
  and REG_5 (R5, Add_B[0], not_4_out, Add_B[2], not_2_out, not_1_out);
  and REG_6 (R6, not_5_out, Add_B[1], Add_B[2], not_2_out, not_1_out);
  and REG_7 (R7, Add_B[0], Add_B[1], Add_B[2], not_2_out, not_1_out);
  and REG_8 (R8, not_5_out, not_4_out, not_3_out, Add_B[3], not_1_out);
  assign bit_extender_1_out = {{15{R5}}, R5};  // Bit_Extender bit_extender_1
  assign bit_extender_2_out = {{15{R6}}, R6};  // Bit_Extender bit_extender_2
  assign bit_extender_3_out = {{15{R7}}, R7};  // Bit_Extender bit_extender_3
  assign bit_extender_4_out = {{15{R8}}, R8};  // Bit_Extender bit_extender_4
  assign and_1_out = Reg5 & bit_extender_1_out;  // AND_Gate and_1, 16 bits wide
  assign and_2_out = Reg6 & bit_extender_2_out;  // AND_Gate and_2, 16 bits wide
  assign and_3_out = Reg7 & bit_extender_3_out;  // AND_Gate and_3, 16 bits wide
  assign and_4_out = Reg8 & bit_extender_4_out;  // AND_Gate and_4, 16 bits wide
  assign OUT_B = and_1_out | and_2_out | and_3_out | and_4_out;  // OR_Gate or_1, 16 bits wide
endmodule
module Final_viva (
  input  in_1,
  input  in_2,
  input  in_3,
  input  in_4,
  input  in_5,
  input  in_6,
  input  in_7,
  input  in_8,
  input  in_9,
  input  in_10,
  input  in_11,
  input  in_12,
  input  in_13,
  input  in_14,
  input  MAR_Z_WE,
  input  MAR_A_WE,
  input  MAR_B_WE,
  input  in_18,
  input  in_19,
  input  in_20,
  input  in_21,
  input  in_22,
  input  in_23,
  input  in_24,
  input  in_25,
  input  in_26,
  input  in_27,
  input  in_28,
  input  in_29,
  input  in_30,
  input  in_31,
  input  in_32,
  input  in_33,
  input  in_34,
  input  in_35,
  input  in_36,
  input  in_37,
  input  in_38,
  input  in_39,
  input  in_40
);

  wire alu_16_bit_1_overflow_addsub, and_1_out, and_2_out, and_3_out, and_4_out, and_5_out, and_6_out,
       and_7_out, and_8_out, and_9_out, and_10_out, and_11_out, bit_extender_2_out, bit_extender_3_out,
       bus_terminus_1_inst_ram, bus_terminus_1_ram_a, bus_terminus_1_ram_b, clock_1_out,
       controlled_buffer_30_out, controlled_buffer_56_out, controlled_buffer_62_out,
       controlled_buffer_73_out, controlled_buffer_74_out, controlled_buffer_79_out,
       controlled_buffer_83_out, Debug_carry, instruction_splitter_1_flag, mat_mult_16_bit_1_out_11,
       mat_mult_16_bit_1_out_13, mat_mult_16_bit_1_out_15, mat_mult_16_bit_1_out_17, not_1_out, not_2_out,
       not_3_out, not_4_out, not_5_out, not_6_out, not_7_out, not_8_out, not_9_out, not_10_out, not_11_out,
       not_12_out, not_13_out, not_14_out, not_15_out, or_1_out, Overflow_q, reg_swap_a_1_r1,
       reg_swap_a_1_r2, reg_swap_a_1_r3, reg_swap_a_1_r4, reg_swap_b_1_r5, reg_swap_b_1_r6, reg_swap_b_1_r7,
       reg_swap_b_1_r8, register_1_q, register_2_q, xor_1_out;
  wire [1:0] rom_1_data_2;
  wire [3:0] counter_1_q, counter_2_q;
  wire [4:0] controlled_buffer_41_out, controlled_buffer_42_out, controlled_buffer_43_out,
       controlled_buffer_53_out, controlled_buffer_64_out, controlled_buffer_69_out,
       controlled_buffer_70_out, controlled_buffer_71_out, controlled_buffer_72_out,
       controlled_buffer_75_out, controlled_buffer_76_out, COUNTER_RAMA_q, COUNTER_RAMB_q, Debug_Reg_q,
       instruction_splitter_1_address_a, instruction_splitter_1_address_b, instruction_splitter_1_opcode,
       MAR_A_q, MAR_B_q, MAR_Z_q, OPCODE_REG_q, PC_counter_q, SYS_counter_q;
  wire [7:0] controlled_buffer_22_out, controlled_buffer_22_out_2, controlled_buffer_29_out,
       controlled_buffer_29_out_2, controlled_buffer_32_out, controlled_buffer_32_out_2,
       controlled_buffer_33_out, controlled_buffer_33_out_2, controlled_buffer_34_out,
       controlled_buffer_34_out_2;
  wire [15:0] alu_16_bit_1_data_out, ALU_DATA_OUT_q, bit_extender_1_out, bit_extender_4_out, C1_1_q, C1_2_q,
       C2_1_q, C2_2_q, controlled_buffer_1_out, controlled_buffer_2_out, controlled_buffer_3_out,
       controlled_buffer_4_out, controlled_buffer_5_out, controlled_buffer_6_out, controlled_buffer_7_out,
       controlled_buffer_8_out, controlled_buffer_9_out, controlled_buffer_27_out, controlled_buffer_28_out,
       controlled_buffer_31_out, controlled_buffer_45_out, controlled_buffer_47_out,
       controlled_buffer_49_out, controlled_buffer_54_out, controlled_buffer_65_out,
       controlled_buffer_66_out, controlled_buffer_67_out, controlled_buffer_87_out, mat_mult_16_bit_1_c_1_1,
       mat_mult_16_bit_1_c_1_2, mat_mult_16_bit_1_c_2_1, mat_mult_16_bit_1_c_2_2, MBR_A_q, MBR_B_q, MBR_Z_q,
       ram_1_dout, ram_2_dout, ram_3_dout, ram_4_dout, REG_1_q, REG_2_q, REG_3_q, REG_4_q, REG_5_q, REG_6_q,
       REG_7_q, REG_8_q, reg_swap_a_1_out_a, reg_swap_b_1_out_b, sixteenbit_mux_1_out_4,
       sixteenbit_mux_2_out_4, TERMINAL_A_q, TERMINAL_B_q;
  wire [39:0] rom_2_data;
  wire [63:0] rom_1_data;

  ALU_16_bit alu_16_bit_1 (
    .A({controlled_buffer_32_out_2, controlled_buffer_32_out}),
    .B({controlled_buffer_34_out_2, controlled_buffer_34_out}), .Opcode(OPCODE_REG_q), .mult(rom_1_data[32]),
    .Sub_control(instruction_splitter_1_flag), .addsub(rom_1_data[31]),
    .Carry_in(instruction_splitter_1_flag), .data_out(alu_16_bit_1_data_out),
    .overflow_addsub(alu_16_bit_1_overflow_addsub));
  Register #(.width(16)) ALU_DATA_OUT (
    .D(alu_16_bit_1_data_out), .en(rom_1_data[33]), .clk(controlled_buffer_62_out), .Q(ALU_DATA_OUT_q));  // open: clr
  Register #(.width(1)) Overflow (
    .D(alu_16_bit_1_overflow_addsub), .en(rom_1_data[30]), .clk(controlled_buffer_62_out), .Q(Overflow_q));  // open: clr
  assign bit_extender_1_out = {{15{Overflow_q}}, Overflow_q};  // Bit_Extender bit_extender_1
  sixteenbit_mux sixteenbit_mux_1 (
    .Flag(instruction_splitter_1_flag), .A(ALU_DATA_OUT_q), .B(bit_extender_1_out),
    .out_4(sixteenbit_mux_1_out_4));
  Register #(.width(5)) OPCODE_REG (
    .D(instruction_splitter_1_opcode), .en(rom_1_data[34]), .clk(controlled_buffer_62_out), .Q(OPCODE_REG_q));  // open: clr
  assign controlled_buffer_1_out = rom_1_data[5] ? sixteenbit_mux_1_out_4 : 16'bz;  // Controlled_Buffer controlled_buffer_1
  assign controlled_buffer_2_out = reg_swap_a_1_r1 ? reg_swap_b_1_out_b : 16'bz;  // Controlled_Buffer controlled_buffer_2
  assign controlled_buffer_3_out = reg_swap_a_1_r2 ? reg_swap_b_1_out_b : 16'bz;  // Controlled_Buffer controlled_buffer_3
  assign controlled_buffer_4_out = reg_swap_a_1_r3 ? reg_swap_b_1_out_b : 16'bz;  // Controlled_Buffer controlled_buffer_4
  assign controlled_buffer_5_out = reg_swap_a_1_r4 ? reg_swap_b_1_out_b : 16'bz;  // Controlled_Buffer controlled_buffer_5
  assign controlled_buffer_6_out = reg_swap_b_1_r5 ? reg_swap_a_1_out_a : 16'bz;  // Controlled_Buffer controlled_buffer_6
  assign controlled_buffer_7_out = reg_swap_b_1_r6 ? reg_swap_a_1_out_a : 16'bz;  // Controlled_Buffer controlled_buffer_7
  assign controlled_buffer_8_out = reg_swap_b_1_r7 ? reg_swap_a_1_out_a : 16'bz;  // Controlled_Buffer controlled_buffer_8
  not not_1 (not_1_out, reg_swap_b_1_r7);
  assign controlled_buffer_9_out = reg_swap_b_1_r8 ? reg_swap_a_1_out_a : 16'bz;  // Controlled_Buffer controlled_buffer_9
  assign controlled_buffer_2_out = rom_2_data[23] ? controlled_buffer_66_out : 16'bz;  // Controlled_Buffer controlled_buffer_10
  assign controlled_buffer_3_out = rom_2_data[22] ? controlled_buffer_66_out : 16'bz;  // Controlled_Buffer controlled_buffer_11
  assign controlled_buffer_6_out = rom_2_data[19] ? controlled_buffer_67_out : 16'bz;  // Controlled_Buffer controlled_buffer_12
  assign controlled_buffer_7_out = rom_2_data[18] ? controlled_buffer_67_out : 16'bz;  // Controlled_Buffer controlled_buffer_13
  assign controlled_buffer_8_out = rom_2_data[17] ? controlled_buffer_67_out : 16'bz;  // Controlled_Buffer controlled_buffer_14
  assign controlled_buffer_9_out = rom_2_data[16] ? controlled_buffer_67_out : 16'bz;  // Controlled_Buffer controlled_buffer_15
  assign controlled_buffer_2_out = not_2_out ? controlled_buffer_27_out : 16'bz;  // Controlled_Buffer controlled_buffer_16
  not not_2 (not_2_out, reg_swap_a_1_r1);
  not not_3 (not_3_out, reg_swap_a_1_r2);
  Register #(.trigger("falling"), .width(16)) REG_3 (
    .D(controlled_buffer_4_out), .en(rom_1_data[39]), .clk(controlled_buffer_62_out), .Q(REG_3_q));  // open: clr
  assign controlled_buffer_4_out = rom_2_data[21] ? controlled_buffer_66_out : 16'bz;  // Controlled_Buffer controlled_buffer_17
  not not_4 (not_4_out, reg_swap_a_1_r3);
  assign controlled_buffer_5_out = rom_2_data[20] ? controlled_buffer_66_out : 16'bz;  // Controlled_Buffer controlled_buffer_18
  not not_5 (not_5_out, reg_swap_a_1_r4);
  assign controlled_buffer_6_out = not_6_out ? controlled_buffer_28_out : 16'bz;  // Controlled_Buffer controlled_buffer_19
  Register #(.trigger("falling"), .width(16)) REG_5 (
    .D(controlled_buffer_6_out), .en(rom_1_data[40]), .clk(controlled_buffer_62_out), .Q(REG_5_q));  // open: clr
  not not_6 (not_6_out, reg_swap_b_1_r5);
  assign controlled_buffer_8_out = not_1_out ? {controlled_buffer_29_out_2, controlled_buffer_29_out} : 16'bz;  // Controlled_Buffer controlled_buffer_20
  Register #(.trigger("falling"), .width(16)) REG_7 (
    .D(controlled_buffer_8_out), .en(rom_1_data[41]), .clk(controlled_buffer_62_out), .Q(REG_7_q));  // open: clr
  // Probe on controlled_buffer_65_out
  Register #(.trigger("falling"), .width(16)) REG_1 (
    .D(controlled_buffer_2_out), .en(rom_1_data[38]), .clk(controlled_buffer_62_out), .Q(REG_1_q));  // open: clr
  assign controlled_buffer_3_out = not_3_out ? controlled_buffer_31_out : 16'bz;  // Controlled_Buffer controlled_buffer_21
  assign {controlled_buffer_22_out_2, controlled_buffer_22_out} = rom_1_data[20] ? REG_3_q : 16'bz;  // Controlled_Buffer controlled_buffer_22
  assign controlled_buffer_4_out = not_4_out ? {controlled_buffer_22_out_2, controlled_buffer_22_out} : 16'bz;  // Controlled_Buffer controlled_buffer_23
  assign controlled_buffer_5_out = not_5_out ? {controlled_buffer_32_out_2, controlled_buffer_32_out} : 16'bz;  // Controlled_Buffer controlled_buffer_24
  assign controlled_buffer_7_out = not_7_out ? {controlled_buffer_33_out_2, controlled_buffer_33_out} : 16'bz;  // Controlled_Buffer controlled_buffer_25
  not not_7 (not_7_out, reg_swap_b_1_r6);
  assign controlled_buffer_9_out = not_8_out ? {controlled_buffer_34_out_2, controlled_buffer_34_out} : 16'bz;  // Controlled_Buffer controlled_buffer_26
  not not_8 (not_8_out, reg_swap_b_1_r8);
  assign controlled_buffer_27_out = rom_1_data[22] ? REG_1_q : 16'bz;  // Controlled_Buffer controlled_buffer_27
  Register #(.trigger("falling"), .width(16)) REG_2 (
    .D(controlled_buffer_3_out), .en(rom_1_data[43]), .clk(controlled_buffer_62_out), .Q(REG_2_q));  // open: clr
  Register #(.trigger("falling"), .width(16)) REG_4 (
    .D(controlled_buffer_5_out), .en(rom_1_data[44]), .clk(controlled_buffer_62_out), .Q(REG_4_q));  // open: clr
  assign controlled_buffer_28_out = rom_1_data[18] ? REG_5_q : 16'bz;  // Controlled_Buffer controlled_buffer_28
  Register #(.trigger("falling"), .width(16)) REG_6 (
    .D(controlled_buffer_7_out), .en(rom_1_data[42]), .clk(controlled_buffer_62_out), .Q(REG_6_q));  // open: clr
  assign {controlled_buffer_29_out_2, controlled_buffer_29_out} = rom_1_data[16] ? REG_7_q : 16'bz;  // Controlled_Buffer controlled_buffer_29
  Register #(.trigger("falling"), .width(16)) REG_8 (
    .D(controlled_buffer_9_out), .en(rom_1_data[45]), .clk(controlled_buffer_62_out), .Q(REG_8_q));  // open: clr
  assign controlled_buffer_30_out = rom_1_data[28] ? controlled_buffer_62_out : 1'bz;  // Controlled_Buffer controlled_buffer_30
  instruction_splitter instruction_splitter_1 (
    .Instruction(controlled_buffer_65_out), .WE(rom_1_data[52]), .Clk(controlled_buffer_62_out),
    .Address_A(instruction_splitter_1_address_a), .Address_B(instruction_splitter_1_address_b),
    .Opcode(instruction_splitter_1_opcode), .Flag(instruction_splitter_1_flag));
  assign controlled_buffer_31_out = rom_1_data[21] ? REG_2_q : 16'bz;  // Controlled_Buffer controlled_buffer_31
  assign {controlled_buffer_32_out_2, controlled_buffer_32_out} = rom_1_data[19] ? REG_4_q : 16'bz;  // Controlled_Buffer controlled_buffer_32
  assign {controlled_buffer_33_out_2, controlled_buffer_33_out} = rom_1_data[17] ? REG_6_q : 16'bz;  // Controlled_Buffer controlled_buffer_33
  assign {controlled_buffer_34_out_2, controlled_buffer_34_out} = rom_1_data[15] ? REG_8_q : 16'bz;  // Controlled_Buffer controlled_buffer_34
  Counter #(.max('h1f), .width(5)) PC_counter (
    .clk(controlled_buffer_30_out), .Q(PC_counter_q));  // open: clr, load, up, count, D, carry
  Controlled_Buffer #(.width(16)) controlled_buffer_35 (
    .in(controlled_buffer_27_out), .out({controlled_buffer_32_out_2, controlled_buffer_32_out}));  // open: en
  Controlled_Buffer #(.width(16)) controlled_buffer_36 (
    .in(controlled_buffer_31_out), .out({controlled_buffer_32_out_2, controlled_buffer_32_out}));  // open: en
  Controlled_Buffer #(.width(16)) controlled_buffer_37 (
    .in({controlled_buffer_22_out_2, controlled_buffer_22_out}),
    .out({controlled_buffer_32_out_2, controlled_buffer_32_out}));  // open: en
  Controlled_Buffer #(.width(16)) controlled_buffer_38 (
    .in(controlled_buffer_28_out), .out({controlled_buffer_34_out_2, controlled_buffer_34_out}));  // open: en
  Controlled_Buffer #(.width(16)) controlled_buffer_39 (
    .in({controlled_buffer_29_out_2, controlled_buffer_29_out}),
    .out({controlled_buffer_34_out_2, controlled_buffer_34_out}));  // open: en
  Controlled_Buffer #(.width(16)) controlled_buffer_40 (
    .in({controlled_buffer_33_out_2, controlled_buffer_33_out}),
    .out({controlled_buffer_34_out_2, controlled_buffer_34_out}));  // open: en
  not not_9 (not_9_out, and_3_out);
  and and_1 (and_1_out, not_9_out, rom_1_data[48]);
  assign controlled_buffer_41_out = and_1_out ? PC_counter_q : 5'bz;  // Controlled_Buffer controlled_buffer_41
  assign controlled_buffer_42_out = and_2_out ? instruction_splitter_1_address_a : 5'bz;  // Controlled_Buffer controlled_buffer_42
  assign controlled_buffer_43_out = and_2_out ? instruction_splitter_1_address_b : 5'bz;  // Controlled_Buffer controlled_buffer_43
  and and_2 (and_2_out, not_10_out, OPCODE_REG_q[1], OPCODE_REG_q[2], not_11_out);
  assign controlled_buffer_41_out = and_3_out ? instruction_splitter_1_address_b : 5'bz;  // Controlled_Buffer controlled_buffer_44
  not not_10 (not_10_out, OPCODE_REG_q[0]);
  not not_11 (not_11_out, OPCODE_REG_q[3]);
  Register #(.width(5)) MAR_Z (
    .D(controlled_buffer_41_out), .en(rom_1_data[48]), .clk(controlled_buffer_62_out), .Q(MAR_Z_q));  // open: clr
  Reg_swap_B reg_swap_b_1 (
    .Add_B(controlled_buffer_43_out), .Reg5(controlled_buffer_28_out),
    .Reg6({controlled_buffer_33_out_2, controlled_buffer_33_out}),
    .Reg7({controlled_buffer_29_out_2, controlled_buffer_29_out}),
    .Reg8({controlled_buffer_34_out_2, controlled_buffer_34_out}), .R5(reg_swap_b_1_r5),
    .OUT_B(reg_swap_b_1_out_b), .R6(reg_swap_b_1_r6), .R7(reg_swap_b_1_r7), .R8(reg_swap_b_1_r8));
  and and_3 (and_3_out, rom_1_data[58], rom_1_data[48]);
  MAT_MULT_16_bit mat_mult_16_bit_1 (
    .Opcode(OPCODE_REG_q), .A11(controlled_buffer_27_out[7:0]), .A12(controlled_buffer_31_out[7:0]),
    .A21(controlled_buffer_22_out), .A22(controlled_buffer_32_out), .B11(controlled_buffer_28_out[7:0]),
    .B12(controlled_buffer_33_out), .B21(controlled_buffer_29_out), .B22(controlled_buffer_34_out),
    .C_1_1(mat_mult_16_bit_1_c_1_1), .out_11(mat_mult_16_bit_1_out_11), .C_1_2(mat_mult_16_bit_1_c_1_2),
    .out_13(mat_mult_16_bit_1_out_13), .C_2_1(mat_mult_16_bit_1_c_2_1), .out_15(mat_mult_16_bit_1_out_15),
    .C_2_2(mat_mult_16_bit_1_c_2_2), .out_17(mat_mult_16_bit_1_out_17));
  Reg_swap_A reg_swap_a_1 (
    .Add_A(controlled_buffer_42_out), .Reg1(controlled_buffer_27_out), .Reg2(controlled_buffer_31_out),
    .Reg3({controlled_buffer_22_out_2, controlled_buffer_22_out}),
    .Reg4({controlled_buffer_32_out_2, controlled_buffer_32_out}), .R1(reg_swap_a_1_r1),
    .OUT_A(reg_swap_a_1_out_a), .R2(reg_swap_a_1_r2), .R3(reg_swap_a_1_r3), .R4(reg_swap_a_1_r4));
  Bit_Extender #(.in_width(16), .out_width(1)) bit_extender_2 (.in(TERMINAL_A_q), .out(bit_extender_2_out));
  or or_1 (or_1_out, bit_extender_2_out, bit_extender_3_out);
  Register #(.width(16)) TERMINAL_A (
    .D(controlled_buffer_66_out), .en(rom_1_data[8]), .clk(controlled_buffer_62_out), .Q(TERMINAL_A_q));  // open: clr
  Register #(.width(16)) TERMINAL_B (
    .D(controlled_buffer_67_out), .en(rom_1_data[7]), .clk(controlled_buffer_62_out), .Q(TERMINAL_B_q));  // open: clr
  Bit_Extender #(.in_width(16), .out_width(1)) bit_extender_3 (.in(TERMINAL_B_q), .out(bit_extender_3_out));
  assign controlled_buffer_45_out = rom_1_data_2[1] ? TERMINAL_A_q : 16'bz;  // Controlled_Buffer controlled_buffer_45
  assign controlled_buffer_45_out = rom_1_data_2[0] ? TERMINAL_B_q : 16'bz;  // Controlled_Buffer controlled_buffer_46
  assign controlled_buffer_47_out = bus_terminus_1_ram_a ? controlled_buffer_45_out : 16'bz;  // Controlled_Buffer controlled_buffer_47
  Bus_terminus bus_terminus_1 (
    .selector(rom_1_data_2), .ENABLE(or_1_out), .RAM_A(bus_terminus_1_ram_a), .RAM_B(bus_terminus_1_ram_b),
    .INST_RAM(bus_terminus_1_inst_ram));  // open: System_RAM
  and and_4 (and_4_out, OPCODE_REG_q[0], OPCODE_REG_q[1], OPCODE_REG_q[2], OPCODE_REG_q[3], rom_1_data_2[0]);
  assign controlled_buffer_47_out = and_4_out ? controlled_buffer_65_out : 16'bz;  // Controlled_Buffer controlled_buffer_48
  assign controlled_buffer_49_out = and_5_out ? controlled_buffer_47_out : 16'bz;  // Controlled_Buffer controlled_buffer_49
  assign controlled_buffer_49_out = bus_terminus_1_ram_b ? controlled_buffer_45_out : 16'bz;  // Controlled_Buffer controlled_buffer_50
  Controlled_Buffer #(.width(16)) controlled_buffer_51 (
    .in(controlled_buffer_45_out), .en(bus_terminus_1_inst_ram));  // open: out
  Controlled_Buffer #(.width(16)) controlled_buffer_52 (.in(controlled_buffer_45_out));  // open: out, en
  and and_5 (and_5_out, OPCODE_REG_q[0], OPCODE_REG_q[1], OPCODE_REG_q[2], OPCODE_REG_q[3], rom_1_data_2[1]);
  Register #(.width(16)) C1_1 (
    .D(mat_mult_16_bit_1_c_1_1), .en(rom_2_data[31]), .clk(controlled_buffer_62_out), .Q(C1_1_q));  // open: clr
  Register #(.width(16)) C2_1 (
    .D(mat_mult_16_bit_1_c_2_1), .en(rom_2_data[29]), .clk(controlled_buffer_62_out), .Q(C2_1_q));  // open: clr
  Register #(.width(1)) register_1 (
    .D(mat_mult_16_bit_1_out_11), .en(rom_2_data[27]), .clk(controlled_buffer_62_out), .Q(register_1_q),
    .clr(rom_2_data[26]));
  Register #(.width(1)) register_2 (
    .D(mat_mult_16_bit_1_out_15), .en(rom_2_data[25]), .clk(controlled_buffer_62_out), .Q(register_2_q));  // open: clr
  Register #(.width(5)) MAR_A (
    .D(instruction_splitter_1_address_a), .en(rom_1_data[47]), .clk(controlled_buffer_62_out), .Q(MAR_A_q));  // open: clr
  assign controlled_buffer_53_out = and_6_out ? instruction_splitter_1_address_b : 5'bz;  // Controlled_Buffer controlled_buffer_53
  and and_6 (and_6_out, rom_1_data[46], not_12_out);
  not not_12 (not_12_out, OPCODE_REG_q[4]);
  assign controlled_buffer_54_out = rom_2_data[39] ? C1_1_q : 16'bz;  // Controlled_Buffer controlled_buffer_54
  assign controlled_buffer_54_out = rom_2_data[37] ? C2_1_q : 16'bz;  // Controlled_Buffer controlled_buffer_55
  assign controlled_buffer_56_out = rom_2_data[35] ? register_1_q : 1'bz;  // Controlled_Buffer controlled_buffer_56
  assign controlled_buffer_56_out = rom_2_data[33] ? register_2_q : 1'bz;  // Controlled_Buffer controlled_buffer_57
  Register #(.width(16)) C1_2 (
    .D(mat_mult_16_bit_1_c_1_2), .en(rom_2_data[30]), .clk(controlled_buffer_62_out), .Q(C1_2_q));  // open: clr
  Register #(.width(16)) C2_2 (
    .D(mat_mult_16_bit_1_c_2_2), .en(rom_2_data[28]), .clk(controlled_buffer_62_out), .Q(C2_2_q));  // open: clr
  Register #(.width(1)) register_3 (
    .D(mat_mult_16_bit_1_out_13), .en(rom_2_data[26]), .clk(controlled_buffer_62_out));  // open: Q, clr
  Register #(.width(1)) register_4 (
    .D(mat_mult_16_bit_1_out_17), .en(rom_2_data[24]), .clk(controlled_buffer_62_out));  // open: Q, clr
  assign controlled_buffer_54_out = rom_2_data[38] ? C1_2_q : 16'bz;  // Controlled_Buffer controlled_buffer_58
  assign controlled_buffer_54_out = rom_2_data[36] ? C2_2_q : 16'bz;  // Controlled_Buffer controlled_buffer_59
  Controlled_Buffer controlled_buffer_60 (.out(controlled_buffer_56_out), .en(rom_2_data[34]));  // open: in
  assign bit_extender_4_out = {{15{controlled_buffer_56_out}}, controlled_buffer_56_out};  // Bit_Extender bit_extender_4
  Controlled_Buffer controlled_buffer_61 (.out(controlled_buffer_56_out), .en(rom_2_data[32]));  // open: in
  Clock clock_1 (.out(clock_1_out));
  assign controlled_buffer_62_out = not_13_out ? clock_1_out : 1'bz;  // Controlled_Buffer controlled_buffer_62
  assign controlled_buffer_53_out = OPCODE_REG_q[4] ? instruction_splitter_1_address_a : 5'bz;  // Controlled_Buffer controlled_buffer_63
  not not_13 (not_13_out, and_7_out);
  Register #(.width(5)) MAR_B (
    .D(controlled_buffer_53_out), .en(rom_1_data[46]), .clk(controlled_buffer_62_out), .Q(MAR_B_q));  // open: clr
  Register #(.width(16)) MBR_Z (
    .D(controlled_buffer_1_out), .en(rom_1_data[53]), .clk(controlled_buffer_62_out), .Q(MBR_Z_q));  // open: clr
  Register #(.width(16)) MBR_A (
    .D(controlled_buffer_47_out), .en(rom_1_data_2[0]), .clk(controlled_buffer_62_out), .Q(MBR_A_q));  // open: clr
  and and_7 (and_7_out, rom_1_data[1], instruction_splitter_1_flag);
  assign controlled_buffer_64_out = rom_1_data[2] ? MAR_A_q : 5'bz;  // Controlled_Buffer controlled_buffer_64
  Register #(.width(16)) MBR_B (
    .D(controlled_buffer_49_out), .en(rom_1_data_2[1]), .clk(controlled_buffer_62_out), .Q(MBR_B_q));  // open: clr
  // Probe on sixteenbit_mux_2_out_4
  sixteenbit_mux sixteenbit_mux_2 (
    .Flag(instruction_splitter_1_flag), .A(controlled_buffer_54_out), .B(bit_extender_4_out),
    .out_4(sixteenbit_mux_2_out_4));
  assign controlled_buffer_65_out = rom_1_data[49] ? MBR_Z_q : 16'bz;  // Controlled_Buffer controlled_buffer_65
  assign controlled_buffer_66_out = rom_1_data[50] ? MBR_A_q : 16'bz;  // Controlled_Buffer controlled_buffer_66
  assign controlled_buffer_67_out = rom_1_data[51] ? MBR_B_q : 16'bz;  // Controlled_Buffer controlled_buffer_67
  // Probe on controlled_buffer_65_out
  assign controlled_buffer_65_out = rom_1_data[4] ? sixteenbit_mux_2_out_4 : 16'bz;  // Controlled_Buffer controlled_buffer_68
  assign controlled_buffer_69_out = rom_1_data[12] ? MAR_A_q : 5'bz;  // Controlled_Buffer controlled_buffer_69
  // Probe on controlled_buffer_71_out
  assign controlled_buffer_70_out = rom_1_data[37] ? MAR_A_q : 5'bz;  // Controlled_Buffer controlled_buffer_70
  // Probe on controlled_buffer_69_out
  assign controlled_buffer_71_out = rom_1_data[13] ? MAR_B_q : 5'bz;  // Controlled_Buffer controlled_buffer_71
  Register #(.width(5)) Debug_Reg (
    .D(MAR_A_q), .en(rom_1_data[3]), .clk(controlled_buffer_62_out), .Q(Debug_Reg_q));  // open: clr
  assign controlled_buffer_72_out = rom_1_data[36] ? MAR_B_q : 5'bz;  // Controlled_Buffer controlled_buffer_72
  Counter #(.max('h1f), .width(5)) COUNTER_RAMA (
    .load(rom_1_data[25]), .clk(controlled_buffer_73_out), .D(controlled_buffer_69_out), .Q(COUNTER_RAMA_q));  // open: clr, up, count, carry
  assign controlled_buffer_73_out = rom_1_data[29] ? controlled_buffer_62_out : 1'bz;  // Controlled_Buffer controlled_buffer_73
  Counter #(.max('h1f), .width(5)) COUNTER_RAMB (
    .load(rom_1_data[26]), .clk(controlled_buffer_74_out), .D(controlled_buffer_71_out), .Q(COUNTER_RAMB_q));  // open: clr, up, count, carry
  assign controlled_buffer_74_out = rom_1_data[35] ? controlled_buffer_62_out : 1'bz;  // Controlled_Buffer controlled_buffer_74
  // Probe on controlled_buffer_1_out
  not not_14 (not_14_out, OPCODE_REG_q[1]);
  not not_15 (not_15_out, OPCODE_REG_q[3]);
  xor xor_1 (xor_1_out, rom_1_data[63], instruction_splitter_1_flag);
  and and_8 (and_8_out, xor_1_out, rom_1_data[63]);
  and and_9 (and_9_out, rom_1_data[60], and_10_out);
  and and_10 (and_10_out, instruction_splitter_1_flag, rom_1_data[60]);
  assign controlled_buffer_75_out = rom_1_data[59] ? MAR_Z_q : 5'bz;  // Controlled_Buffer controlled_buffer_75
  assign controlled_buffer_76_out = rom_1_data[11] ? MAR_Z_q : 5'bz;  // Controlled_Buffer controlled_buffer_76
  assign controlled_buffer_70_out = rom_1_data[27] ? COUNTER_RAMA_q : 5'bz;  // Controlled_Buffer controlled_buffer_77
  assign controlled_buffer_72_out = rom_1_data[10] ? COUNTER_RAMB_q : 5'bz;  // Controlled_Buffer controlled_buffer_78
  and and_11 (and_11_out, OPCODE_REG_q[0], not_14_out, OPCODE_REG_q[2], not_15_out, rom_1_data[60]);
  RAM #(.addrWidth(5), .dataWidth(16), .enables("line"), .\type ("nonvolatile")) ram_1 (
    .addr(controlled_buffer_75_out), .clk(controlled_buffer_62_out), .din(controlled_buffer_65_out),
    .dout(ram_1_dout));  // open: we
  assign controlled_buffer_79_out = and_11_out ? rom_1_data[60] : 1'bz;  // Controlled_Buffer controlled_buffer_79
  assign controlled_buffer_79_out = and_9_out ? rom_1_data[60] : 1'bz;  // Controlled_Buffer controlled_buffer_80
  Counter #(.max('h1f), .ongoal("load"), .width(5)) Debug (
    .up(1'b0), .clk(controlled_buffer_62_out), .D(Debug_Reg_q), .carry(Debug_carry));  // open: clr, load, count, Q
  RAM #(.addrWidth(5), .dataWidth(16), .enables("line"), .\type ("nonvolatile")) ram_2 (
    .addr(controlled_buffer_70_out), .we(and_8_out), .clk(controlled_buffer_62_out),
    .din(controlled_buffer_66_out), .dout(ram_2_dout));
  RAM #(.addrWidth(5), .dataWidth(16), .enables("line"), .\type ("nonvolatile")) ram_3 (
    .addr(controlled_buffer_72_out), .we(controlled_buffer_79_out), .clk(controlled_buffer_62_out),
    .din(controlled_buffer_67_out), .dout(ram_3_dout));
  assign controlled_buffer_64_out = rom_1_data[14] ? MAR_Z_q : 5'bz;  // Controlled_Buffer controlled_buffer_81
  assign controlled_buffer_1_out = rom_1_data[59] ? ram_1_dout : 16'bz;  // Controlled_Buffer controlled_buffer_82
  // Probe on controlled_buffer_49_out
  Counter #(.max('h1f), .width(5)) SYS_counter (
    .load(rom_1_data[24]), .clk(controlled_buffer_83_out), .D(controlled_buffer_64_out), .Q(SYS_counter_q));  // open: clr, up, count, carry
  assign controlled_buffer_83_out = rom_1_data[23] ? controlled_buffer_62_out : 1'bz;  // Controlled_Buffer controlled_buffer_83
  assign controlled_buffer_47_out = rom_1_data[62] ? ram_2_dout : 16'bz;  // Controlled_Buffer controlled_buffer_84
  assign controlled_buffer_49_out = rom_1_data[61] ? ram_3_dout : 16'bz;  // Controlled_Buffer controlled_buffer_85
  // Probe on controlled_buffer_65_out
  assign controlled_buffer_76_out = rom_1_data[9] ? SYS_counter_q : 5'bz;  // Controlled_Buffer controlled_buffer_86
  // Probe on controlled_buffer_87_out
  assign controlled_buffer_87_out = rom_1_data[6] ? controlled_buffer_65_out : 16'bz;  // Controlled_Buffer controlled_buffer_87
  RAM #(.addrWidth(5), .dataWidth(16), .enables("line")) ram_4 (
    .addr(controlled_buffer_76_out), .we(rom_1_data[56]), .clk(controlled_buffer_62_out),
    .din(controlled_buffer_87_out), .dout(ram_4_dout));
  ROM #(.dataWidth(64)) rom_1 (
    .addr({OPCODE_REG_q[3:0], counter_1_q}), .data({rom_1_data[63:56], rom_1_data_2, rom_1_data[53:0]}));
  assign controlled_buffer_1_out = rom_1_data[57] ? ram_4_dout : 16'bz;  // Controlled_Buffer controlled_buffer_88
  Counter #(.max('hf), .width(4)) counter_1 (
    .clr(rom_1_data[0]), .count(Debug_carry), .clk(controlled_buffer_62_out), .Q(counter_1_q));  // open: load, up, D, carry
  ROM #(.dataWidth(40)) rom_2 (.addr({OPCODE_REG_q[3:0], counter_2_q}), .data(rom_2_data));
  Counter #(.max('hf), .width(4)) counter_2 (
    .clr(rom_2_data[0]), .count(Debug_carry), .clk(controlled_buffer_62_out), .Q(counter_2_q));  // open: load, up, D, carry

  // Notes on the sheet:
  //   INSTRUCTION RAM
  //   RAM A
  //   RAM B
  //   MBR_B_CB
  //   MBR_A_CB
  //   MBR_Z_CB
  //   Reg_8_WE
  //    Reg_4_WE
  //   Reg_3_WE
  //   Mult_OE
  //   Addsub_OE
  //   REG_1_OE
  //   REG_2_OE
  //   REG_3_OE
  //   REG_4_OE
  //   REG_5_OE
  //   REG_6_OE
  //   REG_7_OE
  //   REG_8_OE
  //   SYS_counter_address_CB
  //   RAMB_COUNTER_address_CB
  //   RAMA_COUNTER_address_CB
  //   MARZ_SYS_RAM
  //   Address_out_SYS_RAM
  //   RAM_A_WE
  //   RAM_A_OE
  //   RAM_B_OE
  //   RAM_B_WE
  //   INST_RAM_OE
  //   MAR_Z_MOVE_CB
  //   SYSTEM_RAM_OE
  //   SYSTEM_RAM_WE
  //   MBR_B_WE
  //   MBR_A_WE
  //   MBR_Z_WE
  //   INST_SPLITTER_WE
  //   Reg_2_WE
  //   Reg_6_WE
  //   Reg_7_WE
  //   Reg_5_WE
  //   Reg_1_WE
  //   MAR_A-RAM_A_CB
  //   MAR_B_RAM_B_CB
  //   RAM_B_CLOCK_BLOCK-load
  //   Opcode_reg_WE
  //   ALU_out_reg_WE
  //   Overflow_addsub_Reg_WE
  //   RAM_A_CLOCK_BLOCK-load
  //   PC_counter_clock_CB
  //   Address_out_RAM_A_BL
  //   RAM_B_COUNTER_LOAD
  //   RAM_A_COUNTER_LOAD
  //   SYS_RAM_LOAD
  //   SYS_RAM_CLOCK_BLOCK_STORE
  //   Address_OUT_RAMB_CB
  //   TERMINAL_A_WE
  //   TERMINAL_B_WE
  //   Store_sys_CB
  //   BS_CB
  //   DEBUG_Clock_CB
  //   DEBUG_LOAD
  //   HALT_NAND
  //   STORE_CB
  //   SC_clock_reset
  //   SYSTEM RAM
  //   contents of rom_1 (hex, n*v repeats v):
  //   801000000000000 820000000000000 12000000000000 c00400000000 1 11*0 801000000000000 820000000000000
  //   12000000000000 c00400000000 60c0003000000000 c3fc000000000 2d07f8000 1 8*0 801000000000000
  //   820000000000000 12000000000000 c00400000000 1800004 826003204 4*9200000828800600 10000400 1 4*0
  //   801000000000000 820000000000000 12000000000000 c00400000000 60c0003000000000 c3fc000000000 3107f8000
  //   1 8*0 801000000000000 820000000000000 12000000000000 c00400000000 20000000000860 102000010000860 1
  //   9*0 801000000000000 820000000000000 12000000000000 c00400000000 60c0003000000000 c000000000180
  //   44000000000000 88000000000000 900c003000000000 1 6*0 801000000000000 820000000000000 12000000000000
  //   c00400000000 7f8000 3fc0107f8000 1 9*0 801000000000000 820000000000000 12000000000000 c00400000000
  //   826003000 60c0000008000400 60cc014828000400 60cc000828000400 60cc0c0828000400 60cc028828000400
  //   c300830000000 1 4*0 801000000000000 820000000000000 12000000000000 c00400000000 1804000
  //   100000000800250 100000000800250 100000000800250 100000010800250 1 6*0 801000000000000
  //   820000000000000 12000000000000 c00400000000 107f8000 1 10*0 801000000000000 820000000000000
  //   12000000000000 c00400000000 60c0003000000000 c3fc000000000 2107f8000 1 8*0 801000000000000
  //   820000000000000 12000000000000 c00400000000 60c0003000000000 c3fc000000000 2107f8000 1 8*0
  //   801000000000000 820000000000000 12000000000000 c00400000000 60c0003000000000 c3fc000000000 2107f8000
  //   1 8*0 801000000000000 820000000000000 12000000000000 c00400000000 60c0003000000000 c3fc000000000
  //   2107f8000 1 8*0 801000000000000 15*0 801000000000000 820000000000000 12000000000000 c00400000000
  //   401c00000000000 220000000000800 c2000000000000 900c003010000000 1
  //   MATMULT_C1_1_CB
  //   MATMULT_C1_2_CB
  //   MATLMULT_C2_1CB
  //   MATMULT_C2_2_CB
  //   MATMULT_OVERLOW_1
  //   MATMULT_OVERFLOW_2
  //   MATMULT_OVERFLOW_3
  //   MATMULT_OVERFLOW_4
  //   MATMULT_C1_1WE
  //   MATMULT_C1_2WE
  //   MATMULT_C2_1WE
  //   MATMULT_C2_2WE
  //   OVERFLOW_1_WE
  //   OVERFLOW_2_WE
  //   OVERFLOW_3_WE
  //   OVERFLOW_4_WE
  //   REG1_IN
  //   REG2_IN
  //   REG3_IN
  //   REG4_IN
  //   REG5_IN
  //   REG6_IN
  //   REG7_IN
  //   REG8_IN
  //   SC_reset_2
  //   contents of rom_2 (hex, n*v repeats v):
  //   4*0 1 16*0 ff0000 0 1 19*0 1 9*0 ff0000 0 1 14*0 1 31*0 1 15*0 880000 0 440000 220000 110000 1 9*0
  //   8800000000 4400000000 2200000000 1100000000 1 10*0 ff000000 1 31*0 ff0000 0 1 13*0 ff0000 0 1 13*0
  //   ff0000 0 1 15*0 1 16*0 1
endmodule

module CRAZYYY_IDEAA_YAR (
  output [15:0] out_1,
  output [15:0] out_2,
  output [15:0] out_3,
  output [15:0] out_4
);

  Register #(.width(16)) register_1 (.Q(out_1));  // open: D, en, clk, clr
  Register #(.width(16)) register_2 (.Q(out_2));  // open: D, en, clk, clr
  Register #(.width(16)) register_3 (.Q(out_3));  // open: D, en, clk, clr
  Register #(.width(16)) register_4 (.Q(out_4));  // open: D, en, clk, clr
endmodule
