// Logisim project July_18_TA_VIVA.circ as structural Verilog
module half_adder (
  input  A,
  input  B,
  output sum,
  output carry_out
);

  xor xor_1 (sum, A, B);
  and and_1 (carry_out, A, B);
endmodule

module full_adder (
  input  A,
  input  B,
  input  Cin,
  output Sum_out,
  output carry_out
);

  wire half_adder_1_carry_out, half_adder_1_sum, half_adder_2_carry_out;

  half_adder half_adder_1 (.A(A), .B(B), .sum(half_adder_1_sum), .carry_out(half_adder_1_carry_out));
  half_adder half_adder_2 (.A(half_adder_1_sum), .B(Cin), .sum(Sum_out), .carry_out(half_adder_2_carry_out));
  or or_1 (carry_out, half_adder_2_carry_out, half_adder_1_carry_out);
endmodule

module two_bit_adder (
  input  cin,
  input  [1:0] A,
  input  [1:0] B,
  output [1:0] sum_out,
  output carry_out
);

  wire full_adder_1_carry_out;

  full_adder full_adder_1 (.A(A[0]), .B(B[0]), .Cin(cin), .Sum_out(sum_out[0]), .carry_out(full_adder_1_carry_out));
  full_adder full_adder_2 (
    .A(A[1]), .B(B[1]), .Cin(full_adder_1_carry_out), .Sum_out(sum_out[1]), .carry_out(carry_out));
endmodule

module four_bit_adder (
  input  cin,
  input  [3:0] A,
  input  [3:0] B,
  output [3:0] sum_out,
  output cout
);

  wire two_bit_adder_1_carry_out;

  two_bit_adder two_bit_adder_1 (
    .cin(cin), .A(A[1:0]), .B(B[1:0]), .sum_out(sum_out[1:0]), .carry_out(two_bit_adder_1_carry_out));
  two_bit_adder two_bit_adder_2 (
    .cin(two_bit_adder_1_carry_out), .A(A[3:2]), .B(B[3:2]), .sum_out(sum_out[3:2]), .carry_out(cout));
endmodule

module eight_bit_adder (
  input  cin,
  input  [7:0] A,
  input  [7:0] B,
  output [7:0] sum_out,
  output cout
);

  wire four_bit_adder_1_cout;

  four_bit_adder four_bit_adder_1 (
    .cin(cin), .A(A[3:0]), .B(B[3:0]), .sum_out(sum_out[3:0]), .cout(four_bit_adder_1_cout));
  four_bit_adder four_bit_adder_2 (
    .cin(four_bit_adder_1_cout), .A(A[7:4]), .B(B[7:4]), .sum_out(sum_out[7:4]), .cout(cout));
endmodule

module sixteen_bit_adder (
  input  cin,
  input  [15:0] A,
  input  [15:0] B,
  output [15:0] sum_out,
  output cout
);

  wire eight_bit_adder_1_cout;

  eight_bit_adder eight_bit_adder_1 (
    .cin(cin), .A(A[7:0]), .B(B[7:0]), .sum_out(sum_out[7:0]), .cout(eight_bit_adder_1_cout));
  eight_bit_adder eight_bit_adder_2 (
    .cin(eight_bit_adder_1_cout), .A(A[15:8]), .B(B[15:8]), .sum_out(sum_out[15:8]), .cout(cout));
endmodule

module thirtyTwo_bit_Adder (
  input  cin,
  input  [31:0] A,
  input  [31:0] B,
  output [31:0] sum_out,
  output cout
);

  wire sixteen_bit_adder_1_cout;

  sixteen_bit_adder sixteen_bit_adder_1 (
    .cin(cin), .A(A[15:0]), .B(B[15:0]), .sum_out(sum_out[15:0]), .cout(sixteen_bit_adder_1_cout));
  sixteen_bit_adder sixteen_bit_adder_2 (
    .cin(sixteen_bit_adder_1_cout), .A(A[31:16]), .B(B[31:16]), .sum_out(sum_out[31:16]), .cout(cout));
endmodule

module sixtyFour_bit_Adder (
  input  cin,
  input  [63:0] A,
  input  [63:0] B,
  output [63:0] sum_out,
  output cout
);

  wire thirtytwo_bit_adder_1_cout;

  thirtyTwo_bit_Adder thirtytwo_bit_adder_1 (
    .cin(cin), .A(A[31:0]), .B(B[31:0]), .sum_out(sum_out[31:0]), .cout(thirtytwo_bit_adder_1_cout));
  thirtyTwo_bit_Adder thirtytwo_bit_adder_2 (
    .cin(thirtytwo_bit_adder_1_cout), .A(A[63:32]), .B(B[63:32]), .sum_out(sum_out[63:32]), .cout(cout));
endmodule

module matrixAdder2x2Core (
  input  [63:0] A11,
  input  [63:0] A12,
  input  [63:0] A21,
  input  [63:0] A22,
  input  [63:0] B11,
  input  [63:0] B12,
  input  [63:0] B21,
  input  [63:0] B22,
  output [63:0] R11,
  output [63:0] R12,
  output [63:0] R21,
  output [63:0] R22
);

  Adder #(.width(64)) adder_1 (.a(A21), .b(B21), .out(R21));  // open: cin, cout
  Adder #(.width(64)) adder_2 (.a(A11), .b(B11), .out(R11));  // open: cin, cout
  Adder #(.width(64)) adder_3 (.a(A12), .b(B12), .out(R12));  // open: cin, cout
  Adder #(.width(64)) adder_4 (.a(A22), .b(B22), .out(R22));  // open: cin, cout
endmodule

module testBench (
  input  [63:0] in_1,
  input  [63:0] in_2,
  input  [63:0] in_3,
  input  [63:0] in_4,
  input  [63:0] in_5,
  input  [63:0] in_6,
  input  [63:0] in_7,
  input  [63:0] in_8,
  output [63:0] out_9,
  output [63:0] out_10,
  output [63:0] out_11,
  output [63:0] out_12
);

  matrixAdder2x2Core matrixadder2x2core_1 (
    .A11(in_1), .A12(in_2), .A21(in_3), .A22(in_4), .B11(in_5), .B12(in_7), .B21(in_8), .B22(in_6),
    .R11(out_9), .R12(out_10), .R21(out_11), .R22(out_12));
endmodule

module Assembly (
  input  OUTPUT_ENABLE,
  input  write_ENNBLE,
  input  WRITE_ENABLE
);

  wire clock_1_out, Delay_Counter_carry;
  wire [3:0] counter_1_q;
  wire [63:0] mat_mult_node_1_r11, mat_mult_node_1_r12, mat_mult_node_1_r21, mat_mult_node_1_r22, R_11_dout,
       RAM_A11_dout, RAM_A12_dout, RAM_A21_dout, RAM_A22_dout, RAM_B11_dout, RAM_B12_dout, RAM_B21_dout,
       RAM_B22_dout, undriven;

  Clock clock_1 (.out(clock_1_out));
  RAM #(.addrWidth(4), .dataWidth(64), .\type ("nonvolatile")) RAM_A11 (
    .addr(counter_1_q), .we(write_ENNBLE), .oe(1'b1), .clk(clock_1_out), .dout(RAM_A11_dout));  // open: din
  // Probe on RAM_A21_dout
  // Probe on RAM_B21_dout
  Counter #(.max('h2), .width(4)) Delay_Counter (
    .count(clock_1_out), .clk(clock_1_out), .carry(Delay_Counter_carry));  // open: clr, load, up, D, Q
  // Probe on RAM_A11_dout
  RAM #(.addrWidth(4), .dataWidth(64), .\type ("nonvolatile")) RAM_A12 (
    .addr(counter_1_q), .we(write_ENNBLE), .clk(clock_1_out), .dout(RAM_A12_dout));  // open: oe, din
  Counter #(.max('h7), .width(4)) counter_1 (
    .count(Delay_Counter_carry), .clk(clock_1_out), .Q(counter_1_q));  // open: clr, load, up, D, carry
  mat_mult_node mat_mult_node_1 (
    .A11(RAM_A11_dout), .A12(RAM_A12_dout), .A21(RAM_A21_dout), .A22(RAM_A22_dout), .B11(RAM_B11_dout),
    .B12(RAM_B12_dout), .B21(RAM_B21_dout), .B22(RAM_B22_dout), .R11(mat_mult_node_1_r11),
    .R12(mat_mult_node_1_r12), .R21(mat_mult_node_1_r21), .R22(mat_mult_node_1_r22));
  RAM #(.addrWidth(4), .dataWidth(64), .\type ("nonvolatile")) RAM_A21 (
    .addr(counter_1_q), .we(write_ENNBLE), .oe(1'b1), .clk(clock_1_out), .dout(RAM_A21_dout));  // open: din
  // Probe on mat_mult_node_1_r11
  // Probe on mat_mult_node_1_r12
  RAM #(.addrWidth(4), .dataWidth(64), .\type ("nonvolatile")) RAM_A22 (
    .addr(counter_1_q), .we(write_ENNBLE), .oe(1'b1), .clk(clock_1_out), .dout(RAM_A22_dout));  // open: din
  RAM #(.addrWidth(4), .dataWidth(64)) R_11 (
    .addr(counter_1_q), .we(1'b1), .clk(clock_1_out), .din(mat_mult_node_1_r11), .dout(R_11_dout));  // open: oe
  // Probe on mat_mult_node_1_r21
  RAM #(.addrWidth(4), .dataWidth(64), .\type ("nonvolatile")) RAM_B11 (
    .addr(counter_1_q), .we(write_ENNBLE), .oe(1'b1), .clk(clock_1_out), .din(undriven), .dout(RAM_B11_dout));
  // Probe on mat_mult_node_1_r22
  RAM #(.addrWidth(4), .dataWidth(64), .\type ("nonvolatile")) RAM_B12 (
    .addr(counter_1_q), .we(write_ENNBLE), .oe(1'b1), .clk(clock_1_out), .dout(RAM_B12_dout));  // open: din
  RAM #(.addrWidth(4), .dataWidth(64)) R_12 (
    .addr(counter_1_q), .we(1'b1), .clk(clock_1_out), .din(mat_mult_node_1_r12));  // open: oe, dout
  RAM #(.addrWidth(4), .dataWidth(64), .\type ("nonvolatile")) RAM_B21 (
    .addr(counter_1_q), .we(write_ENNBLE), .oe(1'b1), .clk(clock_1_out), .dout(RAM_B21_dout));  // open: din
  // Probe on mat_mult_node_1_r22
  RAM #(.addrWidth(4), .dataWidth(64)) R_21 (
    .addr(counter_1_q), .we(1'b1), .clk(clock_1_out), .din(mat_mult_node_1_r22));  // open: oe, dout
  RAM #(.addrWidth(4), .dataWidth(64), .\type ("nonvolatile")) RAM_B22 (
    .addr(counter_1_q), .we(write_ENNBLE), .oe(1'b1), .clk(clock_1_out), .dout(RAM_B22_dout));  // open: din
  RAM #(.addrWidth(4), .dataWidth(64)) R_22 (
    .addr(counter_1_q), .we(1'b1), .clk(clock_1_out), .din(mat_mult_node_1_r21));  // open: oe, dout

  // Notes on the sheet:
  //   Matrix_A
  //   Matrix_B
endmodule

module counterdemo (
  input  in_1,
  input  in_2,
  input  in_3,
  input  in_4,
  input  [3:0] in_5,
  output [3:0] out_6
);

  Counter #(.max('h3), .ongoal("load"), .width(4)) counter_1 (
    .load(in_1), .up(in_2), .count(in_3), .clk(in_4), .D(in_5), .Q(out_6));  // open: clr, carry
endmodule

module assembly2 (
  input  OUTPUT_ENABLE,
  input  WE,
  input  OE,
  input  WRITE_ENABLE
);

  wire clock_1_out, Delay_Counter_carry;
  wire [4:0] counter_1_q;
  wire [63:0] matrixadder2x2core_1_r11, matrixadder2x2core_1_r12, matrixadder2x2core_1_r21,
       matrixadder2x2core_1_r22, R_11_dout, R_12_dout, R_21_dout, R_22_dout, RAM_A11_dout, RAM_A12_dout,
       RAM_A21_dout, RAM_A22_dout, RAM_B11_dout, RAM_B12_dout, RAM_B21_dout, RAM_B22_dout;

  Clock clock_1 (.out(clock_1_out));
  RAM #(.addrWidth(5), .dataWidth(64), .\type ("nonvolatile")) RAM_A11 (
    .addr(counter_1_q), .we(WE), .oe(1'b1), .clk(clock_1_out), .din(R_11_dout), .dout(RAM_A11_dout));
  // Probe on RAM_B12_dout
  Counter #(.max('h2), .width(4)) Delay_Counter (
    .count(clock_1_out), .clk(clock_1_out), .carry(Delay_Counter_carry));  // open: clr, load, up, D, Q
  // Probe on RAM_A12_dout
  // Probe on RAM_A11_dout
  RAM #(.addrWidth(5), .dataWidth(64), .\type ("nonvolatile")) RAM_A12 (
    .addr(counter_1_q), .oe(1'b1), .clk(clock_1_out), .din(R_21_dout), .dout(RAM_A12_dout));  // open: we
  Counter #(.max('h7), .width(5)) counter_1 (
    .count(Delay_Counter_carry), .clk(clock_1_out), .Q(counter_1_q));  // open: clr, load, up, D, carry
  matrixAdder2x2Core matrixadder2x2core_1 (
    .A11(RAM_A11_dout), .A12(RAM_A12_dout), .A21(RAM_A21_dout), .A22(RAM_A22_dout), .B11(RAM_B11_dout),
    .B12(RAM_B12_dout), .B21(RAM_B21_dout), .B22(RAM_B22_dout), .R11(matrixadder2x2core_1_r11),
    .R12(matrixadder2x2core_1_r12), .R21(matrixadder2x2core_1_r21), .R22(matrixadder2x2core_1_r22));
  RAM #(.addrWidth(5), .dataWidth(64), .\type ("nonvolatile")) RAM_A21 (
    .addr(counter_1_q), .we(WE), .oe(1'b1), .clk(clock_1_out), .dout(RAM_A21_dout));  // open: din
  // Probe on matrixadder2x2core_1_r11
  // Probe on matrixadder2x2core_1_r12
  RAM #(.addrWidth(5), .dataWidth(64), .\type ("nonvolatile")) RAM_A22 (
    .addr(counter_1_q), .we(WE), .oe(1'b1), .clk(clock_1_out), .dout(RAM_A22_dout));  // open: din
  RAM #(.addrWidth(5), .dataWidth(64)) R_11 (
    .addr(counter_1_q), .we(1'b1), .oe(OE), .clk(clock_1_out), .din(matrixadder2x2core_1_r11),
    .dout(R_11_dout));
  // Probe on matrixadder2x2core_1_r21
  RAM #(.addrWidth(5), .dataWidth(64), .\type ("nonvolatile")) RAM_B11 (
    .addr(counter_1_q), .we(WE), .oe(1'b1), .clk(clock_1_out), .din(R_12_dout), .dout(RAM_B11_dout));
  // Probe on matrixadder2x2core_1_r12
  RAM #(.addrWidth(5), .dataWidth(64), .\type ("nonvolatile")) RAM_B12 (
    .addr(counter_1_q), .we(WE), .oe(1'b1), .clk(clock_1_out), .din(R_22_dout), .dout(RAM_B12_dout));
  RAM #(.addrWidth(5), .dataWidth(64)) R_12 (
    .addr(counter_1_q), .we(1'b1), .oe(OE), .clk(clock_1_out), .din(matrixadder2x2core_1_r12),
    .dout(R_12_dout));
  RAM #(.addrWidth(5), .dataWidth(64), .\type ("nonvolatile")) RAM_B21 (
    .addr(counter_1_q), .we(WE), .oe(1'b1), .clk(clock_1_out), .dout(RAM_B21_dout));  // open: din
  RAM #(.addrWidth(5), .dataWidth(64)) R_21 (
    .addr(counter_1_q), .we(1'b1), .oe(OE), .clk(clock_1_out), .din(matrixadder2x2core_1_r22),
    .dout(R_21_dout));
  RAM #(.addrWidth(5), .dataWidth(64), .\type ("nonvolatile")) RAM_B22 (
    .addr(counter_1_q), .we(WE), .oe(1'b1), .clk(clock_1_out), .dout(RAM_B22_dout));  // open: din
  RAM #(.addrWidth(5), .dataWidth(64)) R_22 (
    .addr(counter_1_q), .we(1'b1), .oe(OE), .clk(clock_1_out), .din(matrixadder2x2core_1_r21),
    .dout(R_22_dout));

  // Notes on the sheet:
  //   Matrix_A
  //   Matrix_B
endmodule

module test_assembly (
  input  OUTPUT_ENABLE,
  input  WE,
  input  OE,
  input  WRITE_ENABLE
);

  wire clock_1_out, Delay_Counter_carry;
  wire [4:0] counter_1_q, counter_2_q;
  wire [63:0] matrixadder2x2core_1_r11, matrixadder2x2core_1_r12, matrixadder2x2core_1_r21,
       matrixadder2x2core_1_r22, R_11_dout, R_12_dout, R_21_dout, R_22_dout, RAM_A11_dout, RAM_A12_dout,
       RAM_A21_dout, RAM_A22_dout, RAM_B11_dout, RAM_B12_dout, RAM_B21_dout, RAM_B22_dout;

  Clock clock_1 (.out(clock_1_out));
  RAM #(.addrWidth(5), .dataWidth(64), .\type ("nonvolatile")) RAM_A11 (
    .addr(counter_2_q), .we(WE), .oe(1'b1), .clk(clock_1_out), .din(R_11_dout), .dout(RAM_A11_dout));
  // Probe on RAM_B12_dout
  Counter #(.max('h2), .width(4)) Delay_Counter (
    .count(clock_1_out), .clk(clock_1_out), .carry(Delay_Counter_carry));  // open: clr, load, up, D, Q
  // Probe on RAM_A12_dout
  // Probe on RAM_A11_dout
  Counter #(.max('h7), .width(5)) counter_1 (
    .clk(clock_1_out), .Q(counter_1_q));  // open: clr, load, up, count, D, carry
  RAM #(.addrWidth(5), .dataWidth(64), .\type ("nonvolatile")) RAM_A12 (
    .addr(counter_2_q), .oe(1'b1), .clk(clock_1_out), .din(R_21_dout), .dout(RAM_A12_dout));  // open: we
  Counter #(.max('h18), .width(5)) counter_2 (
    .count(Delay_Counter_carry), .clk(clock_1_out), .Q(counter_2_q));  // open: clr, load, up, D, carry
  matrixAdder2x2Core matrixadder2x2core_1 (
    .A11(RAM_A11_dout), .A12(RAM_A12_dout), .A21(RAM_A21_dout), .A22(RAM_A22_dout), .B11(RAM_B11_dout),
    .B12(RAM_B12_dout), .B21(RAM_B21_dout), .B22(RAM_B22_dout), .R11(matrixadder2x2core_1_r11),
    .R12(matrixadder2x2core_1_r12), .R21(matrixadder2x2core_1_r21), .R22(matrixadder2x2core_1_r22));
  RAM #(.addrWidth(5), .dataWidth(64), .\type ("nonvolatile")) RAM_A21 (
    .addr(counter_2_q), .we(WE), .oe(1'b1), .clk(clock_1_out), .dout(RAM_A21_dout));  // open: din
  // Probe on matrixadder2x2core_1_r11
  // Probe on matrixadder2x2core_1_r12
  RAM #(.addrWidth(5), .dataWidth(64), .\type ("nonvolatile")) RAM_A22 (
    .addr(counter_2_q), .we(WE), .oe(1'b1), .clk(clock_1_out), .dout(RAM_A22_dout));  // open: din
  RAM #(.addrWidth(5), .dataWidth(64)) R_11 (
    .addr(counter_1_q), .we(1'b1), .oe(OE), .clk(clock_1_out), .din(matrixadder2x2core_1_r11),
    .dout(R_11_dout));
  // Probe on matrixadder2x2core_1_r21
  RAM #(.addrWidth(5), .dataWidth(64), .\type ("nonvolatile")) RAM_B11 (
    .addr(counter_2_q), .we(WE), .oe(1'b1), .clk(clock_1_out), .din(R_12_dout), .dout(RAM_B11_dout));
  // Probe on matrixadder2x2core_1_r12
  RAM #(.addrWidth(5), .dataWidth(64), .\type ("nonvolatile")) RAM_B12 (
    .addr(counter_2_q), .we(WE), .oe(1'b1), .clk(clock_1_out), .din(R_22_dout), .dout(RAM_B12_dout));
  RAM #(.addrWidth(5), .dataWidth(64)) R_12 (
    .addr(counter_1_q), .we(1'b1), .oe(OE), .clk(clock_1_out), .din(matrixadder2x2core_1_r12),
    .dout(R_12_dout));
  RAM #(.addrWidth(5), .dataWidth(64), .\type ("nonvolatile")) RAM_B21 (
    .addr(counter_2_q), .we(WE), .oe(1'b1), .clk(clock_1_out), .dout(RAM_B21_dout));  // open: din
  RAM #(.addrWidth(5), .dataWidth(64)) R_21 (
    .addr(counter_1_q), .we(1'b1), .oe(OE), .clk(clock_1_out), .din(matrixadder2x2core_1_r22),
    .dout(R_21_dout));
  RAM #(.addrWidth(5), .dataWidth(64), .\type ("nonvolatile")) RAM_B22 (
    .addr(counter_2_q), .we(WE), .oe(1'b1), .clk(clock_1_out), .dout(RAM_B22_dout));  // open: din
  RAM #(.addrWidth(5), .dataWidth(64)) R_22 (
    .addr(counter_1_q), .we(1'b1), .oe(OE), .clk(clock_1_out), .din(matrixadder2x2core_1_r21),
    .dout(R_22_dout));

  // Notes on the sheet:
  //   Matrix_A
  //   Matrix_B
endmodule

module multiplier_Core (
  input  [63:0] A11,
  input  [63:0] B11,
  input  [63:0] A12,
  input  [63:0] B12,
  input  [63:0] A21,
  input  [63:0] B21,
  input  [63:0] A22,
  input  [63:0] B22,
  output [63:0] R11,
  output [63:0] xtra64bits,
  output [63:0] R12,
  output [63:0] xtra64bits2,
  output [63:0] R21,
  output [63:0] xtra64bits3,
  output [63:0] R22,
  output [63:0] xtra64bits4
);

  // Probe on A11
  // Probe on A12
  // Probe on A21
  // Probe on A22
  // Probe on B11
  // Probe on B12
  // Probe on B21
  // Probe on B22
  Multiplier #(.width(64)) multiplier_1 (.a(A11), .b(B11), .out(R11), .cout(xtra64bits));  // open: cin
  Multiplier #(.width(64)) multiplier_2 (.a(A12), .b(B12), .out(R12), .cout(xtra64bits2));  // open: cin
  Multiplier #(.width(64)) multiplier_3 (.a(A21), .b(B21), .out(R21), .cout(xtra64bits3));  // open: cin
  Multiplier #(.width(64)) multiplier_4 (.a(A22), .b(B22), .out(R22), .cout(xtra64bits4));  // open: cin
  // Probe on R11
  // Probe on R12
  // Probe on R21
  // Probe on R22
endmodule

module mat_mult_node (
  input  [63:0] A11,
  input  [63:0] A12,
  input  [63:0] A21,
  input  [63:0] A22,
  input  [63:0] B11,
  input  [63:0] B12,
  input  [63:0] B21,
  input  [63:0] B22,
  output [63:0] R11,
  output [63:0] R12,
  output [63:0] R21,
  output [63:0] R22
);

  wire [63:0] multiplier_1_out, multiplier_2_out, multiplier_3_out, multiplier_4_out, multiplier_5_out,
       multiplier_6_out, multiplier_7_out, multiplier_8_out;

  // Probe on A12
  // Probe on B11
  // Probe on B21
  // Probe on A11
  // Probe on A21
  // Probe on B11
  Multiplier #(.width(64)) multiplier_1 (.a(A11), .b(B11), .out(multiplier_1_out));  // open: cin, cout
  Multiplier #(.width(64)) multiplier_2 (.a(A12), .b(B21), .out(multiplier_2_out));  // open: cin, cout
  Multiplier #(.width(64)) multiplier_3 (.a(A11), .b(B12), .out(multiplier_3_out));  // open: cin, cout
  Multiplier #(.width(64)) multiplier_4 (.a(A12), .b(B22), .out(multiplier_4_out));  // open: cin, cout
  Multiplier #(.width(64)) multiplier_5 (.a(A21), .b(B11), .out(multiplier_5_out));  // open: cin, cout
  Multiplier #(.width(64)) multiplier_6 (.a(A22), .b(B21), .out(multiplier_6_out));  // open: cin, cout
  Multiplier #(.width(64)) multiplier_7 (.a(A21), .b(B12), .out(multiplier_7_out));  // open: cin, cout
  Multiplier #(.width(64)) multiplier_8 (.a(A22), .b(B22), .out(multiplier_8_out));  // open: cin, cout
  // Probe on multiplier_1_out
  // Probe on multiplier_3_out
  // Probe on multiplier_7_out
  // Probe on multiplier_2_out
  // Probe on multiplier_4_out
  // Probe on multiplier_5_out
  // Probe on multiplier_6_out
  // Probe on multiplier_8_out
  Adder #(.width(64)) adder_1 (.a(multiplier_1_out), .b(multiplier_2_out), .out(R11));  // open: cin, cout
  Adder #(.width(64)) adder_2 (.a(multiplier_3_out), .b(multiplier_4_out), .out(R12));  // open: cin, cout
  Adder #(.width(64)) adder_3 (.a(multiplier_5_out), .b(multiplier_6_out), .out(R21));  // open: cin, cout
  Adder #(.width(64)) adder_4 (.a(multiplier_7_out), .b(multiplier_8_out), .out(R22));  // open: cin, cout
  // Probe on R11
  // Probe on R12
  // Probe on R21
  // Probe on R22
endmodule

module Assembly_With_MatMult (
  input  OUTPUT_ENABLE,
  input  write_ENNBLE,
  input  WRITE_ENABLE
);

  wire clock_1_out, Delay_Counter_carry;
  wire [3:0] counter_1_q;
  wire [63:0] mat_mult_node_1_r11, mat_mult_node_1_r12, mat_mult_node_1_r21, mat_mult_node_1_r22, R_11_dout,
       RAM_A11_dout, RAM_A12_dout, RAM_A21_dout, RAM_A22_dout, RAM_B11_dout, RAM_B12_dout, RAM_B21_dout,
       RAM_B22_dout, undriven;

  Clock clock_1 (.out(clock_1_out));
  RAM #(.addrWidth(4), .dataWidth(64), .\type ("nonvolatile")) RAM_A11 (
    .addr(counter_1_q), .we(write_ENNBLE), .oe(1'b1), .clk(clock_1_out), .dout(RAM_A11_dout));  // open: din
  // Probe on RAM_A21_dout
  // Probe on RAM_B21_dout
  Counter #(.max('h2), .width(4)) Delay_Counter (
    .count(clock_1_out), .clk(clock_1_out), .carry(Delay_Counter_carry));  // open: clr, load, up, D, Q
  // Probe on RAM_A11_dout
  RAM #(.addrWidth(4), .dataWidth(64), .\type ("nonvolatile")) RAM_A12 (
    .addr(counter_1_q), .we(write_ENNBLE), .clk(clock_1_out), .dout(RAM_A12_dout));  // open: oe, din
  Counter #(.max('h7), .width(4)) counter_1 (
    .count(Delay_Counter_carry), .clk(clock_1_out), .Q(counter_1_q));  // open: clr, load, up, D, carry
  mat_mult_node mat_mult_node_1 (
    .A11(RAM_A11_dout), .A12(RAM_A12_dout), .A21(RAM_A21_dout), .A22(RAM_A22_dout), .B11(RAM_B11_dout),
    .B12(RAM_B12_dout), .B21(RAM_B21_dout), .B22(RAM_B22_dout), .R11(mat_mult_node_1_r11),
    .R12(mat_mult_node_1_r12), .R21(mat_mult_node_1_r21), .R22(mat_mult_node_1_r22));
  RAM #(.addrWidth(4), .dataWidth(64), .\type ("nonvolatile")) RAM_A21 (
    .addr(counter_1_q), .we(write_ENNBLE), .oe(1'b1), .clk(clock_1_out), .dout(RAM_A21_dout));  // open: din
  // Probe on mat_mult_node_1_r11
  // Probe on mat_mult_node_1_r12
  RAM #(.addrWidth(4), .dataWidth(64), .\type ("nonvolatile")) RAM_A22 (
    .addr(counter_1_q), .we(write_ENNBLE), .oe(1'b1), .clk(clock_1_out), .dout(RAM_A22_dout));  // open: din
  RAM #(.addrWidth(4), .dataWidth(64)) R_11 (
    .addr(counter_1_q), .we(1'b1), .clk(clock_1_out), .din(mat_mult_node_1_r11), .dout(R_11_dout));  // open: oe
  // Probe on mat_mult_node_1_r21
  RAM #(.addrWidth(4), .dataWidth(64), .\type ("nonvolatile")) RAM_B11 (
    .addr(counter_1_q), .we(write_ENNBLE), .oe(1'b1), .clk(clock_1_out), .din(undriven), .dout(RAM_B11_dout));
  // Probe on mat_mult_node_1_r22
  RAM #(.addrWidth(4), .dataWidth(64), .\type ("nonvolatile")) RAM_B12 (
    .addr(counter_1_q), .we(write_ENNBLE), .oe(1'b1), .clk(clock_1_out), .dout(RAM_B12_dout));  // open: din
  RAM #(.addrWidth(4), .dataWidth(64)) R_12 (
    .addr(counter_1_q), .we(1'b1), .clk(clock_1_out), .din(mat_mult_node_1_r12));  // open: oe, dout
  RAM #(.addrWidth(4), .dataWidth(64), .\type ("nonvolatile")) RAM_B21 (
    .addr(counter_1_q), .we(write_ENNBLE), .oe(1'b1), .clk(clock_1_out), .dout(RAM_B21_dout));  // open: din
  // Probe on mat_mult_node_1_r22
  RAM #(.addrWidth(4), .dataWidth(64)) R_21 (
    .addr(counter_1_q), .we(1'b1), .clk(clock_1_out), .din(mat_mult_node_1_r22));  // open: oe, dout
  RAM #(.addrWidth(4), .dataWidth(64), .\type ("nonvolatile")) RAM_B22 (
    .addr(counter_1_q), .we(write_ENNBLE), .oe(1'b1), .clk(clock_1_out), .dout(RAM_B22_dout));  // open: din
  RAM #(.addrWidth(4), .dataWidth(64)) R_22 (
    .addr(counter_1_q), .we(1'b1), .clk(clock_1_out), .din(mat_mult_node_1_r21));  // open: oe, dout

  // Notes on the sheet:
  //   Matrix_A
  //   Matrix_B
endmodule

module mat_mult_4x4 (
  input  [63:0] A11_11,
  input  [63:0] A11_12,
  input  [63:0] A11_21,
  input  [63:0] A11_22,
  input  [63:0] A12_11,
  input  [63:0] A12_12,
  input  [63:0] A12_21,
  input  [63:0] A12_22,
  input  [63:0] B11_11,
  input  [63:0] B11_12,
  input  [63:0] B11_21,
  input  [63:0] B11_22,
  input  [63:0] B21_11,
  input  [63:0] B21_12,
  input  [63:0] B21_21,
  input  [63:0] B21_22,
  output [63:0] R11,
  output [63:0] R12,
  output [63:0] R21,
  output [63:0] R22
);

  wire [63:0] mat_mult_node_1_r11, mat_mult_node_1_r12, mat_mult_node_1_r21, mat_mult_node_1_r22,
       mat_mult_node_2_r11, mat_mult_node_2_r12, mat_mult_node_2_r21, mat_mult_node_2_r22;

  // Probe on B11_12
  // Probe on B11_11
  // Probe on B21_11
  // Probe on B21_12
  // Probe on B21_21
  // Probe on B11_21
  // Probe on B21_22
  // Probe on A11_11
  // Probe on B11_22
  // Probe on A11_12
  // Probe on A12_11
  // Probe on A11_21
  // Probe on A12_12
  // Probe on A11_22
  // Probe on A12_21
  // Probe on A12_22
  // Probe on mat_mult_node_1_r22
  // Probe on mat_mult_node_1_r21
  // Probe on mat_mult_node_1_r12
  // Probe on mat_mult_node_1_r11
  mat_mult_node mat_mult_node_1 (
    .A11(A12_11), .A12(A12_12), .A21(A12_21), .A22(A12_22), .B11(B21_11), .B12(B21_12), .B21(B21_21),
    .B22(B21_22), .R11(mat_mult_node_1_r11), .R12(mat_mult_node_1_r12), .R21(mat_mult_node_1_r21),
    .R22(mat_mult_node_1_r22));
  // Probe on mat_mult_node_2_r11
  mat_mult_node mat_mult_node_2 (
    .A11(A11_11), .A12(A11_12), .A21(A11_21), .A22(A11_22), .B11(B11_11), .B12(B11_12), .B21(B11_21),
    .B22(B11_22), .R11(mat_mult_node_2_r11), .R12(mat_mult_node_2_r12), .R21(mat_mult_node_2_r21),
    .R22(mat_mult_node_2_r22));
  // Probe on mat_mult_node_2_r12
  // Probe on mat_mult_node_2_r22
  // Probe on mat_mult_node_2_r21
  // Probe on R21
  // Probe on R12
  // Probe on R11
  matrixAdder2x2Core matrixadder2x2core_1 (
    .A11(mat_mult_node_2_r11), .A12(mat_mult_node_2_r12), .A21(mat_mult_node_2_r21),
    .A22(mat_mult_node_2_r22), .B11(mat_mult_node_1_r11), .B12(mat_mult_node_1_r12),
    .B21(mat_mult_node_1_r21), .B22(mat_mult_node_1_r22), .R11(R11), .R12(R12), .R21(R21), .R22(R22));
  // Probe on R22

  // Notes on the sheet:
  //   A11
  //   A12
  //   B11
  //   B21
endmodule

module Assembly_4x4_mat_mult (
);

  wire clock_1_out, counter_1_carry, counter_2_carry, counter_3_carry;
  wire [3:0] counter_3_q, counter_4_q, counter_5_q;
  wire [63:0] A11_11_dout, A11_12_dout, A11_21_dout, A11_22_dout, A12_11_dout, A12_12_dout, A12_21_dout,
       A12_22_dout, B11_11_dout, B11_12_dout, B11_21_dout, B11_22_dout, B12_11_dout, B12_12_dout,
       B12_21_dout, B12_22_dout, mat_mult_4x4_1_r11, mat_mult_4x4_1_r12, mat_mult_4x4_1_r21,
       mat_mult_4x4_1_r22;

  RAM #(.addrWidth(4), .dataWidth(64), .\type ("nonvolatile")) B11_11 (
    .addr(counter_3_q), .oe(1'b1), .clk(clock_1_out), .dout(B11_11_dout));  // open: we, din
  RAM #(.addrWidth(4), .dataWidth(64), .\type ("nonvolatile")) B11_12 (
    .addr(counter_3_q), .oe(1'b1), .clk(clock_1_out), .dout(B11_12_dout));  // open: we, din
  // Probe on B11_11_dout
  // Probe on B11_12_dout
  RAM #(.addrWidth(4), .dataWidth(64), .\type ("nonvolatile")) B11_21 (
    .addr(counter_3_q), .oe(1'b1), .clk(clock_1_out), .dout(B11_21_dout));  // open: we, din
  RAM #(.addrWidth(4), .dataWidth(64), .\type ("nonvolatile")) B11_22 (
    .addr(counter_3_q), .oe(1'b1), .clk(clock_1_out), .dout(B11_22_dout));  // open: we, din
  // Probe on B11_21_dout
  // Probe on B11_22_dout
  RAM #(.addrWidth(4), .dataWidth(64), .\type ("nonvolatile")) B12_11 (
    .addr(counter_3_q), .oe(1'b1), .clk(clock_1_out), .dout(B12_11_dout));  // open: we, din
  RAM #(.addrWidth(4), .dataWidth(64), .\type ("nonvolatile")) B12_12 (
    .addr(counter_3_q), .oe(1'b1), .clk(clock_1_out), .dout(B12_12_dout));  // open: we, din
  // Probe on B12_11_dout
  // Probe on B12_12_dout
  RAM #(.addrWidth(4), .dataWidth(64), .\type ("nonvolatile")) B12_21 (
    .addr(counter_3_q), .oe(1'b1), .clk(clock_1_out), .dout(B12_21_dout));  // open: we, din
  RAM #(.addrWidth(4), .dataWidth(64), .\type ("nonvolatile")) B12_22 (
    .addr(counter_3_q), .oe(1'b1), .clk(clock_1_out), .dout(B12_22_dout));  // open: we, din
  Counter #(.max('h1), .width(2)) counter_1 (
    .count(clock_1_out), .clk(clock_1_out), .carry(counter_1_carry));  // open: clr, load, up, D, Q
  // Probe on B12_22_dout
  Counter #(.max('h1), .width(1)) counter_2 (
    .clk(clock_1_out), .carry(counter_2_carry));  // open: clr, load, up, count, D, Q
  // Probe on B12_21_dout
  Counter #(.max('h1), .width(4)) counter_3 (
    .count(counter_1_carry), .clk(clock_1_out), .carry(counter_3_carry), .Q(counter_3_q));  // open: clr, load, up, D
  Counter #(.max('h1), .ongoal("stay"), .width(4)) counter_4 (
    .count(counter_3_carry), .clk(clock_1_out), .Q(counter_4_q));  // open: clr, load, up, D, carry
  // Probe on B11_11_dout
  Counter #(.max('h3), .width(4)) counter_5 (
    .count(counter_2_carry), .clk(clock_1_out), .Q(counter_5_q));  // open: clr, load, up, D, carry
  Clock clock_1 (.out(clock_1_out));
  // Probe on mat_mult_4x4_1_r22
  // Probe on mat_mult_4x4_1_r21
  // Probe on mat_mult_4x4_1_r12
  // Probe on mat_mult_4x4_1_r11
  mat_mult_4x4 mat_mult_4x4_1 (
    .A11_11(A11_11_dout), .A11_12(A11_12_dout), .A11_21(A11_21_dout), .A11_22(A11_22_dout),
    .A12_11(A12_11_dout), .A12_12(A12_12_dout), .A12_21(A12_21_dout), .A12_22(A12_22_dout),
    .B11_11(B11_11_dout), .B11_12(B11_12_dout), .B11_21(B11_21_dout), .B11_22(B11_22_dout),
    .B21_11(B12_11_dout), .B21_12(B12_12_dout), .B21_21(B12_21_dout), .B21_22(B12_22_dout),
    .R11(mat_mult_4x4_1_r11), .R12(mat_mult_4x4_1_r12), .R21(mat_mult_4x4_1_r21), .R22(mat_mult_4x4_1_r22));
  // Probe on A11_11_dout
  RAM #(.addrWidth(4), .dataWidth(64), .\type ("nonvolatile")) A11_11 (
    .addr(counter_4_q), .oe(1'b1), .clk(clock_1_out), .dout(A11_11_dout));  // open: we, din
  RAM #(.addrWidth(4), .dataWidth(64), .\type ("nonvolatile")) A11_12 (
    .addr(counter_4_q), .oe(1'b1), .clk(clock_1_out), .dout(A11_12_dout));  // open: we, din
  RAM #(.addrWidth(4), .dataWidth(64)) ram_1 (
    .addr(counter_5_q), .we(1'b1), .clk(clock_1_out), .din(mat_mult_4x4_1_r11));  // open: oe, dout
  // Probe on A11_11_dout
  // Probe on A11_12_dout
  RAM #(.addrWidth(4), .dataWidth(64), .\type ("nonvolatile")) A11_21 (
    .addr(counter_4_q), .oe(1'b1), .clk(clock_1_out), .dout(A11_21_dout));  // open: we, din
  RAM #(.addrWidth(4), .dataWidth(64), .\type ("nonvolatile")) A11_22 (
    .addr(counter_4_q), .oe(1'b1), .clk(clock_1_out), .dout(A11_22_dout));  // open: we, din
  RAM #(.addrWidth(4), .dataWidth(64)) ram_2 (
    .addr(counter_5_q), .we(1'b1), .clk(clock_1_out), .din(mat_mult_4x4_1_r12));  // open: oe, dout
  // Probe on A11_21_dout
  // Probe on A11_22_dout
  RAM #(.addrWidth(4), .dataWidth(64), .\type ("nonvolatile")) A12_11 (
    .addr(counter_4_q), .oe(1'b1), .clk(clock_1_out), .dout(A12_11_dout));  // open: we, din
  RAM #(.addrWidth(4), .dataWidth(64), .\type ("nonvolatile")) A12_12 (
    .addr(counter_4_q), .oe(1'b1), .clk(clock_1_out), .dout(A12_12_dout));  // open: we, din
  RAM #(.addrWidth(4), .dataWidth(64)) ram_3 (
    .addr(counter_5_q), .we(1'b1), .clk(clock_1_out), .din(mat_mult_4x4_1_r21));  // open: oe, dout
  // Probe on A12_11_dout
  // Probe on A12_12_dout
  RAM #(.addrWidth(4), .dataWidth(64), .\type ("nonvolatile")) A12_21 (
    .addr(counter_4_q), .oe(1'b1), .clk(clock_1_out), .dout(A12_21_dout));  // open: we, din
  RAM #(.addrWidth(4), .dataWidth(64), .\type ("nonvolatile")) A12_22 (
    .addr(counter_4_q), .oe(1'b1), .clk(clock_1_out), .dout(A12_22_dout));  // open: we, din
  RAM #(.addrWidth(4), .dataWidth(64)) ram_4 (
    .addr(counter_5_q), .we(1'b1), .clk(clock_1_out), .din(mat_mult_4x4_1_r22));  // open: oe, dout
  // Probe on A12_21_dout
  // Probe on A12_22_dout
endmodule

module matrixAdder4x4 (
  input  [63:0] A11_11,
  input  [63:0] A11_12,
  input  [63:0] A11_21,
  input  [63:0] A11_22,
  input  [63:0] A12_11,
  input  [63:0] A12_12,
  input  [63:0] A12_21,
  input  [63:0] A12_22,
  input  [63:0] A21_11,
  input  [63:0] A21_12,
  input  [63:0] A21_21,
  input  [63:0] A21_22,
  input  [63:0] A22_11,
  input  [63:0] A22_12,
  input  [63:0] A22_21,
  input  [63:0] A22_22,
  input  [63:0] B11_11,
  input  [63:0] B11_12,
  input  [63:0] B11_21,
  input  [63:0] B11_22,
  input  [63:0] B12_11,
  input  [63:0] B12_12,
  input  [63:0] B12_21,
  input  [63:0] B12_22,
  input  [63:0] B21_11,
  input  [63:0] B21_12,
  input  [63:0] B21_21,
  input  [63:0] B21_22,
  input  [63:0] B22_11,
  input  [63:0] B22_12,
  input  [63:0] B22_21,
  input  [63:0] B22_22,
  output [63:0] R11_11,
  output [63:0] R11_12,
  output [63:0] R11_21,
  output [63:0] R11_22,
  output [63:0] R12_11,
  output [63:0] R12_12,
  output [63:0] R12_21,
  output [63:0] R12_22,
  output [63:0] R21_11,
  output [63:0] R21_12,
  output [63:0] R21_21,
  output [63:0] R21_22,
  output [63:0] R22_11,
  output [63:0] R22_12,
  output [63:0] R22_21,
  output [63:0] R22_22
);

  matrixAdder2x2Core matrixadder2x2core_1 (
    .A11(A11_11), .A12(A11_12), .A21(A11_21), .A22(A11_22), .B11(B11_11), .B12(B11_12), .B21(B11_21),
    .B22(B11_22), .R11(R11_11), .R12(R11_12), .R21(R11_21), .R22(R11_22));
  matrixAdder2x2Core matrixadder2x2core_2 (
    .A11(A12_11), .A12(A12_12), .A21(A12_21), .A22(A12_22), .B11(B12_11), .B12(B12_12), .B21(B12_21),
    .B22(B12_22), .R11(R12_11), .R12(R12_12), .R21(R12_21), .R22(R12_22));
  matrixAdder2x2Core matrixadder2x2core_3 (
    .A11(A21_11), .A12(A21_12), .A21(A21_21), .A22(A21_22), .B11(B21_11), .B12(B21_12), .B21(B21_21),
    .B22(B21_22), .R11(R21_11), .R12(R21_12), .R21(R21_21), .R22(R21_22));
  matrixAdder2x2Core matrixadder2x2core_4 (
    .A11(A22_11), .A12(A22_12), .A21(A22_21), .A22(A22_22), .B11(B22_11), .B12(B22_12), .B21(B22_21),
    .B22(B22_22), .R11(R22_11), .R12(R22_12), .R21(R22_21), .R22(R22_22));
endmodule

module core_8x8 (
  input  [63:0] A11_11,
  input  [63:0] A11_12,
  input  [63:0] A11_21,
  input  [63:0] A11_22,
  input  [63:0] A12_11,
  input  [63:0] A12_12,
  input  [63:0] A12_21,
  input  [63:0] A12_22,
  input  [63:0] A13_11,
  input  [63:0] A13_12,
  input  [63:0] A13_21,
  input  [63:0] A13_22,
  input  [63:0] A14_11,
  input  [63:0] A14_12,
  input  [63:0] A14_21,
  input  [63:0] A14_22,
  input  [63:0] B11_11,
  input  [63:0] B11_12,
  input  [63:0] B11_21,
  input  [63:0] B11_22,
  input  [63:0] B21_11,
  input  [63:0] B21_12,
  input  [63:0] B21_21,
  input  [63:0] B21_22,
  input  [63:0] B31_11,
  input  [63:0] B31_12,
  input  [63:0] B31_21,
  input  [63:0] B31_22,
  input  [63:0] B41_11,
  input  [63:0] B41_12,
  input  [63:0] B41_21,
  input  [63:0] B41_22,
  output [63:0] R11,
  output [63:0] R12,
  output [63:0] R21,
  output [63:0] R22
);

  wire [63:0] mat_mult_node_1_r11, mat_mult_node_1_r12, mat_mult_node_1_r21, mat_mult_node_1_r22,
       mat_mult_node_2_r11, mat_mult_node_2_r12, mat_mult_node_2_r21, mat_mult_node_2_r22,
       mat_mult_node_3_r11, mat_mult_node_3_r12, mat_mult_node_3_r21, mat_mult_node_3_r22,
       mat_mult_node_4_r11, mat_mult_node_4_r12, mat_mult_node_4_r21, mat_mult_node_4_r22,
       matrixadder2x2core_1_r11, matrixadder2x2core_1_r12, matrixadder2x2core_1_r21,
       matrixadder2x2core_1_r22, matrixadder2x2core_2_r11, matrixadder2x2core_2_r12,
       matrixadder2x2core_2_r21, matrixadder2x2core_2_r22;

  mat_mult_node mat_mult_node_1 (
    .A11(A11_11), .A12(A11_12), .A21(A11_21), .A22(A11_22), .B11(B11_11), .B12(B11_12), .B21(B11_21),
    .B22(B11_22), .R11(mat_mult_node_1_r11), .R12(mat_mult_node_1_r12), .R21(mat_mult_node_1_r21),
    .R22(mat_mult_node_1_r22));
  mat_mult_node mat_mult_node_2 (
    .A11(A12_11), .A12(A12_12), .A21(A12_21), .A22(A12_22), .B11(B21_11), .B12(B21_12), .B21(B21_21),
    .B22(B21_22), .R11(mat_mult_node_2_r11), .R12(mat_mult_node_2_r12), .R21(mat_mult_node_2_r21),
    .R22(mat_mult_node_2_r22));
  mat_mult_node mat_mult_node_3 (
    .A11(A13_11), .A12(A13_12), .A21(A13_21), .A22(A13_22), .B11(B31_11), .B12(B31_12), .B21(B31_21),
    .B22(B31_22), .R11(mat_mult_node_3_r11), .R12(mat_mult_node_3_r12), .R21(mat_mult_node_3_r21),
    .R22(mat_mult_node_3_r22));
  mat_mult_node mat_mult_node_4 (
    .A11(A14_11), .A12(A14_12), .A21(A14_21), .A22(A14_22), .B11(B41_11), .B12(B41_12), .B21(B41_21),
    .B22(B41_22), .R11(mat_mult_node_4_r11), .R12(mat_mult_node_4_r12), .R21(mat_mult_node_4_r21),
    .R22(mat_mult_node_4_r22));
  matrixAdder2x2Core matrixadder2x2core_1 (
    .A11(mat_mult_node_1_r11), .A12(mat_mult_node_1_r12), .A21(mat_mult_node_1_r21),
    .A22(mat_mult_node_1_r22), .B11(mat_mult_node_2_r11), .B12(mat_mult_node_2_r12),
    .B21(mat_mult_node_2_r21), .B22(mat_mult_node_2_r22), .R11(matrixadder2x2core_1_r11),
    .R12(matrixadder2x2core_1_r12), .R21(matrixadder2x2core_1_r21), .R22(matrixadder2x2core_1_r22));
  matrixAdder2x2Core matrixadder2x2core_2 (
    .A11(mat_mult_node_3_r11), .A12(mat_mult_node_3_r12), .A21(mat_mult_node_3_r21),
    .A22(mat_mult_node_3_r22), .B11(mat_mult_node_4_r11), .B12(mat_mult_node_4_r12),
    .B21(mat_mult_node_4_r21), .B22(mat_mult_node_4_r22), .R11(matrixadder2x2core_2_r11),
    .R12(matrixadder2x2core_2_r12), .R21(matrixadder2x2core_2_r21), .R22(matrixadder2x2core_2_r22));
  matrixAdder2x2Core matrixadder2x2core_3 (
    .A11(matrixadder2x2core_1_r11), .A12(matrixadder2x2core_1_r12), .A21(matrixadder2x2core_1_r21),
    .A22(matrixadder2x2core_1_r22), .B11(matrixadder2x2core_2_r11), .B12(matrixadder2x2core_2_r12),
    .B21(matrixadder2x2core_2_r21), .B22(matrixadder2x2core_2_r22), .R11(R11), .R12(R12), .R21(R21), .R22(R22));

  // Notes on the sheet:
  //   B11
  //   B21
  //   B31
  //   B41
  //   A11
  //   A12
  //   A13
  //   A14
endmodule

module assembly_8x8 (
  input  in_1,
  input  [3:0] in_2,
  input  [3:0] in_3,
  input  in_4
);

  wire clock_1_out, counter_1_carry, counter_3_carry, Delay_counter_carry;
  wire [3:0] Address_Counter_A_q, counter_2_q, counter_4_q, multiplexer_1_out;
  wire [63:0] core_8x8_1_r11, core_8x8_1_r12, core_8x8_1_r21, core_8x8_1_r22, ram_1_dout, ram_2_dout,
       ram_3_dout, ram_4_dout, ram_5_dout, ram_6_dout, ram_7_dout, ram_8_dout, ram_9_dout, ram_10_dout,
       ram_11_dout, ram_12_dout, ram_13_dout, ram_14_dout, ram_15_dout, ram_16_dout, ram_17_dout,
       ram_18_dout, ram_19_dout, ram_20_dout, ram_23_dout, ram_24_dout, ram_25_dout, ram_26_dout,
       ram_29_dout, ram_30_dout, ram_31_dout, ram_32_dout, ram_33_dout, ram_34_dout, ram_35_dout, ram_36_dout;

  Multiplexer #(.width(4)) multiplexer_1 (.in0(in_2), .in1(in_3), .out(multiplexer_1_out), .sel(in_4));
  Counter #(.max('h1), .width(2)) Delay_counter (
    .count(clock_1_out), .clk(clock_1_out), .carry(Delay_counter_carry));  // open: clr, load, up, D, Q
  Counter #(.max('h4), .width(4)) Address_Counter_A (
    .up(in_1), .count(Delay_counter_carry), .clk(clock_1_out), .D(multiplexer_1_out), .Q(Address_Counter_A_q));  // open: clr, load, carry
  RAM #(.addrWidth(4), .dataWidth(64), .\type ("nonvolatile")) ram_1 (
    .addr(Address_Counter_A_q), .oe(1'b1), .clk(clock_1_out), .dout(ram_1_dout));  // open: we, din
  RAM #(.addrWidth(4), .dataWidth(64), .\type ("nonvolatile")) ram_2 (
    .addr(Address_Counter_A_q), .oe(1'b1), .clk(clock_1_out), .dout(ram_2_dout));  // open: we, din
  RAM #(.addrWidth(4), .dataWidth(64), .\type ("nonvolatile")) ram_3 (
    .addr(Address_Counter_A_q), .oe(1'b1), .clk(clock_1_out), .dout(ram_3_dout));  // open: we, din
  RAM #(.addrWidth(4), .dataWidth(64), .\type ("nonvolatile")) ram_4 (
    .addr(Address_Counter_A_q), .oe(1'b1), .clk(clock_1_out), .dout(ram_4_dout));  // open: we, din
  Clock clock_1 (.out(clock_1_out));
  RAM #(.addrWidth(4), .dataWidth(64), .\type ("nonvolatile")) ram_5 (
    .addr(Address_Counter_A_q), .clk(clock_1_out), .dout(ram_5_dout));  // open: we, oe, din
  RAM #(.addrWidth(4), .dataWidth(64), .\type ("nonvolatile")) ram_6 (
    .addr(Address_Counter_A_q), .clk(clock_1_out), .dout(ram_6_dout));  // open: we, oe, din
  RAM #(.addrWidth(4), .dataWidth(64), .\type ("nonvolatile")) ram_7 (
    .addr(Address_Counter_A_q), .clk(clock_1_out), .dout(ram_7_dout));  // open: we, oe, din
  RAM #(.addrWidth(4), .dataWidth(64), .\type ("nonvolatile")) ram_8 (
    .addr(Address_Counter_A_q), .clk(clock_1_out), .dout(ram_8_dout));  // open: we, oe, din
  RAM #(.addrWidth(4), .dataWidth(64), .\type ("nonvolatile")) ram_9 (
    .addr(Address_Counter_A_q), .clk(clock_1_out), .dout(ram_9_dout));  // open: we, oe, din
  RAM #(.addrWidth(4), .dataWidth(64), .\type ("nonvolatile")) ram_10 (
    .addr(Address_Counter_A_q), .clk(clock_1_out), .dout(ram_10_dout));  // open: we, oe, din
  RAM #(.addrWidth(4), .dataWidth(64), .\type ("nonvolatile")) ram_11 (
    .addr(Address_Counter_A_q), .clk(clock_1_out), .dout(ram_11_dout));  // open: we, oe, din
  RAM #(.addrWidth(4), .dataWidth(64), .\type ("nonvolatile")) ram_12 (
    .addr(Address_Counter_A_q), .clk(clock_1_out), .dout(ram_12_dout));  // open: we, oe, din
  RAM #(.addrWidth(4), .dataWidth(64), .\type ("nonvolatile")) ram_13 (
    .addr(Address_Counter_A_q), .clk(clock_1_out), .dout(ram_13_dout));  // open: we, oe, din
  RAM #(.addrWidth(4), .dataWidth(64), .\type ("nonvolatile")) ram_14 (
    .addr(Address_Counter_A_q), .clk(clock_1_out), .dout(ram_14_dout));  // open: we, oe, din
  RAM #(.addrWidth(4), .dataWidth(64), .\type ("nonvolatile")) ram_15 (
    .addr(Address_Counter_A_q), .clk(clock_1_out), .dout(ram_15_dout));  // open: we, oe, din
  RAM #(.addrWidth(4), .dataWidth(64), .\type ("nonvolatile")) ram_16 (
    .addr(Address_Counter_A_q), .clk(clock_1_out), .dout(ram_16_dout));  // open: we, oe, din
  Counter #(.max('h1), .width(2)) counter_1 (
    .count(clock_1_out), .clk(clock_1_out), .carry(counter_1_carry));  // open: clr, load, up, D, Q
  Counter #(.max('h4), .width(4)) counter_2 (
    .count(counter_1_carry), .clk(clock_1_out), .Q(counter_2_q));  // open: clr, load, up, D, carry
  RAM #(.addrWidth(4), .dataWidth(64), .\type ("nonvolatile")) ram_17 (
    .addr(counter_2_q), .oe(1'b1), .clk(clock_1_out), .dout(ram_17_dout));  // open: we, din
  RAM #(.addrWidth(4), .dataWidth(64), .\type ("nonvolatile")) ram_18 (
    .addr(counter_2_q), .oe(1'b1), .clk(clock_1_out), .dout(ram_18_dout));  // open: we, din
  RAM #(.addrWidth(4), .dataWidth(64), .\type ("nonvolatile")) ram_19 (
    .addr(counter_2_q), .oe(1'b1), .clk(clock_1_out), .dout(ram_19_dout));  // open: we, din
  RAM #(.addrWidth(4), .dataWidth(64), .\type ("nonvolatile")) ram_20 (
    .addr(counter_2_q), .oe(1'b1), .clk(clock_1_out), .dout(ram_20_dout));  // open: we, din
  Counter #(.max('h1), .width(1)) counter_3 (
    .count(clock_1_out), .clk(clock_1_out), .carry(counter_3_carry));  // open: clr, load, up, D, Q
  core_8x8 core_8x8_1 (
    .A11_11(ram_1_dout), .A11_12(ram_2_dout), .A11_21(ram_3_dout), .A11_22(ram_4_dout), .A12_11(ram_5_dout),
    .A12_12(ram_6_dout), .A12_21(ram_7_dout), .A12_22(ram_8_dout), .A13_11(ram_9_dout), .A13_12(ram_10_dout),
    .A13_21(ram_11_dout), .A13_22(ram_12_dout), .A14_11(ram_13_dout), .A14_12(ram_14_dout),
    .A14_21(ram_15_dout), .A14_22(ram_16_dout), .B11_11(ram_17_dout), .B11_12(ram_18_dout),
    .B11_21(ram_19_dout), .B11_22(ram_20_dout), .B21_11(ram_23_dout), .B21_12(ram_24_dout),
    .B21_21(ram_25_dout), .B21_22(ram_26_dout), .B31_11(ram_29_dout), .B31_12(ram_30_dout),
    .B31_21(ram_31_dout), .B31_22(ram_32_dout), .B41_11(ram_33_dout), .B41_12(ram_34_dout),
    .B41_21(ram_35_dout), .B41_22(ram_36_dout), .R11(core_8x8_1_r11), .R12(core_8x8_1_r12),
    .R21(core_8x8_1_r21), .R22(core_8x8_1_r22));
  Counter #(.max('h4), .width(4)) counter_4 (
    .count(counter_3_carry), .clk(clock_1_out), .Q(counter_4_q));  // open: clr, load, up, D, carry
  ROM #(.addrWidth(4), .dataWidth(64)) rom_1 ();  // open: addr, data
  RAM #(.addrWidth(4), .dataWidth(64), .\type ("nonvolatile")) ram_21 (
    .addr(counter_4_q), .we(1'b1), .clk(clock_1_out), .din(core_8x8_1_r11));  // open: oe, dout
  RAM #(.addrWidth(4), .dataWidth(64), .\type ("nonvolatile")) ram_22 (
    .addr(counter_4_q), .we(1'b1), .clk(clock_1_out), .din(core_8x8_1_r21));  // open: oe, dout
  RAM #(.addrWidth(4), .dataWidth(64), .\type ("nonvolatile")) ram_23 (
    .addr(counter_2_q), .clk(clock_1_out), .dout(ram_23_dout));  // open: we, oe, din
  RAM #(.addrWidth(4), .dataWidth(64), .\type ("nonvolatile")) ram_24 (
    .addr(counter_2_q), .clk(clock_1_out), .dout(ram_24_dout));  // open: we, oe, din
  RAM #(.addrWidth(4), .dataWidth(64), .\type ("nonvolatile")) ram_25 (
    .addr(counter_2_q), .clk(clock_1_out), .dout(ram_25_dout));  // open: we, oe, din
  RAM #(.addrWidth(4), .dataWidth(64), .\type ("nonvolatile")) ram_26 (
    .addr(counter_2_q), .clk(clock_1_out), .dout(ram_26_dout));  // open: we, oe, din
  RAM #(.addrWidth(4), .dataWidth(64), .\type ("nonvolatile")) ram_27 (
    .addr(counter_4_q), .we(1'b1), .clk(clock_1_out), .din(core_8x8_1_r12));  // open: oe, dout
  RAM #(.addrWidth(4), .dataWidth(64), .\type ("nonvolatile")) ram_28 (
    .addr(counter_4_q), .we(1'b1), .clk(clock_1_out), .din(core_8x8_1_r22));  // open: oe, dout
  RAM #(.addrWidth(4), .dataWidth(64), .\type ("nonvolatile")) ram_29 (
    .addr(counter_2_q), .clk(clock_1_out), .dout(ram_29_dout));  // open: we, oe, din
  RAM #(.addrWidth(4), .dataWidth(64), .\type ("nonvolatile")) ram_30 (
    .addr(counter_2_q), .clk(clock_1_out), .dout(ram_30_dout));  // open: we, oe, din
  RAM #(.addrWidth(4), .dataWidth(64), .\type ("nonvolatile")) ram_31 (
    .addr(counter_2_q), .clk(clock_1_out), .dout(ram_31_dout));  // open: we, oe, din
  RAM #(.addrWidth(4), .dataWidth(64), .\type ("nonvolatile")) ram_32 (
    .addr(counter_2_q), .clk(clock_1_out), .dout(ram_32_dout));  // open: we, oe, din
  RAM #(.addrWidth(4), .dataWidth(64), .\type ("nonvolatile")) ram_33 (
    .addr(counter_2_q), .clk(clock_1_out), .dout(ram_33_dout));  // open: we, oe, din
  RAM #(.addrWidth(4), .dataWidth(64), .\type ("nonvolatile")) ram_34 (
    .addr(counter_2_q), .clk(clock_1_out), .dout(ram_34_dout));  // open: we, oe, din
  RAM #(.addrWidth(4), .dataWidth(64), .\type ("nonvolatile")) ram_35 (
    .addr(counter_2_q), .clk(clock_1_out), .dout(ram_35_dout));  // open: we, oe, din
  RAM #(.addrWidth(4), .dataWidth(64), .\type ("nonvolatile")) ram_36 (
    .addr(counter_2_q), .clk(clock_1_out), .dout(ram_36_dout));  // open: we, oe, din

  // Notes on the sheet:
  //   A11
  //   A12
  //   A13
  //   A14
  //   B11
  //   B21
  //   B31
  //   B41
endmodule

module assembly_8x8_working (
);

  wire Address_Counter_A_carry, and_1_out, and_2_out, clock_1_out, counter_1_carry, register_2_q;
  wire [3:0] adder_1_out, adder_2_out, adder_3_out, adder_4_out, Address_Counter_A_q, counter_1_q,
       register_1_q, register_3_q;
  wire [7:0] counter_2_q;
  wire [63:0] core_8x8_1_r11, core_8x8_1_r12, core_8x8_1_r21, core_8x8_1_r22, ram_1_dout, ram_2_dout,
       ram_3_dout, ram_4_dout, ram_5_dout, ram_6_dout, ram_7_dout, ram_8_dout, ram_9_dout, ram_10_dout,
       ram_11_dout, ram_12_dout, ram_13_dout, ram_14_dout, ram_15_dout, ram_16_dout, ram_17_dout,
       ram_18_dout, ram_19_dout, ram_20_dout, ram_23_dout, ram_24_dout, ram_25_dout, ram_26_dout,
       ram_29_dout, ram_30_dout, ram_31_dout, ram_32_dout, ram_33_dout, ram_34_dout, ram_35_dout, ram_36_dout;

  ROM #(.dataWidth(64)) rom_1 ();  // open: addr, data
  and and_1 (and_1_out, Address_Counter_A_carry, counter_1_carry);
  Adder #(.width(4)) adder_1 (.a(register_1_q), .b(4'b0100), .out(adder_1_out));  // open: cin, cout
  Register #(.width(4)) register_1 (.D(adder_1_out), .en(and_1_out), .clk(clock_1_out), .Q(register_1_q));  // open: clr
  // Probe on adder_2_out
  Adder #(.width(4)) adder_2 (.a(Address_Counter_A_q), .b(register_1_q), .out(adder_2_out));  // open: cin, cout
  Counter #(.max('h3), .width(4)) Address_Counter_A (
    .count(counter_1_carry), .clk(clock_1_out), .carry(Address_Counter_A_carry), .Q(Address_Counter_A_q));  // open: clr, load, up, D
  RAM #(.addrWidth(4), .dataWidth(64), .\type ("nonvolatile")) ram_1 (
    .addr(adder_2_out), .oe(1'b1), .clk(clock_1_out), .dout(ram_1_dout));  // open: we, din
  RAM #(.addrWidth(4), .dataWidth(64), .\type ("nonvolatile")) ram_2 (
    .addr(adder_2_out), .oe(1'b1), .clk(clock_1_out), .dout(ram_2_dout));  // open: we, din
  RAM #(.addrWidth(4), .dataWidth(64), .\type ("nonvolatile")) ram_3 (
    .addr(adder_2_out), .oe(1'b1), .clk(clock_1_out), .dout(ram_3_dout));  // open: we, din
  RAM #(.addrWidth(4), .dataWidth(64), .\type ("nonvolatile")) ram_4 (
    .addr(adder_2_out), .oe(1'b1), .clk(clock_1_out), .dout(ram_4_dout));  // open: we, din
  Clock clock_1 (.out(clock_1_out));
  // Probe on ram_3_dout
  // Probe on ram_2_dout
  // Probe on ram_1_dout
  // Probe on ram_4_dout
  RAM #(.addrWidth(4), .dataWidth(64), .\type ("nonvolatile")) ram_5 (
    .addr(adder_2_out), .clk(clock_1_out), .dout(ram_5_dout));  // open: we, oe, din
  RAM #(.addrWidth(4), .dataWidth(64), .\type ("nonvolatile")) ram_6 (
    .addr(adder_2_out), .clk(clock_1_out), .dout(ram_6_dout));  // open: we, oe, din
  RAM #(.addrWidth(4), .dataWidth(64), .\type ("nonvolatile")) ram_7 (
    .addr(adder_2_out), .clk(clock_1_out), .dout(ram_7_dout));  // open: we, oe, din
  RAM #(.addrWidth(4), .dataWidth(64), .\type ("nonvolatile")) ram_8 (
    .addr(adder_2_out), .clk(clock_1_out), .dout(ram_8_dout));  // open: we, oe, din
  // Probe on ram_7_dout
  // Probe on ram_6_dout
  // Probe on ram_5_dout
  // Probe on ram_8_dout
  RAM #(.addrWidth(4), .dataWidth(64), .\type ("nonvolatile")) ram_9 (
    .addr(adder_2_out), .clk(clock_1_out), .dout(ram_9_dout));  // open: we, oe, din
  RAM #(.addrWidth(4), .dataWidth(64), .\type ("nonvolatile")) ram_10 (
    .addr(adder_2_out), .clk(clock_1_out), .dout(ram_10_dout));  // open: we, oe, din
  RAM #(.addrWidth(4), .dataWidth(64), .\type ("nonvolatile")) ram_11 (
    .addr(adder_2_out), .clk(clock_1_out), .dout(ram_11_dout));  // open: we, oe, din
  RAM #(.addrWidth(4), .dataWidth(64), .\type ("nonvolatile")) ram_12 (
    .addr(adder_2_out), .clk(clock_1_out), .dout(ram_12_dout));  // open: we, oe, din
  // Probe on ram_11_dout
  // Probe on ram_10_dout
  // Probe on ram_9_dout
  // Probe on ram_12_dout
  RAM #(.addrWidth(4), .dataWidth(64), .\type ("nonvolatile")) ram_13 (
    .addr(adder_2_out), .clk(clock_1_out), .dout(ram_13_dout));  // open: we, oe, din
  RAM #(.addrWidth(4), .dataWidth(64), .\type ("nonvolatile")) ram_14 (
    .addr(adder_2_out), .clk(clock_1_out), .dout(ram_14_dout));  // open: we, oe, din
  RAM #(.addrWidth(4), .dataWidth(64), .\type ("nonvolatile")) ram_15 (
    .addr(adder_2_out), .clk(clock_1_out), .dout(ram_15_dout));  // open: we, oe, din
  RAM #(.addrWidth(4), .dataWidth(64), .\type ("nonvolatile")) ram_16 (
    .addr(adder_2_out), .clk(clock_1_out), .dout(ram_16_dout));  // open: we, oe, din
  // Probe on ram_13_dout
  // Probe on ram_16_dout
  // Probe on ram_15_dout
  // Probe on ram_14_dout
  Counter #(.max('h3), .width(4)) counter_1 (
    .clk(clock_1_out), .carry(counter_1_carry), .Q(counter_1_q));  // open: clr, load, up, count, D
  // Probe on core_8x8_1_r12
  // Probe on core_8x8_1_r21
  // Probe on core_8x8_1_r11
  // Probe on core_8x8_1_r22
  core_8x8 core_8x8_1 (
    .A11_11(ram_1_dout), .A11_12(ram_2_dout), .A11_21(ram_3_dout), .A11_22(ram_4_dout), .A12_11(ram_5_dout),
    .A12_12(ram_6_dout), .A12_21(ram_7_dout), .A12_22(ram_8_dout), .A13_11(ram_9_dout), .A13_12(ram_10_dout),
    .A13_21(ram_11_dout), .A13_22(ram_12_dout), .A14_11(ram_13_dout), .A14_12(ram_14_dout),
    .A14_21(ram_15_dout), .A14_22(ram_16_dout), .B11_11(ram_17_dout), .B11_12(ram_18_dout),
    .B11_21(ram_19_dout), .B11_22(ram_20_dout), .B21_11(ram_23_dout), .B21_12(ram_24_dout),
    .B21_21(ram_25_dout), .B21_22(ram_26_dout), .B31_11(ram_29_dout), .B31_12(ram_30_dout),
    .B31_21(ram_31_dout), .B31_22(ram_32_dout), .B41_11(ram_33_dout), .B41_12(ram_34_dout),
    .B41_21(ram_35_dout), .B41_22(ram_36_dout), .R11(core_8x8_1_r11), .R12(core_8x8_1_r12),
    .R21(core_8x8_1_r21), .R22(core_8x8_1_r22));
  RAM #(.addrWidth(4), .dataWidth(64), .\type ("nonvolatile")) ram_17 (
    .addr(adder_4_out), .oe(1'b1), .clk(clock_1_out), .dout(ram_17_dout));  // open: we, din
  RAM #(.addrWidth(4), .dataWidth(64), .\type ("nonvolatile")) ram_18 (
    .addr(adder_4_out), .oe(1'b1), .clk(clock_1_out), .dout(ram_18_dout));  // open: we, din
  RAM #(.addrWidth(4), .dataWidth(64), .\type ("nonvolatile")) ram_19 (
    .addr(adder_4_out), .oe(1'b1), .clk(clock_1_out), .dout(ram_19_dout));  // open: we, din
  RAM #(.addrWidth(4), .dataWidth(64), .\type ("nonvolatile")) ram_20 (
    .addr(adder_4_out), .oe(1'b1), .clk(clock_1_out), .dout(ram_20_dout));  // open: we, din
  Hex_Digit_Display hex_digit_display_1 ();  // open: value, dp
  and and_2 (and_2_out, Address_Counter_A_carry, counter_1_carry);
  Register #(.width(1)) register_2 (
    .D(clock_1_out), .en(clock_1_out), .clk(clock_1_out), .Q(register_2_q));  // open: clr
  Register #(.width(4)) register_3 (.D(adder_3_out), .en(and_2_out), .clk(clock_1_out), .Q(register_3_q));  // open: clr
  Adder #(.width(4)) adder_3 (.a(4'b0100), .b(register_3_q), .out(adder_3_out));  // open: cin, cout
  // Probe on ram_17_dout
  Counter counter_2 (.count(register_2_q), .clk(clock_1_out), .Q(counter_2_q));  // open: clr, load, up, D, carry
  // Probe on ram_20_dout
  // Probe on adder_4_out
  Adder #(.width(4)) adder_4 (.a(register_3_q), .b(counter_1_q), .out(adder_4_out));  // open: cin, cout
  // Probe on ram_18_dout
  // Probe on ram_19_dout
  RAM #(.dataWidth(64)) ram_21 (
    .addr(counter_2_q), .we(1'b1), .clk(clock_1_out), .din(core_8x8_1_r11));  // open: oe, dout
  RAM #(.dataWidth(64)) ram_22 (
    .addr(counter_2_q), .we(1'b1), .clk(clock_1_out), .din(core_8x8_1_r21));  // open: oe, dout
  RAM #(.addrWidth(4), .dataWidth(64), .\type ("nonvolatile")) ram_23 (
    .addr(adder_4_out), .clk(clock_1_out), .dout(ram_23_dout));  // open: we, oe, din
  RAM #(.addrWidth(4), .dataWidth(64), .\type ("nonvolatile")) ram_24 (
    .addr(adder_4_out), .clk(clock_1_out), .dout(ram_24_dout));  // open: we, oe, din
  RAM #(.addrWidth(4), .dataWidth(64), .\type ("nonvolatile")) ram_25 (
    .addr(adder_4_out), .clk(clock_1_out), .dout(ram_25_dout));  // open: we, oe, din
  RAM #(.addrWidth(4), .dataWidth(64), .\type ("nonvolatile")) ram_26 (
    .addr(adder_4_out), .clk(clock_1_out), .dout(ram_26_dout));  // open: we, oe, din
  // Probe on ram_24_dout
  // Probe on ram_23_dout
  RAM #(.dataWidth(64)) ram_27 (
    .addr(counter_2_q), .we(1'b1), .clk(clock_1_out), .din(core_8x8_1_r12));  // open: oe, dout
  RAM #(.dataWidth(64)) ram_28 (
    .addr(counter_2_q), .we(1'b1), .clk(clock_1_out), .din(core_8x8_1_r22));  // open: oe, dout
  // Probe on ram_25_dout
  // Probe on ram_26_dout
  RAM #(.addrWidth(4), .dataWidth(64), .\type ("nonvolatile")) ram_29 (
    .addr(adder_4_out), .clk(clock_1_out), .dout(ram_29_dout));  // open: we, oe, din
  RAM #(.addrWidth(4), .dataWidth(64), .\type ("nonvolatile")) ram_30 (
    .addr(adder_4_out), .clk(clock_1_out), .dout(ram_30_dout));  // open: we, oe, din
  RAM #(.addrWidth(4), .dataWidth(64), .\type ("nonvolatile")) ram_31 (
    .addr(adder_4_out), .clk(clock_1_out), .dout(ram_31_dout));  // open: we, oe, din
  RAM #(.addrWidth(4), .dataWidth(64), .\type ("nonvolatile")) ram_32 (
    .addr(adder_4_out), .clk(clock_1_out), .dout(ram_32_dout));  // open: we, oe, din
  // Probe on ram_29_dout
  // Probe on ram_30_dout
  // Probe on ram_32_dout
  // Probe on ram_31_dout
  RAM #(.addrWidth(4), .dataWidth(64), .\type ("nonvolatile")) ram_33 (
    .addr(adder_4_out), .clk(clock_1_out), .dout(ram_33_dout));  // open: we, oe, din
  RAM #(.addrWidth(4), .dataWidth(64), .\type ("nonvolatile")) ram_34 (
    .addr(adder_4_out), .clk(clock_1_out), .dout(ram_34_dout));  // open: we, oe, din
  RAM #(.addrWidth(4), .dataWidth(64), .\type ("nonvolatile")) ram_35 (
    .addr(adder_4_out), .clk(clock_1_out), .dout(ram_35_dout));  // open: we, oe, din
  RAM #(.addrWidth(4), .dataWidth(64), .\type ("nonvolatile")) ram_36 (
    .addr(adder_4_out), .clk(clock_1_out), .dout(ram_36_dout));  // open: we, oe, din
  // Probe on ram_33_dout
  // Probe on ram_35_dout
  // Probe on ram_34_dout
  // Probe on ram_36_dout

  // Notes on the sheet:
  //   A11
  //   A12
  //   A13
  //   A14
  //   B11
  //   B21
  //   B31
  //   B41
endmodule

module instruction_splitter (
  input  WE,
  input  CLOCK,
  input  [23:0] instruction,
  output [3:0] FLG,
  output [3:0] OPCODE,
  output [7:0] ADD_A,
  output [7:0] ADD_B
);

  Register #(.width(24)) register_1 (
    .D(instruction), .en(WE), .clk(CLOCK), .Q({FLG, OPCODE, ADD_A, ADD_B}));  // open: clr
endmodule

module Assembly_16x16_leaving_in_mid (
);

  wire clock_1_out, undriven;
  wire [3:0] instruction_splitter_1_p1, instruction_splitter_1_p2, OP_CODE_REGISTER_q;
  wire [7:0] adder_1_out, adder_2_out, adder_3_out, adder_4_out, adder_5_out, adder_6_out, adder_7_out,
       adder_8_out, counter_1_q, counter_2_q, instruction_splitter_1_p3, instruction_splitter_1_p4, MAR_A_q,
       MAR_B_q, MAR_Z_q, register_1_q;
  wire [23:0] INST_RAM_dout, MBR_Z_q;
  wire [63:0] core_8x8_1_r11, core_8x8_1_r12, core_8x8_1_r21, core_8x8_1_r22, MBR_A_q, MBR_B_q, ram_1_dout,
       ram_2_dout, ram_3_dout, ram_4_dout, ram_5_dout, ram_6_dout, RAM_A_dout, RAM_B_dout, register_2_q,
       register_3_q, register_4_q, register_5_q, register_6_q, register_7_q, register_8_q, register_9_q,
       register_10_q, register_11_q, register_12_q, register_13_q, register_14_q, register_15_q,
       register_16_q, register_17_q, register_18_q, register_19_q, register_20_q, register_21_q,
       register_22_q, register_23_q, register_24_q, register_25_q, register_26_q, register_27_q,
       register_28_q, register_29_q, register_30_q, register_31_q, register_32_q, register_33_q,
       register_34_q, register_35_q, register_36_q, register_41_q, register_42_q, register_43_q,
       register_44_q, register_45_q, register_46_q, register_47_q, register_48_q, register_49_q,
       register_50_q, register_51_q, register_52_q, register_53_q, register_54_q, register_55_q,
       register_56_q, register_57_q, register_58_q, register_59_q, register_60_q, register_61_q,
       register_62_q, register_63_q, register_64_q, register_65_q, register_66_q, register_67_q,
       register_68_q, register_69_q, register_70_q, register_71_q, register_72_q, register_73_q,
       register_74_q, register_75_q;

  Clock clock_1 (.out(clock_1_out));
  Adder adder_1 (.a(register_1_q), .b(8'h4), .out(adder_1_out));  // open: cin, cout
  Register register_1 (.D(adder_1_out), .en(clock_1_out), .clk(clock_1_out), .Q(register_1_q));  // open: clr
  Adder adder_2 (.a(adder_5_out), .b(8'h1), .out(adder_2_out));  // open: cin, cout
  Adder adder_3 (.a(adder_2_out), .b(8'h1), .out(adder_3_out));  // open: cin, cout
  Adder adder_4 (.a(adder_3_out), .b(8'h1), .out(adder_4_out));  // open: cin, cout
  Adder adder_5 (.a(register_1_q), .b(MAR_A_q), .out(adder_5_out));  // open: cin, cout
  RAM #(.dataWidth(64)) RAM_A (.addr(adder_5_out), .clk(clock_1_out), .dout(RAM_A_dout));  // open: we, oe, din
  RAM #(.dataWidth(64)) ram_1 (.addr(adder_2_out), .clk(clock_1_out), .dout(ram_1_dout));  // open: we, oe, din
  RAM #(.dataWidth(64)) ram_2 (.addr(adder_3_out), .clk(clock_1_out), .dout(ram_2_dout));  // open: we, oe, din
  RAM #(.dataWidth(64)) ram_3 (.addr(adder_4_out), .clk(clock_1_out), .dout(ram_3_dout));  // open: we, oe, din
  Register #(.width(64)) MBR_A (.D(RAM_A_dout), .clk(clock_1_out), .Q(MBR_A_q));  // open: en, clr
  Register #(.width(64)) register_2 (.D(ram_1_dout), .clk(clock_1_out), .Q(register_2_q));  // open: en, clr
  Register #(.width(64)) register_3 (.D(ram_2_dout), .clk(clock_1_out), .Q(register_3_q));  // open: en, clr
  Register #(.width(64)) register_4 (.D(ram_3_dout), .clk(clock_1_out), .Q(register_4_q));  // open: en, clr
  Register #(.width(64)) register_5 (.D(MBR_A_q), .clk(clock_1_out), .Q(register_5_q));  // open: en, clr
  Register #(.width(64)) register_6 (.D(MBR_A_q), .clk(clock_1_out), .Q(register_6_q));  // open: en, clr
  Register #(.width(64)) register_7 (.D(MBR_A_q), .clk(clock_1_out), .Q(register_7_q));  // open: en, clr
  Register #(.width(64)) register_8 (.D(MBR_A_q), .clk(clock_1_out), .Q(register_8_q));  // open: en, clr
  Register #(.width(64)) register_9 (.D(MBR_A_q), .clk(clock_1_out), .Q(register_9_q));  // open: en, clr
  Register #(.width(64)) register_10 (.D(MBR_A_q), .clk(clock_1_out), .Q(register_10_q));  // open: en, clr
  Register #(.width(64)) register_11 (.D(MBR_A_q), .clk(clock_1_out), .Q(register_11_q));  // open: en, clr
  Register #(.width(64)) register_12 (.D(MBR_A_q), .clk(clock_1_out), .Q(register_12_q));  // open: en, clr
  RAM #(.dataWidth(64)) SYST_RAM (.clk(clock_1_out));  // open: addr, we, oe, din, dout
  Register #(.width(64)) register_13 (.D(register_2_q), .clk(clock_1_out), .Q(register_13_q));  // open: en, clr
  Register #(.width(64)) register_14 (.D(register_2_q), .clk(clock_1_out), .Q(register_14_q));  // open: en, clr
  Register #(.width(64)) register_15 (.D(register_2_q), .clk(clock_1_out), .Q(register_15_q));  // open: en, clr
  Register #(.width(64)) register_16 (.D(register_2_q), .clk(clock_1_out), .Q(register_16_q));  // open: en, clr
  Register #(.width(64)) register_17 (.D(register_2_q), .clk(clock_1_out), .Q(register_17_q));  // open: en, clr
  Register #(.width(64)) register_18 (.D(register_2_q), .clk(clock_1_out), .Q(register_18_q));  // open: en, clr
  Register #(.width(64)) register_19 (.D(register_2_q), .clk(clock_1_out), .Q(register_19_q));  // open: en, clr
  Register #(.width(64)) register_20 (.D(register_2_q), .clk(clock_1_out), .Q(register_20_q));  // open: en, clr
  Register #(.width(64)) register_21 (.D(register_3_q), .clk(clock_1_out), .Q(register_21_q));  // open: en, clr
  Register #(.width(64)) register_22 (.D(register_3_q), .clk(clock_1_out), .Q(register_22_q));  // open: en, clr
  Register #(.width(64)) register_23 (.D(register_3_q), .clk(clock_1_out), .Q(register_23_q));  // open: en, clr
  Register #(.width(64)) register_24 (.D(register_3_q), .clk(clock_1_out), .Q(register_24_q));  // open: en, clr
  Register #(.width(64)) register_25 (.D(register_3_q), .clk(clock_1_out), .Q(register_25_q));  // open: en, clr
  Register #(.width(64)) register_26 (.D(register_3_q), .clk(clock_1_out), .Q(register_26_q));  // open: en, clr
  Register #(.width(64)) register_27 (.D(register_3_q), .clk(clock_1_out), .Q(register_27_q));  // open: en, clr
  Register #(.width(64)) register_28 (.D(register_3_q), .clk(clock_1_out), .Q(register_28_q));  // open: en, clr
  Register #(.width(64)) register_29 (.clk(clock_1_out), .Q(register_29_q));  // open: D, en, clr
  Register #(.width(64)) register_30 (.clk(clock_1_out), .Q(register_30_q));  // open: D, en, clr
  Register #(.width(64)) register_31 (.D(register_4_q), .clk(clock_1_out), .Q(register_31_q));  // open: en, clr
  Register #(.width(64)) register_32 (.D(register_4_q), .clk(clock_1_out), .Q(register_32_q));  // open: en, clr
  Register #(.width(64)) register_33 (.D(register_4_q), .clk(clock_1_out), .Q(register_33_q));  // open: en, clr
  Register #(.width(64)) register_34 (.D(register_4_q), .clk(clock_1_out), .Q(register_34_q));  // open: en, clr
  Register #(.width(64)) register_35 (.D(register_4_q), .clk(clock_1_out), .Q(register_35_q));  // open: en, clr
  Register #(.width(64)) register_36 (.D(register_4_q), .clk(clock_1_out), .Q(register_36_q));  // open: en, clr
  Counter counter_1 (.clk(clock_1_out), .Q(counter_1_q));  // open: clr, load, up, count, D, carry
  Register MAR_Z (.D(counter_1_q), .clk(clock_1_out), .Q(MAR_Z_q));  // open: en, clr
  RAM #(.dataWidth(24)) INST_RAM (.addr(MAR_Z_q), .clk(clock_1_out), .dout(INST_RAM_dout));  // open: we, oe, din
  core_8x8 core_8x8_1 (
    .A11_11(register_5_q), .A11_12(register_13_q), .A11_21(register_21_q), .A11_22(register_29_q),
    .A12_11(register_6_q), .A12_12(register_14_q), .A12_21(register_22_q), .A12_22(register_30_q),
    .A13_11(register_7_q), .A13_12(register_15_q), .A13_21(register_23_q), .A13_22(register_36_q),
    .A14_11(register_8_q), .A14_12(register_16_q), .A14_21(register_24_q), .A14_22(register_31_q),
    .B11_11(register_9_q), .B11_12(register_17_q), .B11_21(register_25_q), .B11_22(register_32_q),
    .B21_11(register_10_q), .B21_12(register_18_q), .B21_21(register_26_q), .B21_22(register_33_q),
    .B31_11(register_11_q), .B31_12(register_19_q), .B31_21(register_27_q), .B31_22(register_34_q),
    .B41_11(register_12_q), .B41_12(register_20_q), .B41_21(register_28_q), .B41_22(register_35_q),
    .R11(core_8x8_1_r11), .R12(core_8x8_1_r12), .R21(core_8x8_1_r21), .R22(core_8x8_1_r22));
  Register #(.width(64)) register_37 (.D(core_8x8_1_r11), .clk(undriven));  // open: en, Q, clr
  Register #(.width(64)) register_38 (.D(core_8x8_1_r12), .clk(undriven));  // open: en, Q, clr
  Register #(.width(64)) register_39 (.D(core_8x8_1_r21), .clk(undriven));  // open: en, Q, clr
  Register #(.width(64)) register_40 (.D(core_8x8_1_r22), .clk(undriven));  // open: en, Q, clr
  Register #(.width(24)) MBR_Z (.D(INST_RAM_dout), .clk(clock_1_out), .Q(MBR_Z_q));  // open: en, clr
  // instruction_splitter instruction_splitter_1: pin names not known; wires that end beside it: instruction_splitter_1_p1, instruction_splitter_1_p2, instruction_splitter_1_p3, instruction_splitter_1_p4
  Register MAR_A (.D(instruction_splitter_1_p3), .clk(clock_1_out), .Q(MAR_A_q));  // open: en, clr
  Register MAR_B (.D(instruction_splitter_1_p4), .clk(clock_1_out), .Q(MAR_B_q));  // open: en, clr
  Register #(.width(64)) register_41 (.D(MBR_B_q), .clk(clock_1_out), .Q(register_41_q));  // open: en, clr
  Register #(.width(64)) register_42 (.D(MBR_B_q), .clk(clock_1_out), .Q(register_42_q));  // open: en, clr
  Register #(.width(64)) register_43 (.D(MBR_B_q), .clk(clock_1_out), .Q(register_43_q));  // open: en, clr
  Register #(.width(64)) register_44 (.D(MBR_B_q), .clk(clock_1_out), .Q(register_44_q));  // open: en, clr
  Register #(.width(64)) register_45 (.D(MBR_B_q), .clk(clock_1_out), .Q(register_45_q));  // open: en, clr
  Register #(.width(64)) register_46 (.D(MBR_B_q), .clk(clock_1_out), .Q(register_46_q));  // open: en, clr
  Register #(.width(64)) register_47 (.D(MBR_B_q), .clk(clock_1_out), .Q(register_47_q));  // open: en, clr
  Register #(.width(64)) register_48 (.D(MBR_B_q), .clk(clock_1_out), .Q(register_48_q));  // open: en, clr
  Register #(.width(64)) register_49 (.D(register_74_q), .clk(clock_1_out), .Q(register_49_q));  // open: en, clr
  Register #(.width(64)) register_50 (.D(register_74_q), .clk(clock_1_out), .Q(register_50_q));  // open: en, clr
  Register #(.width(64)) register_51 (.D(register_74_q), .clk(clock_1_out), .Q(register_51_q));  // open: en, clr
  Register #(.width(64)) register_52 (.D(register_74_q), .clk(clock_1_out), .Q(register_52_q));  // open: en, clr
  Register #(.width(64)) register_53 (.D(register_74_q), .clk(clock_1_out), .Q(register_53_q));  // open: en, clr
  Register #(.width(64)) register_54 (.D(register_74_q), .clk(clock_1_out), .Q(register_54_q));  // open: en, clr
  Register #(.width(64)) register_55 (.D(register_74_q), .clk(clock_1_out), .Q(register_55_q));  // open: en, clr
  Register #(.width(64)) register_56 (.D(register_74_q), .clk(clock_1_out), .Q(register_56_q));  // open: en, clr
  Register #(.width(64)) register_57 (.D(register_73_q), .clk(clock_1_out), .Q(register_57_q));  // open: en, clr
  Register #(.width(64)) register_58 (.D(register_73_q), .clk(clock_1_out), .Q(register_58_q));  // open: en, clr
  Register #(.width(64)) register_59 (.D(register_73_q), .clk(clock_1_out), .Q(register_59_q));  // open: en, clr
  Register #(.width(64)) register_60 (.D(register_73_q), .clk(clock_1_out), .Q(register_60_q));  // open: en, clr
  Register #(.width(64)) register_61 (.D(register_73_q), .clk(clock_1_out), .Q(register_61_q));  // open: en, clr
  Register #(.width(64)) register_62 (.D(register_73_q), .clk(clock_1_out), .Q(register_62_q));  // open: en, clr
  Register #(.width(64)) register_63 (.D(register_73_q), .clk(clock_1_out), .Q(register_63_q));  // open: en, clr
  Register #(.width(64)) register_64 (.D(register_73_q), .clk(clock_1_out), .Q(register_64_q));  // open: en, clr
  Register #(.width(64)) register_65 (.D(register_75_q), .clk(clock_1_out), .Q(register_65_q));  // open: en, clr
  Register #(.width(64)) register_66 (.D(register_75_q), .clk(clock_1_out), .Q(register_66_q));  // open: en, clr
  Register #(.width(64)) register_67 (.D(register_75_q), .clk(clock_1_out), .Q(register_67_q));  // open: en, clr
  Register #(.width(64)) register_68 (.D(register_75_q), .clk(clock_1_out), .Q(register_68_q));  // open: en, clr
  Register #(.width(64)) register_69 (.D(register_75_q), .clk(clock_1_out), .Q(register_69_q));  // open: en, clr
  Register #(.width(64)) register_70 (.D(register_75_q), .clk(clock_1_out), .Q(register_70_q));  // open: en, clr
  Register #(.width(64)) register_71 (.D(register_75_q), .clk(clock_1_out), .Q(register_71_q));  // open: en, clr
  Register #(.width(64)) register_72 (.D(register_75_q), .clk(clock_1_out), .Q(register_72_q));  // open: en, clr
  Adder adder_6 (.a(adder_7_out), .b(8'h1), .out(adder_6_out));  // open: cin, cout
  Adder adder_7 (.a(MAR_B_q), .b(8'h1), .out(adder_7_out));  // open: cin, cout
  Adder adder_8 (.a(adder_6_out), .b(8'h1), .out(adder_8_out));  // open: cin, cout
  Register #(.width(4)) OP_CODE_REGISTER (
    .D(instruction_splitter_1_p2), .clk(clock_1_out), .Q(OP_CODE_REGISTER_q));  // open: en, clr
  RAM #(.dataWidth(64)) RAM_B (.addr(MAR_B_q), .clk(clock_1_out), .dout(RAM_B_dout));  // open: we, oe, din
  RAM #(.dataWidth(64)) ram_4 (.addr(adder_7_out), .clk(clock_1_out), .dout(ram_4_dout));  // open: we, oe, din
  RAM #(.dataWidth(64)) ram_5 (.addr(adder_6_out), .clk(clock_1_out), .dout(ram_5_dout));  // open: we, oe, din
  RAM #(.dataWidth(64)) ram_6 (.addr(adder_8_out), .clk(clock_1_out), .dout(ram_6_dout));  // open: we, oe, din
  Register #(.width(64)) MBR_B (.D(RAM_B_dout), .clk(clock_1_out), .Q(MBR_B_q));  // open: en, clr
  Register #(.width(64)) register_73 (.D(ram_5_dout), .clk(clock_1_out), .Q(register_73_q));  // open: en, clr
  Register #(.width(64)) register_74 (.D(ram_4_dout), .clk(clock_1_out), .Q(register_74_q));  // open: en, clr
  Register #(.width(64)) register_75 (.D(ram_6_dout), .clk(clock_1_out), .Q(register_75_q));  // open: en, clr
  ROM #(.addrWidth(16), .dataWidth(64)) rom_1 (.addr({instruction_splitter_1_p1, OP_CODE_REGISTER_q, counter_2_q}));  // open: data
  Counter counter_2 (.clk(clock_1_out), .Q(counter_2_q));  // open: clr, load, up, count, D, carry
endmodule

module core_16x16 (
  input  [63:0] A11_11,
  input  [63:0] A11_12,
  input  [63:0] A11_21,
  input  [63:0] A11_22,
  input  [63:0] A12_11,
  input  [63:0] A12_12,
  input  [63:0] A12_21,
  input  [63:0] A12_22,
  input  [63:0] A13_11,
  input  [63:0] A13_12,
  input  [63:0] A13_21,
  input  [63:0] A13_22,
  input  [63:0] A14_11,
  input  [63:0] A14_12,
  input  [63:0] A14_21,
  input  [63:0] A14_22,
  input  [63:0] A15_11,
  input  [63:0] A15_12,
  input  [63:0] A15_21,
  input  [63:0] A15_22,
  input  [63:0] A16_11,
  input  [63:0] A16_12,
  input  [63:0] A16_21,
  input  [63:0] A16_22,
  input  [63:0] A17_11,
  input  [63:0] A17_12,
  input  [63:0] A17_21,
  input  [63:0] A17_22,
  input  [63:0] A18_11,
  input  [63:0] A18_12,
  input  [63:0] A18_21,
  input  [63:0] A18_22,
  input  [63:0] B11_11,
  input  [63:0] B11_12,
  input  [63:0] B11_21,
  input  [63:0] B11_22,
  input  [63:0] B21_11,
  input  [63:0] B21_12,
  input  [63:0] B21_21,
  input  [63:0] B21_22,
  input  [63:0] B31_11,
  input  [63:0] B31_12,
  input  [63:0] B31_21,
  input  [63:0] B31_22,
  input  [63:0] B41_11,
  input  [63:0] B41_12,
  input  [63:0] B41_21,
  input  [63:0] B41_22,
  input  [63:0] B51_11,
  input  [63:0] B51_12,
  input  [63:0] B51_21,
  input  [63:0] B51_22,
  input  [63:0] B61_11,
  input  [63:0] B61_12,
  input  [63:0] B61_21,
  input  [63:0] B61_22,
  input  [63:0] B71_11,
  input  [63:0] B71_12,
  input  [63:0] B71_21,
  input  [63:0] B71_22,
  input  [63:0] B81_11,
  input  [63:0] B81_12,
  input  [63:0] B81_21,
  input  [63:0] B81_22,
  output [63:0] R11,
  output [63:0] R12,
  output [63:0] R21,
  output [63:0] R22
);

  wire [63:0] mat_mult_node_1_r11, mat_mult_node_1_r12, mat_mult_node_1_r21, mat_mult_node_1_r22,
       mat_mult_node_2_r11, mat_mult_node_2_r12, mat_mult_node_2_r21, mat_mult_node_2_r22,
       mat_mult_node_3_r11, mat_mult_node_3_r12, mat_mult_node_3_r21, mat_mult_node_3_r22,
       mat_mult_node_4_r11, mat_mult_node_4_r12, mat_mult_node_4_r21, mat_mult_node_4_r22,
       mat_mult_node_5_r11, mat_mult_node_5_r12, mat_mult_node_5_r21, mat_mult_node_5_r22,
       mat_mult_node_6_r11, mat_mult_node_6_r12, mat_mult_node_6_r21, mat_mult_node_6_r22,
       mat_mult_node_7_r11, mat_mult_node_7_r12, mat_mult_node_7_r21, mat_mult_node_7_r22,
       mat_mult_node_8_r11, mat_mult_node_8_r12, mat_mult_node_8_r21, mat_mult_node_8_r22,
       matrixadder2x2core_1_r11, matrixadder2x2core_1_r12, matrixadder2x2core_1_r21,
       matrixadder2x2core_1_r22, matrixadder2x2core_2_r11, matrixadder2x2core_2_r12,
       matrixadder2x2core_2_r21, matrixadder2x2core_2_r22, matrixadder2x2core_3_r11,
       matrixadder2x2core_3_r12, matrixadder2x2core_3_r21, matrixadder2x2core_3_r22,
       matrixadder2x2core_4_r11, matrixadder2x2core_4_r12, matrixadder2x2core_4_r21,
       matrixadder2x2core_4_r22, matrixadder2x2core_5_r11, matrixadder2x2core_5_r12,
       matrixadder2x2core_5_r21, matrixadder2x2core_5_r22, matrixadder2x2core_6_r11,
       matrixadder2x2core_6_r12, matrixadder2x2core_6_r21, matrixadder2x2core_6_r22;

  mat_mult_node mat_mult_node_1 (
    .A11(A11_11), .A12(A11_12), .A21(A11_21), .A22(A11_22), .B11(B11_11), .B12(B11_12), .B21(B11_21),
    .B22(B11_22), .R11(mat_mult_node_1_r11), .R12(mat_mult_node_1_r12), .R21(mat_mult_node_1_r21),
    .R22(mat_mult_node_1_r22));
  mat_mult_node mat_mult_node_2 (
    .A11(A12_11), .A12(A12_12), .A21(A12_21), .A22(A12_22), .B11(B21_11), .B12(B21_12), .B21(B21_21),
    .B22(B21_22), .R11(mat_mult_node_2_r11), .R12(mat_mult_node_2_r12), .R21(mat_mult_node_2_r21),
    .R22(mat_mult_node_2_r22));
  mat_mult_node mat_mult_node_3 (
    .A11(A13_11), .A12(A13_12), .A21(A13_21), .A22(A13_22), .B11(B31_11), .B12(B31_12), .B21(B31_21),
    .B22(B31_22), .R11(mat_mult_node_3_r11), .R12(mat_mult_node_3_r12), .R21(mat_mult_node_3_r21),
    .R22(mat_mult_node_3_r22));
  mat_mult_node mat_mult_node_4 (
    .A11(A14_11), .A12(A14_12), .A21(A14_21), .A22(A14_22), .B11(B41_11), .B12(B41_12), .B21(B41_21),
    .B22(B41_22), .R11(mat_mult_node_4_r11), .R12(mat_mult_node_4_r12), .R21(mat_mult_node_4_r21),
    .R22(mat_mult_node_4_r22));
  matrixAdder2x2Core matrixadder2x2core_1 (
    .A11(mat_mult_node_1_r11), .A12(mat_mult_node_1_r12), .A21(mat_mult_node_1_r21),
    .A22(mat_mult_node_1_r22), .B11(mat_mult_node_2_r11), .B12(mat_mult_node_2_r12),
    .B21(mat_mult_node_2_r21), .B22(mat_mult_node_2_r22), .R11(matrixadder2x2core_1_r11),
    .R12(matrixadder2x2core_1_r12), .R21(matrixadder2x2core_1_r21), .R22(matrixadder2x2core_1_r22));
  matrixAdder2x2Core matrixadder2x2core_2 (
    .A11(mat_mult_node_3_r11), .A12(mat_mult_node_3_r12), .A21(mat_mult_node_3_r21),
    .A22(mat_mult_node_3_r22), .B11(mat_mult_node_4_r11), .B12(mat_mult_node_4_r12),
    .B21(mat_mult_node_4_r21), .B22(mat_mult_node_4_r22), .R11(matrixadder2x2core_2_r11),
    .R12(matrixadder2x2core_2_r12), .R21(matrixadder2x2core_2_r21), .R22(matrixadder2x2core_2_r22));
  matrixAdder2x2Core matrixadder2x2core_3 (
    .A11(matrixadder2x2core_1_r11), .A12(matrixadder2x2core_1_r12), .A21(matrixadder2x2core_1_r21),
    .A22(matrixadder2x2core_1_r22), .B11(matrixadder2x2core_2_r11), .B12(matrixadder2x2core_2_r12),
    .B21(matrixadder2x2core_2_r21), .B22(matrixadder2x2core_2_r22), .R11(matrixadder2x2core_3_r11),
    .R12(matrixadder2x2core_3_r12), .R21(matrixadder2x2core_3_r21), .R22(matrixadder2x2core_3_r22));
  mat_mult_node mat_mult_node_5 (
    .A11(A15_11), .A12(A15_12), .A21(A15_21), .A22(A15_22), .B11(B51_11), .B12(B51_12), .B21(B51_21),
    .B22(B51_22), .R11(mat_mult_node_5_r11), .R12(mat_mult_node_5_r12), .R21(mat_mult_node_5_r21),
    .R22(mat_mult_node_5_r22));
  mat_mult_node mat_mult_node_6 (
    .A11(A16_11), .A12(A16_12), .A21(A16_21), .A22(A16_22), .B11(B61_11), .B12(B61_12), .B21(B61_21),
    .B22(B61_22), .R11(mat_mult_node_6_r11), .R12(mat_mult_node_6_r12), .R21(mat_mult_node_6_r21),
    .R22(mat_mult_node_6_r22));
  mat_mult_node mat_mult_node_7 (
    .A11(A17_11), .A12(A17_12), .A21(A17_21), .A22(A17_22), .B11(B71_11), .B12(B71_12), .B21(B71_21),
    .B22(B71_22), .R11(mat_mult_node_7_r11), .R12(mat_mult_node_7_r12), .R21(mat_mult_node_7_r21),
    .R22(mat_mult_node_7_r22));
  mat_mult_node mat_mult_node_8 (
    .A11(A18_11), .A12(A18_12), .A21(A18_21), .A22(A18_22), .B11(B81_11), .B12(B81_12), .B21(B81_21),
    .B22(B81_22), .R11(mat_mult_node_8_r11), .R12(mat_mult_node_8_r12), .R21(mat_mult_node_8_r21),
    .R22(mat_mult_node_8_r22));
  matrixAdder2x2Core matrixadder2x2core_4 (
    .A11(mat_mult_node_5_r11), .A12(mat_mult_node_5_r12), .A21(mat_mult_node_5_r21),
    .A22(mat_mult_node_5_r22), .B11(mat_mult_node_6_r11), .B12(mat_mult_node_6_r12),
    .B21(mat_mult_node_6_r21), .B22(mat_mult_node_6_r22), .R11(matrixadder2x2core_4_r11),
    .R12(matrixadder2x2core_4_r12), .R21(matrixadder2x2core_4_r21), .R22(matrixadder2x2core_4_r22));
  matrixAdder2x2Core matrixadder2x2core_5 (
    .A11(mat_mult_node_7_r11), .A12(mat_mult_node_7_r12), .A21(mat_mult_node_7_r21),
    .A22(mat_mult_node_7_r22), .B11(mat_mult_node_8_r11), .B12(mat_mult_node_8_r12),
    .B21(mat_mult_node_8_r21), .B22(mat_mult_node_8_r22), .R11(matrixadder2x2core_5_r11),
    .R12(matrixadder2x2core_5_r12), .R21(matrixadder2x2core_5_r21), .R22(matrixadder2x2core_5_r22));
  matrixAdder2x2Core matrixadder2x2core_6 (
    .A11(matrixadder2x2core_4_r11), .A12(matrixadder2x2core_4_r12), .A21(matrixadder2x2core_4_r21),
    .A22(matrixadder2x2core_4_r22), .B11(matrixadder2x2core_5_r11), .B12(matrixadder2x2core_5_r12),
    .B21(matrixadder2x2core_5_r21), .B22(matrixadder2x2core_5_r22), .R11(matrixadder2x2core_6_r11),
    .R12(matrixadder2x2core_6_r12), .R21(matrixadder2x2core_6_r21), .R22(matrixadder2x2core_6_r22));
  matrixAdder2x2Core matrixadder2x2core_7 (
    .A11(matrixadder2x2core_3_r11), .A12(matrixadder2x2core_3_r12), .A21(matrixadder2x2core_3_r21),
    .A22(matrixadder2x2core_3_r22), .B11(matrixadder2x2core_6_r11), .B12(matrixadder2x2core_6_r12),
    .B21(matrixadder2x2core_6_r21), .B22(matrixadder2x2core_6_r22), .R11(R11), .R12(R12), .R21(R21), .R22(R22));

  // Notes on the sheet:
  //   A15
  //   A16
  //   A17
  //   A18
  //   A11
  //   A12
  //   A13
  //   A14
  //   B11
  //   B21
  //   B31
  //   B41
  //   B51
  //   B61
  //   B71
  //   B81
endmodule

module decoder_3bit (
  input  A,
  input  B,
  input  C,
  output ZERO,
  output ONE,
  output TWO,
  output THREE,
  output FOUR,
  output FIVE,
  output SIX,
  output SEVEN
);

  wire not_1_out, not_2_out, not_3_out;

  not not_1 (not_1_out, A);
  not not_2 (not_2_out, B);
  not not_3 (not_3_out, C);
  and and_1 (ZERO, not_1_out, not_2_out, not_3_out);
  and and_2 (ONE, not_1_out, not_2_out, C);
  and and_3 (TWO, not_1_out, B, not_3_out);
  and and_4 (THREE, not_1_out, B, C);
  and and_5 (FOUR, A, not_2_out, not_3_out);
  and and_6 (FIVE, A, not_2_out, C);
  and and_7 (SIX, A, B, not_3_out);
  and and_8 (SEVEN, A, B, C);
endmodule

module Assembly_latest_final_pakka_leavingagain (
);

  wire [63:0] MBR_A_q, ram_1_dout, RAM_A_dout, RAM_B_dout, register_1_q, register_2_q, register_3_q,
       register_4_q, register_5_q, register_6_q, register_7_q, register_8_q, register_9_q, register_10_q,
       register_11_q, register_12_q, register_13_q, register_14_q, register_15_q, register_16_q,
       register_17_q, register_22_q, register_23_q, register_24_q, register_25_q, register_26_q,
       register_27_q, register_28_q, register_29_q, register_30_q, register_31_q, register_32_q,
       register_33_q, register_34_q, register_35_q, register_36_q, register_37_q;

  RAM #(.dataWidth(64)) RAM_A (.dout(RAM_A_dout));  // open: addr, we, oe, clk, din
  RAM #(.dataWidth(64)) ram_1 (.dout(ram_1_dout));  // open: addr, we, oe, clk, din
  Register #(.width(64)) MBR_A (.D(RAM_A_dout), .Q(MBR_A_q));  // open: en, clk, clr
  Register #(.width(64)) register_1 (.D(ram_1_dout), .Q(register_1_q));  // open: en, clk, clr
  Register #(.width(64)) register_2 (.D(MBR_A_q), .Q(register_2_q));  // open: en, clk, clr
  Register #(.width(64)) register_3 (.D(MBR_A_q), .Q(register_3_q));  // open: en, clk, clr
  Register #(.width(64)) register_4 (.D(MBR_A_q), .Q(register_4_q));  // open: en, clk, clr
  Register #(.width(64)) register_5 (.D(MBR_A_q), .Q(register_5_q));  // open: en, clk, clr
  Register #(.width(64)) register_6 (.D(MBR_A_q), .Q(register_6_q));  // open: en, clk, clr
  Register #(.width(64)) register_7 (.D(MBR_A_q), .Q(register_7_q));  // open: en, clk, clr
  Register #(.width(64)) register_8 (.D(MBR_A_q), .Q(register_8_q));  // open: en, clk, clr
  Register #(.width(64)) register_9 (.D(MBR_A_q), .Q(register_9_q));  // open: en, clk, clr
  Register #(.width(64)) register_10 (.D(register_1_q), .Q(register_10_q));  // open: en, clk, clr
  Register #(.width(64)) register_11 (.D(register_1_q), .Q(register_11_q));  // open: en, clk, clr
  Register #(.width(64)) register_12 (.D(register_1_q), .Q(register_12_q));  // open: en, clk, clr
  Register #(.width(64)) register_13 (.D(register_1_q), .Q(register_13_q));  // open: en, clk, clr
  Register #(.width(64)) register_14 (.D(register_1_q), .Q(register_14_q));  // open: en, clk, clr
  Register #(.width(64)) register_15 (.D(register_1_q), .Q(register_15_q));  // open: en, clk, clr
  Register #(.width(64)) register_16 (.D(register_1_q), .Q(register_16_q));  // open: en, clk, clr
  Register #(.width(64)) register_17 (.D(register_1_q), .Q(register_17_q));  // open: en, clk, clr
  Register #(.width(64)) register_18 ();  // open: D, en, clk, Q, clr
  Register #(.width(64)) register_19 ();  // open: D, en, clk, Q, clr
  core_8x8 core_8x8_1 (
    .A11_11(register_2_q), .A11_12(register_6_q), .A11_21(register_10_q), .A11_22(register_14_q),
    .A12_11(register_3_q), .A12_12(register_7_q), .A12_21(register_11_q), .A12_22(register_15_q),
    .A13_11(register_4_q), .A13_12(register_8_q), .A13_21(register_12_q), .A13_22(register_16_q),
    .A14_11(register_5_q), .A14_12(register_9_q), .A14_21(register_13_q), .A14_22(register_17_q),
    .B11_11(register_22_q), .B11_12(register_26_q), .B11_21(register_30_q), .B11_22(register_34_q),
    .B21_11(register_23_q), .B21_12(register_27_q), .B21_21(register_31_q), .B21_22(register_35_q),
    .B31_11(register_24_q), .B31_12(register_28_q), .B31_21(register_32_q), .B31_22(register_36_q),
    .B41_11(register_25_q), .B41_12(register_29_q), .B41_21(register_33_q), .B41_22(register_37_q));  // open: R11, R12, R21, R22
  Register #(.width(64)) register_20 ();  // open: D, en, clk, Q, clr
  Register #(.width(64)) register_21 ();  // open: D, en, clk, Q, clr
  RAM #(.dataWidth(64)) RAM_B (.dout(RAM_B_dout));  // open: addr, we, oe, clk, din
  RAM #(.dataWidth(64)) ram_2 ();  // open: addr, we, oe, clk, din, dout
  Register #(.width(64)) register_22 (.Q(register_22_q));  // open: D, en, clk, clr
  Register #(.width(64)) register_23 (.Q(register_23_q));  // open: D, en, clk, clr
  Register #(.width(64)) register_24 (.Q(register_24_q));  // open: D, en, clk, clr
  Register #(.width(64)) register_25 (.Q(register_25_q));  // open: D, en, clk, clr
  Register #(.width(64)) register_26 (.Q(register_26_q));  // open: D, en, clk, clr
  Register #(.width(64)) register_27 (.Q(register_27_q));  // open: D, en, clk, clr
  Register #(.width(64)) register_28 (.Q(register_28_q));  // open: D, en, clk, clr
  Register #(.width(64)) register_29 (.Q(register_29_q));  // open: D, en, clk, clr
  Register #(.width(64)) register_30 (.Q(register_30_q));  // open: D, en, clk, clr
  Register #(.width(64)) register_31 (.Q(register_31_q));  // open: D, en, clk, clr
  Register #(.width(64)) register_32 (.Q(register_32_q));  // open: D, en, clk, clr
  Register #(.width(64)) register_33 (.Q(register_33_q));  // open: D, en, clk, clr
  Register #(.width(64)) register_34 (.Q(register_34_q));  // open: D, en, clk, clr
  Register #(.width(64)) register_35 (.Q(register_35_q));  // open: D, en, clk, clr
  Register #(.width(64)) register_36 (.Q(register_36_q));  // open: D, en, clk, clr
  Register #(.width(64)) register_37 (.Q(register_37_q));  // open: D, en, clk, clr
  RAM #(.dataWidth(64)) SYST_RAM ();  // open: addr, we, oe, clk, din, dout
  RAM #(.dataWidth(64)) INS_RAM ();  // open: addr, we, oe, clk, din, dout
endmodule
module Assembly_Latest_Architect (
  input  in_1,
  input  in_2,
  input  in_3,
  input  in_4,
  input  in_5,
  input  in_6,
  input  in_7,
  input  in_8,
  input  in_9,
  input  in_10,
  input  in_11,
  input  in_12,
  input  in_13,
  input  in_14,
  input  in_15,
  input  in_16,
  input  in_17,
  input  in_18,
  input  in_19,
  input  in_20,
  input  in_21,
  input  in_22,
  input  in_23,
  input  in_24,
  input  ADD_B_CTRL_BUFFER,
  input  ADD_A_CTRL_BUFFER,
  input  OPCODE_CTRL_BUFFER,
  input  RAM_A_OE_COPY,
  input  MAR_Z_WE,
  input  OPCODE_REG_WE,
  input  MAR_B_CTRL_BUFF,
  input  MAR_B_WE,
  input  MAR_A_CTRL_BUFF,
  input  MAR_A_WE,
  input  INST_SPLITTER_WE,
  input  in_36,
  input  in_37,
  input  RAM_B_OE_COPY,
  input  OUTER_DIM_REG_B_WE,
  input  OUTER_DIM_REG_A_WE,
  input  INNER_DIM_REG_WE,
  input  DECODER_COUNTER_B_G5,
  input  DECODER_COUNTER_A_G5,
  input  MBR_B_WE,
  input  MBR_A_WE,
  input  SCRATCH_RAM_WE,
  input  SCRATCH_RAM_OE,
  input  RAM_B_OE,
  input  RAM_A_OE,
  input  INST_RAM_OE
);

  wire clock_1_out, comparator_1_gt, decoder_4bit_1_eight, decoder_4bit_1_eleven, decoder_4bit_1_fifteen,
       decoder_4bit_1_five, decoder_4bit_1_four, decoder_4bit_1_fourteen, decoder_4bit_1_nine,
       decoder_4bit_1_one, decoder_4bit_1_seven, decoder_4bit_1_six, decoder_4bit_1_ten,
       decoder_4bit_1_thirteen, decoder_4bit_1_three, decoder_4bit_1_twelve, decoder_4bit_1_two,
       decoder_4bit_1_zero, decoder_4bit_2_eight, decoder_4bit_2_eleven, decoder_4bit_2_fifteen,
       decoder_4bit_2_five, decoder_4bit_2_four, decoder_4bit_2_fourteen, decoder_4bit_2_nine,
       decoder_4bit_2_one, decoder_4bit_2_seven, decoder_4bit_2_six, decoder_4bit_2_ten,
       decoder_4bit_2_thirteen, decoder_4bit_2_three, decoder_4bit_2_twelve, decoder_4bit_2_two,
       decoder_4bit_2_zero, or_25_out, or_26_out, or_27_out, or_28_out, or_29_out, or_30_out, or_31_out,
       or_32_out, or_33_out, or_34_out, or_35_out, or_38_out, or_39_out, or_40_out, or_41_out, or_42_out,
       or_43_out, or_44_out, or_45_out, or_46_out, or_47_out, or_48_out, or_49_out, or_50_out, undriven,
       undriven_2;
  wire [3:0] DECODER_COUNTER_B_q, DECODER_COUNTERRR_q, instruction_splitter_1_flg,
       instruction_splitter_1_opcode, OP_CODE_REGISTER_q;
  wire [7:0] adder_1_out, adder_3_out, adder_4_out, bit_extender_1_out, COL_COUNTER_q,
       controlled_buffer_1_out, controlled_buffer_4_out, controlled_buffer_5_out, counter_1_q, counter_2_q,
       instruction_splitter_1_add_a, instruction_splitter_1_add_b, MAR_A_q, MAR_B_q, MAR_Z_q, OUTER_REG_A_q,
       OUTER_REG_B_q, ROW_COUNTER_q, SCRATCH_PAD_dout, STEP_COUNTER_q;
  wire [23:0] INST_RAM_dout;
  wire [63:0] A1_q, A2_q, A3_q, A4_q, A5_q, A6_q, A7_q, A8_q, A9_q, A10_q, A11_q, A12_q, A13_q, A14_q, A15_q,
       A16_q, A17_q, A18_q, A19_q, A20_q, A21_q, A22_q, A23_q, A24_q, A25_q, A26_q, A27_q, A28_q, A29_q,
       A30_q, A31_q, A32_q, B1_q, B2_q, B3_q, B4_q, B5_q, B6_q, B7_q, B8_q, B9_q, B10_q, B11_q, B12_q, B13_q,
       B14_q, B15_q, B16_q, B17_q, B18_q, B19_q, B20_q, B21_q, B22_q, B23_q, B24_q, B25_q, B26_q, B27_q,
       B28_q, B29_q, B30_q, B31_q, B32_q, core_16x16_1_r11, core_16x16_1_r12, core_16x16_1_r21,
       core_16x16_1_r22, MBR_A_COPY_q, MBR_A_q, MBR_B_COPY_q, MBR_B_q, ram_5_dout, RAM_A_COPY_dout,
       RAM_A_dout, RAM_B_dout, rom_1_data;

  Clock clock_1 (.out(clock_1_out));
  Counter #(.max('hf), .width(4)) DECODER_COUNTERRR (
    .count(or_43_out), .clk(clock_1_out), .Q(DECODER_COUNTERRR_q));  // open: clr, load, up, D, carry
  RAM #(.dataWidth(64), .\type ("nonvolatile")) RAM_A (
    .addr(MAR_A_q), .oe(or_49_out), .clk(clock_1_out), .dout(RAM_A_dout));  // open: we, din
  Adder adder_1 (.a(MAR_A_q), .b(8'h1), .out(adder_1_out));  // open: cin, cout
  RAM #(.dataWidth(64), .\type ("nonvolatile")) RAM_A_COPY (
    .addr(adder_1_out), .oe(or_28_out), .clk(clock_1_out), .dout(RAM_A_COPY_dout));  // open: we, din
  Register #(.width(64)) MBR_A (.D(RAM_A_dout), .en(undriven_2), .clk(undriven), .Q(MBR_A_q));  // open: clr
  Register #(.width(64)) MBR_A_COPY (
    .D(RAM_A_COPY_dout), .en(undriven_2), .clk(undriven), .Q(MBR_A_COPY_q));  // open: clr
  decoder_4bit decoder_4bit_1 (
    .OE(DECODER_COUNTERRR_q[3]), .A(DECODER_COUNTERRR_q[2]), .B(DECODER_COUNTERRR_q[1]),
    .C(DECODER_COUNTERRR_q[0]), .zero(decoder_4bit_1_zero), .one(decoder_4bit_1_one),
    .two(decoder_4bit_1_two), .three(decoder_4bit_1_three), .four(decoder_4bit_1_four),
    .five(decoder_4bit_1_five), .six(decoder_4bit_1_six), .seven(decoder_4bit_1_seven),
    .eight(decoder_4bit_1_eight), .nine(decoder_4bit_1_nine), .ten(decoder_4bit_1_ten),
    .eleven(decoder_4bit_1_eleven), .twelve(decoder_4bit_1_twelve), .thirteen(decoder_4bit_1_thirteen),
    .fourteen(decoder_4bit_1_fourteen), .fifteen(decoder_4bit_1_fifteen));  // open: D
  Counter counter_1 (.clk(clock_1_out), .Q(counter_1_q));  // open: clr, load, up, count, D, carry
  Register #(.width(64)) A1 (.D(MBR_A_q), .en(decoder_4bit_1_zero), .clk(clock_1_out), .Q(A1_q));  // open: clr
  Register #(.width(64)) A5 (.D(MBR_A_q), .en(decoder_4bit_1_two), .clk(clock_1_out), .Q(A5_q));  // open: clr
  Register #(.width(64)) A9 (.D(MBR_A_q), .en(decoder_4bit_1_four), .clk(clock_1_out), .Q(A9_q));  // open: clr
  Register #(.width(64)) A13 (.D(MBR_A_q), .en(decoder_4bit_1_six), .clk(clock_1_out), .Q(A13_q));  // open: clr
  Register #(.width(64)) A17 (.D(MBR_A_q), .en(decoder_4bit_1_eight), .clk(clock_1_out), .Q(A17_q));  // open: clr
  Register #(.width(64)) A21 (.D(MBR_A_q), .en(decoder_4bit_1_ten), .clk(clock_1_out), .Q(A21_q));  // open: clr
  Register #(.width(64)) A25 (.D(MBR_A_q), .en(decoder_4bit_1_twelve), .clk(clock_1_out), .Q(A25_q));  // open: clr
  Register #(.width(64)) A29 (.D(MBR_A_q), .en(decoder_4bit_1_fourteen), .clk(clock_1_out), .Q(A29_q));  // open: clr
  RAM SCRATCH_PAD (
    .addr(counter_1_q), .we(or_46_out), .oe(or_47_out), .clk(clock_1_out), .din(controlled_buffer_1_out),
    .dout(SCRATCH_PAD_dout));
  Register #(.width(64)) A2 (.D(MBR_A_COPY_q), .en(decoder_4bit_1_zero), .clk(clock_1_out), .Q(A2_q));  // open: clr
  Register #(.width(64)) A6 (.D(MBR_A_COPY_q), .en(decoder_4bit_1_two), .clk(clock_1_out), .Q(A6_q));  // open: clr
  Register #(.width(64)) A10 (.D(MBR_A_COPY_q), .en(decoder_4bit_1_four), .clk(clock_1_out), .Q(A10_q));  // open: clr
  Register #(.width(64)) A14 (.D(MBR_A_COPY_q), .en(decoder_4bit_1_six), .clk(clock_1_out), .Q(A14_q));  // open: clr
  Register #(.width(64)) A18 (.D(MBR_A_COPY_q), .en(decoder_4bit_1_eight), .clk(clock_1_out), .Q(A18_q));  // open: clr
  Register #(.width(64)) A22 (.D(MBR_A_COPY_q), .en(decoder_4bit_1_ten), .clk(clock_1_out), .Q(A22_q));  // open: clr
  Register #(.width(64)) A26 (.D(MBR_A_COPY_q), .en(decoder_4bit_1_twelve), .clk(clock_1_out), .Q(A26_q));  // open: clr
  Register #(.width(64)) A30 (
    .D(MBR_A_COPY_q), .en(decoder_4bit_1_fourteen), .clk(clock_1_out), .Q(A30_q));  // open: clr
  Register #(.width(64)) A3 (.D(MBR_A_q), .en(decoder_4bit_1_one), .clk(clock_1_out), .Q(A3_q));  // open: clr
  Register #(.width(64)) A7 (.D(MBR_A_q), .en(decoder_4bit_1_three), .clk(clock_1_out), .Q(A7_q));  // open: clr
  Register #(.width(64)) A11 (.D(MBR_A_q), .en(decoder_4bit_1_five), .clk(clock_1_out), .Q(A11_q));  // open: clr
  Register #(.width(64)) A15 (.D(MBR_A_q), .en(decoder_4bit_1_seven), .clk(clock_1_out), .Q(A15_q));  // open: clr
  Register #(.width(64)) A19 (.D(MBR_A_q), .en(decoder_4bit_1_nine), .clk(clock_1_out), .Q(A19_q));  // open: clr
  Register #(.width(64)) A23 (.D(MBR_A_q), .en(decoder_4bit_1_eleven), .clk(clock_1_out), .Q(A23_q));  // open: clr
  Register #(.width(64)) A27 (.D(MBR_A_q), .en(decoder_4bit_1_thirteen), .clk(clock_1_out), .Q(A27_q));  // open: clr
  Register #(.width(64)) A31 (.D(MBR_A_q), .en(decoder_4bit_1_fifteen), .clk(clock_1_out), .Q(A31_q));  // open: clr
  Register INNER_DIM (.D(SCRATCH_PAD_dout), .en(or_41_out), .clk(clock_1_out));  // open: Q, clr
  Register #(.width(64)) A4 (.D(MBR_A_COPY_q), .en(decoder_4bit_1_one), .clk(clock_1_out), .Q(A4_q));  // open: clr
  Register #(.width(64)) A8 (.D(MBR_A_COPY_q), .en(decoder_4bit_1_three), .clk(clock_1_out), .Q(A8_q));  // open: clr
  Register #(.width(64)) A16 (.D(MBR_A_COPY_q), .en(decoder_4bit_1_seven), .clk(clock_1_out), .Q(A16_q));  // open: clr
  Register #(.width(64)) A20 (.D(MBR_A_COPY_q), .en(decoder_4bit_1_nine), .clk(clock_1_out), .Q(A20_q));  // open: clr
  Register #(.width(64)) A24 (.D(MBR_A_COPY_q), .en(decoder_4bit_1_eleven), .clk(clock_1_out), .Q(A24_q));  // open: clr
  Register #(.width(64)) A28 (
    .D(MBR_A_COPY_q), .en(decoder_4bit_1_thirteen), .clk(clock_1_out), .Q(A28_q));  // open: clr
  Register #(.width(64)) A32 (
    .D(MBR_A_COPY_q), .en(decoder_4bit_1_fifteen), .clk(clock_1_out), .Q(A32_q));  // open: clr
  Register OUTER_REG_A (.D(SCRATCH_PAD_dout), .en(or_40_out), .clk(clock_1_out), .Q(OUTER_REG_A_q));  // open: clr
  Register #(.width(64)) A12 (.D(MBR_A_COPY_q), .en(decoder_4bit_1_five), .clk(clock_1_out), .Q(A12_q));  // open: clr
  Register OUTER_REG_B (.D(SCRATCH_PAD_dout), .en(or_39_out), .clk(clock_1_out), .Q(OUTER_REG_B_q));  // open: clr
  Counter counter_2 (.clk(clock_1_out), .Q(counter_2_q));  // open: clr, load, up, count, D, carry
  Register MAR_Z (.D(counter_2_q), .en(or_29_out), .clk(clock_1_out), .Q(MAR_Z_q));  // open: clr
  RAM #(.dataWidth(24)) INST_RAM (
    .addr(MAR_Z_q), .oe(or_50_out), .clk(clock_1_out), .dout(INST_RAM_dout));  // open: we, din
  // Probe on A3_q
  // Probe on A1_q
  core_16x16 core_16x16_1 (
    .A11_11(A1_q), .A11_12(A2_q), .A11_21(A3_q), .A11_22(A4_q), .A12_11(A5_q), .A12_12(A6_q), .A12_21(A7_q),
    .A12_22(A8_q), .A13_11(A9_q), .A13_12(A10_q), .A13_21(A11_q), .A13_22(A12_q), .A14_11(A13_q),
    .A14_12(A14_q), .A14_21(A15_q), .A14_22(A16_q), .A15_11(A17_q), .A15_12(A18_q), .A15_21(A19_q),
    .A15_22(A20_q), .A16_11(A21_q), .A16_12(A22_q), .A16_21(A23_q), .A16_22(A24_q), .A17_11(A25_q),
    .A17_12(A26_q), .A17_21(A27_q), .A17_22(A28_q), .A18_11(A29_q), .A18_12(A30_q), .A18_21(A31_q),
    .A18_22(A32_q), .B11_11(B1_q), .B11_12(B2_q), .B11_21(B3_q), .B11_22(B4_q), .B21_11(B5_q), .B21_12(B6_q),
    .B21_21(B7_q), .B21_22(B8_q), .B31_11(B9_q), .B31_12(B10_q), .B31_21(B11_q), .B31_22(B12_q),
    .B41_11(B13_q), .B41_12(B14_q), .B41_21(B15_q), .B41_22(B16_q), .B51_11(B17_q), .B51_12(B18_q),
    .B51_21(B19_q), .B51_22(B20_q), .B61_11(B21_q), .B61_12(B22_q), .B61_21(B23_q), .B61_22(B24_q),
    .B71_11(B25_q), .B71_12(B26_q), .B71_21(B27_q), .B71_22(B28_q), .B81_11(B29_q), .B81_12(B30_q),
    .B81_21(B31_q), .B81_22(B32_q), .R11(core_16x16_1_r11), .R12(core_16x16_1_r12), .R21(core_16x16_1_r21),
    .R22(core_16x16_1_r22));
  Counter #(.max('hf)) ROW_COUNTER (.clk(clock_1_out), .Q(ROW_COUNTER_q));  // open: clr, load, up, count, D, carry
  // Probe on A2_q
  // Probe on A4_q
  // Probe on core_16x16_1_r11
  // Probe on core_16x16_1_r12
  // Probe on core_16x16_1_r21
  // Probe on core_16x16_1_r22
  RAM #(.dataWidth(64)) ram_1 (.clk(clock_1_out), .din(core_16x16_1_r11));  // open: addr, we, oe, dout
  RAM #(.dataWidth(64)) ram_2 (.clk(clock_1_out), .din(core_16x16_1_r12));  // open: addr, we, oe, dout
  assign controlled_buffer_1_out = or_26_out ? instruction_splitter_1_add_a : 8'bz;  // Controlled_Buffer controlled_buffer_1
  assign controlled_buffer_1_out = or_27_out ? bit_extender_1_out : 8'bz;  // Controlled_Buffer controlled_buffer_2
  assign controlled_buffer_1_out = or_25_out ? instruction_splitter_1_add_b : 8'bz;  // Controlled_Buffer controlled_buffer_3
  assign controlled_buffer_4_out = or_33_out ? instruction_splitter_1_add_a : 8'bz;  // Controlled_Buffer controlled_buffer_4
  Adder adder_2 (.a(8'h2), .b(ROW_COUNTER_q), .out(controlled_buffer_4_out));  // open: cin, cout
  assign bit_extender_1_out = {{4{instruction_splitter_1_flg[3]}}, instruction_splitter_1_flg};  // Bit_Extender bit_extender_1
  instruction_splitter instruction_splitter_1 (
    .WE(or_35_out), .CLOCK(clock_1_out), .instruction(INST_RAM_dout), .FLG(instruction_splitter_1_flg),
    .OPCODE(instruction_splitter_1_opcode), .ADD_A(instruction_splitter_1_add_a),
    .ADD_B(instruction_splitter_1_add_b));
  Register MAR_A (.D(controlled_buffer_4_out), .en(or_34_out), .clk(clock_1_out), .Q(MAR_A_q));  // open: clr
  RAM #(.dataWidth(64)) ram_3 (.clk(clock_1_out), .din(core_16x16_1_r21));  // open: addr, we, oe, dout
  RAM #(.dataWidth(64)) ram_4 (.clk(clock_1_out), .din(core_16x16_1_r22));  // open: addr, we, oe, dout
  Register MAR_B (.D(instruction_splitter_1_add_b), .en(or_32_out), .clk(clock_1_out), .Q(MAR_B_q));  // open: clr
  Register #(.width(64)) B1 (.D(MBR_B_q), .en(decoder_4bit_2_zero), .clk(clock_1_out), .Q(B1_q));  // open: clr
  Register #(.width(64)) B5 (.D(MBR_B_q), .en(decoder_4bit_2_two), .clk(clock_1_out), .Q(B5_q));  // open: clr
  Register #(.width(64)) B9 (.D(MBR_B_q), .en(decoder_4bit_2_four), .clk(clock_1_out), .Q(B9_q));  // open: clr
  Register #(.width(64)) B13 (.D(MBR_B_q), .en(decoder_4bit_2_six), .clk(clock_1_out), .Q(B13_q));  // open: clr
  Register #(.width(64)) B17 (.D(MBR_B_q), .en(decoder_4bit_2_eight), .clk(clock_1_out), .Q(B17_q));  // open: clr
  Register #(.width(64)) B25 (.D(MBR_B_q), .en(decoder_4bit_2_twelve), .clk(clock_1_out), .Q(B25_q));  // open: clr
  Register #(.width(64)) B21 (.D(MBR_B_q), .en(decoder_4bit_2_ten), .clk(clock_1_out), .Q(B21_q));  // open: clr
  Register #(.width(64)) B29 (.D(MBR_B_q), .en(decoder_4bit_2_fourteen), .clk(clock_1_out), .Q(B29_q));  // open: clr
  Register #(.width(64)) B2 (.D(MBR_B_COPY_q), .en(decoder_4bit_2_zero), .clk(clock_1_out), .Q(B2_q));  // open: clr
  Register #(.width(64)) B6 (.D(MBR_B_COPY_q), .en(decoder_4bit_2_two), .clk(clock_1_out), .Q(B6_q));  // open: clr
  Register #(.width(64)) B10 (.D(MBR_B_COPY_q), .en(decoder_4bit_2_four), .clk(clock_1_out), .Q(B10_q));  // open: clr
  Register #(.width(64)) B14 (.D(MBR_B_COPY_q), .en(decoder_4bit_2_six), .clk(clock_1_out), .Q(B14_q));  // open: clr
  assign controlled_buffer_5_out = or_31_out ? MAR_B_q : 8'bz;  // Controlled_Buffer controlled_buffer_5
  Register #(.width(64)) B18 (.D(MBR_B_COPY_q), .en(decoder_4bit_2_eight), .clk(clock_1_out), .Q(B18_q));  // open: clr
  Register #(.width(64)) B22 (.D(MBR_B_COPY_q), .en(decoder_4bit_2_ten), .clk(clock_1_out), .Q(B22_q));  // open: clr
  Register #(.width(64)) B26 (.D(MBR_B_COPY_q), .en(decoder_4bit_2_twelve), .clk(clock_1_out), .Q(B26_q));  // open: clr
  Register #(.width(64)) B30 (
    .D(MBR_B_COPY_q), .en(decoder_4bit_2_fourteen), .clk(clock_1_out), .Q(B30_q));  // open: clr
  Register #(.width(64)) B3 (.D(MBR_B_q), .en(decoder_4bit_2_one), .clk(clock_1_out), .Q(B3_q));  // open: clr
  Register #(.width(64)) B7 (.D(MBR_B_q), .en(decoder_4bit_2_three), .clk(clock_1_out), .Q(B7_q));  // open: clr
  Register #(.width(64)) B11 (.D(MBR_B_q), .en(decoder_4bit_2_five), .clk(clock_1_out), .Q(B11_q));  // open: clr
  Register #(.width(64)) B15 (.D(MBR_B_q), .en(decoder_4bit_2_seven), .clk(clock_1_out), .Q(B15_q));  // open: clr
  Register #(.width(64)) B19 (.D(MBR_B_q), .en(decoder_4bit_2_nine), .clk(clock_1_out), .Q(B19_q));  // open: clr
  Counter #(.max('hf), .width(4)) DECODER_COUNTER_B (
    .count(or_42_out), .clk(clock_1_out), .Q(DECODER_COUNTER_B_q));  // open: clr, load, up, D, carry
  Register #(.width(64)) B23 (.D(MBR_B_q), .en(decoder_4bit_2_eleven), .clk(clock_1_out), .Q(B23_q));  // open: clr
  Register #(.width(64)) B27 (.D(MBR_B_q), .en(decoder_4bit_2_thirteen), .clk(clock_1_out), .Q(B27_q));  // open: clr
  Register #(.width(64)) B31 (.D(MBR_B_q), .en(decoder_4bit_2_fifteen), .clk(clock_1_out), .Q(B31_q));  // open: clr
  Register #(.width(64)) B4 (.D(MBR_B_COPY_q), .en(decoder_4bit_2_one), .clk(clock_1_out), .Q(B4_q));  // open: clr
  Register #(.width(64)) B8 (.D(MBR_B_COPY_q), .en(decoder_4bit_2_three), .clk(clock_1_out), .Q(B8_q));  // open: clr
  Register #(.width(64)) B12 (.D(MBR_B_COPY_q), .en(decoder_4bit_2_five), .clk(clock_1_out), .Q(B12_q));  // open: clr
  Register #(.width(64)) B16 (.D(MBR_B_COPY_q), .en(decoder_4bit_2_seven), .clk(clock_1_out), .Q(B16_q));  // open: clr
  Register #(.width(64)) B20 (.D(MBR_B_COPY_q), .en(decoder_4bit_2_nine), .clk(clock_1_out), .Q(B20_q));  // open: clr
  Register #(.width(64)) B24 (.D(MBR_B_COPY_q), .en(decoder_4bit_2_eleven), .clk(clock_1_out), .Q(B24_q));  // open: clr
  Register #(.width(64)) B28 (
    .D(MBR_B_COPY_q), .en(decoder_4bit_2_thirteen), .clk(clock_1_out), .Q(B28_q));  // open: clr
  Register #(.width(64)) B32 (
    .D(MBR_B_COPY_q), .en(decoder_4bit_2_fifteen), .clk(clock_1_out), .Q(B32_q));  // open: clr
  decoder_4bit decoder_4bit_2 (
    .OE(DECODER_COUNTER_B_q[3]), .A(DECODER_COUNTER_B_q[2]), .B(DECODER_COUNTER_B_q[1]),
    .C(DECODER_COUNTER_B_q[0]), .zero(decoder_4bit_2_zero), .one(decoder_4bit_2_one),
    .two(decoder_4bit_2_two), .three(decoder_4bit_2_three), .four(decoder_4bit_2_four),
    .five(decoder_4bit_2_five), .six(decoder_4bit_2_six), .seven(decoder_4bit_2_seven),
    .eight(decoder_4bit_2_eight), .nine(decoder_4bit_2_nine), .ten(decoder_4bit_2_ten),
    .eleven(decoder_4bit_2_eleven), .twelve(decoder_4bit_2_twelve), .thirteen(decoder_4bit_2_thirteen),
    .fourteen(decoder_4bit_2_fourteen), .fifteen(decoder_4bit_2_fifteen));  // open: D
  Counter COL_COUNTER (.clk(clock_1_out), .Q(COL_COUNTER_q));  // open: clr, load, up, count, D, carry
  RAM #(.dataWidth(64)) RAM_B (
    .addr(controlled_buffer_5_out), .oe(or_48_out), .clk(clock_1_out), .dout(RAM_B_dout));  // open: we, din
  Register register_1 (.D(adder_4_out), .en(clock_1_out), .clk(clock_1_out), .Q(controlled_buffer_5_out));  // open: clr
  Adder adder_3 (.a(controlled_buffer_5_out), .b(8'h1), .out(adder_3_out));  // open: cin, cout
  Register #(.width(4)) OP_CODE_REGISTER (
    .D(instruction_splitter_1_opcode), .en(or_30_out), .clk(clock_1_out), .Q(OP_CODE_REGISTER_q));  // open: clr
  RAM #(.dataWidth(64)) ram_5 (
    .addr(adder_3_out), .oe(or_38_out), .clk(clock_1_out), .dout(ram_5_dout));  // open: we, din
  Adder adder_4 (.a(controlled_buffer_5_out), .b(8'h2), .out(adder_4_out));  // open: cin, cout
  Register #(.width(64)) MBR_B (.D(RAM_B_dout), .en(or_44_out), .clk(clock_1_out), .Q(MBR_B_q));  // open: clr
  Comparator comparator_1 (
    .a(OUTER_REG_B_q), .b(COL_COUNTER_q), .gt(comparator_1_gt), .eq(comparator_1_gt));  // open: lt
  Register #(.width(64)) MBR_B_COPY (.D(ram_5_dout), .en(or_44_out), .clk(clock_1_out), .Q(MBR_B_COPY_q));  // open: clr
  Counter STEP_COUNTER (.clk(clock_1_out), .Q(STEP_COUNTER_q));  // open: clr, load, up, count, D, carry
  // OR_Gate or_1 has open pins: in0=rom_1_data[14], in1=in_1, out=open
  // OR_Gate or_2 has open pins: in0=rom_1_data[15], in1=in_2, out=open
  // OR_Gate or_3 has open pins: in0=rom_1_data[16], in1=in_3, out=open
  // OR_Gate or_4 has open pins: in0=rom_1_data[17], in1=in_4, out=open
  // OR_Gate or_5 has open pins: in0=rom_1_data[18], in1=in_5, out=open
  // OR_Gate or_6 has open pins: in0=rom_1_data[19], in1=in_6, out=open
  // OR_Gate or_7 has open pins: in0=rom_1_data[20], in1=in_7, out=open
  // OR_Gate or_8 has open pins: in0=rom_1_data[21], in1=in_8, out=open
  // OR_Gate or_9 has open pins: in0=rom_1_data[22], in1=in_9, out=open
  // OR_Gate or_10 has open pins: in0=rom_1_data[23], in1=in_10, out=open
  // OR_Gate or_11 has open pins: in0=rom_1_data[24], in1=in_11, out=open
  // OR_Gate or_12 has open pins: in0=rom_1_data[25], in1=in_12, out=open
  // OR_Gate or_13 has open pins: in0=rom_1_data[26], in1=in_13, out=open
  // OR_Gate or_14 has open pins: in0=rom_1_data[27], in1=in_14, out=open
  // OR_Gate or_15 has open pins: in0=rom_1_data[28], in1=in_15, out=open
  // OR_Gate or_16 has open pins: in0=rom_1_data[29], in1=in_16, out=open
  // OR_Gate or_17 has open pins: in0=rom_1_data[30], in1=in_17, out=open
  // OR_Gate or_18 has open pins: in0=rom_1_data[31], in1=in_18, out=open
  // OR_Gate or_19 has open pins: in0=rom_1_data[32], in1=in_19, out=open
  // OR_Gate or_20 has open pins: in0=rom_1_data[33], in1=in_20, out=open
  // OR_Gate or_21 has open pins: in0=rom_1_data[34], in1=in_21, out=open
  // OR_Gate or_22 has open pins: in0=rom_1_data[35], in1=in_22, out=open
  // OR_Gate or_23 has open pins: in0=rom_1_data[36], in1=in_23, out=open
  // OR_Gate or_24 has open pins: in0=rom_1_data[37], in1=in_24, out=open
  or or_25 (or_25_out, rom_1_data[38], ADD_B_CTRL_BUFFER);
  or or_26 (or_26_out, rom_1_data[39], ADD_A_CTRL_BUFFER);
  or or_27 (or_27_out, rom_1_data[40], OPCODE_CTRL_BUFFER);
  or or_28 (or_28_out, rom_1_data[41], RAM_A_OE_COPY);
  or or_29 (or_29_out, rom_1_data[42], MAR_Z_WE);
  or or_30 (or_30_out, rom_1_data[43], OPCODE_REG_WE);
  or or_31 (or_31_out, rom_1_data[44], MAR_B_CTRL_BUFF);
  or or_32 (or_32_out, rom_1_data[45], MAR_B_WE);
  or or_33 (or_33_out, rom_1_data[46], MAR_A_CTRL_BUFF);
  or or_34 (or_34_out, rom_1_data[47], MAR_A_WE);
  or or_35 (or_35_out, rom_1_data[48], INST_SPLITTER_WE);
  // OR_Gate or_36 has open pins: in0=rom_1_data[49], in1=in_36, out=open
  // OR_Gate or_37 has open pins: in0=rom_1_data[50], in1=in_37, out=open
  or or_38 (or_38_out, rom_1_data[51], RAM_B_OE_COPY);
  or or_39 (or_39_out, rom_1_data[52], OUTER_DIM_REG_B_WE);
  or or_40 (or_40_out, rom_1_data[53], OUTER_DIM_REG_A_WE);
  or or_41 (or_41_out, rom_1_data[54], INNER_DIM_REG_WE);
  or or_42 (or_42_out, rom_1_data[55], DECODER_COUNTER_B_G5);
  or or_43 (or_43_out, rom_1_data[56], DECODER_COUNTER_A_G5);
  or or_44 (or_44_out, rom_1_data[57], MBR_B_WE);
  or or_45 (or_45_out, rom_1_data[58], MBR_A_WE);
  or or_46 (or_46_out, rom_1_data[59], SCRATCH_RAM_WE);
  or or_47 (or_47_out, rom_1_data[60], SCRATCH_RAM_OE);
  or or_48 (or_48_out, rom_1_data[61], RAM_B_OE);
  or or_49 (or_49_out, rom_1_data[62], RAM_A_OE);
  or or_50 (or_50_out, rom_1_data[63], INST_RAM_OE);
  ROM #(.addrWidth(16), .dataWidth(64)) rom_1 (
    .addr({instruction_splitter_1_flg, OP_CODE_REGISTER_q, STEP_COUNTER_q}), .data(rom_1_data));
endmodule

module decoder_4bit (
  input  OE,
  input  A,
  input  B,
  input  C,
  input  D,
  output zero,
  output one,
  output two,
  output three,
  output four,
  output five,
  output six,
  output seven,
  output eight,
  output nine,
  output ten,
  output eleven,
  output twelve,
  output thirteen,
  output fourteen,
  output fifteen
);

  wire not_1_out, not_2_out, not_3_out, not_4_out;
  wire [15:0] and_1_out, bit_extender_1_out;

  not not_1 (not_1_out, A);
  not not_2 (not_2_out, B);
  not not_3 (not_3_out, C);
  not not_4 (not_4_out, D);
  assign bit_extender_1_out = {{15{OE}}, OE};  // Bit_Extender bit_extender_1
  and and_1 (and_1_out[0], not_1_out, not_2_out, not_3_out, not_4_out);
  and and_2 (and_1_out[1], not_1_out, not_2_out, not_3_out, D);
  and and_3 (and_1_out[2], not_1_out, not_2_out, C, not_4_out);
  and and_4 (and_1_out[3], not_1_out, not_2_out, C, D);
  and and_5 (and_1_out[4], not_1_out, B, not_3_out, not_4_out);
  and and_6 (and_1_out[5], not_1_out, B, not_3_out, D);
  and and_7 (and_1_out[6], not_1_out, B, C, not_4_out);
  and and_8 (and_1_out[7], not_1_out, B, C, D);
  and and_9 (and_1_out[8], A, not_2_out, not_3_out, not_4_out);
  and and_10 (and_1_out[9], A, not_2_out, not_3_out, D);
  and and_11 (and_1_out[10], A, not_2_out, C, not_4_out);
  and and_12 (and_1_out[11], A, not_2_out, C, D);
  and and_13 (and_1_out[12], A, B, not_3_out, not_4_out);
  and and_14 (and_1_out[13], A, B, not_3_out, D);
  and and_15 (and_1_out[14], A, B, C, not_4_out);
  and and_16 (and_1_out[15], A, B, C, D);
  assign {fifteen, fourteen, thirteen, twelve, eleven, ten, nine, eight, seven, six, five, four, three, two, one, zero} = bit_extender_1_out & and_1_out;  // AND_Gate and_17, 16 bits wide
endmodule

module assembly_latest_architect_1 (
  input  in_1,
  input  in_2,
  input  in_3,
  input  in_4,
  input  in_5,
  input  in_6,
  input  in_7,
  input  in_8,
  input  in_9,
  input  in_10,
  input  in_11,
  input  in_12,
  input  in_13,
  input  in_14,
  input  in_15,
  input  in_16,
  input  in_17,
  input  in_18,
  input  in_19,
  input  in_20,
  input  in_21,
  input  in_22,
  input  in_23,
  input  in_24,
  input  in_25,
  input  in_26,
  input  ADD_B_CTRL_BUFFER,
  input  ADD_A_CTRL_BUFFER,
  input  OPCODE_CTRL_BUFFER,
  input  RAM_A_OE_COPY,
  input  MAR_Z_WE,
  input  OPCODE_REG_WE,
  input  MAR_B_CTRL_BUFF,
  input  MAR_B_WE,
  input  MAR_A_CTRL_BUFF,
  input  MAR_A_WE,
  input  INST_SPLITTER_WE,
  input  in_38,
  input  in_39,
  input  RAM_B_OE_COPY,
  input  OUTER_DIM_REG_B_WE,
  input  OUTER_DIM_REG_A_WE,
  input  INNER_DIM_REG_WE,
  input  DECODER_COUNTER_B_G5,
  input  DECODER_COUNTER_A_G5,
  input  MBR_B_WE,
  input  MBR_A_WE,
  input  SCRATCH_RAM_WE,
  input  SCRATCH_RAM_OE,
  input  RAM_B_OE,
  input  RAM_A_OE,
  input  INST_RAM_OE
);

  wire clock_1_out, comparator_1_gt, decoder_4bit_1_eight, decoder_4bit_1_eleven, decoder_4bit_1_fifteen,
       decoder_4bit_1_five, decoder_4bit_1_four, decoder_4bit_1_fourteen, decoder_4bit_1_nine,
       decoder_4bit_1_one, decoder_4bit_1_seven, decoder_4bit_1_six, decoder_4bit_1_ten,
       decoder_4bit_1_thirteen, decoder_4bit_1_three, decoder_4bit_1_twelve, decoder_4bit_1_two,
       decoder_4bit_1_zero, decoder_4bit_2_eight, decoder_4bit_2_eleven, decoder_4bit_2_fifteen,
       decoder_4bit_2_five, decoder_4bit_2_four, decoder_4bit_2_fourteen, decoder_4bit_2_nine,
       decoder_4bit_2_one, decoder_4bit_2_seven, decoder_4bit_2_six, decoder_4bit_2_ten,
       decoder_4bit_2_thirteen, decoder_4bit_2_three, decoder_4bit_2_twelve, decoder_4bit_2_two,
       decoder_4bit_2_zero, or_25_out, or_26_out, or_27_out, or_28_out, or_29_out, or_30_out, or_31_out,
       or_32_out, or_33_out, or_34_out, or_35_out, or_38_out, or_39_out, or_40_out, or_41_out, or_42_out,
       or_43_out, or_44_out, or_45_out, or_46_out, or_47_out, or_48_out, or_49_out, or_50_out;
  wire [3:0] DECODER_COUNTER_B_q, DECODER_COUNTERRR_q, instruction_splitter_1_flg,
       instruction_splitter_1_opcode, OP_CODE_REGISTER_q;
  wire [7:0] adder_1_out, adder_2_out, adder_3_out, bit_extender_1_out, COL_COUNTER_q,
       controlled_buffer_1_out, controlled_buffer_4_out, controlled_buffer_6_out, counter_1_q, counter_2_q,
       instruction_splitter_1_add_a, instruction_splitter_1_add_b, MAR_A_q, MAR_B_q, MAR_Z_q, OUTER_REG_A_q,
       OUTER_REG_B_q, ROW_COUNTER_q, SCRATCH_PAD_dout, STEP_COUNTER_q, undriven;
  wire [23:0] INST_RAM_dout;
  wire [63:0] A1_q, A2_q, A3_q, A4_q, A5_q, A6_q, A7_q, A8_q, A9_q, A10_q, A11_q, A12_q, A13_q, A14_q, A15_q,
       A16_q, A17_q, A18_q, A19_q, A20_q, A21_q, A22_q, A23_q, A24_q, A25_q, A26_q, A27_q, A28_q, A29_q,
       A30_q, A31_q, A32_q, B1_q, B2_q, B3_q, B4_q, B5_q, B6_q, B7_q, B8_q, B9_q, B10_q, B11_q, B12_q, B13_q,
       B14_q, B15_q, B16_q, B17_q, B18_q, B19_q, B20_q, B21_q, B22_q, B23_q, B24_q, B25_q, B26_q, B27_q,
       B28_q, B29_q, B30_q, B31_q, B32_q, core_16x16_1_r11, core_16x16_1_r12, core_16x16_1_r21,
       core_16x16_1_r22, MBR_A_COPY_q, MBR_A_q, MBR_B_COPY_q, MBR_B_q, ram_5_dout, RAM_A_COPY_dout,
       RAM_A_dout, RAM_B_dout, rom_1_data;

  Clock clock_1 (.out(clock_1_out));
  Counter #(.max('hf), .width(4)) DECODER_COUNTERRR (
    .count(or_43_out), .clk(clock_1_out), .Q(DECODER_COUNTERRR_q));  // open: clr, load, up, D, carry
  RAM #(.dataWidth(64), .\type ("nonvolatile")) RAM_A (
    .addr(MAR_A_q), .oe(or_49_out), .clk(clock_1_out), .dout(RAM_A_dout));  // open: we, din
  RAM #(.dataWidth(64), .\type ("nonvolatile")) RAM_A_COPY (
    .addr(MAR_A_q), .oe(or_28_out), .clk(clock_1_out), .dout(RAM_A_COPY_dout));  // open: we, din
  Register #(.width(64)) MBR_A (.D(RAM_A_dout), .en(or_45_out), .clk(clock_1_out), .Q(MBR_A_q));  // open: clr
  Register #(.width(64)) MBR_A_COPY (
    .D(RAM_A_COPY_dout), .en(or_45_out), .clk(clock_1_out), .Q(MBR_A_COPY_q));  // open: clr
  decoder_4bit decoder_4bit_1 (
    .OE(DECODER_COUNTERRR_q[3]), .A(DECODER_COUNTERRR_q[2]), .B(DECODER_COUNTERRR_q[1]),
    .C(DECODER_COUNTERRR_q[0]), .zero(decoder_4bit_1_zero), .one(decoder_4bit_1_one),
    .two(decoder_4bit_1_two), .three(decoder_4bit_1_three), .four(decoder_4bit_1_four),
    .five(decoder_4bit_1_five), .six(decoder_4bit_1_six), .seven(decoder_4bit_1_seven),
    .eight(decoder_4bit_1_eight), .nine(decoder_4bit_1_nine), .ten(decoder_4bit_1_ten),
    .eleven(decoder_4bit_1_eleven), .twelve(decoder_4bit_1_twelve), .thirteen(decoder_4bit_1_thirteen),
    .fourteen(decoder_4bit_1_fourteen), .fifteen(decoder_4bit_1_fifteen));  // open: D
  Counter counter_1 (.clk(clock_1_out), .Q(counter_1_q));  // open: clr, load, up, count, D, carry
  Register #(.width(64)) A1 (.D(MBR_A_q), .en(decoder_4bit_1_zero), .clk(clock_1_out), .Q(A1_q));  // open: clr
  Register #(.width(64)) A5 (.D(MBR_A_q), .en(decoder_4bit_1_two), .clk(clock_1_out), .Q(A5_q));  // open: clr
  Register #(.width(64)) A9 (.D(MBR_A_q), .en(decoder_4bit_1_four), .clk(clock_1_out), .Q(A9_q));  // open: clr
  Register #(.width(64)) A13 (.D(MBR_A_q), .en(decoder_4bit_1_six), .clk(clock_1_out), .Q(A13_q));  // open: clr
  Register #(.width(64)) A17 (.D(MBR_A_q), .en(decoder_4bit_1_eight), .clk(clock_1_out), .Q(A17_q));  // open: clr
  Register #(.width(64)) A21 (.D(MBR_A_q), .en(decoder_4bit_1_ten), .clk(clock_1_out), .Q(A21_q));  // open: clr
  Register #(.width(64)) A25 (.D(MBR_A_q), .en(decoder_4bit_1_twelve), .clk(clock_1_out), .Q(A25_q));  // open: clr
  Register #(.width(64)) A29 (.D(MBR_A_q), .en(decoder_4bit_1_fourteen), .clk(clock_1_out), .Q(A29_q));  // open: clr
  RAM SCRATCH_PAD (
    .addr(counter_1_q), .we(or_46_out), .oe(or_47_out), .clk(clock_1_out), .din(controlled_buffer_1_out),
    .dout(SCRATCH_PAD_dout));
  Register #(.width(64)) A2 (.D(MBR_A_COPY_q), .en(decoder_4bit_1_zero), .clk(clock_1_out), .Q(A2_q));  // open: clr
  Register #(.width(64)) A6 (.D(MBR_A_COPY_q), .en(decoder_4bit_1_two), .clk(clock_1_out), .Q(A6_q));  // open: clr
  Register #(.width(64)) A10 (.D(MBR_A_COPY_q), .en(decoder_4bit_1_four), .clk(clock_1_out), .Q(A10_q));  // open: clr
  Register #(.width(64)) A14 (.D(MBR_A_COPY_q), .en(decoder_4bit_1_six), .clk(clock_1_out), .Q(A14_q));  // open: clr
  Register #(.width(64)) A18 (.D(MBR_A_COPY_q), .en(decoder_4bit_1_eight), .clk(clock_1_out), .Q(A18_q));  // open: clr
  Register #(.width(64)) A22 (.D(MBR_A_COPY_q), .en(decoder_4bit_1_ten), .clk(clock_1_out), .Q(A22_q));  // open: clr
  Register #(.width(64)) A26 (.D(MBR_A_COPY_q), .en(decoder_4bit_1_twelve), .clk(clock_1_out), .Q(A26_q));  // open: clr
  Register #(.width(64)) A30 (
    .D(MBR_A_COPY_q), .en(decoder_4bit_1_fourteen), .clk(clock_1_out), .Q(A30_q));  // open: clr
  Register #(.width(64)) A3 (.D(MBR_A_q), .en(decoder_4bit_1_one), .clk(clock_1_out), .Q(A3_q));  // open: clr
  Register #(.width(64)) A7 (.D(MBR_A_q), .en(decoder_4bit_1_three), .clk(clock_1_out), .Q(A7_q));  // open: clr
  Register #(.width(64)) A11 (.D(MBR_A_q), .en(decoder_4bit_1_five), .clk(clock_1_out), .Q(A11_q));  // open: clr
  Register #(.width(64)) A15 (.D(MBR_A_q), .en(decoder_4bit_1_seven), .clk(clock_1_out), .Q(A15_q));  // open: clr
  Register #(.width(64)) A19 (.D(MBR_A_q), .en(decoder_4bit_1_nine), .clk(clock_1_out), .Q(A19_q));  // open: clr
  Register #(.width(64)) A23 (.D(MBR_A_q), .en(decoder_4bit_1_eleven), .clk(clock_1_out), .Q(A23_q));  // open: clr
  Register #(.width(64)) A27 (.D(MBR_A_q), .en(decoder_4bit_1_thirteen), .clk(clock_1_out), .Q(A27_q));  // open: clr
  Register #(.width(64)) A31 (.D(MBR_A_q), .en(decoder_4bit_1_fifteen), .clk(clock_1_out), .Q(A31_q));  // open: clr
  Register INNER_DIM (.D(SCRATCH_PAD_dout), .en(or_41_out), .clk(clock_1_out));  // open: Q, clr
  Register #(.width(64)) A4 (.D(MBR_A_COPY_q), .en(decoder_4bit_1_one), .clk(clock_1_out), .Q(A4_q));  // open: clr
  Register #(.width(64)) A8 (.D(MBR_A_COPY_q), .en(decoder_4bit_1_three), .clk(clock_1_out), .Q(A8_q));  // open: clr
  Register #(.width(64)) A16 (.D(MBR_A_COPY_q), .en(decoder_4bit_1_seven), .clk(clock_1_out), .Q(A16_q));  // open: clr
  Register #(.width(64)) A20 (.D(MBR_A_COPY_q), .en(decoder_4bit_1_nine), .clk(clock_1_out), .Q(A20_q));  // open: clr
  Register #(.width(64)) A24 (.D(MBR_A_COPY_q), .en(decoder_4bit_1_eleven), .clk(clock_1_out), .Q(A24_q));  // open: clr
  Register #(.width(64)) A28 (
    .D(MBR_A_COPY_q), .en(decoder_4bit_1_thirteen), .clk(clock_1_out), .Q(A28_q));  // open: clr
  Register #(.width(64)) A32 (
    .D(MBR_A_COPY_q), .en(decoder_4bit_1_fifteen), .clk(clock_1_out), .Q(A32_q));  // open: clr
  Register OUTER_REG_A (.D(SCRATCH_PAD_dout), .en(or_40_out), .clk(clock_1_out), .Q(OUTER_REG_A_q));  // open: clr
  Register #(.width(64)) A12 (.D(MBR_A_COPY_q), .en(decoder_4bit_1_five), .clk(clock_1_out), .Q(A12_q));  // open: clr
  Register OUTER_REG_B (.D(SCRATCH_PAD_dout), .en(or_39_out), .clk(clock_1_out), .Q(OUTER_REG_B_q));  // open: clr
  Counter counter_2 (.clk(clock_1_out), .Q(counter_2_q));  // open: clr, load, up, count, D, carry
  Register MAR_Z (.D(counter_2_q), .en(or_29_out), .clk(clock_1_out), .Q(MAR_Z_q));  // open: clr
  RAM #(.dataWidth(24)) INST_RAM (
    .addr(MAR_Z_q), .oe(or_50_out), .clk(clock_1_out), .dout(INST_RAM_dout));  // open: we, din
  // Probe on A3_q
  // Probe on A1_q
  core_16x16 core_16x16_1 (
    .A11_11(A1_q), .A11_12(A2_q), .A11_21(A3_q), .A11_22(A4_q), .A12_11(A5_q), .A12_12(A6_q), .A12_21(A7_q),
    .A12_22(A8_q), .A13_11(A9_q), .A13_12(A10_q), .A13_21(A11_q), .A13_22(A12_q), .A14_11(A13_q),
    .A14_12(A14_q), .A14_21(A15_q), .A14_22(A16_q), .A15_11(A17_q), .A15_12(A18_q), .A15_21(A19_q),
    .A15_22(A20_q), .A16_11(A21_q), .A16_12(A22_q), .A16_21(A23_q), .A16_22(A24_q), .A17_11(A25_q),
    .A17_12(A26_q), .A17_21(A27_q), .A17_22(A28_q), .A18_11(A29_q), .A18_12(A30_q), .A18_21(A31_q),
    .A18_22(A32_q), .B11_11(B1_q), .B11_12(B2_q), .B11_21(B3_q), .B11_22(B4_q), .B21_11(B5_q), .B21_12(B6_q),
    .B21_21(B7_q), .B21_22(B8_q), .B31_11(B9_q), .B31_12(B10_q), .B31_21(B11_q), .B31_22(B12_q),
    .B41_11(B13_q), .B41_12(B14_q), .B41_21(B15_q), .B41_22(B16_q), .B51_11(B17_q), .B51_12(B18_q),
    .B51_21(B19_q), .B51_22(B20_q), .B61_11(B21_q), .B61_12(B22_q), .B61_21(B23_q), .B61_22(B24_q),
    .B71_11(B25_q), .B71_12(B26_q), .B71_21(B27_q), .B71_22(B28_q), .B81_11(B29_q), .B81_12(B30_q),
    .B81_21(B31_q), .B81_22(B32_q), .R11(core_16x16_1_r11), .R12(core_16x16_1_r12), .R21(core_16x16_1_r21),
    .R22(core_16x16_1_r22));
  Counter #(.max('hf)) ROW_COUNTER (
    .clk(clock_1_out), .D(undriven), .Q(ROW_COUNTER_q));  // open: clr, load, up, count, carry
  // Probe on A2_q
  // Probe on A4_q
  // Probe on core_16x16_1_r11
  // Probe on core_16x16_1_r12
  // Probe on core_16x16_1_r21
  // Probe on core_16x16_1_r22
  RAM #(.dataWidth(64)) ram_1 (.clk(clock_1_out), .din(core_16x16_1_r11));  // open: addr, we, oe, dout
  RAM #(.dataWidth(64)) ram_2 (.clk(clock_1_out), .din(core_16x16_1_r12));  // open: addr, we, oe, dout
  assign controlled_buffer_1_out = or_26_out ? instruction_splitter_1_add_a : 8'bz;  // Controlled_Buffer controlled_buffer_1
  assign controlled_buffer_1_out = or_27_out ? bit_extender_1_out : 8'bz;  // Controlled_Buffer controlled_buffer_2
  assign controlled_buffer_1_out = or_25_out ? instruction_splitter_1_add_b : 8'bz;  // Controlled_Buffer controlled_buffer_3
  Controlled_Buffer #(.width(8)) controlled_buffer_4 (
    .in(instruction_splitter_1_add_a), .out(controlled_buffer_4_out));  // open: en
  Adder adder_1 (.a(8'h2), .b(ROW_COUNTER_q), .out(adder_1_out));  // open: cin, cout
  assign bit_extender_1_out = {{4{instruction_splitter_1_flg[3]}}, instruction_splitter_1_flg};  // Bit_Extender bit_extender_1
  instruction_splitter instruction_splitter_1 (
    .WE(or_35_out), .CLOCK(clock_1_out), .instruction(INST_RAM_dout), .FLG(instruction_splitter_1_flg),
    .OPCODE(instruction_splitter_1_opcode), .ADD_A(instruction_splitter_1_add_a),
    .ADD_B(instruction_splitter_1_add_b));
  assign controlled_buffer_4_out = in_2 ? adder_1_out : 8'bz;  // Controlled_Buffer controlled_buffer_5
  Register MAR_A (.D(controlled_buffer_4_out), .en(in_1), .clk(clock_1_out), .Q(MAR_A_q));  // open: clr
  RAM #(.dataWidth(64)) ram_3 (.clk(clock_1_out), .din(core_16x16_1_r21));  // open: addr, we, oe, dout
  RAM #(.dataWidth(64)) ram_4 (.clk(clock_1_out), .din(core_16x16_1_r22));  // open: addr, we, oe, dout
  Register MAR_B (.D(instruction_splitter_1_add_b), .en(or_32_out), .clk(clock_1_out), .Q(MAR_B_q));  // open: clr
  Register #(.width(64)) B1 (.D(MBR_B_q), .en(decoder_4bit_2_zero), .clk(clock_1_out), .Q(B1_q));  // open: clr
  Register #(.width(64)) B5 (.D(MBR_B_q), .en(decoder_4bit_2_two), .clk(clock_1_out), .Q(B5_q));  // open: clr
  Register #(.width(64)) B9 (.D(MBR_B_q), .en(decoder_4bit_2_four), .clk(clock_1_out), .Q(B9_q));  // open: clr
  Register #(.width(64)) B13 (.D(MBR_B_q), .en(decoder_4bit_2_six), .clk(clock_1_out), .Q(B13_q));  // open: clr
  Register #(.width(64)) B17 (.D(MBR_B_q), .en(decoder_4bit_2_eight), .clk(clock_1_out), .Q(B17_q));  // open: clr
  Register #(.width(64)) B25 (.D(MBR_B_q), .en(decoder_4bit_2_twelve), .clk(clock_1_out), .Q(B25_q));  // open: clr
  Register #(.width(64)) B21 (.D(MBR_B_q), .en(decoder_4bit_2_ten), .clk(clock_1_out), .Q(B21_q));  // open: clr
  Register #(.width(64)) B29 (.D(MBR_B_q), .en(decoder_4bit_2_fourteen), .clk(clock_1_out), .Q(B29_q));  // open: clr
  Register #(.width(64)) B2 (.D(MBR_B_COPY_q), .en(decoder_4bit_2_zero), .clk(clock_1_out), .Q(B2_q));  // open: clr
  Register #(.width(64)) B6 (.D(MBR_B_COPY_q), .en(decoder_4bit_2_two), .clk(clock_1_out), .Q(B6_q));  // open: clr
  Register #(.width(64)) B10 (.D(MBR_B_COPY_q), .en(decoder_4bit_2_four), .clk(clock_1_out), .Q(B10_q));  // open: clr
  Register #(.width(64)) B14 (.D(MBR_B_COPY_q), .en(decoder_4bit_2_six), .clk(clock_1_out), .Q(B14_q));  // open: clr
  assign controlled_buffer_6_out = or_31_out ? MAR_B_q : 8'bz;  // Controlled_Buffer controlled_buffer_6
  Register #(.width(64)) B18 (.D(MBR_B_COPY_q), .en(decoder_4bit_2_eight), .clk(clock_1_out), .Q(B18_q));  // open: clr
  Register #(.width(64)) B22 (.D(MBR_B_COPY_q), .en(decoder_4bit_2_ten), .clk(clock_1_out), .Q(B22_q));  // open: clr
  Register #(.width(64)) B26 (.D(MBR_B_COPY_q), .en(decoder_4bit_2_twelve), .clk(clock_1_out), .Q(B26_q));  // open: clr
  Register #(.width(64)) B30 (
    .D(MBR_B_COPY_q), .en(decoder_4bit_2_fourteen), .clk(clock_1_out), .Q(B30_q));  // open: clr
  Register #(.width(64)) B3 (.D(MBR_B_q), .en(decoder_4bit_2_one), .clk(clock_1_out), .Q(B3_q));  // open: clr
  Register #(.width(64)) B7 (.D(MBR_B_q), .en(decoder_4bit_2_three), .clk(clock_1_out), .Q(B7_q));  // open: clr
  Register #(.width(64)) B11 (.D(MBR_B_q), .en(decoder_4bit_2_five), .clk(clock_1_out), .Q(B11_q));  // open: clr
  Register #(.width(64)) B15 (.D(MBR_B_q), .en(decoder_4bit_2_seven), .clk(clock_1_out), .Q(B15_q));  // open: clr
  Register #(.width(64)) B19 (.D(MBR_B_q), .en(decoder_4bit_2_nine), .clk(clock_1_out), .Q(B19_q));  // open: clr
  Counter #(.max('hf), .width(4)) DECODER_COUNTER_B (
    .count(or_42_out), .clk(clock_1_out), .Q(DECODER_COUNTER_B_q));  // open: clr, load, up, D, carry
  Register #(.width(64)) B23 (.D(MBR_B_q), .en(decoder_4bit_2_eleven), .clk(clock_1_out), .Q(B23_q));  // open: clr
  Register #(.width(64)) B27 (.D(MBR_B_q), .en(decoder_4bit_2_thirteen), .clk(clock_1_out), .Q(B27_q));  // open: clr
  Register #(.width(64)) B31 (.D(MBR_B_q), .en(decoder_4bit_2_fifteen), .clk(clock_1_out), .Q(B31_q));  // open: clr
  Register #(.width(64)) B4 (.D(MBR_B_COPY_q), .en(decoder_4bit_2_one), .clk(clock_1_out), .Q(B4_q));  // open: clr
  Register #(.width(64)) B8 (.D(MBR_B_COPY_q), .en(decoder_4bit_2_three), .clk(clock_1_out), .Q(B8_q));  // open: clr
  Register #(.width(64)) B12 (.D(MBR_B_COPY_q), .en(decoder_4bit_2_five), .clk(clock_1_out), .Q(B12_q));  // open: clr
  Register #(.width(64)) B16 (.D(MBR_B_COPY_q), .en(decoder_4bit_2_seven), .clk(clock_1_out), .Q(B16_q));  // open: clr
  Register #(.width(64)) B20 (.D(MBR_B_COPY_q), .en(decoder_4bit_2_nine), .clk(clock_1_out), .Q(B20_q));  // open: clr
  Register #(.width(64)) B24 (.D(MBR_B_COPY_q), .en(decoder_4bit_2_eleven), .clk(clock_1_out), .Q(B24_q));  // open: clr
  Register #(.width(64)) B28 (
    .D(MBR_B_COPY_q), .en(decoder_4bit_2_thirteen), .clk(clock_1_out), .Q(B28_q));  // open: clr
  Register #(.width(64)) B32 (
    .D(MBR_B_COPY_q), .en(decoder_4bit_2_fifteen), .clk(clock_1_out), .Q(B32_q));  // open: clr
  decoder_4bit decoder_4bit_2 (
    .OE(DECODER_COUNTER_B_q[3]), .A(DECODER_COUNTER_B_q[2]), .B(DECODER_COUNTER_B_q[1]),
    .C(DECODER_COUNTER_B_q[0]), .zero(decoder_4bit_2_zero), .one(decoder_4bit_2_one),
    .two(decoder_4bit_2_two), .three(decoder_4bit_2_three), .four(decoder_4bit_2_four),
    .five(decoder_4bit_2_five), .six(decoder_4bit_2_six), .seven(decoder_4bit_2_seven),
    .eight(decoder_4bit_2_eight), .nine(decoder_4bit_2_nine), .ten(decoder_4bit_2_ten),
    .eleven(decoder_4bit_2_eleven), .twelve(decoder_4bit_2_twelve), .thirteen(decoder_4bit_2_thirteen),
    .fourteen(decoder_4bit_2_fourteen), .fifteen(decoder_4bit_2_fifteen));  // open: D
  Counter COL_COUNTER (.clk(clock_1_out), .Q(COL_COUNTER_q));  // open: clr, load, up, count, D, carry
  RAM #(.dataWidth(64)) RAM_B (
    .addr(controlled_buffer_6_out), .oe(or_48_out), .clk(clock_1_out), .dout(RAM_B_dout));  // open: we, din
  Register register_1 (.D(adder_3_out), .en(clock_1_out), .clk(clock_1_out), .Q(controlled_buffer_6_out));  // open: clr
  Adder adder_2 (.a(controlled_buffer_6_out), .b(8'h1), .out(adder_2_out));  // open: cin, cout
  Register #(.width(4)) OP_CODE_REGISTER (
    .D(instruction_splitter_1_opcode), .en(or_30_out), .clk(clock_1_out), .Q(OP_CODE_REGISTER_q));  // open: clr
  RAM #(.dataWidth(64)) ram_5 (
    .addr(adder_2_out), .oe(or_38_out), .clk(clock_1_out), .dout(ram_5_dout));  // open: we, din
  Adder adder_3 (.a(controlled_buffer_6_out), .b(8'h2), .out(adder_3_out));  // open: cin, cout
  Register #(.width(64)) MBR_B (.D(RAM_B_dout), .en(or_44_out), .clk(clock_1_out), .Q(MBR_B_q));  // open: clr
  Comparator comparator_1 (
    .a(OUTER_REG_B_q), .b(COL_COUNTER_q), .gt(comparator_1_gt), .eq(comparator_1_gt));  // open: lt
  Register #(.width(64)) MBR_B_COPY (.D(ram_5_dout), .en(or_44_out), .clk(clock_1_out), .Q(MBR_B_COPY_q));  // open: clr
  Counter STEP_COUNTER (.clk(clock_1_out), .Q(STEP_COUNTER_q));  // open: clr, load, up, count, D, carry
  // OR_Gate or_1 has open pins: in0=rom_1_data[14], in1=in_3, out=open
  // OR_Gate or_2 has open pins: in0=rom_1_data[15], in1=in_4, out=open
  // OR_Gate or_3 has open pins: in0=rom_1_data[16], in1=in_5, out=open
  // OR_Gate or_4 has open pins: in0=rom_1_data[17], in1=in_6, out=open
  // OR_Gate or_5 has open pins: in0=rom_1_data[18], in1=in_7, out=open
  // OR_Gate or_6 has open pins: in0=rom_1_data[19], in1=in_8, out=open
  // OR_Gate or_7 has open pins: in0=rom_1_data[20], in1=in_9, out=open
  // OR_Gate or_8 has open pins: in0=rom_1_data[21], in1=in_10, out=open
  // OR_Gate or_9 has open pins: in0=rom_1_data[22], in1=in_11, out=open
  // OR_Gate or_10 has open pins: in0=rom_1_data[23], in1=in_12, out=open
  // OR_Gate or_11 has open pins: in0=rom_1_data[24], in1=in_13, out=open
  // OR_Gate or_12 has open pins: in0=rom_1_data[25], in1=in_14, out=open
  // OR_Gate or_13 has open pins: in0=rom_1_data[26], in1=in_15, out=open
  // OR_Gate or_14 has open pins: in0=rom_1_data[27], in1=in_16, out=open
  // OR_Gate or_15 has open pins: in0=rom_1_data[28], in1=in_17, out=open
  // OR_Gate or_16 has open pins: in0=rom_1_data[29], in1=in_18, out=open
  // OR_Gate or_17 has open pins: in0=rom_1_data[30], in1=in_19, out=open
  // OR_Gate or_18 has open pins: in0=rom_1_data[31], in1=in_20, out=open
  // OR_Gate or_19 has open pins: in0=rom_1_data[32], in1=in_21, out=open
  // OR_Gate or_20 has open pins: in0=rom_1_data[33], in1=in_22, out=open
  // OR_Gate or_21 has open pins: in0=rom_1_data[34], in1=in_23, out=open
  // OR_Gate or_22 has open pins: in0=rom_1_data[35], in1=in_24, out=open
  // OR_Gate or_23 has open pins: in0=rom_1_data[36], in1=in_25, out=open
  // OR_Gate or_24 has open pins: in0=rom_1_data[37], in1=in_26, out=open
  or or_25 (or_25_out, rom_1_data[38], ADD_B_CTRL_BUFFER);
  or or_26 (or_26_out, rom_1_data[39], ADD_A_CTRL_BUFFER);
  or or_27 (or_27_out, rom_1_data[40], OPCODE_CTRL_BUFFER);
  or or_28 (or_28_out, rom_1_data[41], RAM_A_OE_COPY);
  or or_29 (or_29_out, rom_1_data[42], MAR_Z_WE);
  or or_30 (or_30_out, rom_1_data[43], OPCODE_REG_WE);
  or or_31 (or_31_out, rom_1_data[44], MAR_B_CTRL_BUFF);
  or or_32 (or_32_out, rom_1_data[45], MAR_B_WE);
  or or_33 (or_33_out, rom_1_data[46], MAR_A_CTRL_BUFF);
  or or_34 (or_34_out, rom_1_data[47], MAR_A_WE);
  or or_35 (or_35_out, rom_1_data[48], INST_SPLITTER_WE);
  // OR_Gate or_36 has open pins: in0=rom_1_data[49], in1=in_38, out=open
  // OR_Gate or_37 has open pins: in0=rom_1_data[50], in1=in_39, out=open
  or or_38 (or_38_out, rom_1_data[51], RAM_B_OE_COPY);
  or or_39 (or_39_out, rom_1_data[52], OUTER_DIM_REG_B_WE);
  or or_40 (or_40_out, rom_1_data[53], OUTER_DIM_REG_A_WE);
  or or_41 (or_41_out, rom_1_data[54], INNER_DIM_REG_WE);
  or or_42 (or_42_out, rom_1_data[55], DECODER_COUNTER_B_G5);
  or or_43 (or_43_out, rom_1_data[56], DECODER_COUNTER_A_G5);
  or or_44 (or_44_out, rom_1_data[57], MBR_B_WE);
  or or_45 (or_45_out, rom_1_data[58], MBR_A_WE);
  or or_46 (or_46_out, rom_1_data[59], SCRATCH_RAM_WE);
  or or_47 (or_47_out, rom_1_data[60], SCRATCH_RAM_OE);
  or or_48 (or_48_out, rom_1_data[61], RAM_B_OE);
  or or_49 (or_49_out, rom_1_data[62], RAM_A_OE);
  or or_50 (or_50_out, rom_1_data[63], INST_RAM_OE);
  ROM #(.addrWidth(16), .dataWidth(64)) rom_1 (
    .addr({instruction_splitter_1_flg, OP_CODE_REGISTER_q, STEP_COUNTER_q}), .data(rom_1_data));
endmodule

module Assembly_remastered (
  input  PC_G5,
  input  MAR_Z_WE,
  input  INST_RAM_OE,
  input  INST_SPLITTER_WE,
  input  SYST_RAM_CTR_G5,
  input  FLAG_REG_WE,
  input  OPCODE_REG_WE,
  input  MAR_A_WE,
  input  MAR_B_WE,
  input  SYST_RAM_WE,
  input  SYST_RAM_OE,
  input  INNER_DIM_REG_WE,
  input  OUTER_DIM_REG_A_WE,
  input  OUTER_DIM_REG_B_WE,
  input  RAM_A_OE,
  input  RAM_B_OE,
  input  MBR_A_WE,
  input  MBR_B_WE,
  input  MBR_Z_WE,
  input  RAM_A_CTR_CB,
  input  MAR_A_CB,
  input  RAM_A_CTR_G5,
  input  MAR_B_CB,
  input  RAM_B_COUNTER_CB,
  input  RAM_B_COUNTER_G5,
  input  reset,
  input  DECODER_counter_A_G5,
  input  DECODER_OE,
  input  in_29,
  input  in_30,
  input  in_31,
  input  in_32,
  input  in_33,
  input  in_34,
  input  in_35,
  input  in_36,
  input  in_37,
  input  in_38,
  input  in_39,
  input  in_40,
  input  in_41,
  input  in_42,
  input  in_43,
  input  in_44,
  input  in_45,
  input  in_46,
  input  in_47,
  input  in_48,
  input  in_49,
  input  in_50,
  input  in_51,
  input  in_52,
  input  in_53,
  input  in_54,
  input  in_55,
  input  in_56,
  input  in_57,
  input  in_58,
  input  in_59,
  input  in_60,
  input  in_61,
  input  in_62,
  input  in_63,
  input  in_64
);

  wire clock_1_out, decoder_4bit_1_eight, decoder_4bit_1_eleven, decoder_4bit_1_fifteen, decoder_4bit_1_five,
       decoder_4bit_1_four, decoder_4bit_1_fourteen, decoder_4bit_1_nine, decoder_4bit_1_one,
       decoder_4bit_1_seven, decoder_4bit_1_six, decoder_4bit_1_ten, decoder_4bit_1_thirteen,
       decoder_4bit_1_three, decoder_4bit_1_twelve, decoder_4bit_1_two, decoder_4bit_1_zero,
       decoder_4bit_2_eight, decoder_4bit_2_eleven, decoder_4bit_2_fifteen, decoder_4bit_2_five,
       decoder_4bit_2_four, decoder_4bit_2_fourteen, decoder_4bit_2_nine, decoder_4bit_2_one,
       decoder_4bit_2_seven, decoder_4bit_2_six, decoder_4bit_2_ten, decoder_4bit_2_thirteen,
       decoder_4bit_2_three, decoder_4bit_2_twelve, decoder_4bit_2_two, decoder_4bit_2_zero, or_1_out,
       or_2_out, or_3_out, or_4_out, or_5_out, or_6_out, or_7_out, or_8_out, or_9_out, or_10_out, or_11_out,
       or_12_out, or_13_out, or_14_out, or_15_out, or_16_out, or_17_out, or_18_out, or_19_out, or_20_out,
       or_21_out, or_22_out, or_23_out, or_24_out, or_25_out, or_26_out, or_27_out, or_28_out;
  wire [3:0] Decoder_Counter_A_q, dim_splitter_1_flag, FLAG_REG_q, instruction_splitter_1_flg,
       instruction_splitter_1_opcode, OPCODE_REG_q;
  wire [7:0] clock_counter_q, controlled_buffer_1_out, controlled_buffer_2_out, dim_splitter_1_add_a,
       dim_splitter_1_add_b, instruction_splitter_1_add_a, instruction_splitter_1_add_b, MAR_A_q, MAR_B_q,
       RAM_A_COUNTER_q, RAM_B_COUNTER_q, Syst_Ram_Counter_q;
  wire [9:0] MAR_Z_q, Program_Counter_q;
  wire [19:0] SYST_RAM_dout;
  wire [23:0] INST_RAM_dout, MBR_Z_q;
  wire [63:0] A1_q, A2_q, A3_q, A4_q, A5_q, A6_q, A7_q, A8_q, A9_q, A10_q, A11_q, A12_q, MBR_A_COPY_q,
       MBR_A_q, MBR_B_COPY_q, MBR_B_q, RAM_A1_dout, RAM_A2_dout, RAM_B1_dout, RAM_B2_dout, rom_1_data;

  Counter clock_counter (.clr(or_26_out), .clk(clock_1_out), .Q(clock_counter_q));  // open: load, up, count, D, carry
  ROM #(.addrWidth(16), .dataWidth(64)) rom_1 (.addr({FLAG_REG_q, OPCODE_REG_q, clock_counter_q}), .data(rom_1_data));
  or or_1 (or_1_out, rom_1_data[63], PC_G5);
  or or_2 (or_2_out, rom_1_data[62], MAR_Z_WE);
  or or_3 (or_3_out, rom_1_data[61], INST_RAM_OE);
  or or_4 (or_4_out, rom_1_data[60], INST_SPLITTER_WE);
  or or_5 (or_5_out, rom_1_data[59], SYST_RAM_CTR_G5);
  or or_6 (or_6_out, rom_1_data[58], FLAG_REG_WE);
  or or_7 (or_7_out, rom_1_data[57], OPCODE_REG_WE);
  or or_8 (or_8_out, rom_1_data[56], MAR_A_WE);
  or or_9 (or_9_out, rom_1_data[55], MAR_B_WE);
  or or_10 (or_10_out, rom_1_data[54], SYST_RAM_WE);
  or or_11 (or_11_out, rom_1_data[53], SYST_RAM_OE);
  or or_12 (or_12_out, rom_1_data[52], INNER_DIM_REG_WE);
  or or_13 (or_13_out, rom_1_data[51], OUTER_DIM_REG_A_WE);
  or or_14 (or_14_out, rom_1_data[50], OUTER_DIM_REG_B_WE);
  or or_15 (or_15_out, rom_1_data[49], RAM_A_OE);
  or or_16 (or_16_out, rom_1_data[48], RAM_B_OE);
  or or_17 (or_17_out, rom_1_data[47], MBR_A_WE);
  or or_18 (or_18_out, rom_1_data[46], MBR_B_WE);
  or or_19 (or_19_out, rom_1_data[45], MBR_Z_WE);
  or or_20 (or_20_out, rom_1_data[44], RAM_A_CTR_CB);
  or or_21 (or_21_out, rom_1_data[43], MAR_A_CB);
  or or_22 (or_22_out, rom_1_data[42], RAM_A_CTR_G5);
  or or_23 (or_23_out, rom_1_data[41], MAR_B_CB);
  or or_24 (or_24_out, rom_1_data[40], RAM_B_COUNTER_CB);
  or or_25 (or_25_out, rom_1_data[39], RAM_B_COUNTER_G5);
  or or_26 (or_26_out, rom_1_data[38], reset);
  or or_27 (or_27_out, rom_1_data[37], DECODER_counter_A_G5);
  or or_28 (or_28_out, rom_1_data[36], DECODER_OE);
  // OR_Gate or_29 has open pins: in0=rom_1_data[35], in1=in_29, out=open
  // OR_Gate or_30 has open pins: in0=rom_1_data[34], in1=in_30, out=open
  // OR_Gate or_31 has open pins: in0=rom_1_data[33], in1=in_31, out=open
  // OR_Gate or_32 has open pins: in0=rom_1_data[32], in1=in_32, out=open
  // OR_Gate or_33 has open pins: in0=rom_1_data[31], in1=in_33, out=open
  // OR_Gate or_34 has open pins: in0=rom_1_data[30], in1=in_34, out=open
  // OR_Gate or_35 has open pins: in0=rom_1_data[29], in1=in_35, out=open
  // OR_Gate or_36 has open pins: in0=rom_1_data[28], in1=in_36, out=open
  // OR_Gate or_37 has open pins: in0=rom_1_data[27], in1=in_37, out=open
  // OR_Gate or_38 has open pins: in0=rom_1_data[26], in1=in_38, out=open
  // OR_Gate or_39 has open pins: in0=rom_1_data[25], in1=in_39, out=open
  // OR_Gate or_40 has open pins: in0=rom_1_data[24], in1=in_40, out=open
  // OR_Gate or_41 has open pins: in0=rom_1_data[23], in1=in_41, out=open
  // OR_Gate or_42 has open pins: in0=rom_1_data[22], in1=in_42, out=open
  // OR_Gate or_43 has open pins: in0=rom_1_data[21], in1=in_43, out=open
  // OR_Gate or_44 has open pins: in0=rom_1_data[20], in1=in_44, out=open
  // OR_Gate or_45 has open pins: in0=rom_1_data[19], in1=in_45, out=open
  // OR_Gate or_46 has open pins: in0=rom_1_data[18], in1=in_46, out=open
  // OR_Gate or_47 has open pins: in0=rom_1_data[17], in1=in_47, out=open
  // OR_Gate or_48 has open pins: in0=rom_1_data[16], in1=in_48, out=open
  // OR_Gate or_49 has open pins: in0=rom_1_data[15], in1=in_49, out=open
  // OR_Gate or_50 has open pins: in0=rom_1_data[14], in1=in_50, out=open
  // OR_Gate or_51 has open pins: in0=rom_1_data[13], in1=in_51, out=open
  // OR_Gate or_52 has open pins: in0=rom_1_data[12], in1=in_52, out=open
  // OR_Gate or_53 has open pins: in0=rom_1_data[11], in1=in_53, out=open
  // OR_Gate or_54 has open pins: in0=rom_1_data[10], in1=in_54, out=open
  // OR_Gate or_55 has open pins: in0=rom_1_data[9], in1=in_55, out=open
  // OR_Gate or_56 has open pins: in0=rom_1_data[8], in1=in_56, out=open
  // OR_Gate or_57 has open pins: in0=rom_1_data[7], in1=in_57, out=open
  // OR_Gate or_58 has open pins: in0=rom_1_data[6], in1=in_58, out=open
  // OR_Gate or_59 has open pins: in0=rom_1_data[5], in1=in_59, out=open
  // OR_Gate or_60 has open pins: in0=rom_1_data[4], in1=in_60, out=open
  // OR_Gate or_61 has open pins: in0=rom_1_data[3], in1=in_61, out=open
  // OR_Gate or_62 has open pins: in0=rom_1_data[2], in1=in_62, out=open
  // OR_Gate or_63 has open pins: in0=rom_1_data[1], in1=in_63, out=open
  // OR_Gate or_64 has open pins: in0=rom_1_data[0], in1=in_64, out=open
  Counter #(.max('h3ff), .width(10)) Program_Counter (
    .count(or_1_out), .clk(clock_1_out), .Q(Program_Counter_q));  // open: clr, load, up, D, carry
  Register #(.width(10)) MAR_Z (.D(Program_Counter_q), .en(or_2_out), .clk(clock_1_out), .Q(MAR_Z_q));  // open: clr
  RAM #(.addrWidth(10), .dataWidth(24), .\type ("nonvolatile")) INST_RAM (
    .addr(MAR_Z_q), .oe(or_3_out), .clk(clock_1_out), .dout(INST_RAM_dout));  // open: we, din
  Register #(.width(24)) MBR_Z (.D(INST_RAM_dout), .en(or_19_out), .clk(clock_1_out), .Q(MBR_Z_q));  // open: clr
  Clock clock_1 (.out(clock_1_out));
  Counter Syst_Ram_Counter (
    .count(or_5_out), .clk(clock_1_out), .Q(Syst_Ram_Counter_q));  // open: clr, load, up, D, carry
  instruction_splitter instruction_splitter_1 (
    .WE(or_4_out), .CLOCK(clock_1_out), .instruction(MBR_Z_q), .FLG(instruction_splitter_1_flg),
    .OPCODE(instruction_splitter_1_opcode), .ADD_A(instruction_splitter_1_add_a),
    .ADD_B(instruction_splitter_1_add_b));
  Counter RAM_A_COUNTER (.count(or_22_out), .clk(clock_1_out), .Q(RAM_A_COUNTER_q));  // open: clr, load, up, D, carry
  Counter RAM_B_COUNTER (.count(or_25_out), .clk(clock_1_out), .Q(RAM_B_COUNTER_q));  // open: clr, load, up, D, carry
  assign controlled_buffer_1_out = or_24_out ? RAM_B_COUNTER_q : 8'bz;  // Controlled_Buffer controlled_buffer_1
  assign controlled_buffer_2_out = or_21_out ? instruction_splitter_1_add_a : 8'bz;  // Controlled_Buffer controlled_buffer_2
  assign controlled_buffer_2_out = or_20_out ? RAM_A_COUNTER_q : 8'bz;  // Controlled_Buffer controlled_buffer_3
  assign controlled_buffer_1_out = or_23_out ? instruction_splitter_1_add_b : 8'bz;  // Controlled_Buffer controlled_buffer_4
  Register #(.width(4)) FLAG_REG (
    .D(instruction_splitter_1_flg), .en(or_6_out), .clk(clock_1_out), .Q(FLAG_REG_q));  // open: clr
  Register #(.width(4)) OPCODE_REG (
    .D(instruction_splitter_1_opcode), .en(or_7_out), .clk(clock_1_out), .Q(OPCODE_REG_q), .clr(or_26_out));
  Register MAR_A (.D(controlled_buffer_2_out), .en(or_8_out), .clk(clock_1_out), .Q(MAR_A_q));  // open: clr
  Register MAR_B (.D(controlled_buffer_1_out), .en(or_9_out), .clk(clock_1_out), .Q(MAR_B_q));  // open: clr
  RAM #(.dataWidth(20)) SYST_RAM (
    .addr(Syst_Ram_Counter_q), .we(or_10_out), .oe(or_11_out), .clk(clock_1_out),
    .din({instruction_splitter_1_flg, instruction_splitter_1_add_a, instruction_splitter_1_add_b}),
    .dout(SYST_RAM_dout));
  Dim_Splitter dim_splitter_1 (
    .DIN(SYST_RAM_dout), .FLAG(dim_splitter_1_flag), .ADD_A(dim_splitter_1_add_a),
    .ADD_B(dim_splitter_1_add_b));
  RAM #(.asyncread("true"), .dataWidth(64), .\type ("nonvolatile")) RAM_A1 (
    .addr(MAR_A_q), .oe(or_15_out), .clk(clock_1_out), .dout(RAM_A1_dout));  // open: we, din
  RAM #(.asyncread("true"), .dataWidth(64), .\type ("nonvolatile")) RAM_A2 (
    .addr(MAR_A_q), .oe(or_15_out), .clk(clock_1_out), .dout(RAM_A2_dout));  // open: we, din
  Register #(.width(4)) INNER_DIM_REG (.D(dim_splitter_1_flag), .en(or_12_out), .clk(clock_1_out));  // open: Q, clr
  Register OUTER_DIM_A_REG (.D(dim_splitter_1_add_a), .en(or_13_out), .clk(clock_1_out));  // open: Q, clr
  Register OUTER_DIM_B_REG (.D(dim_splitter_1_add_b), .en(or_14_out), .clk(clock_1_out));  // open: Q, clr
  Counter #(.max('hf), .width(4)) Decoder_Counter_A (
    .count(or_27_out), .clk(clock_1_out), .Q(Decoder_Counter_A_q));  // open: clr, load, up, D, carry
  Register #(.width(64)) MBR_A (.D(RAM_A1_dout), .en(or_17_out), .clk(clock_1_out), .Q(MBR_A_q));  // open: clr
  Register #(.width(64)) MBR_A_COPY (
    .D(RAM_A2_dout), .en(or_17_out), .clk(clock_1_out), .Q(MBR_A_COPY_q));  // open: clr
  // Probe on MBR_A_q
  // Probe on MBR_A_COPY_q
  decoder_4bit decoder_4bit_1 (
    .OE(or_28_out), .A(Decoder_Counter_A_q[3]), .B(Decoder_Counter_A_q[2]), .C(Decoder_Counter_A_q[1]),
    .D(Decoder_Counter_A_q[0]), .zero(decoder_4bit_1_zero), .one(decoder_4bit_1_one),
    .two(decoder_4bit_1_two), .three(decoder_4bit_1_three), .four(decoder_4bit_1_four),
    .five(decoder_4bit_1_five), .six(decoder_4bit_1_six), .seven(decoder_4bit_1_seven),
    .eight(decoder_4bit_1_eight), .nine(decoder_4bit_1_nine), .ten(decoder_4bit_1_ten),
    .eleven(decoder_4bit_1_eleven), .twelve(decoder_4bit_1_twelve), .thirteen(decoder_4bit_1_thirteen),
    .fourteen(decoder_4bit_1_fourteen), .fifteen(decoder_4bit_1_fifteen));
  Register #(.width(64)) A1 (.D(MBR_A_q), .en(decoder_4bit_1_zero), .clk(clock_1_out), .Q(A1_q));  // open: clr
  Register #(.width(64)) A5 (.D(MBR_A_q), .en(decoder_4bit_1_two), .clk(clock_1_out), .Q(A5_q));  // open: clr
  Register #(.width(64)) A9 (.D(MBR_A_q), .en(decoder_4bit_1_four), .clk(clock_1_out), .Q(A9_q));  // open: clr
  Register #(.width(64)) A13 (.D(MBR_A_q), .en(decoder_4bit_1_six), .clk(clock_1_out));  // open: Q, clr
  Register #(.width(64)) A17 (.D(MBR_A_q), .en(decoder_4bit_1_eight), .clk(clock_1_out));  // open: Q, clr
  Register #(.width(64)) A21 (.D(MBR_A_q), .en(decoder_4bit_1_ten), .clk(clock_1_out));  // open: Q, clr
  Register #(.width(64)) A25 (.D(MBR_A_q), .en(decoder_4bit_1_twelve), .clk(clock_1_out));  // open: Q, clr
  Register #(.width(64)) A29 (.D(MBR_A_q), .en(decoder_4bit_1_fourteen), .clk(clock_1_out));  // open: Q, clr
  Register #(.width(64)) A2 (.D(MBR_A_COPY_q), .en(decoder_4bit_1_zero), .clk(clock_1_out), .Q(A2_q));  // open: clr
  Register #(.width(64)) A10 (.D(MBR_A_COPY_q), .en(decoder_4bit_1_four), .clk(clock_1_out), .Q(A10_q));  // open: clr
  Register #(.width(64)) A6 (.D(MBR_A_COPY_q), .en(decoder_4bit_1_two), .clk(clock_1_out), .Q(A6_q));  // open: clr
  Register #(.width(64)) A14 (.D(MBR_A_COPY_q), .en(decoder_4bit_1_six), .clk(clock_1_out));  // open: Q, clr
  Register #(.width(64)) A18 (.D(MBR_A_COPY_q), .en(decoder_4bit_1_eight), .clk(clock_1_out));  // open: Q, clr
  Register #(.width(64)) A22 (.D(MBR_A_COPY_q), .en(decoder_4bit_1_ten), .clk(clock_1_out));  // open: Q, clr
  Register #(.width(64)) A26 (.D(MBR_A_COPY_q), .en(decoder_4bit_1_twelve), .clk(clock_1_out));  // open: Q, clr
  Register #(.width(64)) A30 (.D(MBR_A_COPY_q), .en(decoder_4bit_1_fourteen), .clk(clock_1_out));  // open: Q, clr
  Register #(.width(64)) A3 (.D(MBR_A_q), .en(decoder_4bit_1_one), .clk(clock_1_out), .Q(A3_q));  // open: clr
  Register #(.width(64)) A7 (.D(MBR_A_q), .en(decoder_4bit_1_three), .clk(clock_1_out), .Q(A7_q));  // open: clr
  Register #(.width(64)) A11 (.D(MBR_A_q), .en(decoder_4bit_1_five), .clk(clock_1_out), .Q(A11_q));  // open: clr
  Register #(.width(64)) A15 (.D(MBR_A_q), .en(decoder_4bit_1_seven), .clk(clock_1_out));  // open: Q, clr
  Register #(.width(64)) A19 (.D(MBR_A_q), .en(decoder_4bit_1_nine), .clk(clock_1_out));  // open: Q, clr
  Register #(.width(64)) A23 (.D(MBR_A_q), .en(decoder_4bit_1_eleven), .clk(clock_1_out));  // open: Q, clr
  Register #(.width(64)) A27 (.D(MBR_A_q), .en(decoder_4bit_1_thirteen), .clk(clock_1_out));  // open: Q, clr
  Register #(.width(64)) A31 (.D(MBR_A_q), .en(decoder_4bit_1_fifteen), .clk(clock_1_out));  // open: Q, clr
  Register #(.width(64)) A4 (.D(MBR_A_COPY_q), .en(decoder_4bit_1_one), .clk(clock_1_out), .Q(A4_q));  // open: clr
  Register #(.width(64)) A12 (.D(MBR_A_COPY_q), .en(decoder_4bit_1_five), .clk(clock_1_out), .Q(A12_q));  // open: clr
  Register #(.width(64)) A8 (.D(MBR_A_COPY_q), .en(decoder_4bit_1_three), .clk(clock_1_out), .Q(A8_q));  // open: clr
  Register #(.width(64)) A16 (.D(MBR_A_COPY_q), .en(decoder_4bit_1_seven), .clk(clock_1_out));  // open: Q, clr
  Register #(.width(64)) A20 (.D(MBR_A_COPY_q), .en(decoder_4bit_1_nine), .clk(clock_1_out));  // open: Q, clr
  Register #(.width(64)) A24 (.D(MBR_A_COPY_q), .en(decoder_4bit_1_eleven), .clk(clock_1_out));  // open: Q, clr
  Register #(.width(64)) A28 (.D(MBR_A_COPY_q), .en(decoder_4bit_1_thirteen), .clk(clock_1_out));  // open: Q, clr
  Register #(.width(64)) A32 (.D(MBR_A_COPY_q), .en(decoder_4bit_1_fifteen), .clk(clock_1_out));  // open: Q, clr
  RAM #(.dataWidth(64), .\type ("nonvolatile")) RAM_B1 (
    .addr(MAR_B_q), .oe(or_16_out), .clk(clock_1_out), .dout(RAM_B1_dout));  // open: we, din
  RAM #(.dataWidth(64), .\type ("nonvolatile")) RAM_B2 (
    .addr(MAR_B_q), .oe(or_16_out), .clk(clock_1_out), .dout(RAM_B2_dout));  // open: we, din
  core_16x16 core_16x16_1 (
    .A11_11(A1_q), .A11_12(A2_q), .A11_21(A3_q), .A11_22(A4_q), .A12_11(A5_q), .A12_12(A6_q), .A12_21(A7_q),
    .A12_22(A8_q), .A13_11(A9_q), .A13_12(A10_q), .A13_21(A11_q), .A13_22(A12_q));  // open: A14_11, A14_12, A14_21, A14_22, A15_11, A15_12, A15_21, A15_22, A16_11, A16_12, A16_21, A16_22, A17_11, A17_12, A17_21, A17_22, A18_11, A18_12, A18_21, A18_22, B11_11, B11_12, B11_21, B11_22, B21_11, B21_12, B21_21, B21_22, B31_11, B31_12, B31_21, B31_22, B41_11, B41_12, B41_21, B41_22, B51_11, B51_12, B51_21, B51_22, B61_11, B61_12, B61_21, B61_22, B71_11, B71_12, B71_21, B71_22, B81_11, B81_12, B81_21, B81_22, R11, R12, R21, R22
  Register #(.width(64)) MBR_B (.D(RAM_B1_dout), .en(or_18_out), .clk(clock_1_out), .Q(MBR_B_q));  // open: clr
  Register #(.width(64)) MBR_B_COPY (
    .D(RAM_B2_dout), .en(or_18_out), .clk(clock_1_out), .Q(MBR_B_COPY_q));  // open: clr
  decoder_4bit decoder_4bit_2 (
    .OE(Decoder_Counter_A_q[3]), .A(Decoder_Counter_A_q[2]), .B(Decoder_Counter_A_q[1]),
    .C(Decoder_Counter_A_q[0]), .zero(decoder_4bit_2_zero), .one(decoder_4bit_2_one),
    .two(decoder_4bit_2_two), .three(decoder_4bit_2_three), .four(decoder_4bit_2_four),
    .five(decoder_4bit_2_five), .six(decoder_4bit_2_six), .seven(decoder_4bit_2_seven),
    .eight(decoder_4bit_2_eight), .nine(decoder_4bit_2_nine), .ten(decoder_4bit_2_ten),
    .eleven(decoder_4bit_2_eleven), .twelve(decoder_4bit_2_twelve), .thirteen(decoder_4bit_2_thirteen),
    .fourteen(decoder_4bit_2_fourteen), .fifteen(decoder_4bit_2_fifteen));  // open: D
  Register #(.width(64)) B1 (.D(MBR_B_q), .en(decoder_4bit_2_zero), .clk(clock_1_out));  // open: Q, clr
  Register #(.width(64)) B5 (.D(MBR_B_q), .en(decoder_4bit_2_two), .clk(clock_1_out));  // open: Q, clr
  Register #(.width(64)) B9 (.D(MBR_B_q), .en(decoder_4bit_2_four), .clk(clock_1_out));  // open: Q, clr
  Register #(.width(64)) B13 (.D(MBR_B_q), .en(decoder_4bit_2_six), .clk(clock_1_out));  // open: Q, clr
  Register #(.width(64)) B17 (.D(MBR_B_q), .en(decoder_4bit_2_eight), .clk(clock_1_out));  // open: Q, clr
  Register #(.width(64)) B21 (.D(MBR_B_q), .en(decoder_4bit_2_ten), .clk(clock_1_out));  // open: Q, clr
  Register #(.width(64)) B25 (.D(MBR_B_q), .en(decoder_4bit_2_twelve), .clk(clock_1_out));  // open: Q, clr
  Register #(.width(64)) B29 (.D(MBR_B_q), .en(decoder_4bit_2_fourteen), .clk(clock_1_out));  // open: Q, clr
  Register #(.width(64)) B2 (.D(MBR_B_COPY_q), .en(decoder_4bit_2_zero), .clk(clock_1_out));  // open: Q, clr
  Register #(.width(64)) B6 (.D(MBR_B_COPY_q), .en(decoder_4bit_2_two), .clk(clock_1_out));  // open: Q, clr
  Register #(.width(64)) B10 (.D(MBR_B_COPY_q), .en(decoder_4bit_2_four), .clk(clock_1_out));  // open: Q, clr
  Register #(.width(64)) B14 (.D(MBR_B_COPY_q), .en(decoder_4bit_2_six), .clk(clock_1_out));  // open: Q, clr
  Register #(.width(64)) B18 (.D(MBR_B_COPY_q), .en(decoder_4bit_2_eight), .clk(clock_1_out));  // open: Q, clr
  Register #(.width(64)) B22 (.D(MBR_B_COPY_q), .en(decoder_4bit_2_ten), .clk(clock_1_out));  // open: Q, clr
  Register #(.width(64)) B26 (.D(MBR_B_COPY_q), .en(decoder_4bit_2_twelve), .clk(clock_1_out));  // open: Q, clr
  Register #(.width(64)) B30 (.D(MBR_B_COPY_q), .en(decoder_4bit_2_fourteen), .clk(clock_1_out));  // open: Q, clr
  Register #(.width(64)) B3 (.D(MBR_B_q), .en(decoder_4bit_2_one), .clk(clock_1_out));  // open: Q, clr
  Register #(.width(64)) B7 (.D(MBR_B_q), .en(decoder_4bit_2_three), .clk(clock_1_out));  // open: Q, clr
  Register #(.width(64)) B11 (.D(MBR_B_q), .en(decoder_4bit_2_five), .clk(clock_1_out));  // open: Q, clr
  Register #(.width(64)) B15 (.D(MBR_B_q), .en(decoder_4bit_2_seven), .clk(clock_1_out));  // open: Q, clr
  Register #(.width(64)) B19 (.D(MBR_B_q), .en(decoder_4bit_2_nine), .clk(clock_1_out));  // open: Q, clr
  Register #(.width(64)) B23 (.D(MBR_B_q), .en(decoder_4bit_2_eleven), .clk(clock_1_out));  // open: Q, clr
  Register #(.width(64)) B27 (.D(MBR_B_q), .en(decoder_4bit_2_thirteen), .clk(clock_1_out));  // open: Q, clr
  Register #(.width(64)) B31 (.D(MBR_B_q), .en(decoder_4bit_2_fifteen), .clk(clock_1_out));  // open: Q, clr
  Register #(.width(64)) B4 (.D(MBR_B_COPY_q), .en(decoder_4bit_2_one), .clk(clock_1_out));  // open: Q, clr
  Register #(.width(64)) B8 (.D(MBR_B_COPY_q), .en(decoder_4bit_2_three), .clk(clock_1_out));  // open: Q, clr
  Register #(.width(64)) B12 (.D(MBR_B_COPY_q), .en(decoder_4bit_2_five), .clk(clock_1_out));  // open: Q, clr
  Register #(.width(64)) B16 (.D(MBR_B_COPY_q), .en(decoder_4bit_2_seven), .clk(clock_1_out));  // open: Q, clr
  Register #(.width(64)) B20 (.D(MBR_B_COPY_q), .en(decoder_4bit_2_nine), .clk(clock_1_out));  // open: Q, clr
  Register #(.width(64)) B24 (.D(MBR_B_COPY_q), .en(decoder_4bit_2_eleven), .clk(clock_1_out));  // open: Q, clr
  Register #(.width(64)) B28 (.D(MBR_B_COPY_q), .en(decoder_4bit_2_thirteen), .clk(clock_1_out));  // open: Q, clr
  Register #(.width(64)) B32 (.D(MBR_B_COPY_q), .en(decoder_4bit_2_fifteen), .clk(clock_1_out));  // open: Q, clr

  // Notes on the sheet:
  //   contents of rom_1 (hex, n*v repeats v):
  //   80000000000 e000000000000000 e000000000000000 200000000000 1000000000000000 7800a0000000000 256*0
  //   8600a0000000000 1c000000000000 254*0 183d59000000000 183d10000000000 183d5b000000000 3d10000000000
  //   183d59000000000 183d10000000000 183d5b000000000 3d13000000000 183d59000000000 183d13000000000
  //   183d58000000000 3d13000000000 183d5b000000000 183d10000000000 183d5b000000000 183d13000000000
endmodule

module Dim_Splitter (
  input  [19:0] DIN,
  output [3:0] FLAG,
  output [7:0] ADD_A,
  output [7:0] ADD_B
);


  assign ADD_A = DIN[15:8];
  assign ADD_B = DIN[7:0];
  assign FLAG = DIN[19:16];
endmodule
