// Logisim project trailAnother_Circuit.circ as structural Verilog: 2 circuits, main circuit main
module main (
  input  A,
  input  B,
  input  CIn,
  output sout,
  output cout
);

  wire and_1_out, and_2_out, xor_1_out;

  xor xor_1 (xor_1_out, A, B);
  and and_1 (and_1_out, A, A);
  xor xor_2 (sout, xor_1_out, CIn);
  and and_2 (and_2_out, CIn, xor_1_out);
  or or_1 (cout, and_1_out, and_2_out);
endmodule

module two_bit_adder (
  input  [1:0] in_1,
  input  [1:0] in_2,
  input  in_3,
  output [1:0] sout,
  output cout
);

  wire main_1_cout;

  main main_1 (.A(in_1[0]), .B(in_2[0]), .CIn(in_3), .sout(sout[0]), .cout(main_1_cout));
  main main_2 (.A(in_1[1]), .B(in_2[1]), .CIn(main_1_cout), .sout(sout[1]), .cout(cout));
endmodule
